// Logisim project cpu24.circ as structural Verilog: 24 circuits, main circuit ◇单周期MIPS
module \单周期MIPS  (
  input  IR1,
  input  IR2,
  input  IR3,
  output RegWrite,
  output MemWrite,
  output [31:0] PC,
  output [31:0] IR,
  output [31:0] RDin,
  output [31:0] MDin,
  output [31:0] LedData
);

  wire and_1_out, and_2_out, and_3_out, and_4_out, CLK, clock_2_out, comparator_1_eq, comparator_1_lt,
       comparator_2_eq, comparator_3_eq, comparator_4_eq, d_ff_1_q, equal, Go, IR1_t, IR2_t, IR3_t, IRA, IRB,
       IRC, nand_1_out, not_1_out, not_2_out, or_1_out, or_2_out, \PC使能 , SignedExt, Syscall, W1, W2, W3,
       \单周期硬布线控制器_1_beq , \单周期硬布线控制器_1_bne , \单周期硬布线控制器_1_jr , \总复位 ;
  wire [0:0] \单周期硬布线控制器_1_alu_src , \单周期硬布线控制器_1_memtoreg ;
  wire [1:0] byteoff, \单周期硬布线控制器_1_jmp , \单周期硬布线控制器_1_regdst ;
  wire [3:0] \单周期硬布线控制器_1_alu_op ;
  wire [4:0] multiplexer_5_out, multiplexer_6_out, multiplexer_8_out;
  wire [7:0] multiplexer_4_out;
  wire [12:0] CNT_num;
  wire [15:0] \总周期数 ;
  wire [31:0] adder_1_out, adder_2_out, bit_extender_2_out, bit_extender_3_out, bit_extender_4_out,
       mips_regifile_1_r1, multiplexer_2_out, multiplexer_3_out, multiplexer_7_out, multiplexer_9_out,
       multiplexer_10_out, NextPCNormal, ram_1_data, shifter_1_out;
  wire [31:2] result;

  Button button_1 (.out(\总复位 ));
  Clock #(.highDuration(1), .lowDuration(1)) clock_1 ();  // open: out
  Button _1 (.out(IRA));
  Button _2 (.out(IRB));
  Button _3 (.out(IRC));
  Button \u_继续运行  (.out(Go));
  LED #(.active("true")) led_1 (.in(W1));
  LED #(.active("true")) led_2 (.in(W2));
  LED #(.active("true")) led_3 (.in(W3));
  D_Flip_Flop #(.trigger("high"), .Pre_Clr_Positions("LEGACY"), .NegatePresetClear("false"), .enable("true"), .NewFFLayout("false")) d_ff_1 (.Q(d_ff_1_q));  // open: clk, D, Qn, preset, en, reset
  // Probe on 13'hc
  Hex_Digit_Display hex_digit_display_1 (.value(LedData[31:28]));  // open: dp
  not not_1 (not_1_out, Syscall);
  Comparator #(.width(13), .mode("twosComplement")) comparator_1 (
    .a(CNT_num), .b(13'hc), .eq(comparator_1_eq), .lt(comparator_1_lt));  // open: gt
  Clock #(.highDuration(1), .lowDuration(1)) clock_2 (.out(clock_2_out));
  Hex_Digit_Display hex_digit_display_2 (.value(LedData[27:24]));  // open: dp
  Hex_Digit_Display hex_digit_display_3 (.value(LedData[23:20]));  // open: dp
  or or_1 (or_1_out, not_1_out, Go);
  or or_2 (or_2_out, equal, not_1_out);
  Counter #(.width(13), .max('h1fff), .ongoal("stay"), .trigger("rising"), .behavior("old")) counter_1 (
    .count(comparator_1_lt), .Q(CNT_num), .clk(clock_2_out), .clr(\总复位 ));  // open: load, D, carry, preset
  Hex_Digit_Display hex_digit_display_4 (.value(LedData[19:16]));  // open: dp
  Hex_Digit_Display hex_digit_display_5 (.value(LedData[15:12]));  // open: dp
  D_Flip_Flop #(.trigger("falling"), .Pre_Clr_Positions("ABOVE_BELOW"), .NegatePresetClear("false"), .enable("false"), .NewFFLayout("true")) d_ff_2 (
    .clk(CLK), .D(or_2_out), .Q(\PC使能 ), .preset(or_1_out));  // open: Qn, reset
  nand nand_1 (nand_1_out, d_ff_1_q, comparator_1_eq);
  Hex_Digit_Display hex_digit_display_6 (.value(LedData[11:8]));  // open: dp
  Hex_Digit_Display hex_digit_display_7 (.value(LedData[7:4]));  // open: dp
  // Probe on \总周期数 
  assign \总周期数  = {{3{1'b0}}, CNT_num};  // Bit_Extender bit_extender_1
  assign CLK = nand_1_out ? clock_2_out : 1'bz;  // Controlled_Buffer controlled_buffer_1
  Pull_Resistor #(.pull(1)) pull_resistor_1 (.node(CLK));
  Hex_Digit_Display hex_digit_display_8 (.value(LedData[3:0]));  // open: dp
  or or_3 (IR1_t, IR1, IRA);
  Multiplexer #(.select(2), .width(32), .disabled("Z"), .enable("false")) multiplexer_1 (
    .in0(adder_1_out), .in1(multiplexer_3_out), .in2(adder_2_out), .out(NextPCNormal), .sel(\单周期硬布线控制器_1_jmp ));  // open: in3
  Multiplexer #(.select(1), .width(32), .disabled("Z"), .enable("false")) multiplexer_2 (
    .in0(NextPCNormal), .in1({32{1'b0}}), .out(multiplexer_2_out), .sel(1'b0));
  or or_4 (IR2_t, IR2, IRB);
  Register #(.width(32), .trigger("rising"), .Select("low")) u_PC (
    .D(multiplexer_2_out), .en(\PC使能 ), .Q(PC), .clk(CLK), .clr(\总复位 ));
  Adder #(.width(32)) adder_1 (.a(PC), .b(32'h4), .out(adder_1_out));  // open: cin, cout
  or or_5 (IR3_t, IR3, IRC);
  Multiplexer #(.select(1), .width(32), .disabled("Z"), .enable("false")) multiplexer_3 (
    .in0({PC[31:28], IR[25:0], 2'b00}), .in1(mips_regifile_1_r1), .out(multiplexer_3_out),
    .sel(\单周期硬布线控制器_1_jr ));
  // Mips_Probe mips_probe_1: pin names not known; wires that end beside it: IR
  ROM #(.addrWidth(10), .dataWidth(32), .Select("high")) rom_1 (.addr(PC[11:2]), .data(IR));
  Comparator #(.width(6), .mode("twosComplement")) comparator_2 (
    .a(IR[31:26]), .b(6'b100100), .eq(comparator_2_eq));  // open: gt, lt
  Multiplexer #(.select(2), .width(8), .disabled("Z"), .enable("false")) multiplexer_4 (
    .in0(RDin[7:0]), .in1(RDin[15:8]), .in2(RDin[23:16]), .in3(RDin[31:24]), .out(multiplexer_4_out),
    .sel(byteoff));
  \单周期硬布线控制器  \u_单周期硬布线控制器_1  (
    .Func(IR[5:0]), .OP(IR[31:26]), .ALU_OP(\单周期硬布线控制器_1_alu_op ), .MemToReg(\单周期硬布线控制器_1_memtoreg [0]),
    .MemWrite(MemWrite), .ALU_SRC(\单周期硬布线控制器_1_alu_src [0]), .RegWrite(RegWrite), .SysCALL(Syscall),
    .SignedExt(SignedExt), .RegDst(\单周期硬布线控制器_1_regdst [0]), .JR(\单周期硬布线控制器_1_jr ),
    .JMP(\单周期硬布线控制器_1_jmp [0]), .Beq(\单周期硬布线控制器_1_beq ), .JAL(\单周期硬布线控制器_1_regdst [1]),
    .Bne(\单周期硬布线控制器_1_bne ));
  Multiplexer #(.select(1), .width(5), .disabled("Z"), .enable("false")) multiplexer_5 (
    .in0(IR[25:21]), .in1(5'b00010), .out(multiplexer_5_out), .sel(Syscall));
  Multiplexer #(.select(2), .width(5), .disabled("Z"), .enable("false")) multiplexer_6 (
    .in0(IR[20:16]), .in1(IR[15:11]), .in2({5{1'b1}}), .out(multiplexer_6_out), .sel(\单周期硬布线控制器_1_regdst ));  // open: in3
  Multiplexer #(.select(1), .width(32), .disabled("Z"), .enable("false")) multiplexer_7 (
    .in0(RDin), .in1(bit_extender_2_out), .out(multiplexer_7_out), .sel(comparator_2_eq));
  assign bit_extender_2_out = {{24{1'b0}}, multiplexer_4_out};  // Bit_Extender bit_extender_2
  Multiplexer #(.select(1), .width(5), .disabled("Z"), .enable("false")) multiplexer_8 (
    .in0(IR[20:16]), .in1(5'b00100), .out(multiplexer_8_out), .sel(Syscall));
  assign bit_extender_3_out = {{16{1'b0}}, IR[15:0]};  // Bit_Extender bit_extender_3
  assign bit_extender_4_out = {{16{IR[15]}}, IR[15:0]};  // Bit_Extender bit_extender_4
  MIPS_Regifile mips_regifile_1 (
    .Din(multiplexer_7_out), .Clk(CLK), .R1(mips_regifile_1_r1), .R2(MDin), .WE(RegWrite),
    .W_num(multiplexer_6_out), .R1_num(multiplexer_5_out), .R2_num(multiplexer_8_out));
  Multiplexer #(.select(1), .width(32), .disabled("Z"), .enable("false")) multiplexer_9 (
    .in0(bit_extender_3_out), .in1(bit_extender_4_out), .out(multiplexer_9_out), .sel(SignedExt));
  or or_6 (\单周期硬布线控制器_1_jmp [1], and_2_out, and_3_out, and_1_out);
  Multiplexer #(.select(2), .width(32), .disabled("Z"), .enable("false")) multiplexer_10 (
    .in0(MDin), .in1(multiplexer_9_out), .in2(32'h22), .out(multiplexer_10_out),
    .sel({Syscall, \单周期硬布线控制器_1_alu_src [0]}));  // open: in3
  Shifter #(.width(32), .shift("ll")) shifter_1 (.in(multiplexer_9_out), .\dist (5'b00010), .out(shifter_1_out));
  and and_1 (and_1_out, \单周期硬布线控制器_1_beq , equal);
  MIPS_ALU mips_alu_1 (
    .X(mips_regifile_1_r1), .Y(multiplexer_10_out), .AluOP(\单周期硬布线控制器_1_alu_op ), .Equal(equal),
    .Result({result, byteoff}), .shamt(IR[10:6]));  // open: Result_2
  Comparator #(.width(32), .mode("twosComplement")) comparator_3 (
    .a(32'h1), .b({result, byteoff}), .eq(comparator_3_eq));  // open: gt, lt
  Comparator #(.width(6), .mode("twosComplement")) comparator_4 (
    .a(IR[31:26]), .b(6'b000001), .eq(comparator_4_eq));  // open: gt, lt
  and and_2 (and_2_out, comparator_4_eq, comparator_3_eq);
  and and_3 (and_3_out, not_2_out, \单周期硬布线控制器_1_bne );
  not not_2 (not_2_out, equal);
  Adder #(.width(32)) adder_2 (.a(shifter_1_out), .b(adder_1_out), .out(adder_2_out), .cin(1'b0));  // open: cout
  and and_4 (and_4_out, Syscall, equal);
  Register #(.width(32), .trigger("rising"), .Select("low")) register_1 (
    .D(MDin), .en(and_4_out), .Q(LedData), .clk(CLK), .clr(\总复位 ));
  RAM #(.addrWidth(10), .dataWidth(32), .bus("separate"), .Select("high")) ram_1 (
    .addr(result[11:2]), .din(MDin), .data(ram_1_data), .str(MemWrite), .clk(CLK), .clr(\总复位 ));  // open: sel, ld
  Multiplexer #(.select(2), .width(32), .disabled("Z"), .enable("false")) multiplexer_11 (
    .in0({result, byteoff}), .in1(ram_1_data), .in2(adder_1_out), .out(RDin),
    .sel({\单周期硬布线控制器_1_regdst [1], \单周期硬布线控制器_1_memtoreg [0]}));  // open: in3

  // Other names for the same wires on the sheet: Func[5:0] = IR[5:0]; OP[5:0] = IR[31:26]; result[1:0] = byteoff

  // Notes on the sheet:
  //   中断源
  //   中断等待指示
  //   总复位信号应将除ROM以外所有存储组件全部清零
  //   控制位
  //   暂停节拍，不能为0
  //   戳工具置1进入计数暂停模式，ctrl+k时钟自动运行到对应节拍暂停
  //   ctrl+k关闭时钟连续运行，将控制位置零，进入单步调试模式调试
  //   用这个时钟源需要去掉电路中的其他时钟源
  //   Syscall停机功能模块
  //   数码管输出
  //   数码管输出应该用寄存器锁存，否则显示数据只能一闪而过
  //   可计数暂停的时钟源
  //   指令存储器
  //   指令字
  //   contents of rom_1 (hex, n*v repeats v):
  //   20110001 8000c05 20110001 20120002 20130003 8000c09 20110001 20120002 20130003 8000c0d 20110001
  //   20120002 20130003 8000c11 20110001 20120002 20130003 c000cb8 20100001 20110001 118fc0 112020
  //   20020022 c 118882 12200001 8000c15 112020 20020022 c 20110001 118880 112020 20020022 c 12200001
  //   8000c1f 20110001 118fc0 112020 20020022 c 1188c3 112020 20020022 c 118903 112020 20020022 c 118903
  //   112020 20020022 c 118903 112020 20020022 c 118903 112020 20020022 c 118903 112020 20020022 c 118903
  //   112020 20020022 c 118903 112020 20020022 c 20100001 109fc0 139fc3 8021 2012000c 24160003 26100001
  //   3210000f 20080008 20090001 139900 2709825 132020 20020022 c 1094022 1500fff9 22100001 2018000f
  //   2188024 108700 20080008 20090001 139902 2709825 132021 20020022 c 1094022 1500fff9 108702 2c9b022
  //   12c00001 8000c50 4020 1084027 84400 3508ffff 82021 20020022 c 2010ffff 20110000 ae300000 22100001
  //   22310004 ae300000 22100001 22310004 ae300000 22100001 22310004 ae300000 22100001 22310004 ae300000
  //   22100001 22310004 ae300000 22100001 22310004 ae300000 22100001 22310004 ae300000 22100001 22310004
  //   ae300000 22100001 22310004 ae300000 22100001 22310004 ae300000 22100001 22310004 ae300000 22100001
  //   22310004 ae300000 22100001 22310004 ae300000 22100001 22310004 ae300000 22100001 22310004 ae300000
  //   22100001 22310004 22100001 8020 2011003c 8e130000 8e340000 274402a 11000002 ae330000 ae140000
  //   2231fffc 1611fff8 102020 20020022 c 22100004 2011003c 1611fff2 20020032 c 20100000 22100001 102020
  //   20020022 c 22100002 102020 20020022 c 22100003 102020 20020022 c 22100004 102020 20020022 c 22100005
  //   102020 20020022 c 22100006 102020 20020022 c 22100007 102020 20020022 c 22100008 102020 20020022
  //   20020022 c 3e00008
  //   JMP
  //   JR
  //   OP
  //   Func
  //   Syscall
  //   rs
  //   rt
  //   rd
  //   为方便自动评测，需要输出PC，IR，寄存器堆写如数据RDin
  //   Beq
  //   Bne
  //   MemToReg
  //   MemWrite
  //   AluOP
  //   AluSrcB
  //   RegWrite
  //   JAL
  //   RegDst
  //   RAM写使能MemWrite、RAM写入数据MDin等信号
endmodule

// 单周期硬布线控制器
module \单周期硬布线控制器  (
  input  [5:0] OP,
  input  [5:0] Func,
  output [3:0] ALU_OP,
  output MemToReg,
  output MemWrite,
  output ALU_SRC,
  output RegWrite,
  output SysCALL,
  output SignedExt,
  output RegDst,
  output Beq,
  output Bne,
  output JR,
  output JMP,
  output JAL
);

  \运算控制器自动生成  \u_运算控制器自动生成_1  (
    .OP0(OP[0]), .OP1(OP[1]), .OP2(OP[2]), .OP3(OP[3]), .OP4(OP[4]), .OP5(OP[5]), .F0(Func[0]), .F1(Func[1]),
    .F2(Func[2]), .F3(Func[3]), .F4(Func[4]), .F5(Func[5]), .S0(ALU_OP[0]), .S1(ALU_OP[1]), .S2(ALU_OP[2]),
    .S3(ALU_OP[3]));
  \控制信号自动生成  \u_控制信号自动生成_1  (
    .OP0(OP[0]), .OP1(OP[1]), .OP2(OP[2]), .OP3(OP[3]), .OP4(OP[4]), .OP5(OP[5]), .F0(Func[0]), .F1(Func[1]),
    .F2(Func[2]), .F3(Func[3]), .F4(Func[4]), .F5(Func[5]), .MemToReg(MemToReg), .MemWrite(MemWrite),
    .ALU_SRC(ALU_SRC), .RegWrite(RegWrite), .SysCALL(SysCALL), .SignedExt(SignedExt), .RegDst(RegDst),
    .BEQ(Beq), .BNE(Bne), .JR(JR), .JUMP(JMP), .JAL(JAL));

  // Other names for the same wires on the sheet: OP_CODE[5:0] = OP

  // Notes on the sheet:
  //   运算器控制器，根据指令生成运算器功能选择信号
  //   控制信号生成，产生数据通路需要的其他控制信号
endmodule

// 运算器控制器
module \运算控制器自动生成  (
  input  OP0,
  input  OP1,
  input  OP2,
  input  OP3,
  input  OP4,
  input  OP5,
  input  F0,
  input  F1,
  input  F2,
  input  F3,
  input  F4,
  input  F5,
  output S0,
  output S1,
  output S2,
  output S3
);

  wire and_1_out, and_2_out, and_3_out, and_4_out, and_5_out, and_6_out, and_7_out, and_8_out, and_9_out,
       and_10_out, and_11_out, and_12_out, and_13_out, and_14_out, and_15_out, and_16_out, and_17_out,
       and_18_out, and_19_out, and_20_out, and_21_out, and_22_out, and_23_out, and_24_out, and_25_out,
       and_26_out, and_27_out, and_28_out, and_29_out, and_30_out, and_31_out, and_32_out, and_33_out,
       and_34_out, and_35_out, and_36_out, and_37_out, and_38_out, and_39_out, and_40_out, and_41_out,
       and_42_out, and_43_out, and_44_out, and_45_out, and_46_out, not_1_out, not_2_out, not_3_out,
       not_4_out, not_5_out, not_6_out, not_7_out, not_8_out, not_9_out, not_10_out, not_11_out, not_12_out,
       not_13_out, not_14_out, not_15_out, not_16_out, not_17_out, not_18_out, not_19_out, not_20_out,
       not_21_out, not_22_out, not_23_out, not_24_out, not_25_out, not_26_out, not_27_out, not_28_out,
       not_29_out, not_30_out, not_31_out, not_32_out, not_33_out, not_34_out, not_35_out, not_36_out,
       not_37_out, not_38_out, not_39_out, not_40_out, not_41_out, not_42_out, not_43_out, not_44_out,
       not_45_out, not_46_out, not_47_out, not_48_out, not_49_out, not_50_out, not_51_out, not_52_out,
       not_53_out, not_54_out, not_55_out, not_56_out, not_57_out, not_58_out, not_59_out, not_60_out,
       not_61_out, not_62_out, not_63_out, not_64_out, not_65_out, not_66_out, not_67_out, not_68_out,
       not_69_out, not_70_out, not_71_out, not_72_out, not_73_out, not_74_out, not_75_out, not_76_out,
       not_77_out, not_78_out, not_79_out, not_80_out, not_81_out, not_82_out, not_83_out, not_84_out,
       not_85_out, not_86_out, not_87_out, not_88_out, not_89_out, not_90_out, not_91_out, not_92_out,
       not_93_out, not_94_out, not_95_out, not_96_out, not_97_out, not_98_out, not_99_out, not_100_out,
       not_101_out, not_102_out, not_103_out, not_104_out, not_105_out, not_106_out, not_107_out,
       not_108_out, not_109_out, not_110_out, not_111_out, not_112_out, not_113_out, not_114_out,
       not_115_out, not_116_out, not_117_out, not_118_out, not_119_out, not_120_out, not_121_out,
       not_122_out, not_123_out, not_124_out, not_125_out, not_126_out, not_127_out, not_128_out,
       not_129_out, not_130_out, not_131_out, not_132_out, not_133_out, not_134_out, not_135_out,
       not_136_out, not_137_out, not_138_out, not_139_out, not_140_out, not_141_out, not_142_out,
       not_143_out, not_144_out, not_145_out, not_146_out, not_147_out, not_148_out, not_149_out,
       not_150_out, not_151_out, not_152_out, not_153_out, not_154_out, not_155_out, not_156_out,
       not_157_out, not_158_out, not_159_out, not_160_out, not_161_out, not_162_out, not_163_out,
       not_164_out, not_165_out, not_166_out, not_167_out, not_168_out, not_169_out, not_170_out,
       not_171_out, not_172_out, not_173_out, not_174_out, not_175_out, not_176_out, not_177_out,
       not_178_out, not_179_out, not_180_out, not_181_out, not_182_out, not_183_out, not_184_out,
       not_185_out, not_186_out, not_187_out, not_188_out, not_189_out, not_190_out, not_191_out,
       not_192_out, not_193_out, not_194_out, not_195_out, not_196_out, not_197_out, not_198_out,
       not_199_out, not_200_out, not_201_out, not_202_out, not_203_out, not_204_out, not_205_out,
       not_206_out, not_207_out, not_208_out, not_209_out, not_210_out, not_211_out, not_212_out,
       not_213_out, not_214_out, not_215_out, not_216_out, not_217_out, not_218_out, not_219_out,
       not_220_out, not_221_out, not_222_out, not_223_out, not_224_out, not_225_out, not_226_out,
       not_227_out, not_228_out, not_229_out, not_230_out, not_231_out, not_232_out, not_233_out,
       not_234_out, not_235_out, not_236_out, not_237_out, not_238_out, not_239_out, not_240_out,
       not_241_out, not_242_out, not_243_out, not_244_out, not_245_out, not_246_out, not_247_out,
       not_248_out, not_249_out, not_250_out, not_251_out, not_252_out, not_253_out, not_254_out,
       not_255_out, not_256_out, not_257_out, not_258_out, not_259_out, not_260_out, not_261_out,
       not_262_out, not_263_out, not_264_out, not_265_out, not_266_out, not_267_out, not_268_out,
       not_269_out, not_270_out, not_271_out, not_272_out, not_273_out, not_274_out, not_275_out,
       not_276_out, not_277_out, not_278_out, not_279_out, not_280_out, not_281_out, not_282_out,
       not_283_out, not_284_out, not_285_out, not_286_out, not_287_out, not_288_out, not_289_out,
       not_290_out, not_291_out, not_292_out, not_293_out, not_294_out, not_295_out, not_296_out,
       not_297_out, not_298_out, not_299_out, not_300_out, not_301_out, not_302_out, not_303_out,
       not_304_out, not_305_out, not_306_out;

  not not_1 (not_1_out, OP5);
  not not_2 (not_2_out, OP4);
  not not_3 (not_3_out, OP3);
  not not_4 (not_4_out, OP2);
  not not_5 (not_5_out, OP1);
  not not_6 (not_6_out, OP0);
  not not_7 (not_7_out, F5);
  not not_8 (not_8_out, F4);
  not not_9 (not_9_out, F3);
  not not_10 (not_10_out, F2);
  not not_11 (not_11_out, OP5);
  not not_12 (not_12_out, OP4);
  not not_13 (not_13_out, OP3);
  not not_14 (not_14_out, OP2);
  not not_15 (not_15_out, OP1);
  not not_16 (not_16_out, OP0);
  not not_17 (not_17_out, F4);
  not not_18 (not_18_out, F3);
  not not_19 (not_19_out, F2);
  not not_20 (not_20_out, F1);
  not not_21 (not_21_out, F0);
  not not_22 (not_22_out, OP5);
  not not_23 (not_23_out, OP4);
  not not_24 (not_24_out, OP3);
  not not_25 (not_25_out, OP2);
  not not_26 (not_26_out, OP1);
  not not_27 (not_27_out, OP0);
  not not_28 (not_28_out, F4);
  not not_29 (not_29_out, F3);
  not not_30 (not_30_out, F2);
  not not_31 (not_31_out, F1);
  not not_32 (not_32_out, OP5);
  not not_33 (not_33_out, OP4);
  not not_34 (not_34_out, OP3);
  not not_35 (not_35_out, OP2);
  not not_36 (not_36_out, OP1);
  not not_37 (not_37_out, OP0);
  not not_38 (not_38_out, F4);
  not not_39 (not_39_out, F3);
  not not_40 (not_40_out, F1);
  not not_41 (not_41_out, F0);
  not not_42 (not_42_out, OP5);
  not not_43 (not_43_out, OP4);
  not not_44 (not_44_out, OP3);
  not not_45 (not_45_out, OP2);
  not not_46 (not_46_out, OP1);
  not not_47 (not_47_out, OP0);
  not not_48 (not_48_out, F4);
  not not_49 (not_49_out, F2);
  not not_50 (not_50_out, F0);
  not not_51 (not_51_out, OP5);
  not not_52 (not_52_out, OP4);
  not not_53 (not_53_out, OP2);
  not not_54 (not_54_out, OP1);
  not not_55 (not_55_out, OP0);
  not not_56 (not_56_out, OP5);
  not not_57 (not_57_out, OP4);
  not not_58 (not_58_out, OP1);
  not not_59 (not_59_out, OP0);
  not not_60 (not_60_out, OP5);
  not not_61 (not_61_out, OP4);
  not not_62 (not_62_out, OP2);
  not not_63 (not_63_out, OP1);
  not not_64 (not_64_out, OP5);
  not not_65 (not_65_out, OP4);
  not not_66 (not_66_out, OP2);
  not not_67 (not_67_out, OP0);
  not not_68 (not_68_out, OP4);
  not not_69 (not_69_out, OP3);
  not not_70 (not_70_out, OP2);
  not not_71 (not_71_out, OP4);
  not not_72 (not_72_out, OP2);
  not not_73 (not_73_out, OP5);
  not not_74 (not_74_out, OP4);
  not not_75 (not_75_out, OP3);
  not not_76 (not_76_out, OP2);
  not not_77 (not_77_out, OP1);
  not not_78 (not_78_out, OP0);
  not not_79 (not_79_out, F5);
  not not_80 (not_80_out, F4);
  not not_81 (not_81_out, F3);
  not not_82 (not_82_out, F1);
  not not_83 (not_83_out, F0);
  not not_84 (not_84_out, OP4);
  not not_85 (not_85_out, OP3);
  not not_86 (not_86_out, OP1);
  not not_87 (not_87_out, OP0);
  not not_88 (not_88_out, OP5);
  not not_89 (not_89_out, OP4);
  not not_90 (not_90_out, OP3);
  not not_91 (not_91_out, OP2);
  not not_92 (not_92_out, OP1);
  not not_93 (not_93_out, OP5);
  not not_94 (not_94_out, OP4);
  not not_95 (not_95_out, OP3);
  not not_96 (not_96_out, OP2);
  not not_97 (not_97_out, OP1);
  not not_98 (not_98_out, OP0);
  not not_99 (not_99_out, F5);
  not not_100 (not_100_out, F4);
  not not_101 (not_101_out, F3);
  not not_102 (not_102_out, F2);
  not not_103 (not_103_out, F0);
  not not_104 (not_104_out, OP5);
  not not_105 (not_105_out, OP4);
  not not_106 (not_106_out, OP3);
  not not_107 (not_107_out, OP2);
  not not_108 (not_108_out, OP1);
  not not_109 (not_109_out, OP0);
  not not_110 (not_110_out, F4);
  not not_111 (not_111_out, F3);
  not not_112 (not_112_out, F2);
  not not_113 (not_113_out, F0);
  not not_114 (not_114_out, OP5);
  not not_115 (not_115_out, OP4);
  not not_116 (not_116_out, OP3);
  not not_117 (not_117_out, OP2);
  not not_118 (not_118_out, OP1);
  not not_119 (not_119_out, OP0);
  not not_120 (not_120_out, F4);
  not not_121 (not_121_out, F3);
  not not_122 (not_122_out, F1);
  not not_123 (not_123_out, F0);
  not not_124 (not_124_out, OP5);
  not not_125 (not_125_out, OP4);
  not not_126 (not_126_out, OP3);
  not not_127 (not_127_out, OP2);
  not not_128 (not_128_out, OP1);
  not not_129 (not_129_out, OP0);
  not not_130 (not_130_out, F4);
  not not_131 (not_131_out, F3);
  not not_132 (not_132_out, OP5);
  not not_133 (not_133_out, OP4);
  not not_134 (not_134_out, OP3);
  not not_135 (not_135_out, OP2);
  not not_136 (not_136_out, OP1);
  not not_137 (not_137_out, OP0);
  not not_138 (not_138_out, F4);
  not not_139 (not_139_out, F2);
  not not_140 (not_140_out, F0);
  not not_141 (not_141_out, OP5);
  not not_142 (not_142_out, OP4);
  not not_143 (not_143_out, OP1);
  not not_144 (not_144_out, OP0);
  not not_145 (not_145_out, OP5);
  not not_146 (not_146_out, OP4);
  not not_147 (not_147_out, OP2);
  not not_148 (not_148_out, OP0);
  not not_149 (not_149_out, OP5);
  not not_150 (not_150_out, OP4);
  not not_151 (not_151_out, OP2);
  not not_152 (not_152_out, OP5);
  not not_153 (not_153_out, OP4);
  not not_154 (not_154_out, OP3);
  not not_155 (not_155_out, OP2);
  not not_156 (not_156_out, OP1);
  not not_157 (not_157_out, OP5);
  not not_158 (not_158_out, OP4);
  not not_159 (not_159_out, OP3);
  not not_160 (not_160_out, OP2);
  not not_161 (not_161_out, OP1);
  not not_162 (not_162_out, OP0);
  not not_163 (not_163_out, F4);
  not not_164 (not_164_out, F3);
  not not_165 (not_165_out, F2);
  not not_166 (not_166_out, F1);
  not not_167 (not_167_out, F0);
  not not_168 (not_168_out, OP5);
  not not_169 (not_169_out, OP4);
  not not_170 (not_170_out, OP3);
  not not_171 (not_171_out, OP2);
  not not_172 (not_172_out, OP1);
  not not_173 (not_173_out, OP0);
  not not_174 (not_174_out, F4);
  not not_175 (not_175_out, F3);
  not not_176 (not_176_out, F2);
  not not_177 (not_177_out, F1);
  not not_178 (not_178_out, OP5);
  not not_179 (not_179_out, OP4);
  not not_180 (not_180_out, OP3);
  not not_181 (not_181_out, OP2);
  not not_182 (not_182_out, OP1);
  not not_183 (not_183_out, OP0);
  not not_184 (not_184_out, F4);
  not not_185 (not_185_out, F3);
  not not_186 (not_186_out, F2);
  not not_187 (not_187_out, F0);
  not not_188 (not_188_out, OP5);
  not not_189 (not_189_out, OP4);
  not not_190 (not_190_out, OP3);
  not not_191 (not_191_out, OP2);
  not not_192 (not_192_out, OP1);
  not not_193 (not_193_out, OP0);
  not not_194 (not_194_out, F4);
  not not_195 (not_195_out, F3);
  not not_196 (not_196_out, F1);
  not not_197 (not_197_out, F0);
  not not_198 (not_198_out, OP5);
  not not_199 (not_199_out, OP4);
  not not_200 (not_200_out, OP3);
  not not_201 (not_201_out, OP2);
  not not_202 (not_202_out, OP1);
  not not_203 (not_203_out, OP0);
  not not_204 (not_204_out, F4);
  not not_205 (not_205_out, F2);
  not not_206 (not_206_out, OP5);
  not not_207 (not_207_out, OP4);
  not not_208 (not_208_out, OP2);
  not not_209 (not_209_out, OP1);
  not not_210 (not_210_out, OP0);
  not not_211 (not_211_out, OP5);
  not not_212 (not_212_out, OP4);
  not not_213 (not_213_out, OP1);
  not not_214 (not_214_out, OP0);
  not not_215 (not_215_out, OP5);
  not not_216 (not_216_out, OP4);
  not not_217 (not_217_out, OP2);
  not not_218 (not_218_out, OP1);
  not not_219 (not_219_out, OP4);
  not not_220 (not_220_out, OP3);
  not not_221 (not_221_out, OP2);
  not not_222 (not_222_out, OP4);
  not not_223 (not_223_out, OP2);
  not not_224 (not_224_out, OP5);
  not not_225 (not_225_out, OP4);
  not not_226 (not_226_out, OP3);
  not not_227 (not_227_out, OP2);
  not not_228 (not_228_out, OP1);
  not not_229 (not_229_out, OP0);
  not not_230 (not_230_out, F5);
  not not_231 (not_231_out, F4);
  not not_232 (not_232_out, F3);
  not not_233 (not_233_out, F1);
  not not_234 (not_234_out, F0);
  not not_235 (not_235_out, OP5);
  not not_236 (not_236_out, OP4);
  not not_237 (not_237_out, OP2);
  not not_238 (not_238_out, OP4);
  not not_239 (not_239_out, OP3);
  not not_240 (not_240_out, OP1);
  not not_241 (not_241_out, OP0);
  not not_242 (not_242_out, OP5);
  not not_243 (not_243_out, OP4);
  not not_244 (not_244_out, OP3);
  not not_245 (not_245_out, OP2);
  not not_246 (not_246_out, OP1);
  not not_247 (not_247_out, OP5);
  not not_248 (not_248_out, OP4);
  not not_249 (not_249_out, OP3);
  not not_250 (not_250_out, OP2);
  not not_251 (not_251_out, OP1);
  not not_252 (not_252_out, OP0);
  not not_253 (not_253_out, F4);
  not not_254 (not_254_out, F3);
  not not_255 (not_255_out, F1);
  not not_256 (not_256_out, OP5);
  not not_257 (not_257_out, OP4);
  not not_258 (not_258_out, OP3);
  not not_259 (not_259_out, OP2);
  not not_260 (not_260_out, OP1);
  not not_261 (not_261_out, OP0);
  not not_262 (not_262_out, F4);
  not not_263 (not_263_out, F3);
  not not_264 (not_264_out, OP5);
  not not_265 (not_265_out, OP4);
  not not_266 (not_266_out, OP3);
  not not_267 (not_267_out, OP2);
  not not_268 (not_268_out, OP1);
  not not_269 (not_269_out, OP0);
  not not_270 (not_270_out, F4);
  not not_271 (not_271_out, F2);
  not not_272 (not_272_out, F0);
  not not_273 (not_273_out, OP5);
  not not_274 (not_274_out, OP4);
  not not_275 (not_275_out, OP3);
  not not_276 (not_276_out, OP2);
  not not_277 (not_277_out, OP1);
  not not_278 (not_278_out, OP0);
  not not_279 (not_279_out, F4);
  not not_280 (not_280_out, F2);
  not not_281 (not_281_out, OP5);
  not not_282 (not_282_out, OP4);
  not not_283 (not_283_out, OP2);
  not not_284 (not_284_out, OP0);
  not not_285 (not_285_out, OP5);
  not not_286 (not_286_out, OP4);
  not not_287 (not_287_out, OP1);
  not not_288 (not_288_out, OP5);
  not not_289 (not_289_out, OP4);
  not not_290 (not_290_out, OP3);
  not not_291 (not_291_out, OP2);
  not not_292 (not_292_out, OP1);
  not not_293 (not_293_out, OP0);
  not not_294 (not_294_out, F5);
  not not_295 (not_295_out, F4);
  not not_296 (not_296_out, F3);
  not not_297 (not_297_out, F1);
  not not_298 (not_298_out, F0);
  not not_299 (not_299_out, OP5);
  not not_300 (not_300_out, OP4);
  not not_301 (not_301_out, OP2);
  not not_302 (not_302_out, OP5);
  not not_303 (not_303_out, OP4);
  not not_304 (not_304_out, OP3);
  not not_305 (not_305_out, OP2);
  not not_306 (not_306_out, OP1);
  and and_1 (and_1_out, not_1_out, not_2_out, not_3_out, not_4_out, not_5_out, not_6_out, not_7_out, not_8_out, not_9_out, not_10_out, F1, F0);
  and and_2 (and_2_out, not_11_out, not_12_out, not_13_out, not_14_out, not_15_out, not_16_out, F5, not_17_out, not_18_out, not_19_out, not_20_out, not_21_out);
  and and_3 (and_3_out, not_22_out, not_23_out, not_24_out, not_25_out, not_26_out, not_27_out, F5, not_28_out, not_29_out, not_30_out, not_31_out, F0);
  and and_4 (and_4_out, not_32_out, not_33_out, not_34_out, not_35_out, not_36_out, not_37_out, F5, not_38_out, not_39_out, F2, not_40_out, not_41_out);
  and and_5 (and_5_out, not_42_out, not_43_out, not_44_out, not_45_out, not_46_out, not_47_out, F5, not_48_out, F3, not_49_out, F1, not_50_out);
  and and_6 (and_6_out, not_51_out, not_52_out, OP3, not_53_out, not_54_out, not_55_out);
  and and_7 (and_7_out, not_56_out, not_57_out, OP3, OP2, not_58_out, not_59_out);
  and and_8 (and_8_out, not_60_out, not_61_out, OP3, not_62_out, not_63_out, OP0);
  and and_9 (and_9_out, not_64_out, not_65_out, OP3, not_66_out, OP1, not_67_out);
  and and_10 (and_10_out, OP5, not_68_out, not_69_out, not_70_out, OP1, OP0);
  and and_11 (and_11_out, OP5, not_71_out, OP3, not_72_out, OP1, OP0);
  and and_12 (and_12_out, not_73_out, not_74_out, not_75_out, not_76_out, not_77_out, not_78_out, not_79_out, not_80_out, not_81_out, F2, not_82_out, not_83_out);
  and and_13 (and_13_out, OP5, not_84_out, not_85_out, OP2, not_86_out, not_87_out);
  and and_14 (and_14_out, not_88_out, not_89_out, not_90_out, not_91_out, not_92_out, OP0);
  and and_15 (and_15_out, not_93_out, not_94_out, not_95_out, not_96_out, not_97_out, not_98_out, not_99_out, not_100_out, not_101_out, not_102_out, F1, not_103_out);
  and and_16 (and_16_out, not_104_out, not_105_out, not_106_out, not_107_out, not_108_out, not_109_out, F5, not_110_out, not_111_out, not_112_out, F1, not_113_out);
  and and_17 (and_17_out, not_114_out, not_115_out, not_116_out, not_117_out, not_118_out, not_119_out, F5, not_120_out, not_121_out, F2, not_122_out, not_123_out);
  and and_18 (and_18_out, not_124_out, not_125_out, not_126_out, not_127_out, not_128_out, not_129_out, F5, not_130_out, not_131_out, F2, F1, F0);
  and and_19 (and_19_out, not_132_out, not_133_out, not_134_out, not_135_out, not_136_out, not_137_out, F5, not_138_out, F3, not_139_out, F1, not_140_out);
  and and_20 (and_20_out, not_141_out, not_142_out, OP3, OP2, not_143_out, not_144_out);
  and and_21 (and_21_out, not_145_out, not_146_out, OP3, not_147_out, OP1, not_148_out);
  and and_22 (and_22_out, not_149_out, not_150_out, OP3, not_151_out, OP1, OP0);
  and and_23 (and_23_out, not_152_out, not_153_out, not_154_out, not_155_out, not_156_out, OP0);
  and and_24 (and_24_out, not_157_out, not_158_out, not_159_out, not_160_out, not_161_out, not_162_out, F5, not_163_out, not_164_out, not_165_out, not_166_out, not_167_out);
  and and_25 (and_25_out, not_168_out, not_169_out, not_170_out, not_171_out, not_172_out, not_173_out, F5, not_174_out, not_175_out, not_176_out, not_177_out, F0);
  and and_26 (and_26_out, not_178_out, not_179_out, not_180_out, not_181_out, not_182_out, not_183_out, F5, not_184_out, not_185_out, not_186_out, F1, not_187_out);
  and and_27 (and_27_out, not_188_out, not_189_out, not_190_out, not_191_out, not_192_out, not_193_out, F5, not_194_out, not_195_out, F2, not_196_out, not_197_out);
  and and_28 (and_28_out, not_198_out, not_199_out, not_200_out, not_201_out, not_202_out, not_203_out, F5, not_204_out, F3, not_205_out, F1, F0);
  and and_29 (and_29_out, not_206_out, not_207_out, OP3, not_208_out, not_209_out, not_210_out);
  and and_30 (and_30_out, not_211_out, not_212_out, OP3, OP2, not_213_out, not_214_out);
  and and_31 (and_31_out, not_215_out, not_216_out, OP3, not_217_out, not_218_out, OP0);
  and and_32 (and_32_out, OP5, not_219_out, not_220_out, not_221_out, OP1, OP0);
  and and_33 (and_33_out, OP5, not_222_out, OP3, not_223_out, OP1, OP0);
  and and_34 (and_34_out, not_224_out, not_225_out, not_226_out, not_227_out, not_228_out, not_229_out, not_230_out, not_231_out, not_232_out, F2, not_233_out, not_234_out);
  and and_35 (and_35_out, not_235_out, not_236_out, OP3, not_237_out, OP1, OP0);
  and and_36 (and_36_out, OP5, not_238_out, not_239_out, OP2, not_240_out, not_241_out);
  and and_37 (and_37_out, not_242_out, not_243_out, not_244_out, not_245_out, not_246_out, OP0);
  and and_38 (and_38_out, not_247_out, not_248_out, not_249_out, not_250_out, not_251_out, not_252_out, F5, not_253_out, not_254_out, F2, not_255_out, F0);
  and and_39 (and_39_out, not_256_out, not_257_out, not_258_out, not_259_out, not_260_out, not_261_out, F5, not_262_out, not_263_out, F2, F1, F0);
  and and_40 (and_40_out, not_264_out, not_265_out, not_266_out, not_267_out, not_268_out, not_269_out, F5, not_270_out, F3, not_271_out, F1, not_272_out);
  and and_41 (and_41_out, not_273_out, not_274_out, not_275_out, not_276_out, not_277_out, not_278_out, F5, not_279_out, F3, not_280_out, F1, F0);
  and and_42 (and_42_out, not_281_out, not_282_out, OP3, not_283_out, OP1, not_284_out);
  and and_43 (and_43_out, not_285_out, not_286_out, OP3, OP2, not_287_out, OP0);
  and and_44 (and_44_out, not_288_out, not_289_out, not_290_out, not_291_out, not_292_out, not_293_out, not_294_out, not_295_out, not_296_out, F2, not_297_out, not_298_out);
  and and_45 (and_45_out, not_299_out, not_300_out, OP3, not_301_out, OP1, OP0);
  and and_46 (and_46_out, not_302_out, not_303_out, not_304_out, not_305_out, not_306_out, OP0);
  or or_1 (S1, and_15_out, and_16_out, and_17_out, and_18_out, and_19_out, and_20_out, and_21_out, and_22_out, and_23_out);
  or or_2 (S3, and_38_out, and_39_out, and_40_out, and_41_out, and_42_out, and_43_out, and_44_out, and_45_out, and_46_out);
  or or_3 (S0, and_1_out, and_2_out, and_3_out, and_4_out, and_5_out, and_6_out, and_7_out, and_8_out, and_9_out, and_10_out, and_11_out, and_12_out, and_13_out, and_14_out);
  or or_4 (S2, and_24_out, and_25_out, and_26_out, and_27_out, and_28_out, and_29_out, and_30_out, and_31_out, and_32_out, and_33_out, and_34_out, and_35_out, and_36_out, and_37_out);
endmodule

// 控制信号生成
module \控制信号自动生成  (
  input  OP0,
  input  OP1,
  input  OP2,
  input  OP3,
  input  OP4,
  input  OP5,
  input  F0,
  input  F1,
  input  F2,
  input  F3,
  input  F4,
  input  F5,
  output MemToReg,
  output MemWrite,
  output ALU_SRC,
  output RegWrite,
  output SysCALL,
  output SignedExt,
  output RegDst,
  output BEQ,
  output BNE,
  output JR,
  output JUMP,
  output JAL
);

  wire and_1_out, and_2_out, and_4_out, and_5_out, and_6_out, and_7_out, and_8_out, and_9_out, and_10_out,
       and_11_out, and_12_out, and_13_out, and_14_out, and_15_out, and_16_out, and_17_out, and_18_out,
       and_20_out, and_21_out, and_22_out, and_23_out, and_24_out, and_25_out, and_26_out, and_27_out,
       and_28_out, and_32_out, and_33_out, not_1_out, not_2_out, not_3_out, not_4_out, not_5_out, not_6_out,
       not_7_out, not_8_out, not_9_out, not_10_out, not_11_out, not_12_out, not_13_out, not_14_out,
       not_15_out, not_16_out, not_17_out, not_18_out, not_19_out, not_20_out, not_21_out, not_22_out,
       not_23_out, not_24_out, not_25_out, not_26_out, not_27_out, not_28_out, not_29_out, not_30_out,
       not_31_out, not_32_out, not_33_out, not_34_out, not_35_out, not_36_out, not_37_out, not_38_out,
       not_39_out, not_40_out, not_41_out, not_42_out, not_43_out, not_44_out, not_45_out, not_46_out,
       not_47_out, not_48_out, not_49_out, not_50_out, not_51_out, not_52_out, not_53_out, not_54_out,
       not_55_out, not_56_out, not_57_out, not_58_out, not_59_out, not_60_out, not_61_out, not_62_out,
       not_63_out, not_64_out, not_65_out, not_66_out, not_67_out, not_68_out, not_69_out, not_70_out,
       not_71_out, not_72_out, not_73_out, not_74_out, not_75_out, not_76_out, not_77_out, not_78_out,
       not_79_out, not_80_out, not_81_out, not_82_out, not_83_out, not_84_out, not_85_out, not_86_out,
       not_87_out, not_88_out, not_89_out, not_90_out, not_91_out, not_92_out, not_93_out, not_94_out,
       not_95_out, not_96_out, not_97_out, not_98_out, not_99_out, not_100_out, not_101_out, not_102_out,
       not_103_out, not_104_out, not_105_out, not_106_out, not_107_out, not_108_out, not_109_out,
       not_110_out, not_111_out, not_112_out, not_113_out, not_114_out, not_115_out, not_116_out,
       not_117_out, not_118_out, not_119_out, not_120_out, not_121_out, not_122_out, not_123_out,
       not_124_out, not_125_out, not_126_out, not_127_out, not_128_out, not_129_out, not_130_out,
       not_131_out, not_132_out, not_133_out, not_134_out, not_135_out, not_136_out, not_137_out,
       not_138_out, not_139_out, not_140_out, not_141_out, not_142_out, not_143_out, not_144_out,
       not_145_out, not_146_out, not_147_out, not_148_out, not_149_out, not_150_out, not_151_out,
       not_152_out, not_153_out, not_154_out, not_155_out, not_156_out, not_157_out, not_158_out,
       not_159_out, not_160_out, not_161_out, not_162_out, not_163_out, not_164_out, not_165_out,
       not_166_out, not_167_out, not_168_out, not_169_out, not_170_out, not_171_out, not_172_out,
       not_173_out, not_174_out, not_175_out, not_176_out, not_177_out, not_178_out, not_179_out,
       not_180_out, not_181_out, not_182_out, not_183_out, not_184_out, not_185_out, not_186_out,
       not_187_out, not_188_out, not_189_out, not_190_out, not_191_out, not_192_out, not_193_out,
       not_194_out, not_195_out, not_196_out, not_197_out, not_198_out, not_199_out, not_200_out, not_201_out;

  not not_1 (not_1_out, OP0);
  not not_2 (not_2_out, OP1);
  not not_3 (not_3_out, OP3);
  not not_4 (not_4_out, OP4);
  not not_5 (not_5_out, OP2);
  not not_6 (not_6_out, OP3);
  not not_7 (not_7_out, OP4);
  not not_8 (not_8_out, OP2);
  not not_9 (not_9_out, OP4);
  not not_10 (not_10_out, OP1);
  not not_11 (not_11_out, OP4);
  not not_12 (not_12_out, OP5);
  not not_13 (not_13_out, OP2);
  not not_14 (not_14_out, OP4);
  not not_15 (not_15_out, OP5);
  not not_16 (not_16_out, OP0);
  not not_17 (not_17_out, OP1);
  not not_18 (not_18_out, OP3);
  not not_19 (not_19_out, OP4);
  not not_20 (not_20_out, OP1);
  not not_21 (not_21_out, OP2);
  not not_22 (not_22_out, OP4);
  not not_23 (not_23_out, OP5);
  not not_24 (not_24_out, OP2);
  not not_25 (not_25_out, OP4);
  not not_26 (not_26_out, OP0);
  not not_27 (not_27_out, OP1);
  not not_28 (not_28_out, OP2);
  not not_29 (not_29_out, OP4);
  not not_30 (not_30_out, OP5);
  not not_31 (not_31_out, F0);
  not not_32 (not_32_out, F1);
  not not_33 (not_33_out, F3);
  not not_34 (not_34_out, F4);
  not not_35 (not_35_out, OP0);
  not not_36 (not_36_out, OP1);
  not not_37 (not_37_out, OP2);
  not not_38 (not_38_out, OP4);
  not not_39 (not_39_out, OP5);
  not not_40 (not_40_out, F0);
  not not_41 (not_41_out, F2);
  not not_42 (not_42_out, F3);
  not not_43 (not_43_out, F4);
  not not_44 (not_44_out, OP0);
  not not_45 (not_45_out, OP1);
  not not_46 (not_46_out, OP2);
  not not_47 (not_47_out, OP4);
  not not_48 (not_48_out, OP5);
  not not_49 (not_49_out, F1);
  not not_50 (not_50_out, F3);
  not not_51 (not_51_out, F4);
  not not_52 (not_52_out, OP0);
  not not_53 (not_53_out, OP1);
  not not_54 (not_54_out, OP2);
  not not_55 (not_55_out, OP4);
  not not_56 (not_56_out, OP5);
  not not_57 (not_57_out, F2);
  not not_58 (not_58_out, F3);
  not not_59 (not_59_out, F4);
  not not_60 (not_60_out, F5);
  not not_61 (not_61_out, OP0);
  not not_62 (not_62_out, OP1);
  not not_63 (not_63_out, OP2);
  not not_64 (not_64_out, OP4);
  not not_65 (not_65_out, OP5);
  not not_66 (not_66_out, F2);
  not not_67 (not_67_out, F4);
  not not_68 (not_68_out, OP0);
  not not_69 (not_69_out, OP1);
  not not_70 (not_70_out, OP2);
  not not_71 (not_71_out, OP4);
  not not_72 (not_72_out, OP5);
  not not_73 (not_73_out, F3);
  not not_74 (not_74_out, F4);
  not not_75 (not_75_out, OP1);
  not not_76 (not_76_out, OP4);
  not not_77 (not_77_out, OP5);
  not not_78 (not_78_out, OP2);
  not not_79 (not_79_out, OP4);
  not not_80 (not_80_out, OP5);
  not not_81 (not_81_out, OP0);
  not not_82 (not_82_out, OP1);
  not not_83 (not_83_out, OP3);
  not not_84 (not_84_out, OP4);
  not not_85 (not_85_out, OP2);
  not not_86 (not_86_out, OP3);
  not not_87 (not_87_out, OP4);
  not not_88 (not_88_out, OP0);
  not not_89 (not_89_out, OP1);
  not not_90 (not_90_out, OP2);
  not not_91 (not_91_out, OP3);
  not not_92 (not_92_out, OP4);
  not not_93 (not_93_out, OP5);
  not not_94 (not_94_out, F0);
  not not_95 (not_95_out, F1);
  not not_96 (not_96_out, F4);
  not not_97 (not_97_out, F5);
  not not_98 (not_98_out, OP2);
  not not_99 (not_99_out, OP4);
  not not_100 (not_100_out, OP5);
  not not_101 (not_101_out, OP1);
  not not_102 (not_102_out, OP3);
  not not_103 (not_103_out, OP4);
  not not_104 (not_104_out, OP5);
  not not_105 (not_105_out, OP1);
  not not_106 (not_106_out, OP2);
  not not_107 (not_107_out, OP4);
  not not_108 (not_108_out, OP5);
  not not_109 (not_109_out, OP0);
  not not_110 (not_110_out, OP1);
  not not_111 (not_111_out, OP2);
  not not_112 (not_112_out, OP3);
  not not_113 (not_113_out, OP4);
  not not_114 (not_114_out, OP5);
  not not_115 (not_115_out, F0);
  not not_116 (not_116_out, F1);
  not not_117 (not_117_out, F3);
  not not_118 (not_118_out, F4);
  not not_119 (not_119_out, OP0);
  not not_120 (not_120_out, OP1);
  not not_121 (not_121_out, OP2);
  not not_122 (not_122_out, OP3);
  not not_123 (not_123_out, OP4);
  not not_124 (not_124_out, OP5);
  not not_125 (not_125_out, F0);
  not not_126 (not_126_out, F2);
  not not_127 (not_127_out, F3);
  not not_128 (not_128_out, F4);
  not not_129 (not_129_out, OP0);
  not not_130 (not_130_out, OP1);
  not not_131 (not_131_out, OP2);
  not not_132 (not_132_out, OP3);
  not not_133 (not_133_out, OP4);
  not not_134 (not_134_out, OP5);
  not not_135 (not_135_out, F1);
  not not_136 (not_136_out, F3);
  not not_137 (not_137_out, F4);
  not not_138 (not_138_out, OP0);
  not not_139 (not_139_out, OP1);
  not not_140 (not_140_out, OP2);
  not not_141 (not_141_out, OP3);
  not not_142 (not_142_out, OP4);
  not not_143 (not_143_out, OP5);
  not not_144 (not_144_out, F2);
  not not_145 (not_145_out, F3);
  not not_146 (not_146_out, F4);
  not not_147 (not_147_out, F5);
  not not_148 (not_148_out, OP0);
  not not_149 (not_149_out, OP1);
  not not_150 (not_150_out, OP2);
  not not_151 (not_151_out, OP3);
  not not_152 (not_152_out, OP4);
  not not_153 (not_153_out, OP5);
  not not_154 (not_154_out, F2);
  not not_155 (not_155_out, F4);
  not not_156 (not_156_out, OP0);
  not not_157 (not_157_out, OP1);
  not not_158 (not_158_out, OP2);
  not not_159 (not_159_out, OP3);
  not not_160 (not_160_out, OP4);
  not not_161 (not_161_out, OP5);
  not not_162 (not_162_out, F3);
  not not_163 (not_163_out, F4);
  not not_164 (not_164_out, OP0);
  not not_165 (not_165_out, OP1);
  not not_166 (not_166_out, OP3);
  not not_167 (not_167_out, OP4);
  not not_168 (not_168_out, OP5);
  not not_169 (not_169_out, OP1);
  not not_170 (not_170_out, OP3);
  not not_171 (not_171_out, OP4);
  not not_172 (not_172_out, OP5);
  not not_173 (not_173_out, OP0);
  not not_174 (not_174_out, OP1);
  not not_175 (not_175_out, OP2);
  not not_176 (not_176_out, OP3);
  not not_177 (not_177_out, OP4);
  not not_178 (not_178_out, OP5);
  not not_179 (not_179_out, F0);
  not not_180 (not_180_out, F1);
  not not_181 (not_181_out, F2);
  not not_182 (not_182_out, F4);
  not not_183 (not_183_out, F5);
  not not_184 (not_184_out, OP0);
  not not_185 (not_185_out, OP2);
  not not_186 (not_186_out, OP3);
  not not_187 (not_187_out, OP4);
  not not_188 (not_188_out, OP5);
  not not_189 (not_189_out, F0);
  not not_190 (not_190_out, F1);
  not not_191 (not_191_out, F2);
  not not_192 (not_192_out, F4);
  not not_193 (not_193_out, F5);
  not not_194 (not_194_out, OP2);
  not not_195 (not_195_out, OP3);
  not not_196 (not_196_out, OP4);
  not not_197 (not_197_out, OP5);
  not not_198 (not_198_out, OP2);
  not not_199 (not_199_out, OP3);
  not not_200 (not_200_out, OP4);
  not not_201 (not_201_out, OP5);
  and and_1 (and_1_out, not_1_out, not_2_out, OP2, not_3_out, not_4_out, OP5);
  and and_2 (and_2_out, OP0, OP1, not_5_out, not_6_out, not_7_out, OP5);
  and and_3 (MemWrite, OP0, OP1, not_8_out, OP3, not_9_out, OP5);
  and and_4 (and_4_out, not_10_out, OP3, not_11_out, not_12_out);
  and and_5 (and_5_out, not_13_out, OP3, not_14_out, not_15_out);
  and and_6 (and_6_out, not_16_out, not_17_out, OP2, not_18_out, not_19_out, OP5);
  and and_7 (and_7_out, OP0, not_20_out, not_21_out, not_22_out, not_23_out);
  and and_8 (and_8_out, OP0, OP1, not_24_out, not_25_out, OP5);
  and and_9 (and_9_out, not_26_out, not_27_out, not_28_out, not_29_out, not_30_out, not_31_out, not_32_out, not_33_out, not_34_out);
  and and_10 (and_10_out, not_35_out, not_36_out, not_37_out, not_38_out, not_39_out, not_40_out, not_41_out, not_42_out, not_43_out);
  and and_11 (and_11_out, not_44_out, not_45_out, not_46_out, not_47_out, not_48_out, not_49_out, not_50_out, not_51_out, F5);
  and and_12 (and_12_out, not_52_out, not_53_out, not_54_out, not_55_out, not_56_out, F1, not_57_out, not_58_out, not_59_out, not_60_out);
  and and_13 (and_13_out, not_61_out, not_62_out, not_63_out, not_64_out, not_65_out, F1, not_66_out, F3, not_67_out, F5);
  and and_14 (and_14_out, not_68_out, not_69_out, not_70_out, not_71_out, not_72_out, F0, F2, not_73_out, not_74_out, F5);
  and and_15 (and_15_out, not_75_out, OP3, not_76_out, not_77_out);
  and and_16 (and_16_out, not_78_out, OP3, not_79_out, not_80_out);
  and and_17 (and_17_out, not_81_out, not_82_out, OP2, not_83_out, not_84_out, OP5);
  and and_18 (and_18_out, OP0, OP1, not_85_out, not_86_out, not_87_out);
  and and_19 (SysCALL, not_88_out, not_89_out, not_90_out, not_91_out, not_92_out, not_93_out, not_94_out, not_95_out, F2, F3, not_96_out, not_97_out);
  and and_20 (and_20_out, not_98_out, OP3, not_99_out, not_100_out);
  and and_21 (and_21_out, not_101_out, OP2, not_102_out, not_103_out, not_104_out);
  or or_1 (SignedExt, and_20_out, and_21_out, and_22_out);
  and and_22 (and_22_out, OP0, not_105_out, not_106_out, not_107_out, not_108_out);
  and and_23 (and_23_out, not_109_out, not_110_out, not_111_out, not_112_out, not_113_out, not_114_out, not_115_out, not_116_out, not_117_out, not_118_out);
  and and_24 (and_24_out, not_119_out, not_120_out, not_121_out, not_122_out, not_123_out, not_124_out, not_125_out, not_126_out, not_127_out, not_128_out);
  and and_25 (and_25_out, not_129_out, not_130_out, not_131_out, not_132_out, not_133_out, not_134_out, not_135_out, not_136_out, not_137_out, F5);
  and and_26 (and_26_out, not_138_out, not_139_out, not_140_out, not_141_out, not_142_out, not_143_out, F1, not_144_out, not_145_out, not_146_out, not_147_out);
  and and_27 (and_27_out, not_148_out, not_149_out, not_150_out, not_151_out, not_152_out, not_153_out, F1, not_154_out, F3, not_155_out, F5);
  and and_28 (and_28_out, not_156_out, not_157_out, not_158_out, not_159_out, not_160_out, not_161_out, F0, F2, not_162_out, not_163_out, F5);
  and and_29 (BEQ, not_164_out, not_165_out, OP2, not_166_out, not_167_out, not_168_out);
  and and_30 (BNE, OP0, not_169_out, OP2, not_170_out, not_171_out, not_172_out);
  and and_31 (JR, not_173_out, not_174_out, not_175_out, not_176_out, not_177_out, not_178_out, not_179_out, not_180_out, not_181_out, F3, not_182_out, not_183_out);
  and and_32 (and_32_out, not_184_out, not_185_out, not_186_out, not_187_out, not_188_out, not_189_out, not_190_out, not_191_out, F3, not_192_out, not_193_out);
  and and_33 (and_33_out, OP1, not_194_out, not_195_out, not_196_out, not_197_out);
  and and_34 (JAL, OP0, OP1, not_198_out, not_199_out, not_200_out, not_201_out);
  or or_2 (MemToReg, and_1_out, and_2_out);
  or or_3 (ALU_SRC, and_4_out, and_5_out, and_6_out, and_7_out, and_8_out);
  or or_4 (RegWrite, and_9_out, and_10_out, and_11_out, and_12_out, and_13_out, and_14_out, and_15_out, and_16_out, and_17_out, and_18_out);
  or or_5 (RegDst, and_23_out, and_24_out, and_25_out, and_26_out, and_27_out, and_28_out);
  or or_6 (JUMP, and_32_out, and_33_out);
endmodule

// ALU
module MIPS_ALU (
  input  [4:0] shamt,
  input  [31:0] X,
  input  [31:0] Y,
  input  [3:0] AluOP,
  output Equal,
  output [31:0] Result,
  output [31:0] Result_2
);

  wire comparator_3_lt, comparator_4_lt;
  wire [0:0] comparator_1_lt, comparator_2_lt;
  wire [31:0] adder_1_out, AND_out, bit_extender_1_out, bit_extender_2_out, divider_1_out, divider_1_rem,
       multiplier_1_cout, multiplier_1_out, NOR_out, OR_out, shifter_1_out, shifter_2_out, shifter_3_out,
       shifter_4_out, subtractor_1_out, XOR_out;

  assign AND_out = X & Y;  // AND_Gate AND, 32 bits wide
  assign OR_out = X | Y;  // OR_Gate OR, 32 bits wide
  Shifter #(.width(32), .shift("ll")) shifter_1 (.in(Y), .\dist (shamt), .out(shifter_1_out));
  Shifter #(.width(32), .shift("ar")) shifter_2 (.in(Y), .\dist (shamt), .out(shifter_2_out));
  Shifter #(.width(32), .shift("lr")) shifter_3 (.in(Y), .\dist (shamt), .out(shifter_3_out));
  Multiplier #(.width(32)) multiplier_1 (.a(X), .b(Y), .out(multiplier_1_out), .cout(multiplier_1_cout));  // open: cin
  Divider #(.width(32)) divider_1 (.a(X), .b(Y), .out(divider_1_out), .rem(divider_1_rem));  // open: upper
  Adder #(.width(32)) adder_1 (.a(X), .b(Y), .out(adder_1_out));  // open: cin, cout
  Subtractor #(.width(32)) subtractor_1 (.a(X), .b(Y), .out(subtractor_1_out));  // open: bin, bout
  assign XOR_out = X ^ Y;  // XOR_Gate XOR, 32 bits wide
  assign NOR_out = ~(X | Y);  // NOR_Gate NOR, 32 bits wide
  Comparator #(.width(32), .mode("twosComplement")) comparator_1 (
    .a(X), .b(Y), .eq(Equal), .lt(comparator_1_lt[0]));  // open: gt
  Comparator #(.width(32), .mode("unsigned")) comparator_2 (.a(X), .b(Y), .lt(comparator_2_lt[0]));  // open: gt, eq
  Shifter #(.width(32), .shift("ll")) shifter_4 (.in(Y), .\dist (X[4:0]), .out(shifter_4_out));
  Comparator #(.width(32), .mode("unsigned")) comparator_3 (.a(X), .b(Y), .lt(comparator_3_lt));  // open: gt, eq
  Comparator #(.width(32), .mode("twosComplement")) comparator_4 (
    .a(X), .b({32{1'b0}}), .lt(comparator_4_lt));  // open: gt, eq
  assign bit_extender_1_out = {{31{1'b0}}, comparator_3_lt};  // Bit_Extender bit_extender_1
  assign bit_extender_2_out = {{31{1'b0}}, comparator_4_lt};  // Bit_Extender bit_extender_2
  Multiplexer #(.select(4), .width(32), .disabled("Z"), .enable("false")) multiplexer_1 (
    .in0(shifter_1_out), .in1(shifter_2_out), .in2(shifter_3_out), .in3(multiplier_1_out),
    .in4(divider_1_out), .in5(adder_1_out), .in6(subtractor_1_out), .in7(AND_out), .in8(OR_out),
    .in9(XOR_out), .in10(NOR_out), .in11({{31{1'b0}}, comparator_1_lt[0]}),
    .in12({{31{1'b0}}, comparator_2_lt[0]}), .in13(shifter_4_out), .in14(bit_extender_1_out),
    .in15(bit_extender_2_out), .out(Result), .sel(AluOP));
  Multiplexer #(.select(4), .width(32), .disabled("Z"), .enable("false")) multiplexer_2 (
    .in0({32{1'b0}}), .in1({32{1'b0}}), .in2({32{1'b0}}), .in3(multiplier_1_cout), .in4(divider_1_rem),
    .in5({32{1'b0}}), .in6({32{1'b0}}), .in7({32{1'b0}}), .in8({32{1'b0}}), .in9({32{1'b0}}),
    .in10({32{1'b0}}), .in11({32{1'b0}}), .in12({32{1'b0}}), .in13({32{1'b0}}), .in14({32{1'b0}}),
    .in15({32{1'b0}}), .out(Result_2), .sel(AluOP));

  // Other names for the same wires on the sheet: Result2[31:0] = Result_2; S[3:0] = AluOP

  // Notes on the sheet:
  //   不要改变此引脚区域内容，也不要改变ALU封装形式
  //   输入引脚
  //   输出引脚
endmodule

module MIPS_Regifile (
  input  [31:0] Din,
  input  Clk,
  input  WE,
  input  [4:0] R1_num,
  input  [4:0] W_num,
  input  [4:0] R2_num,
  output [31:0] R1,
  output [31:0] R2
);

  // RegisterFile registerfile_1: pin names not known; wires that end beside it: Din, Clk, WE, W_num, R1_num, R2_num, R1, R2
endmodule

module \理想流水线  (
  output RegWrite,
  output MemWrite,
  output [31:0] IF_PC,
  output [31:0] ID_PC,
  output [31:0] EX_PC,
  output [31:0] M_PC,
  output [31:0] WB_PC,
  output [31:0] RDin,
  output [31:0] MDin,
  output [31:0] LedData
);

  wire ALuSrcB2, ALuSrcB3, and_1_out, and_2_out, and_3_out, and_4_out, and_5_out, CLK, clock_1_out,
       clock_2_out, comparator_1_eq, comparator_1_lt, comparator_2_eq, comparator_3_eq, comparator_4_eq,
       d_ff_2_q, equal3, equal4, equal5, Go, IR1, IR2, IR3, JR3_undefined, MemToReg2, MemToReg5,
       MemToReg_2_q, MemToReg_q, MemWrite2, MemWrite_q, mips_probe_4_p2, mips_probe_4_p3, nand_1_out,
       not_1_out, not_2_out, or_1_out, or_2_out, \PC使能 , RegDst2, RegDst5, RegDst_2_q, RegDst_q, RegWrite2,
       RegWrite_2_q, RegWrite_q, RST, SignedExt, Syscall, Syscall3, Syscall4, Syscall5, undriven_3,
       undriven_4, W1, W2, W3;
  wire [3:0] ALuOP2, ALuOP3;
  wire [4:0] multiplexer_3_out, multiplexer_5_out, multiplexer_6_out, Shmat3;
  wire [5:0] Func;
  wire [7:0] multiplexer_4_out;
  wire [12:0] CNT_num;
  wire [15:0] \LoadUse次数 , \总周期数 , \插入气泡数 , \无条件分支数 , \条件分支成功数 ;
  wire [31:0] A2, A3, adder_1_out, adder_2_out, ALU3, ALU4, ALU5, B2, B3, bit_extender_1_out,
       bit_extender_2_out, bit_extender_3_out, EX_IR, ID_IR, IF_IR, Imm2, Imm3, IR5, IR_3_q, IRNO1, IRNO3,
       MD4, MD5, MEM_IR, multiplexer_2_out, multiplexer_7_out, multiplexer_9_out, multiplexer_10_out,
       NextPCNormal, shifter_1_out, undriven, undriven_2, WB_IR;
  wire [31:6] IR;

  Button \u_总复位  (.out(RST));
  Button _1 (.out(IR1));
  Button _2 (.out(IR2));
  Button _3 (.out(IR3));
  // Probe on \总周期数 
  // Probe on \总周期数 
  Button \u_继续运行  (.out(Go));
  LED #(.active("true")) led_1 (.in(W1));
  LED #(.active("true")) led_2 (.in(W2));
  LED #(.active("true")) led_3 (.in(W3));
  Hex_Digit_Display hex_digit_display_1 (.value(LedData[31:28]));  // open: dp
  // Probe on IF_PC[19:0]
  // Mips_Probe mips_probe_1: pin names not known; wires that end beside it: IF_IR
  not not_1 (not_1_out, Syscall5);
  Hex_Digit_Display hex_digit_display_2 (.value(LedData[27:24]));  // open: dp
  Hex_Digit_Display hex_digit_display_3 (.value(LedData[23:20]));  // open: dp
  // Probe on ID_PC[19:0]
  // Mips_Probe mips_probe_2: pin names not known; wires that end beside it: ID_IR
  or or_1 (or_1_out, not_1_out, Go);
  or or_2 (or_2_out, equal5, not_1_out);
  Hex_Digit_Display hex_digit_display_4 (.value(LedData[19:16]));  // open: dp
  Hex_Digit_Display hex_digit_display_5 (.value(LedData[15:12]));  // open: dp
  D_Flip_Flop #(.trigger("falling"), .Pre_Clr_Positions("ABOVE_BELOW"), .NegatePresetClear("false"), .enable("false"), .NewFFLayout("true")) d_ff_1 (
    .clk(CLK), .D(or_2_out), .Q(\PC使能 ), .preset(or_1_out));  // open: Qn, reset
  Hex_Digit_Display hex_digit_display_6 (.value(LedData[7:4]));  // open: dp
  Hex_Digit_Display hex_digit_display_7 (.value(LedData[11:8]));  // open: dp
  Clock #(.highDuration(1), .lowDuration(1)) clock_1 (.out(clock_1_out));
  // Probe on EX_PC[19:0]
  // Mips_Probe mips_probe_3: pin names not known; wires that end beside it: clock_1_out, EX_IR, CLK
  Hex_Digit_Display hex_digit_display_8 (.value(LedData[3:0]));  // open: dp
  and and_1 (and_1_out, \PC使能 , CLK);
  // Probe on \总周期数 
  // Probe on M_PC[19:0]
  // Mips_Probe mips_probe_4: pin names not known; wires that end beside it: MEM_IR, mips_probe_4_p2, mips_probe_4_p3
  // Probe on \总周期数 
  // Probe on \无条件分支数 
  // Probe on \条件分支成功数 
  // Probe on \插入气泡数 
  // Probe on \LoadUse次数 
  Multiplexer #(.select(2), .width(32), .disabled("Z"), .enable("false")) multiplexer_1 (
    .in0(adder_1_out), .in1(multiplexer_9_out), .in2(adder_2_out), .out(NextPCNormal), .sel(2'b00));  // open: in3
  Multiplexer #(.select(1), .width(32), .disabled("Z"), .enable("false")) multiplexer_2 (
    .in0(NextPCNormal), .in1({32{1'b0}}), .out(multiplexer_2_out), .sel(1'b0));
  // Probe on IF_PC[11:0]
  // Probe on WB_PC[19:0]
  // Mips_Probe mips_probe_5: pin names not known; wires that end beside it: WB_IR
  Register #(.width(32), .trigger("rising"), .Select("low")) PC (
    .D(multiplexer_2_out), .en(\PC使能 ), .Q(IF_PC), .clk(CLK), .clr(RST));
  // Probe on EX_PC[11:0]
  // Probe on ID_PC[11:0]
  // Probe on M_PC[11:0]
  D_Flip_Flop #(.trigger("high"), .Pre_Clr_Positions("LEGACY"), .NegatePresetClear("false"), .enable("true"), .NewFFLayout("false")) d_ff_2 (.Q(d_ff_2_q));  // open: clk, D, Qn, preset, en, reset
  // Probe on 13'h20
  // Probe on WB_PC[11:0]
  Comparator #(.width(13), .mode("twosComplement")) comparator_1 (
    .a(CNT_num), .b(13'h20), .eq(comparator_1_eq), .lt(comparator_1_lt));  // open: gt
  Clock #(.highDuration(1), .lowDuration(1)) clock_2 (.out(clock_2_out));
  Adder #(.width(32)) adder_1 (.a(IF_PC), .b(32'h4), .out(adder_1_out));  // open: cin, cout
  nand nand_1 (nand_1_out, d_ff_2_q, comparator_1_eq);
  Counter #(.width(13), .max('h1fff), .ongoal("stay"), .trigger("rising"), .behavior("old")) counter_1 (
    .count(comparator_1_lt), .Q(CNT_num), .clk(clock_2_out));  // open: load, D, carry, clr, preset
  ROM #(.addrWidth(10), .dataWidth(32), .Select("high")) rom_1 (.addr(IF_PC[11:2]), .data(IRNO1));
  assign CLK = nand_1_out ? clock_2_out : 1'bz;  // Controlled_Buffer controlled_buffer_1
  Register #(.width(32), .trigger("rising"), .Select("low")) u_IR (
    .D(IRNO1), .Q({IR, Func}), .clk(and_1_out), .clr(RST));  // open: en
  Register #(.width(32), .trigger("rising"), .Select("low")) PC_2 (
    .D(IF_PC), .Q(ID_PC), .clk(and_1_out), .clr(RST));  // open: en
  Pull_Resistor #(.pull(1)) pull_resistor_1 (.node(CLK));
  // Mips_Probe mips_probe_6: pin names not known; wires that end beside it: {IR, Func}
  \单周期硬布线控制器  \u_单周期硬布线控制器_1  (
    .Func(Func), .OP(IR[31:26]), .ALU_OP(ALuOP2), .MemToReg(MemToReg2), .MemWrite(MemWrite2),
    .ALU_SRC(ALuSrcB2), .RegWrite(RegWrite2), .SysCALL(Syscall), .SignedExt(SignedExt), .RegDst(RegDst2),
    .JR(JR3_undefined), .JMP(mips_probe_4_p3));  // open: Beq, JAL, Bne
  Multiplexer #(.select(1), .width(5), .disabled("Z"), .enable("false")) multiplexer_3 (
    .in0(IR[25:21]), .in1(5'b00010), .out(multiplexer_3_out), .sel(Syscall));
  Comparator #(.width(6), .mode("twosComplement")) comparator_2 (
    .a(IR[31:26]), .b(6'b100100), .eq(comparator_2_eq));  // open: gt, lt
  assign bit_extender_1_out = {{24{1'b0}}, multiplexer_4_out};  // Bit_Extender bit_extender_1
  Multiplexer #(.select(2), .width(8), .disabled("Z"), .enable("false")) multiplexer_4 (
    .in0(RDin[7:0]), .in1(RDin[15:8]), .in2(RDin[23:16]), .in3(RDin[31:24]), .out(multiplexer_4_out),
    .sel(ALU4[1:0]));
  Multiplexer #(.select(1), .width(5), .disabled("Z"), .enable("false")) multiplexer_5 (
    .in0(IR[20:16]), .in1(5'b00100), .out(multiplexer_5_out), .sel(Syscall));
  Multiplexer #(.select(2), .width(5), .disabled("Z"), .enable("false")) multiplexer_6 (
    .in0(IR5[20:16]), .in1(IR5[15:11]), .in2({5{1'b1}}), .out(multiplexer_6_out), .sel({1'b0, RegDst5}));  // open: in3
  Multiplexer #(.select(1), .width(32), .disabled("Z"), .enable("false")) multiplexer_7 (
    .in0(RDin), .in1(bit_extender_1_out), .out(multiplexer_7_out), .sel(comparator_2_eq));
  assign bit_extender_2_out = {{16{1'b0}}, {IR[15:6], Func}};  // Bit_Extender bit_extender_2
  assign bit_extender_3_out = {{16{IR[15]}}, {IR[15:6], Func}};  // Bit_Extender bit_extender_3
  MIPS_Regifile mips_regifile_1 (
    .Din(multiplexer_7_out), .Clk(CLK), .R1(A2), .R2(B2), .WE(RegWrite), .W_num(multiplexer_6_out),
    .R1_num(multiplexer_3_out), .R2_num(multiplexer_5_out));
  Multiplexer #(.select(1), .width(32), .disabled("Z"), .enable("false")) multiplexer_8 (
    .in0(bit_extender_2_out), .in1(bit_extender_3_out), .out(Imm2), .sel(SignedExt));
  Multiplexer #(.select(1), .width(32), .disabled("Z"), .enable("false")) multiplexer_9 (
    .in0({EX_PC[31:28], IRNO3[25:0], 2'b00}), .in1(undriven), .out(multiplexer_9_out), .sel(JR3_undefined));
  Register #(.width(1), .trigger("rising"), .Select("low")) MemToReg (
    .D(MemToReg2), .Q(MemToReg_q), .clk(and_1_out), .clr(RST));  // open: en
  Register #(.width(1), .trigger("rising"), .Select("low")) RegDst (
    .Q(RegDst_q), .clk(and_1_out), .clr(RST));  // open: D, en
  Register #(.width(1), .trigger("rising"), .Select("low")) u_RegWrite (
    .D(RegWrite2), .Q(RegWrite_q), .clk(and_1_out), .clr(RST));  // open: en
  Register #(.width(1), .trigger("rising"), .Select("low")) u_MemWrite (
    .D(MemWrite2), .Q(MemWrite_q), .clk(and_1_out), .clr(RST));  // open: en
  Register #(.width(4), .trigger("rising"), .Select("low")) ALuOP (
    .D(ALuOP2), .Q(ALuOP3), .clk(and_1_out), .clr(RST));  // open: en
  Register #(.width(1), .trigger("rising"), .Select("low")) ALuSrcB (
    .D(ALuSrcB2), .Q(ALuSrcB3), .clk(and_1_out), .clr(RST));  // open: en
  Register #(.width(1), .trigger("rising"), .Select("low")) u_Syscall (
    .D(Syscall), .Q(Syscall3), .clk(and_1_out), .clr(RST));  // open: en
  Register #(.width(32), .trigger("rising"), .Select("low")) IR_2 (
    .D({IR, Func}), .Q(IRNO3), .clk(and_1_out), .clr(RST));  // open: en
  Register #(.width(32), .trigger("rising"), .Select("low")) PC_3 (
    .D(ID_PC), .Q(EX_PC), .clk(and_1_out), .clr(RST));  // open: en
  Register #(.width(32), .trigger("rising"), .Select("low")) A (
    .D(A2), .Q(A3), .clk(and_1_out), .clr(RST));  // open: en
  Register #(.width(32), .trigger("rising"), .Select("low")) B (
    .D(B2), .Q(B3), .clk(and_1_out), .clr(RST));  // open: en
  Register #(.width(32), .trigger("rising"), .Select("low")) Imm (
    .D(Imm2), .Q(Imm3), .clk(and_1_out), .clr(RST));  // open: en
  Register #(.width(5), .trigger("rising"), .Select("low")) Shmat (
    .D(IR[10:6]), .Q(Shmat3), .clk(and_1_out), .clr(RST));  // open: en
  or or_3 (mips_probe_4_p2, and_3_out, and_4_out, and_2_out);
  Multiplexer #(.select(2), .width(32), .disabled("Z"), .enable("false")) multiplexer_10 (
    .in0(B3), .in1(Imm3), .in2(32'h22), .out(multiplexer_10_out), .sel({Syscall3, ALuSrcB3}));  // open: in3
  Shifter #(.width(32), .shift("ll")) shifter_1 (.in(undriven_2), .\dist (5'b00010), .out(shifter_1_out));
  Comparator #(.width(32), .mode("twosComplement")) comparator_3 (
    .a(32'h1), .b(ALU3), .eq(comparator_3_eq));  // open: gt, lt
  Comparator #(.width(6), .mode("twosComplement")) comparator_4 (
    .a(IR[31:26]), .b(6'b000001), .eq(comparator_4_eq));  // open: gt, lt
  and and_2 (and_2_out, undriven_3, equal3);
  not not_2 (not_2_out, equal3);
  MIPS_ALU mips_alu_1 (
    .X(A3), .Y(multiplexer_10_out), .AluOP(ALuOP3), .Equal(equal3), .Result(ALU3), .shamt(Shmat3));  // open: Result_2
  Adder #(.width(32)) adder_2 (.a(shifter_1_out), .b(EX_PC), .out(adder_2_out), .cin(1'b0));  // open: cout
  and and_3 (and_3_out, comparator_4_eq, comparator_3_eq);
  and and_4 (and_4_out, not_2_out, undriven_4);
  Register #(.width(32), .trigger("rising"), .Select("low")) register_1 (
    .D(B3), .en(and_5_out), .Q(LedData), .clk(CLK), .clr(RST));
  and and_5 (and_5_out, Syscall3, equal3);
  Register #(.width(1), .trigger("rising"), .Select("low")) MemToReg_2 (
    .D(MemToReg_q), .Q(MemToReg_2_q), .clk(and_1_out), .clr(RST));  // open: en
  Register #(.width(1), .trigger("rising"), .Select("low")) RegDst_2 (
    .D(RegDst_q), .Q(RegDst_2_q), .clk(and_1_out), .clr(RST));  // open: en
  Register #(.width(1), .trigger("rising"), .Select("low")) RegWrite_2 (
    .D(RegWrite_q), .Q(RegWrite_2_q), .clk(and_1_out), .clr(RST));  // open: en
  Register #(.width(1), .trigger("rising"), .Select("low")) MemWrite_2 (
    .D(MemWrite_q), .Q(MemWrite), .clk(and_1_out), .clr(RST));  // open: en
  Register #(.width(1), .trigger("rising"), .Select("low")) Syscall_2 (
    .D(Syscall3), .Q(Syscall4), .clk(and_1_out), .clr(RST));  // open: en
  Register #(.width(1), .trigger("rising"), .Select("low")) equal (
    .D(equal3), .Q(equal4), .clk(and_1_out), .clr(RST));  // open: en
  Register #(.width(32), .trigger("rising"), .Select("low")) IR_3 (
    .D(IRNO3), .Q(IR_3_q), .clk(and_1_out), .clr(RST));  // open: en
  Register #(.width(32), .trigger("rising"), .Select("low")) PC_4 (
    .D(EX_PC), .Q(M_PC), .clk(and_1_out), .clr(RST));  // open: en
  Register #(.width(32), .trigger("rising"), .Select("low")) B_2 (
    .D(B3), .Q(MDin), .clk(and_1_out), .clr(RST));  // open: en
  Register #(.width(32), .trigger("rising"), .Select("low")) ALU (
    .D(ALU3), .Q(ALU4), .clk(and_1_out), .clr(RST));  // open: en
  RAM #(.addrWidth(10), .dataWidth(32), .bus("separate"), .Select("high")) ram_1 (
    .addr(ALU4[11:2]), .din(MDin), .data(MD4), .str(MemWrite), .clk(CLK), .clr(RST));  // open: sel, ld
  Register #(.width(1), .trigger("rising"), .Select("low")) MemToReg_3 (
    .D(MemToReg_2_q), .Q(MemToReg5), .clk(and_1_out), .clr(RST));  // open: en
  Register #(.width(1), .trigger("rising"), .Select("low")) RegDst_3 (
    .D(RegDst_2_q), .en(RegDst_2_q), .Q(RegDst5), .clk(and_1_out), .clr(RST));
  Register #(.width(1), .trigger("rising"), .Select("low")) RegWrite_3 (
    .D(RegWrite_2_q), .Q(RegWrite), .clk(and_1_out), .clr(RST));  // open: en
  Register #(.width(1), .trigger("rising"), .Select("low")) Syscall_3 (
    .D(Syscall4), .Q(Syscall5), .clk(and_1_out), .clr(RST));  // open: en
  Register #(.width(1), .trigger("rising"), .Select("low")) equal_2 (
    .D(equal4), .Q(equal5), .clk(and_1_out), .clr(RST));  // open: en
  Register #(.width(32), .trigger("rising"), .Select("low")) IR_4 (
    .D(IR_3_q), .Q(IR5), .clk(and_1_out), .clr(RST));  // open: en
  Register #(.width(32), .trigger("rising"), .Select("low")) PC_5 (
    .D(M_PC), .Q(WB_PC), .clk(and_1_out), .clr(RST));  // open: en
  Register #(.width(32), .trigger("rising"), .Select("low")) ALU_2 (
    .D(ALU4), .Q(ALU5), .clk(and_1_out), .clr(RST));  // open: en
  Register #(.width(32), .trigger("rising"), .Select("low")) MD (
    .D(MD4), .Q(MD5), .clk(and_1_out), .clr(RST));  // open: en
  Multiplexer #(.select(2), .width(32), .disabled("Z"), .enable("false")) multiplexer_11 (
    .in0(ALU5), .in1(MD5), .in2(WB_PC), .out(RDin), .sel({1'b0, MemToReg5}));  // open: in3

  // Other names for the same wires on the sheet: byteoff[1:0] = ALU4[1:0]; B4[31:0] = MDin; IR[5:0] = Func;
  //   IRNO2[31:0] = {IR, Func}; Shmat2[4:0] = IR[10:6]; OP[5:0] = IR[31:26]; MEM_PC[31:0] = M_PC;
  //   MemWrite4 = MemWrite; PC[31:0] = IF_PC; PC1[31:0] = IF_PC; PC2[31:0] = ID_PC; PC3[31:0] = EX_PC;
  //   PC5[31:0] = WB_PC; RegWrite5 = RegWrite; result[31:0] = ALU3; Syscall2 = Syscall; 总复位 = RST

  // Notes on the sheet:
  //   中断源
  //   时空图监测，可删除
  //   中断等待指示
  //   Syscall停机功能模块
  //   数码管输出
  //   控制位
  //   流水调试日志用
  //   暂停节拍，不能为0
  //   戳工具置1进入计数暂停模式，ctrl+k时钟自动运行到对应节拍暂停
  //   ctrl+k关闭时钟连续运行，将控制位置零，进入单步调试模式调试
  //   用这个时钟源需要去掉电路中的其他时钟源
  //   指令存储器
  //   contents of rom_1 (hex, n*v repeats v):
  //   20100000 20110000 20120000 20130000 36100000 36310001 36520002 36730003 ae100000 ae110004 ae120008
  //   ae13000c 2002000a 20110000 20120000 20130000 c
  //   IF/ID
  //   可计数暂停的时钟源
  //   rs
  //   指令字
  //   rt
  //   rd
  //   Beq
  //   JMP
  //   JR
  //   Bne
  //   OP
  //   JAL
  //   Func
  //   Syscall
  //   为方便自动评测，需要输出流水线各段保存的PC值，注意是PC不是PC+4，另外ID段寄存器写入信息，Mem段内存写入信息也要输出
  //   ID/EX
  //   EX/MEM
  //   MEM/WB
endmodule

module \气泡流水线  (
  output RegWrite,
  output MemWrite,
  output [31:0] IF_PC,
  output [31:0] ID_PC,
  output [31:0] EX_PC,
  output [31:0] M_PC,
  output [31:0] WB_PC,
  output [31:0] RDin,
  output [31:0] MDin,
  output [31:0] LedData
);

  wire ALuSrcB2, ALuSrcB3, and_1_out, and_2_out, and_3_out, and_4_out, and_5_out, and_6_out, Beq2, Beq3,
       Bne2, Bne3, \B系列3 , CLK, clock_1_out, clock_2_out, comparator_1_eq, comparator_2_eq, comparator_2_lt,
       comparator_3_eq, comparator_4_eq, comparator_5_eq, d_ff_2_q, equal3, equal4, equal5, Go, IR1, IR2,
       IR3, Jal2, Jal3, Jal5, Jal_2_q, Jmp2, Jmp3, JR2, JR3, MemToReg2, MemToReg5, MemToReg_2_q, MemToReg_q,
       MemWrite2, MemWrite_q, multiplexer_14_out, multiplexer_15_out, multiplexer_16_out, multiplexer_17_out,
       multiplexer_19_out, multiplexer_20_out, multiplexer_21_out, multiplexer_22_out, multiplexer_23_out,
       multiplexer_24_out, multiplexer_25_out, nand_1_out, not_1_out, not_2_out, not_4_out, not_5_out,
       or_1_out, or_2_out, or_3_out, \PC使能 , RegDst2, RegDst5, RegDst_2_q, RegDst_q, RegWrite2, RegWrite3,
       RegWrite4, RST, SignedExt, Syscall, Syscall3, Syscall4, Syscall5, W1, W2, W3, \分支气泡 , \数据相关 ,
       \源寄存器使用情况_1_r1_used , \源寄存器使用情况_1_r2_used ;
  wire [1:0] byteoff5;
  wire [3:0] ALuOP2, ALuOP3, multiplexer_18_out;
  wire [4:0] EX_WriteReg_num, MEM_WriteReg_num, multiplexer_7_out, multiplexer_8_out, multiplexer_9_out,
       multiplexer_12_out, multiplexer_13_out, multiplexer_31_out, Shmat3;
  wire [5:0] Func;
  wire [7:0] multiplexer_6_out;
  wire [12:0] CNT_num;
  wire [15:0] \LoadUse次数 , \总周期数 , \插入气泡数 , \无条件分支数 , \条件分支成功数 ;
  wire [31:0] A2, A3, ALU3, ALU4, ALU5, B2, B3, bit_extender_1_out, bit_extender_2_out, bit_extender_3_out,
       \B系列地址3 , EX_IR, IF_IR, Imm2, Imm3, IR4, IR5, \J系列地址3 , MD4, MD5, multiplexer_2_out,
       multiplexer_3_out, multiplexer_4_out, multiplexer_5_out, multiplexer_26_out, multiplexer_27_out,
       multiplexer_28_out, multiplexer_29_out, multiplexer_30_out, multiplexer_32_out, multiplexer_34_out,
       NextPCNormal, PC1, PC2, PC3, PC5, PC_4_q, RDin1, shifter_1_out;
  wire [31:6] ID_IR;

  Button \u_总复位  (.out(RST));
  Button _1 (.out(IR1));
  Button _2 (.out(IR2));
  Button _3 (.out(IR3));
  // Probe on \总周期数 
  // Probe on \总周期数 
  Button \u_继续运行  (.out(Go));
  LED #(.active("true")) led_1 (.in(W1));
  LED #(.active("true")) led_2 (.in(W2));
  LED #(.active("true")) led_3 (.in(W3));
  Hex_Digit_Display hex_digit_display_1 (.value(LedData[31:28]));  // open: dp
  // Probe on IF_PC[19:0]
  // Mips_Probe mips_probe_1: pin names not known; wires that end beside it: IF_IR
  not not_1 (not_1_out, Syscall5);
  Hex_Digit_Display hex_digit_display_2 (.value(LedData[27:24]));  // open: dp
  Hex_Digit_Display hex_digit_display_3 (.value(LedData[23:20]));  // open: dp
  // Probe on ID_PC[19:0]
  // Mips_Probe mips_probe_2: pin names not known; wires that end beside it: {ID_IR, Func}
  or or_1 (or_1_out, not_1_out, Go);
  or or_2 (or_2_out, equal5, not_1_out);
  Hex_Digit_Display hex_digit_display_4 (.value(LedData[15:12]));  // open: dp
  Hex_Digit_Display hex_digit_display_5 (.value(LedData[19:16]));  // open: dp
  D_Flip_Flop #(.trigger("falling"), .Pre_Clr_Positions("ABOVE_BELOW"), .NegatePresetClear("false"), .enable("false"), .NewFFLayout("true")) d_ff_1 (
    .clk(CLK), .D(or_2_out), .Q(\PC使能 ), .preset(or_1_out));  // open: Qn, reset
  Hex_Digit_Display hex_digit_display_6 (.value(LedData[7:4]));  // open: dp
  Hex_Digit_Display hex_digit_display_7 (.value(LedData[11:8]));  // open: dp
  Clock #(.highDuration(1), .lowDuration(1)) clock_1 (.out(clock_1_out));
  // Probe on EX_PC[19:0]
  // Mips_Probe mips_probe_3: pin names not known; wires that end beside it: clock_1_out, EX_IR, CLK
  Hex_Digit_Display hex_digit_display_8 (.value(LedData[3:0]));  // open: dp
  // Probe on \总周期数 
  // Probe on M_PC[19:0]
  // Mips_Probe mips_probe_4: pin names not known; wires that end beside it: IR4
  // Probe on \总周期数 
  // Probe on \无条件分支数 
  // Probe on \条件分支成功数 
  // Probe on \插入气泡数 
  // Probe on \LoadUse次数 
  Comparator #(.width(2), .mode("twosComplement")) comparator_1 (
    .a({\B系列3 , Jmp3}), .b(2'b00), .eq(comparator_1_eq));  // open: gt, lt
  Multiplexer #(.select(2), .width(32), .disabled("Z"), .enable("false")) multiplexer_1 (
    .in0(PC1), .in1(\J系列地址3 ), .in2(\B系列地址3 ), .out(NextPCNormal), .sel({\B系列3 , Jmp3}));  // open: in3
  Multiplexer #(.select(1), .width(32), .disabled("Z"), .enable("false")) multiplexer_2 (
    .in0(NextPCNormal), .in1({32{1'b0}}), .out(multiplexer_2_out), .sel(1'b0));
  and and_1 (and_1_out, \PC使能 , not_2_out);
  not not_2 (not_2_out, \数据相关 );
  and and_2 (and_2_out, \PC使能 , CLK);
  // Probe on IF_PC[11:0]
  // Probe on WB_PC[19:0]
  // Mips_Probe mips_probe_5: pin names not known; wires that end beside it: IR5
  not not_3 (\分支气泡 , comparator_1_eq);
  Register #(.width(32), .trigger("rising"), .Select("low")) PC (
    .D(multiplexer_2_out), .en(and_1_out), .Q(IF_PC), .clk(CLK), .clr(RST));
  Adder #(.width(32)) adder_1 (.a(IF_PC), .b(32'h4), .out(PC1));  // open: cin, cout
  not not_4 (not_4_out, \数据相关 );
  // Probe on EX_PC[11:0]
  // Probe on ID_PC[11:0]
  // Probe on M_PC[11:0]
  D_Flip_Flop #(.trigger("high"), .Pre_Clr_Positions("LEGACY"), .NegatePresetClear("false"), .enable("true"), .NewFFLayout("false")) d_ff_2 (.Q(d_ff_2_q));  // open: clk, D, Qn, preset, en, reset
  // Probe on 13'hfff
  // Probe on WB_PC[11:0]
  Comparator #(.width(13), .mode("twosComplement")) comparator_2 (
    .a(CNT_num), .b(13'hfff), .eq(comparator_2_eq), .lt(comparator_2_lt));  // open: gt
  Clock #(.highDuration(1), .lowDuration(1)) clock_2 (.out(clock_2_out));
  ROM #(.addrWidth(10), .dataWidth(32), .Select("high")) rom_1 (.addr(IF_PC[11:2]), .data(IF_IR));
  nand nand_1 (nand_1_out, d_ff_2_q, comparator_2_eq);
  Counter #(.width(13), .max('h1fff), .ongoal("stay"), .trigger("rising"), .behavior("old")) counter_1 (
    .count(comparator_2_lt), .Q(CNT_num), .clk(clock_2_out));  // open: load, D, carry, clr, preset
  // Mips_Probe mips_probe_6: pin names not known; wires that end beside it: IF_IR
  assign CLK = nand_1_out ? clock_2_out : 1'bz;  // Controlled_Buffer controlled_buffer_1
  Multiplexer #(.select(1), .width(32), .disabled("Z"), .enable("false")) multiplexer_3 (
    .in0(IF_IR), .in1({32{1'b0}}), .out(multiplexer_3_out), .sel(\分支气泡 ));
  Multiplexer #(.select(1), .width(32), .disabled("Z"), .enable("false")) multiplexer_4 (
    .in0(PC1), .in1({32{1'b0}}), .out(multiplexer_4_out), .sel(\分支气泡 ));
  Multiplexer #(.select(1), .width(32), .disabled("Z"), .enable("false")) multiplexer_5 (
    .in0(IF_PC), .in1({32{1'b0}}), .out(multiplexer_5_out), .sel(\分支气泡 ));
  Pull_Resistor #(.pull(1)) pull_resistor_1 (.node(CLK));
  Register #(.width(32), .trigger("rising"), .Select("low")) IR (
    .D(multiplexer_3_out), .en(not_4_out), .Q({ID_IR, Func}), .clk(and_2_out), .clr(RST));
  Register #(.width(32), .trigger("rising"), .Select("low")) PC_2 (
    .D(multiplexer_4_out), .en(not_4_out), .Q(PC2), .clk(and_2_out), .clr(RST));
  Register #(.width(32), .trigger("rising"), .Select("low")) PCO (
    .D(multiplexer_5_out), .en(not_4_out), .Q(ID_PC), .clk(and_2_out), .clr(RST));
  // Mips_Probe mips_probe_7: pin names not known; wires that end beside it: {ID_IR, Func}
  Multiplexer #(.select(2), .width(8), .disabled("Z"), .enable("false")) multiplexer_6 (
    .in0(RDin1[7:0]), .in1(RDin1[15:8]), .in2(RDin1[23:16]), .in3(RDin1[31:24]), .out(multiplexer_6_out),
    .sel(byteoff5));
  \单周期硬布线控制器  \u_单周期硬布线控制器_1  (
    .Func(Func), .OP(ID_IR[31:26]), .ALU_OP(ALuOP2), .MemToReg(MemToReg2), .MemWrite(MemWrite2),
    .ALU_SRC(ALuSrcB2), .RegWrite(RegWrite2), .SysCALL(Syscall), .SignedExt(SignedExt), .RegDst(RegDst2),
    .JR(JR2), .JMP(Jmp2), .Beq(Beq2), .JAL(Jal2), .Bne(Bne2));
  Multiplexer #(.select(1), .width(5), .disabled("Z"), .enable("false")) multiplexer_7 (
    .in0(ID_IR[25:21]), .in1(5'b00010), .out(multiplexer_7_out), .sel(Syscall));
  Multiplexer #(.select(2), .width(5), .disabled("Z"), .enable("false")) multiplexer_8 (
    .in0(IR5[20:16]), .in1(IR5[15:11]), .in2({5{1'b1}}), .out(multiplexer_8_out), .sel({Jal5, RegDst5}));  // open: in3
  Comparator #(.width(6), .mode("twosComplement")) comparator_3 (
    .a(IR5[31:26]), .b(6'b100100), .eq(comparator_3_eq));  // open: gt, lt
  assign bit_extender_1_out = {{24{1'b0}}, multiplexer_6_out};  // Bit_Extender bit_extender_1
  Multiplexer #(.select(1), .width(5), .disabled("Z"), .enable("false")) multiplexer_9 (
    .in0(ID_IR[20:16]), .in1(5'b00100), .out(multiplexer_9_out), .sel(Syscall));
  Multiplexer #(.select(1), .width(32), .disabled("Z"), .enable("false")) multiplexer_10 (
    .in0(RDin1), .in1(bit_extender_1_out), .out(RDin), .sel(comparator_3_eq));
  or or_3 (or_3_out, \分支气泡 , \数据相关 );
  assign bit_extender_2_out = {{16{1'b0}}, {ID_IR[15:6], Func}};  // Bit_Extender bit_extender_2
  Multiplexer #(.select(1), .width(32), .disabled("Z"), .enable("false")) multiplexer_11 (
    .in0(bit_extender_2_out), .in1(bit_extender_3_out), .out(Imm2), .sel(SignedExt));
  assign bit_extender_3_out = {{16{ID_IR[15]}}, {ID_IR[15:6], Func}};  // Bit_Extender bit_extender_3
  Multiplexer #(.select(2), .width(5), .disabled("Z"), .enable("false")) multiplexer_12 (
    .in0(ID_IR[20:16]), .in1(ID_IR[15:11]), .in2({5{1'b1}}), .out(multiplexer_12_out), .sel({Jal2, RegDst2}));  // open: in3
  \源寄存器使用情况  \u_源寄存器使用情况_1  (
    .OP0(ID_IR[26]), .OP1(ID_IR[27]), .OP2(ID_IR[28]), .OP3(ID_IR[29]), .OP4(ID_IR[30]), .OP5(ID_IR[31]),
    .F0(Func[0]), .F1(Func[1]), .F2(Func[2]), .F3(Func[3]), .F4(Func[4]), .F5(Func[5]),
    .R1_used(\源寄存器使用情况_1_r1_used ), .R2_used(\源寄存器使用情况_1_r2_used ));
  MIPS_Regifile mips_regifile_1 (
    .Din(RDin), .Clk(CLK), .R1(A2), .R2(B2), .WE(RegWrite), .W_num(multiplexer_8_out),
    .R1_num(multiplexer_7_out), .R2_num(multiplexer_9_out));
  Multiplexer #(.select(1), .width(5), .disabled("Z"), .enable("false")) multiplexer_13 (
    .in0(multiplexer_12_out), .in1({5{1'b0}}), .out(multiplexer_13_out), .sel(or_3_out));
  Multiplexer #(.select(1), .width(1), .disabled("Z"), .enable("false")) multiplexer_14 (
    .in0(MemToReg2), .in1(1'b0), .out(multiplexer_14_out), .sel(or_3_out));
  Multiplexer #(.select(1), .width(1), .disabled("Z"), .enable("false")) multiplexer_15 (
    .in0(RegDst2), .in1(1'b0), .out(multiplexer_15_out), .sel(or_3_out));
  Multiplexer #(.select(1), .width(1), .disabled("Z"), .enable("false")) multiplexer_16 (
    .in0(RegWrite2), .in1(1'b0), .out(multiplexer_16_out), .sel(or_3_out));
  Multiplexer #(.select(1), .width(1), .disabled("Z"), .enable("false")) multiplexer_17 (
    .in0(MemWrite2), .in1(1'b0), .out(multiplexer_17_out), .sel(or_3_out));
  Multiplexer #(.select(1), .width(4), .disabled("Z"), .enable("false")) multiplexer_18 (
    .in0(ALuOP2), .in1(4'b0000), .out(multiplexer_18_out), .sel(or_3_out));
  Multiplexer #(.select(1), .width(1), .disabled("Z"), .enable("false")) multiplexer_19 (
    .in0(ALuSrcB2), .in1(1'b0), .out(multiplexer_19_out), .sel(or_3_out));
  Multiplexer #(.select(1), .width(1), .disabled("Z"), .enable("false")) multiplexer_20 (
    .in0(Syscall), .in1(1'b0), .out(multiplexer_20_out), .sel(or_3_out));
  Multiplexer #(.select(1), .width(1), .disabled("Z"), .enable("false")) multiplexer_21 (
    .in0(Bne2), .in1(1'b0), .out(multiplexer_21_out), .sel(or_3_out));
  Multiplexer #(.select(1), .width(1), .disabled("Z"), .enable("false")) multiplexer_22 (
    .in0(Beq2), .in1(1'b0), .out(multiplexer_22_out), .sel(or_3_out));
  Multiplexer #(.select(1), .width(1), .disabled("Z"), .enable("false")) multiplexer_23 (
    .in0(Jal2), .in1(1'b0), .out(multiplexer_23_out), .sel(or_3_out));
  Multiplexer #(.select(1), .width(1), .disabled("Z"), .enable("false")) multiplexer_24 (
    .in0(Jmp2), .in1(1'b0), .out(multiplexer_24_out), .sel(or_3_out));
  Multiplexer #(.select(1), .width(1), .disabled("Z"), .enable("false")) multiplexer_25 (
    .in0(JR2), .in1(1'b0), .out(multiplexer_25_out), .sel(or_3_out));
  Multiplexer #(.select(1), .width(32), .disabled("Z"), .enable("false")) multiplexer_26 (
    .in0({ID_IR, Func}), .in1({32{1'b0}}), .out(multiplexer_26_out), .sel(or_3_out));
  Multiplexer #(.select(1), .width(32), .disabled("Z"), .enable("false")) multiplexer_27 (
    .in0(PC2), .in1({32{1'b0}}), .out(multiplexer_27_out), .sel(or_3_out));
  Multiplexer #(.select(1), .width(32), .disabled("Z"), .enable("false")) multiplexer_28 (
    .in0(A2), .in1({32{1'b0}}), .out(multiplexer_28_out), .sel(or_3_out));
  Multiplexer #(.select(1), .width(32), .disabled("Z"), .enable("false")) multiplexer_29 (
    .in0(B2), .in1({32{1'b0}}), .out(multiplexer_29_out), .sel(or_3_out));
  Multiplexer #(.select(1), .width(32), .disabled("Z"), .enable("false")) multiplexer_30 (
    .in0(Imm2), .in1({32{1'b0}}), .out(multiplexer_30_out), .sel(or_3_out));
  Multiplexer #(.select(1), .width(5), .disabled("Z"), .enable("false")) multiplexer_31 (
    .in0(ID_IR[10:6]), .in1({5{1'b0}}), .out(multiplexer_31_out), .sel(or_3_out));
  Multiplexer #(.select(1), .width(32), .disabled("Z"), .enable("false")) multiplexer_32 (
    .in0(ID_PC), .in1({32{1'b0}}), .out(multiplexer_32_out), .sel(or_3_out));
  Register #(.width(5), .trigger("rising"), .Select("low")) \u_假WriteReg_num  (
    .D(multiplexer_13_out), .Q(EX_WriteReg_num), .clk(and_2_out), .clr(RST));  // open: en
  Register #(.width(1), .trigger("rising"), .Select("low")) MemToReg (
    .D(multiplexer_14_out), .Q(MemToReg_q), .clk(and_2_out), .clr(RST));  // open: en
  Register #(.width(1), .trigger("rising"), .Select("low")) RegDst (
    .D(multiplexer_15_out), .Q(RegDst_q), .clk(and_2_out), .clr(RST));  // open: en
  Register #(.width(1), .trigger("rising"), .Select("low")) u_RegWrite (
    .D(multiplexer_16_out), .Q(RegWrite3), .clk(and_2_out), .clr(RST));  // open: en
  Register #(.width(1), .trigger("rising"), .Select("low")) u_MemWrite (
    .D(multiplexer_17_out), .Q(MemWrite_q), .clk(and_2_out), .clr(RST));  // open: en
  Register #(.width(4), .trigger("rising"), .Select("low")) ALuOP (
    .D(multiplexer_18_out), .Q(ALuOP3), .clk(and_2_out), .clr(RST));  // open: en
  Register #(.width(1), .trigger("rising"), .Select("low")) ALuSrcB (
    .D(multiplexer_19_out), .Q(ALuSrcB3), .clk(and_2_out), .clr(RST));  // open: en
  Register #(.width(1), .trigger("rising"), .Select("low")) u_Syscall (
    .D(multiplexer_20_out), .Q(Syscall3), .clk(and_2_out), .clr(RST));  // open: en
  Register #(.width(1), .trigger("rising"), .Select("low")) Bne (
    .D(multiplexer_21_out), .Q(Bne3), .clk(and_2_out), .clr(RST));  // open: en
  Register #(.width(1), .trigger("rising"), .Select("low")) Beq (
    .D(multiplexer_22_out), .Q(Beq3), .clk(and_2_out), .clr(RST));  // open: en
  Register #(.width(1), .trigger("rising"), .Select("low")) Jal (
    .D(multiplexer_23_out), .Q(Jal3), .clk(and_2_out), .clr(RST));  // open: en
  Register #(.width(1), .trigger("rising"), .Select("low")) Jmp (
    .D(multiplexer_24_out), .Q(Jmp3), .clk(and_2_out), .clr(RST));  // open: en
  Register #(.width(1), .trigger("rising"), .Select("low")) JR (
    .D(multiplexer_25_out), .Q(JR3), .clk(and_2_out), .clr(RST));  // open: en
  Register #(.width(32), .trigger("rising"), .Select("low")) IR_2 (
    .D(multiplexer_26_out), .Q(EX_IR), .clk(and_2_out), .clr(RST));  // open: en
  Register #(.width(32), .trigger("rising"), .Select("low")) PC_3 (
    .D(multiplexer_27_out), .Q(PC3), .clk(and_2_out), .clr(RST));  // open: en
  Register #(.width(32), .trigger("rising"), .Select("low")) A (
    .D(multiplexer_28_out), .Q(A3), .clk(and_2_out), .clr(RST));  // open: en
  Register #(.width(32), .trigger("rising"), .Select("low")) B (
    .D(multiplexer_29_out), .Q(B3), .clk(and_2_out), .clr(RST));  // open: en
  Register #(.width(32), .trigger("rising"), .Select("low")) Imm (
    .D(multiplexer_30_out), .Q(Imm3), .clk(and_2_out), .clr(RST));  // open: en
  Register #(.width(5), .trigger("rising"), .Select("low")) Shmat (
    .D(multiplexer_31_out), .Q(Shmat3), .clk(and_2_out), .clr(RST));  // open: en
  Register #(.width(32), .trigger("rising"), .Select("low")) PCO_2 (
    .D(multiplexer_32_out), .Q(EX_PC), .clk(and_2_out), .clr(RST));  // open: en
  \数据相关检测  \u_数据相关检测_1  (
    .EX_WriteReg_num(EX_WriteReg_num), .R1_Used(\源寄存器使用情况_1_r1_used ), .R1_num(multiplexer_7_out),
    .R2_Used(\源寄存器使用情况_1_r2_used ), .R2_num(multiplexer_9_out), .MEM_WriteReg_num(MEM_WriteReg_num),
    .RegWrite_EX(RegWrite3), .Yes(\数据相关 ), .RegWrite_MEM(RegWrite4));
  Multiplexer #(.select(1), .width(32), .disabled("Z"), .enable("false")) multiplexer_33 (
    .in0({EX_PC[31:28], EX_IR[25:0], 2'b00}), .in1(A3), .out(\J系列地址3 ), .sel(JR3));
  // Mips_Probe mips_probe_8: pin names not known; wires that end beside it: EX_IR
  or or_4 (\B系列3 , and_4_out, and_5_out, and_3_out);
  Multiplexer #(.select(2), .width(32), .disabled("Z"), .enable("false")) multiplexer_34 (
    .in0(B3), .in1(Imm3), .in2(32'h22), .out(multiplexer_34_out), .sel({Syscall3, ALuSrcB3}));  // open: in3
  Shifter #(.width(32), .shift("ll")) shifter_1 (.in(Imm3), .\dist (5'b00010), .out(shifter_1_out));
  and and_3 (and_3_out, Beq3, equal3);
  MIPS_ALU mips_alu_1 (
    .X(A3), .Y(multiplexer_34_out), .AluOP(ALuOP3), .Equal(equal3), .Result(ALU3), .shamt(Shmat3));  // open: Result_2
  Adder #(.width(32)) adder_2 (.a(shifter_1_out), .b(PC3), .out(\B系列地址3 ), .cin(1'b0));  // open: cout
  Register #(.width(5), .trigger("rising"), .Select("low")) \u_假WriteReg_num_2  (
    .D(EX_WriteReg_num), .Q(MEM_WriteReg_num), .clk(and_2_out), .clr(RST));  // open: en
  Register #(.width(1), .trigger("rising"), .Select("low")) MemToReg_2 (
    .D(MemToReg_q), .Q(MemToReg_2_q), .clk(and_2_out), .clr(RST));  // open: en
  Register #(.width(1), .trigger("rising"), .Select("low")) RegDst_2 (
    .D(RegDst_q), .Q(RegDst_2_q), .clk(and_2_out), .clr(RST));  // open: en
  Register #(.width(1), .trigger("rising"), .Select("low")) RegWrite_2 (
    .D(RegWrite3), .Q(RegWrite4), .clk(and_2_out), .clr(RST));  // open: en
  Register #(.width(1), .trigger("rising"), .Select("low")) MemWrite_2 (
    .D(MemWrite_q), .Q(MemWrite), .clk(and_2_out), .clr(RST));  // open: en
  Register #(.width(1), .trigger("rising"), .Select("low")) Syscall_2 (
    .D(Syscall3), .Q(Syscall4), .clk(and_2_out), .clr(RST));  // open: en
  Register #(.width(1), .trigger("rising"), .Select("low")) equal (
    .D(equal3), .Q(equal4), .clk(and_2_out), .clr(RST));  // open: en
  Register #(.width(1), .trigger("rising"), .Select("low")) Jal_2 (
    .D(Jal3), .Q(Jal_2_q), .clk(and_2_out), .clr(RST));  // open: en
  Register #(.width(32), .trigger("rising"), .Select("low")) IR_3 (
    .D(EX_IR), .Q(IR4), .clk(and_2_out), .clr(RST));  // open: en
  Register #(.width(32), .trigger("rising"), .Select("low")) PC_4 (
    .D(PC3), .Q(PC_4_q), .clk(and_2_out), .clr(RST));  // open: en
  Register #(.width(32), .trigger("rising"), .Select("low")) B_2 (
    .D(B3), .Q(MDin), .clk(and_2_out), .clr(RST));  // open: en
  Register #(.width(32), .trigger("rising"), .Select("low")) ALU (
    .D(ALU3), .Q(ALU4), .clk(and_2_out), .clr(RST));  // open: en
  Register #(.width(32), .trigger("rising"), .Select("low")) PCO_3 (
    .D(EX_PC), .Q(M_PC), .clk(and_2_out), .clr(RST));  // open: en
  Comparator #(.width(32), .mode("twosComplement")) comparator_4 (
    .a(32'h1), .b(ALU3), .eq(comparator_4_eq));  // open: gt, lt
  Comparator #(.width(6), .mode("twosComplement")) comparator_5 (
    .a(EX_IR[31:26]), .b(6'b000001), .eq(comparator_5_eq));  // open: gt, lt
  and and_4 (and_4_out, comparator_5_eq, comparator_4_eq);
  and and_5 (and_5_out, not_5_out, Bne3);
  not not_5 (not_5_out, equal3);
  and and_6 (and_6_out, Syscall3, equal3);
  Register #(.width(32), .trigger("rising"), .Select("low")) register_1 (
    .D(B3), .en(and_6_out), .Q(LedData), .clk(CLK), .clr(RST));
  // Mips_Probe mips_probe_9: pin names not known; wires that end beside it: IR4
  Register #(.width(1), .trigger("rising"), .Select("low")) MemToReg_3 (
    .D(MemToReg_2_q), .Q(MemToReg5), .clk(and_2_out), .clr(RST));  // open: en
  Register #(.width(1), .trigger("rising"), .Select("low")) RegDst_3 (
    .D(RegDst_2_q), .Q(RegDst5), .clk(and_2_out), .clr(RST));  // open: en
  Register #(.width(1), .trigger("rising"), .Select("low")) RegWrite_3 (
    .D(RegWrite4), .Q(RegWrite), .clk(and_2_out), .clr(RST));  // open: en
  Register #(.width(1), .trigger("rising"), .Select("low")) Syscall_3 (
    .D(Syscall4), .Q(Syscall5), .clk(and_2_out), .clr(RST));  // open: en
  Register #(.width(1), .trigger("rising"), .Select("low")) equal_2 (
    .D(equal4), .Q(equal5), .clk(and_2_out), .clr(RST));  // open: en
  Register #(.width(1), .trigger("rising"), .Select("low")) Jal_3 (
    .D(Jal_2_q), .Q(Jal5), .clk(and_2_out), .clr(RST));  // open: en
  Register #(.width(32), .trigger("rising"), .Select("low")) IR_4 (
    .D(IR4), .Q(IR5), .clk(and_2_out), .clr(RST));  // open: en
  Register #(.width(32), .trigger("rising"), .Select("low")) PC_5 (
    .D(PC_4_q), .Q(PC5), .clk(and_2_out), .clr(RST));  // open: en
  Register #(.width(32), .trigger("rising"), .Select("low")) ALU_2 (
    .D(ALU4), .Q(ALU5), .clk(and_2_out), .clr(RST));  // open: en
  Register #(.width(32), .trigger("rising"), .Select("low")) MD (
    .D(MD4), .Q(MD5), .clk(and_2_out), .clr(RST));  // open: en
  Register #(.width(32), .trigger("rising"), .Select("low")) PCO_4 (
    .D(M_PC), .Q(WB_PC), .clk(and_2_out), .clr(RST));  // open: en
  Register #(.width(2), .trigger("rising"), .Select("low")) byteoff (
    .D(ALU4[1:0]), .Q(byteoff5), .clk(and_2_out), .clr(RST));  // open: en
  RAM #(.addrWidth(10), .dataWidth(32), .bus("separate"), .Select("high")) ram_1 (
    .addr(ALU4[11:2]), .din(MDin), .data(MD4), .str(MemWrite), .clk(CLK), .clr(RST));  // open: sel, ld
  // Mips_Probe mips_probe_10: pin names not known; wires that end beside it: IR5
  Multiplexer #(.select(2), .width(32), .disabled("Z"), .enable("false")) multiplexer_35 (
    .in0(ALU5), .in1(MD5), .in2(PC5), .out(RDin1), .sel({Jal5, MemToReg5}));  // open: in3

  // Other names for the same wires on the sheet: byteoff[1:0] = ALU4[1:0]; B4[31:0] = MDin; IRNO1[31:0] = IF_IR;
  //   ID_IR[5:0] = Func; IR[31:0] = {ID_IR, Func}; IRNO2[31:0] = {ID_IR, Func}; Shmat2[4:0] = ID_IR[10:6];
  //   OP[5:0] = ID_IR[31:26]; IRNO3[31:0] = EX_IR; MEM_IR[31:0] = IR4; MEM_PC[31:0] = M_PC; MemWrite4 = MemWrite;
  //   PC[31:0] = IF_PC; PCO1[31:0] = IF_PC; PCO3[31:0] = EX_PC; RegWrite5 = RegWrite; result[31:0] = ALU3;
  //   Syscall2 = Syscall; WB_IR[31:0] = IR5; 总复位 = RST

  // Notes on the sheet:
  //   中断源
  //   时空图监测，可删除
  //   中断等待指示
  //   Syscall停机功能模块
  //   数码管输出
  //   控制位
  //   流水调试日志用
  //   暂停节拍，不能为0
  //   戳工具置1进入计数暂停模式，ctrl+k时钟自动运行到对应节拍暂停
  //   ctrl+k关闭时钟连续运行，将控制位置零，进入单步调试模式调试
  //   指令存储器
  //   contents of rom_1 (hex, n*v repeats v):
  //   20110001 8000c05 20110001 20120002 20130003 8000c09 20110001 20120002 20130003 8000c0d 20110001
  //   20120002 20130003 8000c11 20110001 20120002 20130003 c000cb8 20100001 20110001 118fc0 112020
  //   20020022 c 118882 12200001 8000c15 112020 20020022 c 20110001 118880 112020 20020022 c 12200001
  //   8000c1f 20110001 118fc0 112020 20020022 c 1188c3 112020 20020022 c 118903 112020 20020022 c 118903
  //   112020 20020022 c 118903 112020 20020022 c 118903 112020 20020022 c 118903 112020 20020022 c 118903
  //   112020 20020022 c 118903 112020 20020022 c 20100001 109fc0 139fc3 8021 2012000c 24160003 26100001
  //   3210000f 20080008 20090001 139900 2709825 132020 20020022 c 1094022 1500fff9 22100001 2018000f
  //   2188024 108700 20080008 20090001 139902 2709825 132021 20020022 c 1094022 1500fff9 108702 2c9b022
  //   12c00001 8000c50 4020 1084027 84400 3508ffff 82021 20020022 c 2010ffff 20110000 ae300000 22100001
  //   22310004 ae300000 22100001 22310004 ae300000 22100001 22310004 ae300000 22100001 22310004 ae300000
  //   22100001 22310004 ae300000 22100001 22310004 ae300000 22100001 22310004 ae300000 22100001 22310004
  //   ae300000 22100001 22310004 ae300000 22100001 22310004 ae300000 22100001 22310004 ae300000 22100001
  //   22310004 ae300000 22100001 22310004 ae300000 22100001 22310004 ae300000 22100001 22310004 ae300000
  //   22100001 22310004 22100001 8020 2011003c 8e130000 8e340000 274402a 11000002 ae330000 ae140000
  //   2231fffc 1611fff8 102020 20020022 c 22100004 2011003c 1611fff2 20020032 c 20100000 22100001 102020
  //   20020022 c 22100002 102020 20020022 c 22100003 102020 20020022 c 22100004 102020 20020022 c 22100005
  //   102020 20020022 c 22100006 102020 20020022 c 22100007 102020 20020022 c 22100008 102020 20020022
  //   20020022 c 3e00008
  //   可计数暂停的时钟源
  //   IF/ID
  //   指令字
  //   JMP
  //   JR
  //   OP
  //   Func
  //   Syscall
  //   rs
  //   rt
  //   rd
  //   为方便自动评测，需要输出流水线各段保存的PC值，注意是PC不是PC+4，另外ID段寄存器写入信息，Mem段内存写入信息也要输出
  //   Beq
  //   Bne
  //   rd
  //   ID/EX
  //   EX/MEM
  //   MEM/WB
endmodule
module \重定向流水线  (
  output RegWrite,
  output MemWrite,
  output [31:0] IF_PC,
  output [31:0] ID_PC,
  output [31:0] EX_PC,
  output [31:0] M_PC,
  output [31:0] WB_PC,
  output [31:0] RDin,
  output [31:0] MDin,
  output [31:0] LedData
);

  wire ALuSrcB2, ALuSrcB3, and_1_out, and_2_out, and_3_out, and_4_out, and_5_out, and_6_out, Beq2, Beq3,
       Bne2, Bne3, \B系列3 , CLK, clock_1_out, clock_2_out, comparator_1_eq, comparator_2_eq, comparator_2_lt,
       comparator_3_eq, comparator_4_eq, comparator_5_eq, d_ff_2_q, equal3, equal4, equal5, Go, IR1, IR2,
       IR3, Jal2, Jal3, Jal5, Jal_2_q, Jmp2, Jmp3, JR2, JR3, Loaduse, MemToReg2, MemToReg3, MemToReg5,
       MemToReg_2_q, MemWrite2, MemWrite_q, multiplexer_12_out, multiplexer_13_out, multiplexer_14_out,
       multiplexer_15_out, multiplexer_17_out, multiplexer_18_out, multiplexer_19_out, multiplexer_20_out,
       multiplexer_21_out, multiplexer_22_out, multiplexer_23_out, nand_1_out, not_1_out, not_2_out,
       not_4_out, not_5_out, or_1_out, or_2_out, or_3_out, \PC使能 , RegDst2, RegDst5, RegDst_2_q, RegDst_q,
       RegWrite2, RegWrite3, RegWrite4, RST, SignedExt, Syscall, Syscall3, Syscall4, Syscall5, W1, W2, W3,
       \分支气泡 , \数据相关 , \源寄存器使用情况_1_r1_used , \源寄存器使用情况_1_r2_used ;
  wire [1:0] byteoff5, multiplexer_31_out, multiplexer_32_out, RsForward2, RsForward3, RtForward2, RtForward3;
  wire [3:0] ALuOP2, ALuOP3, multiplexer_16_out;
  wire [4:0] EX_WriteReg_num, MEM_WriteReg_num, multiplexer_6_out, multiplexer_7_out, multiplexer_8_out,
       multiplexer_10_out, multiplexer_11_out, multiplexer_29_out, Shmat3;
  wire [5:0] Func;
  wire [7:0] multiplexer_37_out;
  wire [12:0] CNT_num;
  wire [15:0] \LoadUse次数 , \总周期数 , \插入气泡数 , \无条件分支数 , \条件分支成功数 ;
  wire [31:0] A2, A3, ALU3, ALU4, ALU5, B2, B3, B4, bit_extender_1_out, bit_extender_2_out,
       bit_extender_3_out, \B系列地址3 , EX_IR, IF_IR, Imm2, Imm3, IR4, IR5, \J系列地址3 , MD4, MD5,
       multiplexer_2_out, multiplexer_3_out, multiplexer_4_out, multiplexer_5_out, multiplexer_24_out,
       multiplexer_25_out, multiplexer_26_out, multiplexer_27_out, multiplexer_28_out, multiplexer_30_out,
       multiplexer_35_out, multiplexer_36_out, NextPCNormal, PC1, PC2, PC3, PC5, PC_4_q, ram_1_data, RealB3,
       shifter_1_out;
  wire [31:6] ID_IR;

  Button \u_总复位  (.out(RST));
  Button _1 (.out(IR1));
  Button _2 (.out(IR2));
  Button _3 (.out(IR3));
  // Probe on \总周期数 
  // Probe on \总周期数 
  Button \u_继续运行  (.out(Go));
  LED #(.active("true")) led_1 (.in(W1));
  LED #(.active("true")) led_2 (.in(W2));
  LED #(.active("true")) led_3 (.in(W3));
  Hex_Digit_Display hex_digit_display_1 (.value(LedData[31:28]));  // open: dp
  // Probe on IF_PC[19:0]
  // Mips_Probe mips_probe_1: pin names not known; wires that end beside it: IF_IR
  not not_1 (not_1_out, Syscall5);
  Hex_Digit_Display hex_digit_display_2 (.value(LedData[23:20]));  // open: dp
  Hex_Digit_Display hex_digit_display_3 (.value(LedData[27:24]));  // open: dp
  // Probe on ID_PC[19:0]
  // Mips_Probe mips_probe_2: pin names not known; wires that end beside it: {ID_IR, Func}
  or or_1 (or_1_out, not_1_out, Go);
  or or_2 (or_2_out, equal5, not_1_out);
  Hex_Digit_Display hex_digit_display_4 (.value(LedData[19:16]));  // open: dp
  Hex_Digit_Display hex_digit_display_5 (.value(LedData[15:12]));  // open: dp
  D_Flip_Flop #(.trigger("falling"), .Pre_Clr_Positions("ABOVE_BELOW"), .NegatePresetClear("false"), .enable("false"), .NewFFLayout("true")) d_ff_1 (
    .clk(CLK), .D(or_2_out), .Q(\PC使能 ), .preset(or_1_out));  // open: Qn, reset
  Hex_Digit_Display hex_digit_display_6 (.value(LedData[7:4]));  // open: dp
  Hex_Digit_Display hex_digit_display_7 (.value(LedData[11:8]));  // open: dp
  Clock #(.highDuration(1), .lowDuration(1)) clock_1 (.out(clock_1_out));
  // Probe on EX_PC[19:0]
  // Mips_Probe mips_probe_3: pin names not known; wires that end beside it: clock_1_out, EX_IR, CLK
  Hex_Digit_Display hex_digit_display_8 (.value(LedData[3:0]));  // open: dp
  // Probe on \总周期数 
  // Probe on M_PC[19:0]
  // Mips_Probe mips_probe_4: pin names not known; wires that end beside it: IR4
  // Probe on \总周期数 
  // Probe on \无条件分支数 
  // Probe on \条件分支成功数 
  // Probe on \插入气泡数 
  // Probe on \LoadUse次数 
  Comparator #(.width(2), .mode("twosComplement")) comparator_1 (
    .a({\B系列3 , Jmp3}), .b(2'b00), .eq(comparator_1_eq));  // open: gt, lt
  Multiplexer #(.select(2), .width(32), .disabled("Z"), .enable("false")) multiplexer_1 (
    .in0(PC1), .in1(\J系列地址3 ), .in2(\B系列地址3 ), .out(NextPCNormal), .sel({\B系列3 , Jmp3}));  // open: in3
  Multiplexer #(.select(1), .width(32), .disabled("Z"), .enable("false")) multiplexer_2 (
    .in0(NextPCNormal), .in1({32{1'b0}}), .out(multiplexer_2_out), .sel(1'b0));
  and and_1 (and_1_out, \PC使能 , not_2_out);
  not not_2 (not_2_out, Loaduse);
  and and_2 (and_2_out, \PC使能 , CLK);
  // Probe on IF_PC[11:0]
  // Probe on WB_PC[19:0]
  // Mips_Probe mips_probe_5: pin names not known; wires that end beside it: IR5
  not not_3 (\分支气泡 , comparator_1_eq);
  Register #(.width(32), .trigger("rising"), .Select("low")) PC (
    .D(multiplexer_2_out), .en(and_1_out), .Q(IF_PC), .clk(CLK), .clr(RST));
  Adder #(.width(32)) adder_1 (.a(IF_PC), .b(32'h4), .out(PC1));  // open: cin, cout
  not not_4 (not_4_out, Loaduse);
  // Probe on EX_PC[11:0]
  // Probe on ID_PC[11:0]
  // Probe on M_PC[11:0]
  D_Flip_Flop #(.trigger("high"), .Pre_Clr_Positions("LEGACY"), .NegatePresetClear("false"), .enable("true"), .NewFFLayout("false")) d_ff_2 (.Q(d_ff_2_q));  // open: clk, D, Qn, preset, en, reset
  // Probe on 13'h378
  // Probe on WB_PC[11:0]
  Comparator #(.width(13), .mode("twosComplement")) comparator_2 (
    .a(CNT_num), .b(13'h378), .eq(comparator_2_eq), .lt(comparator_2_lt));  // open: gt
  Clock #(.highDuration(1), .lowDuration(1)) clock_2 (.out(clock_2_out));
  ROM #(.addrWidth(10), .dataWidth(32), .Select("high")) rom_1 (.addr(IF_PC[11:2]), .data(IF_IR));
  nand nand_1 (nand_1_out, d_ff_2_q, comparator_2_eq);
  Counter #(.width(13), .max('h1fff), .ongoal("stay"), .trigger("rising"), .behavior("old")) counter_1 (
    .count(comparator_2_lt), .Q(CNT_num), .clk(clock_2_out));  // open: load, D, carry, clr, preset
  // Mips_Probe mips_probe_6: pin names not known; wires that end beside it: IF_IR
  assign CLK = nand_1_out ? clock_2_out : 1'bz;  // Controlled_Buffer controlled_buffer_1
  Multiplexer #(.select(1), .width(32), .disabled("Z"), .enable("false")) multiplexer_3 (
    .in0(IF_IR), .in1({32{1'b0}}), .out(multiplexer_3_out), .sel(\分支气泡 ));
  Multiplexer #(.select(1), .width(32), .disabled("Z"), .enable("false")) multiplexer_4 (
    .in0(PC1), .in1({32{1'b0}}), .out(multiplexer_4_out), .sel(\分支气泡 ));
  Multiplexer #(.select(1), .width(32), .disabled("Z"), .enable("false")) multiplexer_5 (
    .in0(IF_PC), .in1({32{1'b0}}), .out(multiplexer_5_out), .sel(\分支气泡 ));
  Pull_Resistor #(.pull(1)) pull_resistor_1 (.node(CLK));
  Register #(.width(32), .trigger("rising"), .Select("low")) IR (
    .D(multiplexer_3_out), .en(not_4_out), .Q({ID_IR, Func}), .clk(and_2_out), .clr(RST));
  Register #(.width(32), .trigger("rising"), .Select("low")) PC_2 (
    .D(multiplexer_4_out), .en(not_4_out), .Q(PC2), .clk(and_2_out), .clr(RST));
  Register #(.width(32), .trigger("rising"), .Select("low")) PCO (
    .D(multiplexer_5_out), .en(not_4_out), .Q(ID_PC), .clk(and_2_out), .clr(RST));
  // Mips_Probe mips_probe_7: pin names not known; wires that end beside it: {ID_IR, Func}
  \单周期硬布线控制器  \u_单周期硬布线控制器_1  (
    .Func(Func), .OP(ID_IR[31:26]), .ALU_OP(ALuOP2), .MemToReg(MemToReg2), .MemWrite(MemWrite2),
    .ALU_SRC(ALuSrcB2), .RegWrite(RegWrite2), .SysCALL(Syscall), .SignedExt(SignedExt), .RegDst(RegDst2),
    .JR(JR2), .JMP(Jmp2), .Beq(Beq2), .JAL(Jal2), .Bne(Bne2));
  Multiplexer #(.select(1), .width(5), .disabled("Z"), .enable("false")) multiplexer_6 (
    .in0(ID_IR[25:21]), .in1(5'b00010), .out(multiplexer_6_out), .sel(Syscall));
  Multiplexer #(.select(2), .width(5), .disabled("Z"), .enable("false")) multiplexer_7 (
    .in0(IR5[20:16]), .in1(IR5[15:11]), .in2({5{1'b1}}), .out(multiplexer_7_out), .sel({Jal5, RegDst5}));  // open: in3
  Multiplexer #(.select(1), .width(5), .disabled("Z"), .enable("false")) multiplexer_8 (
    .in0(ID_IR[20:16]), .in1(5'b00100), .out(multiplexer_8_out), .sel(Syscall));
  or or_3 (or_3_out, \分支气泡 , Loaduse);
  assign bit_extender_1_out = {{16{1'b0}}, {ID_IR[15:6], Func}};  // Bit_Extender bit_extender_1
  Multiplexer #(.select(1), .width(32), .disabled("Z"), .enable("false")) multiplexer_9 (
    .in0(bit_extender_1_out), .in1(bit_extender_2_out), .out(Imm2), .sel(SignedExt));
  assign bit_extender_2_out = {{16{ID_IR[15]}}, {ID_IR[15:6], Func}};  // Bit_Extender bit_extender_2
  Multiplexer #(.select(2), .width(5), .disabled("Z"), .enable("false")) multiplexer_10 (
    .in0(ID_IR[20:16]), .in1(ID_IR[15:11]), .in2({5{1'b1}}), .out(multiplexer_10_out), .sel({Jal2, RegDst2}));  // open: in3
  \源寄存器使用情况  \u_源寄存器使用情况_1  (
    .OP0(ID_IR[26]), .OP1(ID_IR[27]), .OP2(ID_IR[28]), .OP3(ID_IR[29]), .OP4(ID_IR[30]), .OP5(ID_IR[31]),
    .F0(Func[0]), .F1(Func[1]), .F2(Func[2]), .F3(Func[3]), .F4(Func[4]), .F5(Func[5]),
    .R1_used(\源寄存器使用情况_1_r1_used ), .R2_used(\源寄存器使用情况_1_r2_used ));
  MIPS_Regifile mips_regifile_1 (
    .Din(RDin), .Clk(CLK), .R1(A2), .R2(B2), .WE(RegWrite), .W_num(multiplexer_7_out),
    .R1_num(multiplexer_6_out), .R2_num(multiplexer_8_out));
  Multiplexer #(.select(1), .width(5), .disabled("Z"), .enable("false")) multiplexer_11 (
    .in0(multiplexer_10_out), .in1({5{1'b0}}), .out(multiplexer_11_out), .sel(or_3_out));
  Multiplexer #(.select(1), .width(1), .disabled("Z"), .enable("false")) multiplexer_12 (
    .in0(MemToReg2), .in1(1'b0), .out(multiplexer_12_out), .sel(or_3_out));
  Multiplexer #(.select(1), .width(1), .disabled("Z"), .enable("false")) multiplexer_13 (
    .in0(RegDst2), .in1(1'b0), .out(multiplexer_13_out), .sel(or_3_out));
  Multiplexer #(.select(1), .width(1), .disabled("Z"), .enable("false")) multiplexer_14 (
    .in0(RegWrite2), .in1(1'b0), .out(multiplexer_14_out), .sel(or_3_out));
  Multiplexer #(.select(1), .width(1), .disabled("Z"), .enable("false")) multiplexer_15 (
    .in0(MemWrite2), .in1(1'b0), .out(multiplexer_15_out), .sel(or_3_out));
  Multiplexer #(.select(1), .width(4), .disabled("Z"), .enable("false")) multiplexer_16 (
    .in0(ALuOP2), .in1(4'b0000), .out(multiplexer_16_out), .sel(or_3_out));
  Multiplexer #(.select(1), .width(1), .disabled("Z"), .enable("false")) multiplexer_17 (
    .in0(ALuSrcB2), .in1(1'b0), .out(multiplexer_17_out), .sel(or_3_out));
  Multiplexer #(.select(1), .width(1), .disabled("Z"), .enable("false")) multiplexer_18 (
    .in0(Syscall), .in1(1'b0), .out(multiplexer_18_out), .sel(or_3_out));
  Multiplexer #(.select(1), .width(1), .disabled("Z"), .enable("false")) multiplexer_19 (
    .in0(Bne2), .in1(1'b0), .out(multiplexer_19_out), .sel(or_3_out));
  Multiplexer #(.select(1), .width(1), .disabled("Z"), .enable("false")) multiplexer_20 (
    .in0(Beq2), .in1(1'b0), .out(multiplexer_20_out), .sel(or_3_out));
  Multiplexer #(.select(1), .width(1), .disabled("Z"), .enable("false")) multiplexer_21 (
    .in0(Jal2), .in1(1'b0), .out(multiplexer_21_out), .sel(or_3_out));
  Multiplexer #(.select(1), .width(1), .disabled("Z"), .enable("false")) multiplexer_22 (
    .in0(Jmp2), .in1(1'b0), .out(multiplexer_22_out), .sel(or_3_out));
  Multiplexer #(.select(1), .width(1), .disabled("Z"), .enable("false")) multiplexer_23 (
    .in0(JR2), .in1(1'b0), .out(multiplexer_23_out), .sel(or_3_out));
  Multiplexer #(.select(1), .width(32), .disabled("Z"), .enable("false")) multiplexer_24 (
    .in0({ID_IR, Func}), .in1({32{1'b0}}), .out(multiplexer_24_out), .sel(or_3_out));
  Multiplexer #(.select(1), .width(32), .disabled("Z"), .enable("false")) multiplexer_25 (
    .in0(PC2), .in1({32{1'b0}}), .out(multiplexer_25_out), .sel(or_3_out));
  Multiplexer #(.select(1), .width(32), .disabled("Z"), .enable("false")) multiplexer_26 (
    .in0(A2), .in1({32{1'b0}}), .out(multiplexer_26_out), .sel(or_3_out));
  Multiplexer #(.select(1), .width(32), .disabled("Z"), .enable("false")) multiplexer_27 (
    .in0(B2), .in1({32{1'b0}}), .out(multiplexer_27_out), .sel(or_3_out));
  Multiplexer #(.select(1), .width(32), .disabled("Z"), .enable("false")) multiplexer_28 (
    .in0(Imm2), .in1({32{1'b0}}), .out(multiplexer_28_out), .sel(or_3_out));
  Multiplexer #(.select(1), .width(5), .disabled("Z"), .enable("false")) multiplexer_29 (
    .in0(ID_IR[10:6]), .in1({5{1'b0}}), .out(multiplexer_29_out), .sel(or_3_out));
  Multiplexer #(.select(1), .width(32), .disabled("Z"), .enable("false")) multiplexer_30 (
    .in0(ID_PC), .in1({32{1'b0}}), .out(multiplexer_30_out), .sel(or_3_out));
  Multiplexer #(.select(1), .width(2), .disabled("Z"), .enable("false")) multiplexer_31 (
    .in0(RsForward2), .in1(2'b00), .out(multiplexer_31_out), .sel(or_3_out));
  Multiplexer #(.select(1), .width(2), .disabled("Z"), .enable("false")) multiplexer_32 (
    .in0(RtForward2), .in1(2'b00), .out(multiplexer_32_out), .sel(or_3_out));
  Register #(.width(5), .trigger("rising"), .Select("low")) \u_假WriteReg_num  (
    .D(multiplexer_11_out), .Q(EX_WriteReg_num), .clk(and_2_out), .clr(RST));  // open: en
  Register #(.width(1), .trigger("rising"), .Select("low")) MemToReg (
    .D(multiplexer_12_out), .Q(MemToReg3), .clk(and_2_out), .clr(RST));  // open: en
  Register #(.width(1), .trigger("rising"), .Select("low")) RegDst (
    .D(multiplexer_13_out), .Q(RegDst_q), .clk(and_2_out), .clr(RST));  // open: en
  Register #(.width(1), .trigger("rising"), .Select("low")) u_RegWrite (
    .D(multiplexer_14_out), .Q(RegWrite3), .clk(and_2_out), .clr(RST));  // open: en
  Register #(.width(1), .trigger("rising"), .Select("low")) u_MemWrite (
    .D(multiplexer_15_out), .Q(MemWrite_q), .clk(and_2_out), .clr(RST));  // open: en
  Register #(.width(4), .trigger("rising"), .Select("low")) ALuOP (
    .D(multiplexer_16_out), .Q(ALuOP3), .clk(and_2_out), .clr(RST));  // open: en
  Register #(.width(1), .trigger("rising"), .Select("low")) ALuSrcB (
    .D(multiplexer_17_out), .Q(ALuSrcB3), .clk(and_2_out), .clr(RST));  // open: en
  Register #(.width(1), .trigger("rising"), .Select("low")) u_Syscall (
    .D(multiplexer_18_out), .Q(Syscall3), .clk(and_2_out), .clr(RST));  // open: en
  Register #(.width(1), .trigger("rising"), .Select("low")) Bne (
    .D(multiplexer_19_out), .Q(Bne3), .clk(and_2_out), .clr(RST));  // open: en
  Register #(.width(1), .trigger("rising"), .Select("low")) Beq (
    .D(multiplexer_20_out), .Q(Beq3), .clk(and_2_out), .clr(RST));  // open: en
  Register #(.width(1), .trigger("rising"), .Select("low")) Jal (
    .D(multiplexer_21_out), .Q(Jal3), .clk(and_2_out), .clr(RST));  // open: en
  Register #(.width(1), .trigger("rising"), .Select("low")) Jmp (
    .D(multiplexer_22_out), .Q(Jmp3), .clk(and_2_out), .clr(RST));  // open: en
  Register #(.width(1), .trigger("rising"), .Select("low")) JR (
    .D(multiplexer_23_out), .Q(JR3), .clk(and_2_out), .clr(RST));  // open: en
  Register #(.width(32), .trigger("rising"), .Select("low")) IR_2 (
    .D(multiplexer_24_out), .Q(EX_IR), .clk(and_2_out), .clr(RST));  // open: en
  Register #(.width(32), .trigger("rising"), .Select("low")) PC_3 (
    .D(multiplexer_25_out), .Q(PC3), .clk(and_2_out), .clr(RST));  // open: en
  Register #(.width(32), .trigger("rising"), .Select("low")) A (
    .D(multiplexer_26_out), .Q(A3), .clk(and_2_out), .clr(RST));  // open: en
  Register #(.width(32), .trigger("rising"), .Select("low")) B (
    .D(multiplexer_27_out), .Q(B3), .clk(and_2_out), .clr(RST));  // open: en
  Register #(.width(32), .trigger("rising"), .Select("low")) Imm (
    .D(multiplexer_28_out), .Q(Imm3), .clk(and_2_out), .clr(RST));  // open: en
  Register #(.width(5), .trigger("rising"), .Select("low")) Shmat (
    .D(multiplexer_29_out), .Q(Shmat3), .clk(and_2_out), .clr(RST));  // open: en
  Register #(.width(32), .trigger("rising"), .Select("low")) PCO_2 (
    .D(multiplexer_30_out), .Q(EX_PC), .clk(and_2_out), .clr(RST));  // open: en
  Register #(.width(2), .trigger("rising"), .Select("low")) RsForward (
    .D(multiplexer_31_out), .Q(RsForward3), .clk(and_2_out), .clr(RST));  // open: en
  Register #(.width(2), .trigger("rising"), .Select("low")) RtForward (
    .D(multiplexer_32_out), .Q(RtForward3), .clk(and_2_out), .clr(RST));  // open: en
  \重定向数据相关检测  \u_重定向数据相关检测_1  (
    .EX_WriteReg_num(EX_WriteReg_num), .R1_Used(\源寄存器使用情况_1_r1_used ), .R1_num(multiplexer_6_out),
    .R2_Used(\源寄存器使用情况_1_r2_used ), .R2_num(multiplexer_8_out), .MEM_WriteReg_num(MEM_WriteReg_num),
    .RegWrite3(RegWrite3), .Yes(\数据相关 ), .LoadUse(Loaduse), .EX_MemRead(MemToReg3), .RsForward(RsForward2),
    .RtForward(RtForward2), .RegWrite4(RegWrite4));
  Multiplexer #(.select(2), .width(32), .disabled("Z"), .enable("false")) multiplexer_33 (
    .in0(B3), .in1(RDin), .in2(ALU4), .out(RealB3), .sel(RtForward3));  // open: in3
  Multiplexer #(.select(1), .width(32), .disabled("Z"), .enable("false")) multiplexer_34 (
    .in0({EX_PC[31:28], EX_IR[25:0], 2'b00}), .in1(A3), .out(\J系列地址3 ), .sel(JR3));
  // Mips_Probe mips_probe_8: pin names not known; wires that end beside it: EX_IR
  Multiplexer #(.select(2), .width(32), .disabled("Z"), .enable("false")) multiplexer_35 (
    .in0(RealB3), .in1(Imm3), .in2(32'h22), .out(multiplexer_35_out), .sel({Syscall3, ALuSrcB3}));  // open: in3
  Shifter #(.width(32), .shift("ll")) shifter_1 (.in(Imm3), .\dist (5'b00010), .out(shifter_1_out));
  Adder #(.width(32)) adder_2 (.a(shifter_1_out), .b(PC3), .out(\B系列地址3 ), .cin(1'b0));  // open: cout
  Register #(.width(5), .trigger("rising"), .Select("low")) \u_假WriteReg_num_2  (
    .D(EX_WriteReg_num), .Q(MEM_WriteReg_num), .clk(and_2_out), .clr(RST));  // open: en
  Register #(.width(1), .trigger("rising"), .Select("low")) MemToReg_2 (
    .D(MemToReg3), .Q(MemToReg_2_q), .clk(and_2_out), .clr(RST));  // open: en
  Register #(.width(1), .trigger("rising"), .Select("low")) RegDst_2 (
    .D(RegDst_q), .Q(RegDst_2_q), .clk(and_2_out), .clr(RST));  // open: en
  Register #(.width(1), .trigger("rising"), .Select("low")) RegWrite_2 (
    .D(RegWrite3), .Q(RegWrite4), .clk(and_2_out), .clr(RST));  // open: en
  Register #(.width(1), .trigger("rising"), .Select("low")) MemWrite_2 (
    .D(MemWrite_q), .Q(MemWrite), .clk(and_2_out), .clr(RST));  // open: en
  Register #(.width(1), .trigger("rising"), .Select("low")) Syscall_2 (
    .D(Syscall3), .Q(Syscall4), .clk(and_2_out), .clr(RST));  // open: en
  Register #(.width(1), .trigger("rising"), .Select("low")) equal (
    .D(equal3), .Q(equal4), .clk(and_2_out), .clr(RST));  // open: en
  Register #(.width(1), .trigger("rising"), .Select("low")) Jal_2 (
    .D(Jal3), .Q(Jal_2_q), .clk(and_2_out), .clr(RST));  // open: en
  Register #(.width(32), .trigger("rising"), .Select("low")) IR_3 (
    .D(EX_IR), .Q(IR4), .clk(and_2_out), .clr(RST));  // open: en
  Register #(.width(32), .trigger("rising"), .Select("low")) PC_4 (
    .D(PC3), .Q(PC_4_q), .clk(and_2_out), .clr(RST));  // open: en
  Register #(.width(32), .trigger("rising"), .Select("low")) B_2 (
    .D(B3), .Q(B4), .clk(and_2_out), .clr(RST));  // open: en
  Register #(.width(32), .trigger("rising"), .Select("low")) ALU (
    .D(ALU3), .Q(ALU4), .clk(and_2_out), .clr(RST));  // open: en
  Register #(.width(32), .trigger("rising"), .Select("low")) RealB (
    .D(RealB3), .Q(MDin), .clk(and_2_out), .clr(RST));  // open: en
  Register #(.width(32), .trigger("rising"), .Select("low")) PCO_3 (
    .D(EX_PC), .Q(M_PC), .clk(and_2_out), .clr(RST));  // open: en
  or or_4 (\B系列3 , and_4_out, and_5_out, and_3_out);
  Multiplexer #(.select(2), .width(32), .disabled("Z"), .enable("false")) multiplexer_36 (
    .in0(A3), .in1(RDin), .in2(ALU4), .out(multiplexer_36_out), .sel(RsForward3));  // open: in3
  Comparator #(.width(32), .mode("twosComplement")) comparator_3 (
    .a(32'h1), .b(ALU3), .eq(comparator_3_eq));  // open: gt, lt
  Comparator #(.width(6), .mode("twosComplement")) comparator_4 (
    .a(EX_IR[31:26]), .b(6'b000001), .eq(comparator_4_eq));  // open: gt, lt
  and and_3 (and_3_out, Beq3, equal3);
  MIPS_ALU mips_alu_1 (
    .X(multiplexer_36_out), .Y(multiplexer_35_out), .AluOP(ALuOP3), .Equal(equal3), .Result(ALU3),
    .shamt(Shmat3));  // open: Result_2
  and and_4 (and_4_out, comparator_4_eq, comparator_3_eq);
  and and_5 (and_5_out, not_5_out, Bne3);
  not not_5 (not_5_out, equal3);
  Register #(.width(32), .trigger("rising"), .Select("low")) register_1 (
    .D(RealB3), .en(and_6_out), .Q(LedData), .clk(CLK), .clr(RST));
  and and_6 (and_6_out, Syscall3, equal3);
  Register #(.width(1), .trigger("rising"), .Select("low")) MemToReg_3 (
    .D(MemToReg_2_q), .Q(MemToReg5), .clk(and_2_out), .clr(RST));  // open: en
  Register #(.width(1), .trigger("rising"), .Select("low")) RegDst_3 (
    .D(RegDst_2_q), .Q(RegDst5), .clk(and_2_out), .clr(RST));  // open: en
  Register #(.width(1), .trigger("rising"), .Select("low")) RegWrite_3 (
    .D(RegWrite4), .Q(RegWrite), .clk(and_2_out), .clr(RST));  // open: en
  Register #(.width(1), .trigger("rising"), .Select("low")) Syscall_3 (
    .D(Syscall4), .Q(Syscall5), .clk(and_2_out), .clr(RST));  // open: en
  Register #(.width(1), .trigger("rising"), .Select("low")) equal_2 (
    .D(equal4), .Q(equal5), .clk(and_2_out), .clr(RST));  // open: en
  Register #(.width(1), .trigger("rising"), .Select("low")) Jal_3 (
    .D(Jal_2_q), .Q(Jal5), .clk(and_2_out), .clr(RST));  // open: en
  Register #(.width(32), .trigger("rising"), .Select("low")) IR_4 (
    .D(IR4), .Q(IR5), .clk(and_2_out), .clr(RST));  // open: en
  Register #(.width(32), .trigger("rising"), .Select("low")) PC_5 (
    .D(PC_4_q), .Q(PC5), .clk(and_2_out), .clr(RST));  // open: en
  Register #(.width(32), .trigger("rising"), .Select("low")) ALU_2 (
    .D(ALU4), .Q(ALU5), .clk(and_2_out), .clr(RST));  // open: en
  Register #(.width(32), .trigger("rising"), .Select("low")) MD (
    .D(MD4), .Q(MD5), .clk(and_2_out), .clr(RST));  // open: en
  Register #(.width(32), .trigger("rising"), .Select("low")) PCO_4 (
    .D(M_PC), .Q(WB_PC), .clk(and_2_out), .clr(RST));  // open: en
  Register #(.width(2), .trigger("rising"), .Select("low")) byteoff (
    .D(ALU4[1:0]), .Q(byteoff5), .clk(and_2_out), .clr(RST));  // open: en
  // Mips_Probe mips_probe_9: pin names not known; wires that end beside it: IR4
  RAM #(.addrWidth(10), .dataWidth(32), .bus("separate"), .Select("high")) ram_1 (
    .addr(ALU4[11:2]), .din(MDin), .data(ram_1_data), .str(MemWrite), .clk(CLK), .clr(RST));  // open: sel, ld
  Comparator #(.width(6), .mode("twosComplement")) comparator_5 (
    .a(IR4[31:26]), .b(6'b100100), .eq(comparator_5_eq));  // open: gt, lt
  Multiplexer #(.select(2), .width(8), .disabled("Z"), .enable("false")) multiplexer_37 (
    .in0(ram_1_data[7:0]), .in1(ram_1_data[15:8]), .in2(ram_1_data[23:16]), .in3(ram_1_data[31:24]),
    .out(multiplexer_37_out), .sel(ALU4[1:0]));
  Multiplexer #(.select(1), .width(32), .disabled("Z"), .enable("false")) multiplexer_38 (
    .in0(ram_1_data), .in1(bit_extender_3_out), .out(MD4), .sel(comparator_5_eq));
  assign bit_extender_3_out = {{24{1'b0}}, multiplexer_37_out};  // Bit_Extender bit_extender_3
  // Mips_Probe mips_probe_10: pin names not known; wires that end beside it: IR5
  Multiplexer #(.select(2), .width(32), .disabled("Z"), .enable("false")) multiplexer_39 (
    .in0(ALU5), .in1(MD5), .in2(PC5), .out(RDin), .sel({Jal5, MemToReg5}));  // open: in3

  // Other names for the same wires on the sheet: IRNO3[31:0] = EX_IR; byteoff[1:0] = ALU4[1:0]; IRNO1[31:0] = IF_IR;
  //   ID_IR[5:0] = Func; IR[31:0] = {ID_IR, Func}; IRNO2[31:0] = {ID_IR, Func}; Shmat2[4:0] = ID_IR[10:6];
  //   OP[5:0] = ID_IR[31:26]; MEM_IR[31:0] = IR4; MEM_PC[31:0] = M_PC; MemWrite4 = MemWrite; PC[31:0] = IF_PC;
  //   PCO1[31:0] = IF_PC; PCO3[31:0] = EX_PC; RDin1[31:0] = RDin; RealB4[31:0] = MDin; RegWrite5 = RegWrite;
  //   result[31:0] = ALU3; Syscall2 = Syscall; WB_IR[31:0] = IR5; 总复位 = RST

  // Notes on the sheet:
  //   中断源
  //   时空图监测，可删除
  //   中断等待指示
  //   Syscall停机功能模块
  //   数码管输出
  //   控制位
  //   流水调试日志用
  //   暂停节拍，不能为0
  //   戳工具置1进入计数暂停模式，ctrl+k时钟自动运行到对应节拍暂停
  //   ctrl+k关闭时钟连续运行，将控制位置零，进入单步调试模式调试
  //   指令存储器
  //   contents of rom_1 (hex, n*v repeats v):
  //   20110001 8000c05 20110001 20120002 20130003 8000c09 20110001 20120002 20130003 8000c0d 20110001
  //   20120002 20130003 8000c11 20110001 20120002 20130003 c000cb8 20100001 20110001 118fc0 112020
  //   20020022 c 118882 12200001 8000c15 112020 20020022 c 20110001 118880 112020 20020022 c 12200001
  //   8000c1f 20110001 118fc0 112020 20020022 c 1188c3 112020 20020022 c 118903 112020 20020022 c 118903
  //   112020 20020022 c 118903 112020 20020022 c 118903 112020 20020022 c 118903 112020 20020022 c 118903
  //   112020 20020022 c 118903 112020 20020022 c 20100001 109fc0 139fc3 8021 2012000c 24160003 26100001
  //   3210000f 20080008 20090001 139900 2709825 132020 20020022 c 1094022 1500fff9 22100001 2018000f
  //   2188024 108700 20080008 20090001 139902 2709825 132021 20020022 c 1094022 1500fff9 108702 2c9b022
  //   12c00001 8000c50 4020 1084027 84400 3508ffff 82021 20020022 c 2010ffff 20110000 ae300000 22100001
  //   22310004 ae300000 22100001 22310004 ae300000 22100001 22310004 ae300000 22100001 22310004 ae300000
  //   22100001 22310004 ae300000 22100001 22310004 ae300000 22100001 22310004 ae300000 22100001 22310004
  //   ae300000 22100001 22310004 ae300000 22100001 22310004 ae300000 22100001 22310004 ae300000 22100001
  //   22310004 ae300000 22100001 22310004 ae300000 22100001 22310004 ae300000 22100001 22310004 ae300000
  //   22100001 22310004 22100001 8020 2011003c 8e130000 8e340000 274402a 11000002 ae330000 ae140000
  //   2231fffc 1611fff8 102020 20020022 c 22100004 2011003c 1611fff2 20020032 c 20100000 22100001 102020
  //   20020022 c 22100002 102020 20020022 c 22100003 102020 20020022 c 22100004 102020 20020022 c 22100005
  //   102020 20020022 c 22100006 102020 20020022 c 22100007 102020 20020022 c 22100008 102020 20020022
  //   20020022 c 3e00008
  //   可计数暂停的时钟源
  //   IF/ID
  //   指令字
  //   JMP
  //   JR
  //   OP
  //   Func
  //   Syscall
  //   rs
  //   rt
  //   rd
  //   为方便自动评测，需要输出流水线各段保存的PC值，注意是PC不是PC+4，另外ID段寄存器写入信息，Mem段内存写入信息也要输出
  //   Beq
  //   Bne
  //   rd
  //   ID/EX
  //   EX/MEM
  //   MEM/WB
endmodule

module \中断按键参考电路  (
  input  eret,
  input  \时钟 ,
  input  \_1号中断 ,
  input  \中断可接收 ,
  input  \异步清零信号 ,
  input  \_2号中断 ,
  input  \_3号中断 ,
  output [1:0] \优先中断编号 ,
  output \有新中断 
);

  wire \_1号中断屏蔽寄存器_qn , \_2号中断屏蔽寄存器_qn , \_3号中断屏蔽寄存器_qn , and_1_out, and_2_out, and_3_out, and_4_out,
       and_5_out, and_6_out, Clr1, Clr2, Clr3, comparator_1_eq, comparator_2_eq, comparator_3_eq,
       comparator_4_eq, d_ff_1_q, d_ff_2_q, d_ff_3_q, IR1_2_q, IR1_3_q, IR1_q, not_1_out, not_2_out,
       not_3_out, or_1_out, or_2_out, or_3_out, or_4_out, or_5_out, or_6_out, or_7_out, or_8_out,
       priority_encoder_1_gs;
  wire [1:0] \实际中断编号 ;
  wire [31:0] bit_extender_1_out, \硬件堆栈_1_popeddata ;

  LED #(.active("true")) \_1号中断等待指示灯  (.in(or_1_out));
  LED #(.active("true")) \_2号中断等待指示灯  (.in(or_2_out));
  LED #(.active("true")) \_3号中断等待指示灯  (.in(or_3_out));
  D_Flip_Flop #(.trigger("rising"), .Pre_Clr_Positions("LEGACY"), .NegatePresetClear("false"), .enable("true"), .NewFFLayout("false")) d_ff_1 (
    .clk(\_1号中断 ), .D(1'b1), .Q(d_ff_1_q), .reset(IR1_q));  // open: Qn, preset, en
  or or_1 (or_1_out, IR1_q, d_ff_1_q);
  D_Flip_Flop #(.trigger("rising"), .Pre_Clr_Positions("LEGACY"), .NegatePresetClear("false"), .enable("true"), .NewFFLayout("false")) d_ff_2 (
    .clk(\_2号中断 ), .D(1'b1), .Q(d_ff_2_q), .reset(IR1_2_q));  // open: Qn, preset, en
  or or_2 (or_2_out, IR1_2_q, d_ff_2_q);
  D_Flip_Flop #(.trigger("rising"), .Pre_Clr_Positions("LEGACY"), .NegatePresetClear("false"), .enable("true"), .NewFFLayout("false")) d_ff_3 (
    .clk(\_3号中断 ), .D(1'b1), .Q(d_ff_3_q), .reset(IR1_3_q));  // open: Qn, preset, en
  or or_3 (or_3_out, IR1_3_q, d_ff_3_q);
  or or_4 (or_4_out, d_ff_1_q, IR1_q);
  and and_1 (and_1_out, or_4_out, ~Clr1);  // AND_Gate
  or or_5 (or_5_out, d_ff_2_q, IR1_2_q);
  and and_2 (and_2_out, or_5_out, ~Clr2);  // AND_Gate
  or or_6 (or_6_out, d_ff_3_q, IR1_3_q);
  and and_3 (and_3_out, or_6_out, ~Clr3);  // AND_Gate
  D_Flip_Flop #(.trigger("rising"), .Pre_Clr_Positions("LEGACY"), .NegatePresetClear("false"), .enable("true"), .NewFFLayout("false")) IR1 (
    .clk(\时钟 ), .D(and_1_out), .Q(IR1_q), .reset(\异步清零信号 ));  // open: Qn, preset, en
  D_Flip_Flop #(.trigger("rising"), .Pre_Clr_Positions("LEGACY"), .NegatePresetClear("false"), .enable("true"), .NewFFLayout("false")) IR1_2 (
    .clk(\时钟 ), .D(and_2_out), .Q(IR1_2_q), .reset(\异步清零信号 ));  // open: Qn, preset, en
  D_Flip_Flop #(.trigger("rising"), .Pre_Clr_Positions("LEGACY"), .NegatePresetClear("false"), .enable("true"), .NewFFLayout("false")) IR1_3 (
    .clk(\时钟 ), .D(and_3_out), .Q(IR1_3_q), .reset(\异步清零信号 ));  // open: Qn, preset, en
  Comparator #(.width(2), .mode("twosComplement")) comparator_1 (
    .a(\实际中断编号 ), .b(2'b11), .eq(comparator_1_eq));  // open: gt, lt
  or or_7 (or_7_out, comparator_1_eq, comparator_2_eq);
  Comparator #(.width(2), .mode("twosComplement")) comparator_2 (
    .a(\实际中断编号 ), .b(2'b10), .eq(comparator_2_eq));  // open: gt, lt
  Comparator #(.width(2), .mode("twosComplement")) comparator_3 (
    .a(\实际中断编号 ), .b(2'b11), .eq(comparator_3_eq));  // open: gt, lt
  D_Flip_Flop #(.trigger("rising"), .Pre_Clr_Positions("LEGACY"), .NegatePresetClear("false"), .enable("true"), .NewFFLayout("false")) \_1号中断屏蔽寄存器  (
    .clk(\时钟 ), .Qn(\_1号中断屏蔽寄存器_qn ), .preset(or_7_out), .reset(not_1_out));  // open: D, Q, en
  not not_1 (not_1_out, or_7_out);
  D_Flip_Flop #(.trigger("rising"), .Pre_Clr_Positions("LEGACY"), .NegatePresetClear("false"), .enable("true"), .NewFFLayout("false")) \_2号中断屏蔽寄存器  (
    .clk(\时钟 ), .Qn(\_2号中断屏蔽寄存器_qn ), .preset(comparator_3_eq), .reset(not_2_out));  // open: D, Q, en
  not not_2 (not_2_out, comparator_3_eq);
  D_Flip_Flop #(.trigger("rising"), .Pre_Clr_Positions("LEGACY"), .NegatePresetClear("false"), .enable("true"), .NewFFLayout("false")) \_3号中断屏蔽寄存器  (
    .clk(\时钟 ), .D(1'b0), .Qn(\_3号中断屏蔽寄存器_qn ));  // open: Q, preset, en, reset
  and and_4 (and_4_out, IR1_q, \_1号中断屏蔽寄存器_qn );
  and and_5 (and_5_out, IR1_2_q, \_2号中断屏蔽寄存器_qn );
  and and_6 (and_6_out, IR1_3_q, \_3号中断屏蔽寄存器_qn );
  Priority_Encoder #(.select(2), .disabled("Z")) priority_encoder_1 (
    .in0(1'b0), .in1(and_4_out), .in2(and_5_out), .in3(and_6_out), .out(\优先中断编号 ), .gs(priority_encoder_1_gs));  // open: en_out, en_in
  Pull_Resistor #(.pull(0)) pull_resistor_1 (.node(\优先中断编号 ));
  not not_3 (not_3_out, \中断可接收 );
  assign bit_extender_1_out = {{30{1'b0}}, \优先中断编号 };  // Bit_Extender bit_extender_1
  or or_8 (or_8_out, eret, \中断可接收 );
  \硬件堆栈  \u_硬件堆栈_1  (
    .push_pop(not_3_out), .Enable(or_8_out), .CLK(\时钟 ), .\总复位 (\异步清零信号 ), .pusheddata(bit_extender_1_out),
    .popeddata(\硬件堆栈_1_popeddata ));
  Decoder #(.select(2), .tristate("false"), .disabled(0), .enable("true")) decoder_1 (
    .out1(Clr1), .out2(Clr2), .out3(Clr3), .sel(\优先中断编号 ), .en(\中断可接收 ));  // open: out0
  Bit_Extender #(.in_width(32), .out_width(2), .\type ("zero")) bit_extender_2 (
    .in(\硬件堆栈_1_popeddata ), .out(\实际中断编号 ));
  Comparator #(.width(2), .mode("twosComplement")) comparator_4 (
    .a(\实际中断编号 ), .b(\优先中断编号 ), .eq(comparator_4_eq));  // open: gt, lt
  and and_7 (\有新中断 , ~comparator_4_eq, priority_encoder_1_gs);  // AND_Gate

  // Notes on the sheet:
  //   中断信号采样参考电路
  //   中断信号采样参考电路
  //   中断信号采样参考电路
  //   Reset 
  //   Reset 
  //   Reset 
  //   负责中断优先级的仲裁
endmodule

module \单周期MIPS_单级中断  (
  input  IR1,
  input  IR2,
  input  IR3,
  output RegWrite,
  output MemWrite,
  output [31:0] PC,
  output [31:0] IR,
  output [31:0] RDin,
  output [31:0] MDin,
  output [31:0] LedData
);

  wire and_3_out, and_4_out, and_5_out, and_6_out, CLK, clock_2_out, comparator_1_eq, comparator_2_eq,
       comparator_3_eq, comparator_4_eq, comparator_5_eq, comparator_6_eq, comparator_7_eq, comparator_7_lt,
       comparator_8_eq, comparator_9_eq, comparator_10_eq, d_ff_1_q, d_ff_2_q, d_ff_3_q, d_ff_4_qn, equal,
       Go, IR1_t, IR2_t, IR3_t, IRA, IRB, IRC, nand_1_out, not_1_out, not_2_out, or_1_out, or_2_out,
       or_3_out, or_4_out, \PC使能 , SignedExt, Syscall, W1, W2, W3, \中断可接收 , \中断按键参考电路单级_1_p6 ,
       \中断按键参考电路单级_1_p8 , \单周期硬布线控制器_1_beq , \单周期硬布线控制器_1_bne , \单周期硬布线控制器_1_jr , \总复位 , \有中断_Eret ;
  wire [0:0] \单周期硬布线控制器_1_alu_src , \单周期硬布线控制器_1_memtoreg ;
  wire [1:0] byteoff, \中断按键参考电路单级_1_p7 , \单周期硬布线控制器_1_jmp , \单周期硬布线控制器_1_regdst ;
  wire [3:0] \单周期硬布线控制器_1_alu_op ;
  wire [4:0] multiplexer_6_out, multiplexer_7_out, multiplexer_9_out;
  wire [7:0] multiplexer_8_out;
  wire [12:0] CNT_num;
  wire [15:0] \总周期数 ;
  wire [31:0] adder_1_out, adder_2_out, bit_extender_2_out, bit_extender_3_out, bit_extender_4_out, EPCR_q,
       mips_regifile_1_r1, multiplexer_1_out, multiplexer_4_out, multiplexer_5_out, multiplexer_10_out,
       multiplexer_11_out, multiplexer_12_out, NextPCNormal, ram_1_data, shifter_1_out, \中断入口_返回地址 ;
  wire [31:2] result;

  Button button_1 (.out(\总复位 ));
  Clock #(.highDuration(1), .lowDuration(1)) clock_1 ();  // open: out
  Button _1 ();  // open: out
  Button _2 ();  // open: out
  Button _3 ();  // open: out
  Button \u_继续运行  (.out(Go));
  LED #(.active("true")) led_1 (.in(W1));
  LED #(.active("true")) led_2 (.in(W2));
  LED #(.active("true")) led_3 (.in(W3));
  D_Flip_Flop #(.trigger("high"), .Pre_Clr_Positions("LEGACY"), .NegatePresetClear("false"), .enable("true"), .NewFFLayout("false")) d_ff_1 (.Q(d_ff_1_q));  // open: clk, D, Qn, preset, en, reset
  Hex_Digit_Display hex_digit_display_1 (.value(LedData[31:28]));  // open: dp
  Comparator #(.width(16), .mode("twosComplement")) comparator_1 (
    .a(16'h23b), .b(\总周期数 ), .eq(comparator_1_eq));  // open: gt, lt
  Comparator #(.width(16), .mode("twosComplement")) comparator_2 (
    .a(\总周期数 ), .b(16'h1), .eq(comparator_2_eq));  // open: gt, lt
  Comparator #(.width(16), .mode("twosComplement")) comparator_3 (
    .a(\总周期数 ), .b(16'h4), .eq(comparator_3_eq));  // open: gt, lt
  Comparator #(.width(16), .mode("twosComplement")) comparator_4 (
    .a(\总周期数 ), .b(16'h7), .eq(comparator_4_eq));  // open: gt, lt
  // 中断按键参考电路单级 中断按键参考电路单级_1: pin names not known; wires that end beside it: IR1_t, IR2_t, IR3_t, \总复位 , CLK, \中断按键参考电路单级_1_p6 , \中断按键参考电路单级_1_p7 , \中断按键参考电路单级_1_p8 , \中断可接收 
  Comparator #(.width(6), .mode("twosComplement")) comparator_5 (
    .a(IR[31:26]), .b(6'b010000), .eq(comparator_5_eq));  // open: gt, lt
  and and_1 (\中断按键参考电路单级_1_p6 , comparator_5_eq, comparator_6_eq);
  Comparator #(.width(6), .mode("twosComplement")) comparator_6 (
    .a(IR[5:0]), .b(6'b011000), .eq(comparator_6_eq));  // open: gt, lt
  not not_1 (not_1_out, Syscall);
  // Probe on 13'hfff
  Clock #(.highDuration(1), .lowDuration(1)) clock_2 (.out(clock_2_out));
  Hex_Digit_Display hex_digit_display_2 (.value(LedData[27:24]));  // open: dp
  Hex_Digit_Display hex_digit_display_3 (.value(LedData[23:20]));  // open: dp
  or or_1 (or_1_out, comparator_1_eq, comparator_2_eq);
  assign IRA = or_1_out ? ~CLK : 1'bz;  // Controlled_Inverter controlled_inverter_1
  assign IRB = comparator_3_eq ? ~CLK : 1'bz;  // Controlled_Inverter controlled_inverter_2
  assign IRC = comparator_4_eq ? ~CLK : 1'bz;  // Controlled_Inverter controlled_inverter_3
  D_Flip_Flop #(.trigger("rising"), .Pre_Clr_Positions("LEGACY"), .NegatePresetClear("false"), .enable("true"), .NewFFLayout("false")) d_ff_2 (
    .clk(CLK), .D(\中断可接收 ), .Q(d_ff_2_q), .reset(\总复位 ));  // open: Qn, preset, en
  D_Flip_Flop #(.trigger("rising"), .Pre_Clr_Positions("LEGACY"), .NegatePresetClear("false"), .enable("true"), .NewFFLayout("false")) d_ff_3 (
    .clk(CLK), .D(\中断按键参考电路单级_1_p6 ), .Q(d_ff_3_q), .reset(\总复位 ));  // open: Qn, preset, en
  or or_2 (or_2_out, not_1_out, Go);
  or or_3 (or_3_out, equal, not_1_out);
  Comparator #(.width(13), .mode("twosComplement")) comparator_7 (
    .a(CNT_num), .b(13'hfff), .eq(comparator_7_eq), .lt(comparator_7_lt));  // open: gt
  Hex_Digit_Display hex_digit_display_4 (.value(LedData[15:12]));  // open: dp
  Hex_Digit_Display hex_digit_display_5 (.value(LedData[19:16]));  // open: dp
  Pull_Resistor #(.pull(0)) pull_resistor_1 (.node(IRA));
  Pull_Resistor #(.pull(0)) pull_resistor_2 (.node(IRB));
  Pull_Resistor #(.pull(0)) pull_resistor_3 (.node(IRC));
  D_Flip_Flop #(.trigger("rising"), .Pre_Clr_Positions("LEGACY"), .NegatePresetClear("false"), .enable("true"), .NewFFLayout("false")) d_ff_4 (
    .Qn(d_ff_4_qn), .preset(d_ff_2_q), .reset(or_4_out));  // open: clk, D, Q, en
  or or_4 (or_4_out, \总复位 , d_ff_3_q);
  D_Flip_Flop #(.trigger("falling"), .Pre_Clr_Positions("ABOVE_BELOW"), .NegatePresetClear("false"), .enable("false"), .NewFFLayout("true")) d_ff_5 (
    .clk(CLK), .D(or_3_out), .Q(\PC使能 ), .preset(or_2_out));  // open: Qn, reset
  nand nand_1 (nand_1_out, d_ff_1_q, comparator_7_eq);
  Counter #(.width(13), .max('h1fff), .ongoal("stay"), .trigger("rising"), .behavior("old")) counter_1 (
    .count(comparator_7_lt), .Q(CNT_num), .clk(clock_2_out), .clr(\总复位 ));  // open: load, D, carry, preset
  Hex_Digit_Display hex_digit_display_6 (.value(LedData[7:4]));  // open: dp
  Hex_Digit_Display hex_digit_display_7 (.value(LedData[11:8]));  // open: dp
  // Probe on \总周期数 
  Multiplexer #(.select(2), .width(32), .disabled("Z"), .enable("false")) multiplexer_1 (
    .in1(32'h30ac), .in2(32'h3150), .in3(32'h31f4), .out(multiplexer_1_out), .sel(\中断按键参考电路单级_1_p7 ));  // open: in0
  assign \总周期数  = {{3{1'b0}}, CNT_num};  // Bit_Extender bit_extender_1
  assign CLK = nand_1_out ? clock_2_out : 1'bz;  // Controlled_Buffer controlled_buffer_1
  Pull_Resistor #(.pull(1)) pull_resistor_4 (.node(CLK));
  Hex_Digit_Display hex_digit_display_8 (.value(LedData[3:0]));  // open: dp
  and and_2 (\中断可接收 , \中断按键参考电路单级_1_p8 , d_ff_4_qn);
  Register #(.width(32), .trigger("rising"), .Select("low")) EPCR (
    .D(NextPCNormal), .en(\中断可接收 ), .Q(EPCR_q), .clk(CLK), .clr(\总复位 ));
  or or_5 (IR1_t, IR1, IRA);
  or or_6 (\有中断_Eret , \中断可接收 , \中断按键参考电路单级_1_p6 );
  Multiplexer #(.select(1), .width(32), .disabled("Z"), .enable("false")) multiplexer_2 (
    .in0(multiplexer_1_out), .in1(EPCR_q), .out(\中断入口_返回地址 ), .sel(\中断按键参考电路单级_1_p6 ));
  or or_7 (IR2_t, IR2, IRB);
  or or_8 (IR3_t, IR3, IRC);
  Multiplexer #(.select(2), .width(32), .disabled("Z"), .enable("false")) multiplexer_3 (
    .in0(adder_1_out), .in1(multiplexer_5_out), .in2(adder_2_out), .out(NextPCNormal), .sel(\单周期硬布线控制器_1_jmp ));  // open: in3
  Register #(.width(32), .trigger("rising"), .Select("low")) u_PC (
    .D(multiplexer_4_out), .en(\PC使能 ), .Q(PC), .clk(CLK), .clr(\总复位 ));
  Multiplexer #(.select(1), .width(32), .disabled("Z"), .enable("false")) multiplexer_4 (
    .in0(NextPCNormal), .in1(\中断入口_返回地址 ), .out(multiplexer_4_out), .sel(\有中断_Eret ));
  Adder #(.width(32)) adder_1 (.a(PC), .b(32'h4), .out(adder_1_out));  // open: cin, cout
  Multiplexer #(.select(1), .width(32), .disabled("Z"), .enable("false")) multiplexer_5 (
    .in0({PC[31:28], IR[25:0], 2'b00}), .in1(mips_regifile_1_r1), .out(multiplexer_5_out),
    .sel(\单周期硬布线控制器_1_jr ));
  ROM #(.addrWidth(10), .dataWidth(32), .Select("high")) rom_1 (.addr(PC[11:2]), .data(IR));
  // Mips_Probe mips_probe_1: pin names not known; wires that end beside it: IR
  \单周期硬布线控制器  \u_单周期硬布线控制器_1  (
    .Func(IR[5:0]), .OP(IR[31:26]), .ALU_OP(\单周期硬布线控制器_1_alu_op ), .MemToReg(\单周期硬布线控制器_1_memtoreg [0]),
    .MemWrite(MemWrite), .ALU_SRC(\单周期硬布线控制器_1_alu_src [0]), .RegWrite(RegWrite), .SysCALL(Syscall),
    .SignedExt(SignedExt), .RegDst(\单周期硬布线控制器_1_regdst [0]), .JR(\单周期硬布线控制器_1_jr ),
    .JMP(\单周期硬布线控制器_1_jmp [0]), .Beq(\单周期硬布线控制器_1_beq ), .JAL(\单周期硬布线控制器_1_regdst [1]),
    .Bne(\单周期硬布线控制器_1_bne ));
  Multiplexer #(.select(1), .width(5), .disabled("Z"), .enable("false")) multiplexer_6 (
    .in0(IR[25:21]), .in1(5'b00010), .out(multiplexer_6_out), .sel(Syscall));
  Multiplexer #(.select(2), .width(5), .disabled("Z"), .enable("false")) multiplexer_7 (
    .in0(IR[20:16]), .in1(IR[15:11]), .in2({5{1'b1}}), .out(multiplexer_7_out), .sel(\单周期硬布线控制器_1_regdst ));  // open: in3
  Comparator #(.width(6), .mode("twosComplement")) comparator_8 (
    .a(IR[31:26]), .b(6'b100100), .eq(comparator_8_eq));  // open: gt, lt
  assign bit_extender_2_out = {{24{1'b0}}, multiplexer_8_out};  // Bit_Extender bit_extender_2
  Multiplexer #(.select(2), .width(8), .disabled("Z"), .enable("false")) multiplexer_8 (
    .in0(RDin[7:0]), .in1(RDin[15:8]), .in2(RDin[23:16]), .in3(RDin[31:24]), .out(multiplexer_8_out),
    .sel(byteoff));
  Multiplexer #(.select(1), .width(5), .disabled("Z"), .enable("false")) multiplexer_9 (
    .in0(IR[20:16]), .in1(5'b00100), .out(multiplexer_9_out), .sel(Syscall));
  Multiplexer #(.select(1), .width(32), .disabled("Z"), .enable("false")) multiplexer_10 (
    .in0(RDin), .in1(bit_extender_2_out), .out(multiplexer_10_out), .sel(comparator_8_eq));
  MIPS_Regifile mips_regifile_1 (
    .Din(multiplexer_10_out), .Clk(CLK), .R1(mips_regifile_1_r1), .R2(MDin), .WE(RegWrite),
    .W_num(multiplexer_7_out), .R1_num(multiplexer_6_out), .R2_num(multiplexer_9_out));
  assign bit_extender_3_out = {{16{1'b0}}, IR[15:0]};  // Bit_Extender bit_extender_3
  Multiplexer #(.select(1), .width(32), .disabled("Z"), .enable("false")) multiplexer_11 (
    .in0(bit_extender_3_out), .in1(bit_extender_4_out), .out(multiplexer_11_out), .sel(SignedExt));
  assign bit_extender_4_out = {{16{IR[15]}}, IR[15:0]};  // Bit_Extender bit_extender_4
  Shifter #(.width(32), .shift("ll")) shifter_1 (.in(multiplexer_11_out), .\dist (5'b00010), .out(shifter_1_out));
  or or_9 (\单周期硬布线控制器_1_jmp [1], and_3_out, and_5_out, and_4_out);
  Multiplexer #(.select(2), .width(32), .disabled("Z"), .enable("false")) multiplexer_12 (
    .in0(MDin), .in1(multiplexer_11_out), .in2(32'h22), .out(multiplexer_12_out),
    .sel({Syscall, \单周期硬布线控制器_1_alu_src [0]}));  // open: in3
  Comparator #(.width(32), .mode("twosComplement")) comparator_9 (
    .a(32'h1), .b({result, byteoff}), .eq(comparator_9_eq));  // open: gt, lt
  Comparator #(.width(6), .mode("twosComplement")) comparator_10 (
    .a(IR[31:26]), .b(6'b000001), .eq(comparator_10_eq));  // open: gt, lt
  and and_3 (and_3_out, comparator_10_eq, comparator_9_eq);
  and and_4 (and_4_out, \单周期硬布线控制器_1_beq , equal);
  and and_5 (and_5_out, not_2_out, \单周期硬布线控制器_1_bne );
  not not_2 (not_2_out, equal);
  MIPS_ALU mips_alu_1 (
    .X(mips_regifile_1_r1), .Y(multiplexer_12_out), .AluOP(\单周期硬布线控制器_1_alu_op ), .Equal(equal),
    .Result({result, byteoff}), .shamt(IR[10:6]));  // open: Result_2
  Adder #(.width(32)) adder_2 (.a(shifter_1_out), .b(adder_1_out), .out(adder_2_out), .cin(1'b0));  // open: cout
  and and_6 (and_6_out, Syscall, equal);
  Register #(.width(32), .trigger("rising"), .Select("low")) register_1 (
    .D(MDin), .en(and_6_out), .Q(LedData), .clk(CLK), .clr(\总复位 ));
  RAM #(.addrWidth(10), .dataWidth(32), .bus("separate"), .Select("high")) ram_1 (
    .addr(result[11:2]), .din(MDin), .data(ram_1_data), .str(MemWrite), .clk(CLK), .clr(\总复位 ));  // open: sel, ld
  Multiplexer #(.select(2), .width(32), .disabled("Z"), .enable("false")) multiplexer_13 (
    .in0({result, byteoff}), .in1(ram_1_data), .in2(adder_1_out), .out(RDin),
    .sel({\单周期硬布线控制器_1_regdst [1], \单周期硬布线控制器_1_memtoreg [0]}));  // open: in3

  // Other names for the same wires on the sheet: Func[5:0] = IR[5:0]; OP[5:0] = IR[31:26]; result[1:0] = byteoff

  // Notes on the sheet:
  //   中断源
  //   中断等待指示
  //   总复位信号应将除ROM以外所有存储组件全部清零
  //   Eret指令支持
  //   控制位
  //   暂停节拍，不能为0
  //   单级中断测试信号模拟器
  //   用这个时钟源需要去掉电路中的其他时钟源
  //   负责一部分中断信号的生成
  //   Syscall停机功能模块
  //   戳工具置1进入计数暂停模式，ctrl+k时钟自动运行到对应节拍暂停
  //   ctrl+k关闭时钟连续运行，将控制位置零，进入单步调试模式调试
  //   数码管输出
  //   关中断与开中断寄存器
  //   数码管输出应该用寄存器锁存，否则显示数据只能一闪而过
  //   中断支持硬件
  //   可计数暂停的时钟源
  //   为方便自动评测，需要输出PC，IR，寄存器堆写如数据RDin
  //   指令存储器
  //   RAM写使能MemWrite、RAM写入数据MDin等信号
  //   指令字
  //   contents of rom_1 (hex, n*v repeats v):
  //   201d07d0 20100001 109fc0 139fc3 8021 2012000c 24160008 26100001 3210000f 20080008 20090001 139900
  //   2709825 132020 20020022 c 1094022 1500fff9 22100001 2018000f 2188024 108700 20080008 20090001 139902
  //   2709825 132021 20020022 c 1094022 1500fff9 108702 2c9b022 12c00001 8000c07 4020 1084027 84400
  //   3508ffff 82021 20020022 c 8000c01 afa20000 23bd0004 afa40000 23bd0004 afb00000 23bd0004 afb30000
  //   23bd0004 afb40000 23bd0004 afb50000 23bd0004 afb60000 23bd0004 20160001 20140003 20150001 168020
  //   108100 2149825 132020 20020022 c 1600fffa 295a022 1680fff7 23bdfffc 8fb60000 23bdfffc 8fb50000
  //   23bdfffc 8fb40000 23bdfffc 8fb30000 23bdfffc 8fb00000 23bdfffc 8fa40000 23bdfffc 8fa20000 42000018
  //   afa20000 23bd0004 afa40000 23bd0004 afb00000 23bd0004 afb30000 23bd0004 afb40000 23bd0004 afb50000
  //   23bd0004 afb60000 23bd0004 20160002 20140003 20150001 168020 108100 2149825 132020 20020022 c
  //   1600fffa 295a022 1680fff7 23bdfffc 8fb60000 23bdfffc 8fb50000 23bdfffc 8fb40000 23bdfffc 8fb30000
  //   23bdfffc 8fb00000 23bdfffc 8fa40000 23bdfffc 8fa20000 42000018 afa20000 23bd0004 afa40000 23bd0004
  //   afb00000 23bd0004 afb30000 23bd0004 afb40000 23bd0004 afb50000 23bd0004 afb60000 23bd0004 20160003
  //   20140003 20150001 168020 108100 2149825 132020 20020022 c 1600fffa 295a022 1680fff7 23bdfffc
  //   8fb60000 23bdfffc 8fb50000 23bdfffc 8fb40000 23bdfffc 8fb30000 23bdfffc 8fb00000 23bdfffc 8fa40000
  //   23bdfffc 8fa20000 42000018
  //   JMP
  //   JR
  //   OP
  //   Func
  //   rs
  //   rt
  //   rd
  //   Beq
  //   Bne
  //   AluOP
  //   AluSrcB
  //   RegWrite
  //   JAL
  //   RegDst
  //   Syscall
  //   MemToReg
  //   MemWrite
endmodule

module \单周期MIPS_多级中断  (
  input  IR1,
  input  IR2,
  input  IR3,
  output RegWrite,
  output MemWrite,
  output [31:0] PC,
  output [31:0] IR,
  output [31:0] RDin,
  output [31:0] MDin,
  output [31:0] LedData
);

  wire and_3_out, and_4_out, and_5_out, and_6_out, CLK, clock_2_out, comparator_1_eq, comparator_2_eq,
       comparator_3_eq, comparator_4_eq, comparator_5_eq, comparator_6_eq, comparator_6_lt, comparator_7_eq,
       comparator_8_eq, comparator_9_eq, comparator_10_eq, comparator_11_eq, comparator_12_eq,
       comparator_13_eq, d_ff_1_q, d_ff_2_q, d_ff_3_q, d_ff_5_qn, equal, Eret, Go, IR1_t, IR2_t, IR3_t, IRA,
       IRB, IRC, nand_1_out, not_1_out, not_2_out, or_1_out, or_2_out, or_3_out, or_4_out, or_5_out,
       or_6_out, or_7_out, or_8_out, \PC使能 , SignedExt, Syscall, W1, W2, W3, \中断可接收 , \中断按键参考电路_1_有新中断 ,
       \单周期硬布线控制器_1_beq , \单周期硬布线控制器_1_bne , \单周期硬布线控制器_1_jr , \总复位 , \有中断_Eret ;
  wire [0:0] \单周期硬布线控制器_1_alu_src , \单周期硬布线控制器_1_memtoreg ;
  wire [1:0] byteoff, \中断按键参考电路_1_优先中断编号 , \单周期硬布线控制器_1_jmp , \单周期硬布线控制器_1_regdst ;
  wire [3:0] \单周期硬布线控制器_1_alu_op ;
  wire [4:0] multiplexer_6_out, multiplexer_7_out, multiplexer_9_out;
  wire [7:0] multiplexer_8_out;
  wire [12:0] CNT_num;
  wire [15:0] \总周期数 ;
  wire [31:0] adder_1_out, adder_2_out, bit_extender_2_out, bit_extender_3_out, bit_extender_4_out,
       mips_regifile_1_r1, multiplexer_1_out, multiplexer_4_out, multiplexer_5_out, multiplexer_10_out,
       multiplexer_11_out, multiplexer_12_out, NextPCNormal, popeddata, ram_1_data, shifter_1_out,
       \中断入口_返回地址 ;
  wire [31:2] result;

  Button button_1 (.out(\总复位 ));
  Clock #(.highDuration(1), .lowDuration(1)) clock_1 ();  // open: out
  Button _1 ();  // open: out
  Button _2 ();  // open: out
  Button _3 ();  // open: out
  Button \u_继续运行  (.out(Go));
  LED #(.active("true")) led_1 (.in(W1));
  LED #(.active("true")) led_2 (.in(W2));
  LED #(.active("true")) led_3 (.in(W3));
  D_Flip_Flop #(.trigger("high"), .Pre_Clr_Positions("LEGACY"), .NegatePresetClear("false"), .enable("true"), .NewFFLayout("false")) d_ff_1 (.Q(d_ff_1_q));  // open: clk, D, Qn, preset, en, reset
  // Probe on 13'hfff
  Hex_Digit_Display hex_digit_display_1 (.value(LedData[31:28]));  // open: dp
  Comparator #(.width(16), .mode("twosComplement")) comparator_1 (
    .a(\总周期数 ), .b(16'h7), .eq(comparator_1_eq));  // open: gt, lt
  Comparator #(.width(16), .mode("twosComplement")) comparator_2 (
    .a(\总周期数 ), .b(16'h241), .eq(comparator_2_eq));  // open: gt, lt
  Comparator #(.width(32), .mode("twosComplement")) comparator_3 (
    .a(IR), .b(32'h40800000), .eq(comparator_3_eq));  // open: gt, lt
  Comparator #(.width(6), .mode("twosComplement")) comparator_4 (
    .a(IR[31:26]), .b(6'b010000), .eq(comparator_4_eq));  // open: gt, lt
  Comparator #(.width(6), .mode("twosComplement")) comparator_5 (
    .a(IR[5:0]), .b(6'b011000), .eq(comparator_5_eq));  // open: gt, lt
  or or_1 (or_1_out, \中断可接收 , Eret);
  not not_1 (not_1_out, Syscall);
  Comparator #(.width(13), .mode("twosComplement")) comparator_6 (
    .a(CNT_num), .b(13'hfff), .eq(comparator_6_eq), .lt(comparator_6_lt));  // open: gt
  Clock #(.highDuration(1), .lowDuration(1)) clock_2 (.out(clock_2_out));
  Hex_Digit_Display hex_digit_display_2 (.value(LedData[23:20]));  // open: dp
  Hex_Digit_Display hex_digit_display_3 (.value(LedData[27:24]));  // open: dp
  Comparator #(.width(16), .mode("twosComplement")) comparator_7 (
    .a(16'h258), .b(\总周期数 ), .eq(comparator_7_eq));  // open: gt, lt
  or or_2 (or_2_out, comparator_7_eq, comparator_8_eq);
  Comparator #(.width(16), .mode("twosComplement")) comparator_8 (
    .a(\总周期数 ), .b(16'h1), .eq(comparator_8_eq));  // open: gt, lt
  Comparator #(.width(16), .mode("twosComplement")) comparator_9 (
    .a(\总周期数 ), .b(16'h4), .eq(comparator_9_eq));  // open: gt, lt
  or or_3 (or_3_out, comparator_1_eq, comparator_2_eq);
  \中断按键参考电路  \u_中断按键参考电路_1  (
    .\优先中断编号 (\中断按键参考电路_1_优先中断编号 ), .\_1号中断 (IR1_t), .\_2号中断 (IR2_t), .\_3号中断 (IR3_t), .\时钟 (CLK),
    .\异步清零信号 (\总复位 ), .\中断可接收 (\中断可接收 ), .\有新中断 (\中断按键参考电路_1_有新中断 ), .eret(Eret));
  or or_4 (or_4_out, comparator_3_eq, \中断可接收 );
  and and_1 (Eret, comparator_4_eq, comparator_5_eq);
  or or_5 (or_5_out, Eret, comparator_10_eq);
  Comparator #(.width(32), .mode("twosComplement")) comparator_10 (
    .a(IR), .b(32'h40000000), .eq(comparator_10_eq));  // open: gt, lt
  or or_6 (or_6_out, not_1_out, Go);
  or or_7 (or_7_out, equal, not_1_out);
  Counter #(.width(13), .max('h1fff), .ongoal("stay"), .trigger("rising"), .behavior("old")) counter_1 (
    .count(comparator_6_lt), .Q(CNT_num), .clk(clock_2_out), .clr(\总复位 ));  // open: load, D, carry, preset
  Hex_Digit_Display hex_digit_display_4 (.value(LedData[19:16]));  // open: dp
  Hex_Digit_Display hex_digit_display_5 (.value(LedData[15:12]));  // open: dp
  Pull_Resistor #(.pull(0)) pull_resistor_1 (.node(IRA));
  assign IRA = or_2_out ? ~CLK : 1'bz;  // Controlled_Inverter controlled_inverter_1
  Pull_Resistor #(.pull(0)) pull_resistor_2 (.node(IRB));
  assign IRB = comparator_9_eq ? ~CLK : 1'bz;  // Controlled_Inverter controlled_inverter_2
  Pull_Resistor #(.pull(0)) pull_resistor_3 (.node(IRC));
  assign IRC = or_3_out ? ~CLK : 1'bz;  // Controlled_Inverter controlled_inverter_3
  D_Flip_Flop #(.trigger("rising"), .Pre_Clr_Positions("LEGACY"), .NegatePresetClear("false"), .enable("true"), .NewFFLayout("false")) d_ff_2 (
    .clk(CLK), .D(or_4_out), .Q(d_ff_2_q), .reset(\总复位 ));  // open: Qn, preset, en
  D_Flip_Flop #(.trigger("rising"), .Pre_Clr_Positions("LEGACY"), .NegatePresetClear("false"), .enable("true"), .NewFFLayout("false")) d_ff_3 (
    .clk(CLK), .D(or_5_out), .Q(d_ff_3_q), .reset(\总复位 ));  // open: Qn, preset, en
  \硬件堆栈  \u_硬件堆栈_1  (
    .push_pop(Eret), .Enable(or_1_out), .CLK(CLK), .\总复位 (\总复位 ), .pusheddata(NextPCNormal),
    .popeddata(popeddata));
  D_Flip_Flop #(.trigger("falling"), .Pre_Clr_Positions("ABOVE_BELOW"), .NegatePresetClear("false"), .enable("false"), .NewFFLayout("true")) d_ff_4 (
    .clk(CLK), .D(or_7_out), .Q(\PC使能 ), .preset(or_6_out));  // open: Qn, reset
  nand nand_1 (nand_1_out, d_ff_1_q, comparator_6_eq);
  Hex_Digit_Display hex_digit_display_6 (.value(LedData[11:8]));  // open: dp
  Hex_Digit_Display hex_digit_display_7 (.value(LedData[7:4]));  // open: dp
  // Probe on \总周期数 
  D_Flip_Flop #(.trigger("rising"), .Pre_Clr_Positions("LEGACY"), .NegatePresetClear("false"), .enable("true"), .NewFFLayout("false")) d_ff_5 (
    .Qn(d_ff_5_qn), .preset(d_ff_2_q), .reset(or_8_out));  // open: clk, D, Q, en
  or or_8 (or_8_out, \总复位 , d_ff_3_q);
  assign \总周期数  = {{3{1'b0}}, CNT_num};  // Bit_Extender bit_extender_1
  assign CLK = nand_1_out ? clock_2_out : 1'bz;  // Controlled_Buffer controlled_buffer_1
  Pull_Resistor #(.pull(1)) pull_resistor_4 (.node(CLK));
  Hex_Digit_Display hex_digit_display_8 (.value(LedData[3:0]));  // open: dp
  Multiplexer #(.select(2), .width(32), .disabled("Z"), .enable("false")) multiplexer_1 (
    .in1(32'h30ac), .in2(32'h3158), .in3(32'h3204), .out(multiplexer_1_out), .sel(\中断按键参考电路_1_优先中断编号 ));  // open: in0
  and and_2 (\中断可接收 , \中断按键参考电路_1_有新中断 , d_ff_5_qn);
  or or_9 (IR1_t, IR1, IRA);
  Multiplexer #(.select(1), .width(32), .disabled("Z"), .enable("false")) multiplexer_2 (
    .in0(multiplexer_1_out), .in1(popeddata), .out(\中断入口_返回地址 ), .sel(Eret));
  or or_10 (IR2_t, IR2, IRB);
  or or_11 (\有中断_Eret , \中断可接收 , Eret);
  or or_12 (IR3_t, IR3, IRC);
  Multiplexer #(.select(2), .width(32), .disabled("Z"), .enable("false")) multiplexer_3 (
    .in0(adder_1_out), .in1(multiplexer_5_out), .in2(adder_2_out), .out(NextPCNormal), .sel(\单周期硬布线控制器_1_jmp ));  // open: in3
  Register #(.width(32), .trigger("rising"), .Select("low")) u_PC (
    .D(multiplexer_4_out), .en(\PC使能 ), .Q(PC), .clk(CLK), .clr(\总复位 ));
  Multiplexer #(.select(1), .width(32), .disabled("Z"), .enable("false")) multiplexer_4 (
    .in0(NextPCNormal), .in1(\中断入口_返回地址 ), .out(multiplexer_4_out), .sel(\有中断_Eret ));
  Adder #(.width(32)) adder_1 (.a(PC), .b(32'h4), .out(adder_1_out));  // open: cin, cout
  Multiplexer #(.select(1), .width(32), .disabled("Z"), .enable("false")) multiplexer_5 (
    .in0({PC[31:28], IR[25:0], 2'b00}), .in1(mips_regifile_1_r1), .out(multiplexer_5_out),
    .sel(\单周期硬布线控制器_1_jr ));
  // Mips_Probe mips_probe_1: pin names not known; wires that end beside it: IR
  ROM #(.addrWidth(10), .dataWidth(32), .Select("high")) rom_1 (.addr(PC[11:2]), .data(IR));
  \单周期硬布线控制器  \u_单周期硬布线控制器_1  (
    .Func(IR[5:0]), .OP(IR[31:26]), .ALU_OP(\单周期硬布线控制器_1_alu_op ), .MemToReg(\单周期硬布线控制器_1_memtoreg [0]),
    .MemWrite(MemWrite), .ALU_SRC(\单周期硬布线控制器_1_alu_src [0]), .RegWrite(RegWrite), .SysCALL(Syscall),
    .SignedExt(SignedExt), .RegDst(\单周期硬布线控制器_1_regdst [0]), .JR(\单周期硬布线控制器_1_jr ),
    .JMP(\单周期硬布线控制器_1_jmp [0]), .Beq(\单周期硬布线控制器_1_beq ), .JAL(\单周期硬布线控制器_1_regdst [1]),
    .Bne(\单周期硬布线控制器_1_bne ));
  Multiplexer #(.select(1), .width(5), .disabled("Z"), .enable("false")) multiplexer_6 (
    .in0(IR[25:21]), .in1(5'b00010), .out(multiplexer_6_out), .sel(Syscall));
  Multiplexer #(.select(2), .width(5), .disabled("Z"), .enable("false")) multiplexer_7 (
    .in0(IR[20:16]), .in1(IR[15:11]), .in2({5{1'b1}}), .out(multiplexer_7_out), .sel(\单周期硬布线控制器_1_regdst ));  // open: in3
  Comparator #(.width(6), .mode("twosComplement")) comparator_11 (
    .a(IR[31:26]), .b(6'b100100), .eq(comparator_11_eq));  // open: gt, lt
  assign bit_extender_2_out = {{24{1'b0}}, multiplexer_8_out};  // Bit_Extender bit_extender_2
  Multiplexer #(.select(2), .width(8), .disabled("Z"), .enable("false")) multiplexer_8 (
    .in0(RDin[7:0]), .in1(RDin[15:8]), .in2(RDin[23:16]), .in3(RDin[31:24]), .out(multiplexer_8_out),
    .sel(byteoff));
  Multiplexer #(.select(1), .width(5), .disabled("Z"), .enable("false")) multiplexer_9 (
    .in0(IR[20:16]), .in1(5'b00100), .out(multiplexer_9_out), .sel(Syscall));
  Multiplexer #(.select(1), .width(32), .disabled("Z"), .enable("false")) multiplexer_10 (
    .in0(RDin), .in1(bit_extender_2_out), .out(multiplexer_10_out), .sel(comparator_11_eq));
  MIPS_Regifile mips_regifile_1 (
    .Din(multiplexer_10_out), .Clk(CLK), .R1(mips_regifile_1_r1), .R2(MDin), .WE(RegWrite),
    .W_num(multiplexer_7_out), .R1_num(multiplexer_6_out), .R2_num(multiplexer_9_out));
  assign bit_extender_3_out = {{16{1'b0}}, IR[15:0]};  // Bit_Extender bit_extender_3
  Multiplexer #(.select(1), .width(32), .disabled("Z"), .enable("false")) multiplexer_11 (
    .in0(bit_extender_3_out), .in1(bit_extender_4_out), .out(multiplexer_11_out), .sel(SignedExt));
  assign bit_extender_4_out = {{16{IR[15]}}, IR[15:0]};  // Bit_Extender bit_extender_4
  Shifter #(.width(32), .shift("ll")) shifter_1 (.in(multiplexer_11_out), .\dist (5'b00010), .out(shifter_1_out));
  or or_13 (\单周期硬布线控制器_1_jmp [1], and_4_out, and_5_out, and_3_out);
  and and_3 (and_3_out, \单周期硬布线控制器_1_beq , equal);
  Multiplexer #(.select(2), .width(32), .disabled("Z"), .enable("false")) multiplexer_12 (
    .in0(MDin), .in1(multiplexer_11_out), .in2(32'h22), .out(multiplexer_12_out),
    .sel({Syscall, \单周期硬布线控制器_1_alu_src [0]}));  // open: in3
  Comparator #(.width(32), .mode("twosComplement")) comparator_12 (
    .a(32'h1), .b({result, byteoff}), .eq(comparator_12_eq));  // open: gt, lt
  Comparator #(.width(6), .mode("twosComplement")) comparator_13 (
    .a(IR[31:26]), .b(6'b000001), .eq(comparator_13_eq));  // open: gt, lt
  and and_4 (and_4_out, comparator_13_eq, comparator_12_eq);
  and and_5 (and_5_out, not_2_out, \单周期硬布线控制器_1_bne );
  not not_2 (not_2_out, equal);
  MIPS_ALU mips_alu_1 (
    .X(mips_regifile_1_r1), .Y(multiplexer_12_out), .AluOP(\单周期硬布线控制器_1_alu_op ), .Equal(equal),
    .Result({result, byteoff}), .shamt(IR[10:6]));  // open: Result_2
  Adder #(.width(32)) adder_2 (.a(shifter_1_out), .b(adder_1_out), .out(adder_2_out), .cin(1'b0));  // open: cout
  Register #(.width(32), .trigger("rising"), .Select("low")) register_1 (
    .D(MDin), .en(and_6_out), .Q(LedData), .clk(CLK), .clr(\总复位 ));
  and and_6 (and_6_out, Syscall, equal);
  RAM #(.addrWidth(10), .dataWidth(32), .bus("separate"), .Select("high")) ram_1 (
    .addr(result[11:2]), .din(MDin), .data(ram_1_data), .str(MemWrite), .clk(CLK), .clr(\总复位 ));  // open: sel, ld
  Multiplexer #(.select(2), .width(32), .disabled("Z"), .enable("false")) multiplexer_13 (
    .in0({result, byteoff}), .in1(ram_1_data), .in2(adder_1_out), .out(RDin),
    .sel({\单周期硬布线控制器_1_regdst [1], \单周期硬布线控制器_1_memtoreg [0]}));  // open: in3

  // Other names for the same wires on the sheet: Func[5:0] = IR[5:0]; OP[5:0] = IR[31:26]; result[1:0] = byteoff

  // Notes on the sheet:
  //   中断源
  //   中断等待指示
  //   总复位信号应将除ROM以外所有存储组件全部清零
  //   控制位
  //   暂停节拍，不能为0
  //   多级中断测试信号模拟器
  //   简化mtc0指令支持
  //   Eret指令支持
  //   简化mfc0指令支持
  //   戳工具置1进入计数暂停模式，ctrl+k时钟自动运行到对应节拍暂停
  //   ctrl+k关闭时钟连续运行，将控制位置零，进入单步调试模式调试
  //   用这个时钟源需要去掉电路中的其他时钟源
  //   EPC硬件堆栈
  //   Syscall停机功能模块
  //   数码管输出
  //   数码管输出应该用寄存器锁存，否则显示数据只能一闪而过
  //   关中断与开中断寄存器
  //   可计数暂停的时钟源
  //   中断支持硬件
  //   为方便自动评测，需要输出PC，IR，寄存器堆写如数据RDin
  //   RAM写使能MemWrite、RAM写入数据MDin等信号
  //   指令存储器
  //   指令字
  //   contents of rom_1 (hex, n*v repeats v):
  //   201d07d0 20100001 109fc0 139fc3 8021 2012000c 24160008 26100001 3210000f 20080008 20090001 139900
  //   2709825 132020 20020022 c 1094022 1500fff9 22100001 2018000f 2188024 108700 20080008 20090001 139902
  //   2709825 132021 20020022 c 1094022 1500fff9 108702 2c9b022 12c00001 8000c07 4020 1084027 84400
  //   3508ffff 82021 20020022 c 8000c01 afa20000 23bd0004 afa40000 23bd0004 afb00000 23bd0004 afb30000
  //   23bd0004 afb40000 23bd0004 afb50000 23bd0004 afb60000 23bd0004 40000000 20160001 20140003 20150001
  //   168020 108100 2149825 132020 20020022 c 1600fffa 295a022 1680fff7 40800000 23bdfffc 8fb60000
  //   23bdfffc 8fb50000 23bdfffc 8fb40000 23bdfffc 8fb30000 23bdfffc 8fb00000 23bdfffc 8fa40000 23bdfffc
  //   8fa20000 42000018 afa20000 23bd0004 afa40000 23bd0004 afb00000 23bd0004 afb30000 23bd0004 afb40000
  //   23bd0004 afb50000 23bd0004 afb60000 23bd0004 40000000 20160002 20140003 20150001 168020 108100
  //   2149825 132020 20020022 c 1600fffa 295a022 1680fff7 40800000 23bdfffc 8fb60000 23bdfffc 8fb50000
  //   23bdfffc 8fb40000 23bdfffc 8fb30000 23bdfffc 8fb00000 23bdfffc 8fa40000 23bdfffc 8fa20000 42000018
  //   afa20000 23bd0004 afa40000 23bd0004 afb00000 23bd0004 afb30000 23bd0004 afb40000 23bd0004 afb50000
  //   23bd0004 afb60000 23bd0004 40000000 20160003 20140003 20150001 168020 108100 2149825 132020 20020022
  //   c 1600fffa 295a022 1680fff7 40800000 23bdfffc 8fb60000 23bdfffc 8fb50000 23bdfffc 8fb40000 23bdfffc
  //   8fb30000 23bdfffc 8fb00000 23bdfffc 8fa40000 23bdfffc 8fa20000 42000018
  //   JMP
  //   JR
  //   OP
  //   Func
  //   Syscall
  //   rs
  //   rt
  //   rd
  //   Beq
  //   Bne
  //   MemToReg
  //   MemWrite
  //   AluOP
  //   AluSrcB
  //   RegWrite
  //   JAL
  //   RegDst
endmodule

module \封装正确性测试  (
);

  wire IR1, IR2, IR3, MemW, RegW;
  wire [31:0] EX_PC, ID_PC, IF_PC, IR, LED, MDin, MDinr, MEM_PC, PC, RDin, RDinr, WB_PC;

  \单周期MIPS  \u_单周期mips_1  (
    .RegWrite(RegW), .MemWrite(MemW), .PC(PC), .IR(IR), .RDin(RDin), .MDin(MDin), .LedData(LED));  // open: IR1, IR2, IR3
  \气泡流水线  \u_气泡流水线_1  (
    .RegWrite(RegW), .MemWrite(MemW), .IF_PC(IF_PC), .ID_PC(ID_PC), .EX_PC(EX_PC), .M_PC(MEM_PC),
    .WB_PC(WB_PC), .RDin(RDinr), .MDin(MDinr), .LedData(LED));
  \单周期MIPS_单级中断  \u_单周期mips_单级中断_1  (
    .IR1(IR1), .IR2(IR2), .IR3(IR3), .RegWrite(RegW), .MemWrite(MemW), .PC(PC), .IR(IR), .RDin(RDin),
    .MDin(MDin), .LedData(LED));
  \理想流水线  \u_理想流水线_1  (
    .RegWrite(RegW), .MemWrite(MemW), .IF_PC(IF_PC), .ID_PC(ID_PC), .EX_PC(EX_PC), .M_PC(MEM_PC),
    .WB_PC(WB_PC), .RDin(RDinr), .MDin(MDinr), .LedData(LED));
  \重定向流水线  \u_重定向流水线_1  (
    .RegWrite(RegW), .MemWrite(MemW), .IF_PC(IF_PC), .ID_PC(ID_PC), .EX_PC(EX_PC), .M_PC(MEM_PC),
    .WB_PC(WB_PC), .RDin(RDinr), .MDin(MDinr), .LedData(LED));
  \单周期MIPS_多级中断  \u_单周期mips_多级中断_1  (
    .IR1(IR1), .IR2(IR2), .IR3(IR3), .RegWrite(RegW), .MemWrite(MemW), .PC(PC), .IR(IR), .RDin(RDin),
    .MDin(MDin), .LedData(LED));

  // Notes on the sheet:
  //   单周期封装测试
  //   气泡流水封装测试
  //   单周期+单级中断封装测试
  //   请检查上面封装有无位宽不匹配，引脚标签是否和连接的标签相对应，否则无法在educoder平台上正确测试
  //   理想流水封装测试
  //   重定向流水封装测试
  //   单周期+多级中断封装测试
endmodule

module \硬件堆栈  (
  input  [31:0] pusheddata,
  input  push_pop,
  input  Enable,
  input  CLK,
  input  \总复位 ,
  output [31:0] popeddata
);

  wire [31:0] multiplexer_1_out, multiplexer_2_out, multiplexer_3_out, multiplexer_4_out, multiplexer_5_out,
       multiplexer_6_out, multiplexer_7_out, multiplexer_8_out, register_2_q, register_3_q, register_4_q,
       register_5_q, register_6_q, register_7_q, register_8_q;

  Multiplexer #(.select(1), .width(32), .disabled("Z"), .enable("false")) multiplexer_1 (
    .in0(pusheddata), .in1(register_2_q), .out(multiplexer_1_out), .sel(push_pop));
  Register #(.width(32), .trigger("rising"), .Select("low")) register_1 (
    .D(multiplexer_1_out), .en(Enable), .Q(popeddata), .clk(CLK), .clr(\总复位 ));
  Multiplexer #(.select(1), .width(32), .disabled("Z"), .enable("false")) multiplexer_2 (
    .in0(popeddata), .in1(register_3_q), .out(multiplexer_2_out), .sel(push_pop));
  Register #(.width(32), .trigger("rising"), .Select("low")) register_2 (
    .D(multiplexer_2_out), .en(Enable), .Q(register_2_q), .clk(CLK), .clr(\总复位 ));
  Multiplexer #(.select(1), .width(32), .disabled("Z"), .enable("false")) multiplexer_3 (
    .in0(register_2_q), .in1(register_4_q), .out(multiplexer_3_out), .sel(push_pop));
  Multiplexer #(.select(1), .width(32), .disabled("Z"), .enable("false")) multiplexer_4 (
    .in0(register_3_q), .in1(register_5_q), .out(multiplexer_4_out), .sel(push_pop));
  Register #(.width(32), .trigger("rising"), .Select("low")) register_3 (
    .D(multiplexer_3_out), .en(Enable), .Q(register_3_q), .clk(CLK), .clr(\总复位 ));
  Register #(.width(32), .trigger("rising"), .Select("low")) register_4 (
    .D(multiplexer_4_out), .en(Enable), .Q(register_4_q), .clk(CLK), .clr(\总复位 ));
  Multiplexer #(.select(1), .width(32), .disabled("Z"), .enable("false")) multiplexer_5 (
    .in0(register_4_q), .in1(register_6_q), .out(multiplexer_5_out), .sel(push_pop));
  Register #(.width(32), .trigger("rising"), .Select("low")) register_5 (
    .D(multiplexer_5_out), .en(Enable), .Q(register_5_q), .clk(CLK), .clr(\总复位 ));
  Multiplexer #(.select(1), .width(32), .disabled("Z"), .enable("false")) multiplexer_6 (
    .in0(register_5_q), .in1(register_7_q), .out(multiplexer_6_out), .sel(push_pop));
  Multiplexer #(.select(1), .width(32), .disabled("Z"), .enable("false")) multiplexer_7 (
    .in0(register_6_q), .in1(register_8_q), .out(multiplexer_7_out), .sel(push_pop));
  Register #(.width(32), .trigger("rising"), .Select("low")) register_6 (
    .D(multiplexer_6_out), .en(Enable), .Q(register_6_q), .clk(CLK), .clr(\总复位 ));
  Register #(.width(32), .trigger("rising"), .Select("low")) register_7 (
    .D(multiplexer_7_out), .en(Enable), .Q(register_7_q), .clk(CLK), .clr(\总复位 ));
  Multiplexer #(.select(1), .width(32), .disabled("Z"), .enable("false")) multiplexer_8 (
    .in0(register_7_q), .in1({32{1'b0}}), .out(multiplexer_8_out), .sel(push_pop));
  Register #(.width(32), .trigger("rising"), .Select("low")) register_8 (
    .D(multiplexer_8_out), .en(Enable), .Q(register_8_q), .clk(CLK), .clr(\总复位 ));

  // Notes on the sheet:
  //   硬件堆栈
endmodule

module \中断按键参考电路单级  (
  input  \中断可接收 ,
  input  \时钟 ,
  input  \_1号中断 ,
  input  \异步清零信号 ,
  input  \_2号中断 ,
  input  \_3号中断 ,
  input  \_1号屏蔽 ,
  input  \_2号屏蔽 ,
  input  \_3号屏蔽 ,
  output [1:0] \优先中断编号 ,
  output \有中断 
);

  wire \_1号中断屏蔽寄存器_qn , \_2号中断屏蔽寄存器_qn , \_3号中断屏蔽寄存器_qn , and_1_out, and_2_out, and_3_out, and_4_out,
       and_5_out, and_6_out, Clr1, Clr2, Clr3, d_ff_1_q, d_ff_2_q, d_ff_3_q, IR1_2_q, IR1_3_q, IR1_q,
       or_1_out, or_2_out, or_3_out, or_4_out, or_5_out, or_6_out;

  LED #(.active("true")) \_1号中断等待指示灯  (.in(or_1_out));
  LED #(.active("true")) \_2号中断等待指示灯  (.in(or_2_out));
  LED #(.active("true")) \_3号中断等待指示灯  (.in(or_3_out));
  D_Flip_Flop #(.trigger("rising"), .Pre_Clr_Positions("LEGACY"), .NegatePresetClear("false"), .enable("true"), .NewFFLayout("false")) d_ff_1 (
    .clk(\_1号中断 ), .D(1'b1), .Q(d_ff_1_q), .reset(IR1_q));  // open: Qn, preset, en
  or or_1 (or_1_out, IR1_q, d_ff_1_q);
  D_Flip_Flop #(.trigger("rising"), .Pre_Clr_Positions("LEGACY"), .NegatePresetClear("false"), .enable("true"), .NewFFLayout("false")) d_ff_2 (
    .clk(\_2号中断 ), .D(1'b1), .Q(d_ff_2_q), .reset(IR1_2_q));  // open: Qn, preset, en
  or or_2 (or_2_out, IR1_2_q, d_ff_2_q);
  D_Flip_Flop #(.trigger("rising"), .Pre_Clr_Positions("LEGACY"), .NegatePresetClear("false"), .enable("true"), .NewFFLayout("false")) d_ff_3 (
    .clk(\_3号中断 ), .D(1'b1), .Q(d_ff_3_q), .reset(IR1_3_q));  // open: Qn, preset, en
  or or_3 (or_3_out, IR1_3_q, d_ff_3_q);
  or or_4 (or_4_out, d_ff_1_q, IR1_q);
  and and_1 (and_1_out, or_4_out, ~Clr1);  // AND_Gate
  or or_5 (or_5_out, d_ff_2_q, IR1_2_q);
  and and_2 (and_2_out, or_5_out, ~Clr2);  // AND_Gate
  or or_6 (or_6_out, d_ff_3_q, IR1_3_q);
  and and_3 (and_3_out, or_6_out, ~Clr3);  // AND_Gate
  D_Flip_Flop #(.trigger("rising"), .Pre_Clr_Positions("LEGACY"), .NegatePresetClear("false"), .enable("true"), .NewFFLayout("false")) IR1 (
    .clk(\时钟 ), .D(and_1_out), .Q(IR1_q), .reset(\异步清零信号 ));  // open: Qn, preset, en
  D_Flip_Flop #(.trigger("rising"), .Pre_Clr_Positions("LEGACY"), .NegatePresetClear("false"), .enable("true"), .NewFFLayout("false")) IR1_2 (
    .clk(\时钟 ), .D(and_2_out), .Q(IR1_2_q), .reset(\异步清零信号 ));  // open: Qn, preset, en
  D_Flip_Flop #(.trigger("rising"), .Pre_Clr_Positions("LEGACY"), .NegatePresetClear("false"), .enable("true"), .NewFFLayout("false")) IR1_3 (
    .clk(\时钟 ), .D(and_3_out), .Q(IR1_3_q), .reset(\异步清零信号 ));  // open: Qn, preset, en
  D_Flip_Flop #(.trigger("rising"), .Pre_Clr_Positions("LEGACY"), .NegatePresetClear("false"), .enable("true"), .NewFFLayout("false")) \_1号中断屏蔽寄存器  (
    .clk(\时钟 ), .D(\_1号屏蔽 ), .Qn(\_1号中断屏蔽寄存器_qn ));  // open: Q, preset, en, reset
  D_Flip_Flop #(.trigger("rising"), .Pre_Clr_Positions("LEGACY"), .NegatePresetClear("false"), .enable("true"), .NewFFLayout("false")) \_2号中断屏蔽寄存器  (
    .clk(\时钟 ), .D(\_2号屏蔽 ), .Qn(\_2号中断屏蔽寄存器_qn ));  // open: Q, preset, en, reset
  D_Flip_Flop #(.trigger("rising"), .Pre_Clr_Positions("LEGACY"), .NegatePresetClear("false"), .enable("true"), .NewFFLayout("false")) \_3号中断屏蔽寄存器  (
    .clk(\时钟 ), .D(\_3号屏蔽 ), .Qn(\_3号中断屏蔽寄存器_qn ));  // open: Q, preset, en, reset
  and and_4 (and_4_out, IR1_q, \_1号中断屏蔽寄存器_qn );
  and and_5 (and_5_out, IR1_2_q, \_2号中断屏蔽寄存器_qn );
  and and_6 (and_6_out, IR1_3_q, \_3号中断屏蔽寄存器_qn );
  Priority_Encoder #(.select(2), .disabled("Z")) priority_encoder_1 (
    .in0(1'b0), .in1(and_4_out), .in2(and_5_out), .in3(and_6_out), .out(\优先中断编号 ), .gs(\有中断 ));  // open: en_out, en_in
  Decoder #(.select(2), .tristate("false"), .disabled(0), .enable("true")) decoder_1 (
    .out1(Clr1), .out2(Clr2), .out3(Clr3), .sel(\优先中断编号 ), .en(\中断可接收 ));  // open: out0

  // Notes on the sheet:
  //   中断信号采样参考电路
  //   中断信号采样参考电路
  //   中断信号采样参考电路
  //   Reset 
  //   Reset 
  //   Reset 
  //   负责中断优先级的仲裁
endmodule

module \气泡流水线仅分支相关  (
  output RegWrite,
  output MemWrite,
  output [31:0] IF_PC,
  output [31:0] ID_PC,
  output [31:0] EX_PC,
  output [31:0] M_PC,
  output [31:0] WB_PC,
  output [31:0] RDin,
  output [31:0] MDin,
  output [31:0] LedData
);

  wire ALuSrcB2, ALuSrcB3, and_1_out, and_2_out, and_3_out, and_4_out, and_5_out, Beq2, Beq3, Bne2, Bne3,
       CLK, clock_1_out, clock_2_out, comparator_1_eq, comparator_2_eq, comparator_2_lt, comparator_3_eq,
       comparator_4_eq, comparator_5_eq, d_ff_2_q, equal3, equal4, equal5, Go, IR1, IR2, IR3, Jal2, Jal3,
       Jal5, Jal_2_q, Jmp2, Jmp3, JR2, JR3, MemToReg2, MemToReg5, MemToReg_2_q, MemToReg_q, MemWrite2,
       MemWrite_q, multiplexer_13_out, multiplexer_14_out, multiplexer_15_out, multiplexer_16_out,
       multiplexer_18_out, multiplexer_19_out, multiplexer_20_out, multiplexer_21_out, multiplexer_22_out,
       multiplexer_23_out, multiplexer_24_out, nand_1_out, not_1_out, not_3_out, or_1_out, or_2_out, \PC使能 ,
       RegDst2, RegDst5, RegDst_2_q, RegDst_q, RegWrite2, RegWrite3, RegWrite_2_q, RST, SignedExt, Syscall,
       Syscall3, Syscall4, Syscall5, W1, W2, W3, \分支气泡 ;
  wire [1:1] or_3_out;
  wire [3:0] ALuOP2, ALuOP3, multiplexer_17_out;
  wire [4:0] multiplexer_7_out, multiplexer_9_out, multiplexer_10_out, multiplexer_30_out, Shmat3;
  wire [5:0] Func;
  wire [7:0] multiplexer_8_out;
  wire [12:0] CNT_num;
  wire [15:0] \LoadUse次数 , \总周期数 , \插入气泡数 , \无条件分支数 , \条件分支成功数 ;
  wire [31:0] A2, A3, adder_2_out, ALU3, ALU4, ALU5, B2, B3, bit_extender_1_out, bit_extender_2_out,
       bit_extender_3_out, EX_IR, ID_IR, IF_IR, Imm2, Imm3, IR4, IR5, IRNO1, IRNO3, MD4, MD5, MEM_IR,
       multiplexer_2_out, multiplexer_3_out, multiplexer_4_out, multiplexer_5_out, multiplexer_6_out,
       multiplexer_25_out, multiplexer_26_out, multiplexer_27_out, multiplexer_28_out, multiplexer_29_out,
       multiplexer_31_out, multiplexer_32_out, multiplexer_33_out, NextPCNormal, PC1, PC2, PC3, PC5, PC_4_q,
       RDin1, shifter_1_out, WB_IR;
  wire [31:6] IR;

  Button \u_总复位  (.out(RST));
  Button _1 (.out(IR1));
  Button _2 (.out(IR2));
  Button _3 (.out(IR3));
  // Probe on \总周期数 
  // Probe on \总周期数 
  Button \u_继续运行  (.out(Go));
  LED #(.active("true")) led_1 (.in(W1));
  LED #(.active("true")) led_2 (.in(W2));
  LED #(.active("true")) led_3 (.in(W3));
  Hex_Digit_Display hex_digit_display_1 (.value(LedData[31:28]));  // open: dp
  // Probe on IF_PC[19:0]
  // Mips_Probe mips_probe_1: pin names not known; wires that end beside it: IF_IR
  not not_1 (not_1_out, Syscall5);
  Hex_Digit_Display hex_digit_display_2 (.value(LedData[27:24]));  // open: dp
  Hex_Digit_Display hex_digit_display_3 (.value(LedData[23:20]));  // open: dp
  // Probe on ID_PC[19:0]
  // Mips_Probe mips_probe_2: pin names not known; wires that end beside it: ID_IR
  or or_1 (or_1_out, equal5, not_1_out);
  Hex_Digit_Display hex_digit_display_4 (.value(LedData[19:16]));  // open: dp
  Hex_Digit_Display hex_digit_display_5 (.value(LedData[15:12]));  // open: dp
  or or_2 (or_2_out, not_1_out, Go);
  D_Flip_Flop #(.trigger("falling"), .Pre_Clr_Positions("ABOVE_BELOW"), .NegatePresetClear("false"), .enable("false"), .NewFFLayout("true")) d_ff_1 (
    .clk(CLK), .D(or_1_out), .Q(\PC使能 ), .preset(or_2_out));  // open: Qn, reset
  Hex_Digit_Display hex_digit_display_6 (.value(LedData[11:8]));  // open: dp
  Hex_Digit_Display hex_digit_display_7 (.value(LedData[7:4]));  // open: dp
  Clock #(.highDuration(1), .lowDuration(1)) clock_1 (.out(clock_1_out));
  // Probe on EX_PC[19:0]
  // Mips_Probe mips_probe_3: pin names not known; wires that end beside it: clock_1_out, EX_IR, CLK
  Hex_Digit_Display hex_digit_display_8 (.value(LedData[3:0]));  // open: dp
  // Probe on \总周期数 
  // Probe on M_PC[19:0]
  // Mips_Probe mips_probe_4: pin names not known; wires that end beside it: MEM_IR
  // Probe on \总周期数 
  // Probe on \无条件分支数 
  // Probe on \条件分支成功数 
  // Probe on \插入气泡数 
  // Probe on \LoadUse次数 
  Comparator #(.width(2), .mode("twosComplement")) comparator_1 (
    .a({or_3_out[1], Jmp3}), .b(2'b00), .eq(comparator_1_eq));  // open: gt, lt
  Multiplexer #(.select(2), .width(32), .disabled("Z"), .enable("false")) multiplexer_1 (
    .in0(PC1), .in1(multiplexer_32_out), .in2(adder_2_out), .out(NextPCNormal), .sel({or_3_out[1], Jmp3}));  // open: in3
  and and_1 (and_1_out, \PC使能 , CLK);
  // Probe on IF_PC[11:0]
  // Probe on WB_PC[19:0]
  // Mips_Probe mips_probe_5: pin names not known; wires that end beside it: WB_IR
  not not_2 (\分支气泡 , comparator_1_eq);
  Register #(.width(32), .trigger("rising"), .Select("low")) PC (
    .D(multiplexer_2_out), .en(\PC使能 ), .Q(IF_PC), .clk(CLK), .clr(RST));
  Multiplexer #(.select(1), .width(32), .disabled("Z"), .enable("false")) multiplexer_2 (
    .in0(NextPCNormal), .in1({32{1'b0}}), .out(multiplexer_2_out), .sel(1'b0));
  Adder #(.width(32)) adder_1 (.a(IF_PC), .b(32'h4), .out(PC1));  // open: cin, cout
  // Probe on ID_PC[11:0]
  // Probe on EX_PC[11:0]
  // Probe on M_PC[11:0]
  D_Flip_Flop #(.trigger("high"), .Pre_Clr_Positions("LEGACY"), .NegatePresetClear("false"), .enable("true"), .NewFFLayout("false")) d_ff_2 (.Q(d_ff_2_q));  // open: clk, D, Qn, preset, en, reset
  // Probe on 13'hc
  // Probe on WB_PC[11:0]
  Comparator #(.width(13), .mode("twosComplement")) comparator_2 (
    .a(CNT_num), .b(13'hc), .eq(comparator_2_eq), .lt(comparator_2_lt));  // open: gt
  Clock #(.highDuration(1), .lowDuration(1)) clock_2 (.out(clock_2_out));
  nand nand_1 (nand_1_out, d_ff_2_q, comparator_2_eq);
  Counter #(.width(13), .max('h1fff), .ongoal("stay"), .trigger("rising"), .behavior("old")) counter_1 (
    .count(comparator_2_lt), .Q(CNT_num), .clk(clock_2_out));  // open: load, D, carry, clr, preset
  // Mips_Probe mips_probe_6: pin names not known; wires that end beside it: IRNO1
  ROM #(.addrWidth(10), .dataWidth(32), .Select("high")) rom_1 (.addr(IF_PC[11:2]), .data(IRNO1));
  Multiplexer #(.select(1), .width(32), .disabled("Z"), .enable("false")) multiplexer_3 (
    .in0(IRNO1), .in1({32{1'b0}}), .out(multiplexer_3_out), .sel(\分支气泡 ));
  Multiplexer #(.select(1), .width(32), .disabled("Z"), .enable("false")) multiplexer_4 (
    .in0(PC1), .in1({32{1'b0}}), .out(multiplexer_4_out), .sel(\分支气泡 ));
  Multiplexer #(.select(1), .width(32), .disabled("Z"), .enable("false")) multiplexer_5 (
    .in0(IF_PC), .in1({32{1'b0}}), .out(multiplexer_5_out), .sel(\分支气泡 ));
  assign CLK = nand_1_out ? clock_2_out : 1'bz;  // Controlled_Buffer controlled_buffer_1
  Pull_Resistor #(.pull(1)) pull_resistor_1 (.node(CLK));
  Register #(.width(32), .trigger("rising"), .Select("low")) u_IR (
    .D(multiplexer_3_out), .Q({IR, Func}), .clk(and_1_out), .clr(RST));  // open: en
  Register #(.width(32), .trigger("rising"), .Select("low")) PC_2 (
    .D(multiplexer_4_out), .Q(PC2), .clk(and_1_out), .clr(RST));  // open: en
  Register #(.width(32), .trigger("rising"), .Select("low")) PCO (
    .D(multiplexer_5_out), .Q(ID_PC), .clk(and_1_out), .clr(RST));  // open: en
  // Mips_Probe mips_probe_7: pin names not known; wires that end beside it: {IR, Func}
  Multiplexer #(.select(1), .width(32), .disabled("Z"), .enable("false")) multiplexer_6 (
    .in0(RDin1), .in1(PC5), .out(multiplexer_6_out), .sel(Jal5));
  \单周期硬布线控制器  \u_单周期硬布线控制器_1  (
    .Func(Func), .OP(IR[31:26]), .ALU_OP(ALuOP2), .MemToReg(MemToReg2), .MemWrite(MemWrite2),
    .ALU_SRC(ALuSrcB2), .RegWrite(RegWrite2), .SysCALL(Syscall), .SignedExt(SignedExt), .RegDst(RegDst2),
    .JR(JR2), .JMP(Jmp2), .Beq(Beq2), .JAL(Jal2), .Bne(Bne2));
  Multiplexer #(.select(1), .width(5), .disabled("Z"), .enable("false")) multiplexer_7 (
    .in0(IR[25:21]), .in1(5'b00010), .out(multiplexer_7_out), .sel(Syscall));
  Comparator #(.width(6), .mode("twosComplement")) comparator_3 (
    .a(IR[31:26]), .b(6'b100100), .eq(comparator_3_eq));  // open: gt, lt
  Multiplexer #(.select(2), .width(8), .disabled("Z"), .enable("false")) multiplexer_8 (
    .in0(multiplexer_6_out[7:0]), .in1(multiplexer_6_out[15:8]), .in2(multiplexer_6_out[23:16]),
    .in3(multiplexer_6_out[31:24]), .out(multiplexer_8_out), .sel(ALU4[1:0]));
  assign bit_extender_1_out = {{24{1'b0}}, multiplexer_8_out};  // Bit_Extender bit_extender_1
  Multiplexer #(.select(1), .width(5), .disabled("Z"), .enable("false")) multiplexer_9 (
    .in0(IR[20:16]), .in1(5'b00100), .out(multiplexer_9_out), .sel(Syscall));
  Multiplexer #(.select(2), .width(5), .disabled("Z"), .enable("false")) multiplexer_10 (
    .in0(IR5[20:16]), .in1(IR5[15:11]), .in2({5{1'b1}}), .out(multiplexer_10_out), .sel({Jal5, RegDst5}));  // open: in3
  Multiplexer #(.select(1), .width(32), .disabled("Z"), .enable("false")) multiplexer_11 (
    .in0(multiplexer_6_out), .in1(bit_extender_1_out), .out(RDin), .sel(comparator_3_eq));
  assign bit_extender_2_out = {{16{1'b0}}, {IR[15:6], Func}};  // Bit_Extender bit_extender_2
  assign bit_extender_3_out = {{16{IR[15]}}, {IR[15:6], Func}};  // Bit_Extender bit_extender_3
  MIPS_Regifile mips_regifile_1 (
    .Din(RDin), .Clk(CLK), .R1(A2), .R2(B2), .WE(RegWrite), .W_num(multiplexer_10_out),
    .R1_num(multiplexer_7_out), .R2_num(multiplexer_9_out));
  Multiplexer #(.select(1), .width(32), .disabled("Z"), .enable("false")) multiplexer_12 (
    .in0(bit_extender_2_out), .in1(bit_extender_3_out), .out(Imm2), .sel(SignedExt));
  Multiplexer #(.select(1), .width(1), .disabled("Z"), .enable("false")) multiplexer_13 (
    .in0(MemToReg2), .in1(1'b0), .out(multiplexer_13_out), .sel(\分支气泡 ));
  Multiplexer #(.select(1), .width(1), .disabled("Z"), .enable("false")) multiplexer_14 (
    .in0(RegDst2), .in1(1'b0), .out(multiplexer_14_out), .sel(\分支气泡 ));
  Multiplexer #(.select(1), .width(1), .disabled("Z"), .enable("false")) multiplexer_15 (
    .in0(RegWrite2), .in1(1'b0), .out(multiplexer_15_out), .sel(\分支气泡 ));
  Multiplexer #(.select(1), .width(1), .disabled("Z"), .enable("false")) multiplexer_16 (
    .in0(MemWrite2), .in1(1'b0), .out(multiplexer_16_out), .sel(\分支气泡 ));
  Multiplexer #(.select(1), .width(4), .disabled("Z"), .enable("false")) multiplexer_17 (
    .in0(ALuOP2), .in1(4'b0000), .out(multiplexer_17_out), .sel(\分支气泡 ));
  Multiplexer #(.select(1), .width(1), .disabled("Z"), .enable("false")) multiplexer_18 (
    .in0(ALuSrcB2), .in1(1'b0), .out(multiplexer_18_out), .sel(\分支气泡 ));
  Multiplexer #(.select(1), .width(1), .disabled("Z"), .enable("false")) multiplexer_19 (
    .in0(Syscall), .in1(1'b0), .out(multiplexer_19_out), .sel(\分支气泡 ));
  Multiplexer #(.select(1), .width(1), .disabled("Z"), .enable("false")) multiplexer_20 (
    .in0(Bne2), .in1(1'b0), .out(multiplexer_20_out), .sel(\分支气泡 ));
  Multiplexer #(.select(1), .width(1), .disabled("Z"), .enable("false")) multiplexer_21 (
    .in0(Beq2), .in1(1'b0), .out(multiplexer_21_out), .sel(\分支气泡 ));
  Multiplexer #(.select(1), .width(1), .disabled("Z"), .enable("false")) multiplexer_22 (
    .in0(Jal2), .in1(1'b0), .out(multiplexer_22_out), .sel(\分支气泡 ));
  Multiplexer #(.select(1), .width(1), .disabled("Z"), .enable("false")) multiplexer_23 (
    .in0(Jmp2), .in1(1'b0), .out(multiplexer_23_out), .sel(\分支气泡 ));
  Multiplexer #(.select(1), .width(1), .disabled("Z"), .enable("false")) multiplexer_24 (
    .in0(JR2), .in1(1'b0), .out(multiplexer_24_out), .sel(\分支气泡 ));
  Multiplexer #(.select(1), .width(32), .disabled("Z"), .enable("false")) multiplexer_25 (
    .in0({IR, Func}), .in1({32{1'b0}}), .out(multiplexer_25_out), .sel(\分支气泡 ));
  Multiplexer #(.select(1), .width(32), .disabled("Z"), .enable("false")) multiplexer_26 (
    .in0(PC2), .in1({32{1'b0}}), .out(multiplexer_26_out), .sel(\分支气泡 ));
  Multiplexer #(.select(1), .width(32), .disabled("Z"), .enable("false")) multiplexer_27 (
    .in0(A2), .in1({32{1'b0}}), .out(multiplexer_27_out), .sel(\分支气泡 ));
  Multiplexer #(.select(1), .width(32), .disabled("Z"), .enable("false")) multiplexer_28 (
    .in0(B2), .in1({32{1'b0}}), .out(multiplexer_28_out), .sel(\分支气泡 ));
  Multiplexer #(.select(1), .width(32), .disabled("Z"), .enable("false")) multiplexer_29 (
    .in0(Imm2), .in1({32{1'b0}}), .out(multiplexer_29_out), .sel(\分支气泡 ));
  Multiplexer #(.select(1), .width(5), .disabled("Z"), .enable("false")) multiplexer_30 (
    .in0(IR[10:6]), .in1({5{1'b0}}), .out(multiplexer_30_out), .sel(\分支气泡 ));
  Multiplexer #(.select(1), .width(32), .disabled("Z"), .enable("false")) multiplexer_31 (
    .in0(ID_PC), .in1({32{1'b0}}), .out(multiplexer_31_out), .sel(\分支气泡 ));
  Register #(.width(1), .trigger("rising"), .Select("low")) MemToReg (
    .D(multiplexer_13_out), .Q(MemToReg_q), .clk(and_1_out), .clr(RST));  // open: en
  Register #(.width(1), .trigger("rising"), .Select("low")) RegDst (
    .D(multiplexer_14_out), .Q(RegDst_q), .clk(and_1_out), .clr(RST));  // open: en
  Register #(.width(1), .trigger("rising"), .Select("low")) u_RegWrite (
    .D(multiplexer_15_out), .Q(RegWrite3), .clk(and_1_out), .clr(RST));  // open: en
  Register #(.width(1), .trigger("rising"), .Select("low")) u_MemWrite (
    .D(multiplexer_16_out), .Q(MemWrite_q), .clk(and_1_out), .clr(RST));  // open: en
  Register #(.width(4), .trigger("rising"), .Select("low")) ALuOP (
    .D(multiplexer_17_out), .Q(ALuOP3), .clk(and_1_out), .clr(RST));  // open: en
  Register #(.width(1), .trigger("rising"), .Select("low")) ALuSrcB (
    .D(multiplexer_18_out), .Q(ALuSrcB3), .clk(and_1_out), .clr(RST));  // open: en
  Register #(.width(1), .trigger("rising"), .Select("low")) u_Syscall (
    .D(multiplexer_19_out), .Q(Syscall3), .clk(and_1_out), .clr(RST));  // open: en
  Register #(.width(1), .trigger("rising"), .Select("low")) Bne (
    .D(multiplexer_20_out), .Q(Bne3), .clk(and_1_out), .clr(RST));  // open: en
  Register #(.width(1), .trigger("rising"), .Select("low")) Beq (
    .D(multiplexer_21_out), .Q(Beq3), .clk(and_1_out), .clr(RST));  // open: en
  Register #(.width(1), .trigger("rising"), .Select("low")) Jal (
    .D(multiplexer_22_out), .Q(Jal3), .clk(and_1_out), .clr(RST));  // open: en
  Register #(.width(1), .trigger("rising"), .Select("low")) Jmp (
    .D(multiplexer_23_out), .Q(Jmp3), .clk(and_1_out), .clr(RST));  // open: en
  Register #(.width(1), .trigger("rising"), .Select("low")) JR (
    .D(multiplexer_24_out), .Q(JR3), .clk(and_1_out), .clr(RST));  // open: en
  Register #(.width(32), .trigger("rising"), .Select("low")) IR_2 (
    .D(multiplexer_25_out), .Q(IRNO3), .clk(and_1_out), .clr(RST));  // open: en
  Register #(.width(32), .trigger("rising"), .Select("low")) PC_3 (
    .D(multiplexer_26_out), .Q(PC3), .clk(and_1_out), .clr(RST));  // open: en
  Register #(.width(32), .trigger("rising"), .Select("low")) A (
    .D(multiplexer_27_out), .Q(A3), .clk(and_1_out), .clr(RST));  // open: en
  Register #(.width(32), .trigger("rising"), .Select("low")) B (
    .D(multiplexer_28_out), .Q(B3), .clk(and_1_out), .clr(RST));  // open: en
  Register #(.width(32), .trigger("rising"), .Select("low")) Imm (
    .D(multiplexer_29_out), .Q(Imm3), .clk(and_1_out), .clr(RST));  // open: en
  Register #(.width(5), .trigger("rising"), .Select("low")) Shmat (
    .D(multiplexer_30_out), .Q(Shmat3), .clk(and_1_out), .clr(RST));  // open: en
  Register #(.width(32), .trigger("rising"), .Select("low")) PCO_2 (
    .D(multiplexer_31_out), .Q(EX_PC), .clk(and_1_out), .clr(RST));  // open: en
  // Mips_Probe mips_probe_8: pin names not known; wires that end beside it: IRNO3
  Multiplexer #(.select(1), .width(32), .disabled("Z"), .enable("false")) multiplexer_32 (
    .in0({EX_PC[31:28], IRNO3[25:0], 2'b00}), .in1(A3), .out(multiplexer_32_out), .sel(JR3));
  or or_3 (or_3_out[1], and_3_out, and_4_out, and_2_out);
  Multiplexer #(.select(2), .width(32), .disabled("Z"), .enable("false")) multiplexer_33 (
    .in0(B3), .in1(Imm3), .in2(32'h22), .out(multiplexer_33_out), .sel({Syscall3, ALuSrcB3}));  // open: in3
  Shifter #(.width(32), .shift("ll")) shifter_1 (.in(Imm3), .\dist (5'b00010), .out(shifter_1_out));
  Comparator #(.width(32), .mode("twosComplement")) comparator_4 (
    .a(32'h1), .b(ALU3), .eq(comparator_4_eq));  // open: gt, lt
  Comparator #(.width(6), .mode("twosComplement")) comparator_5 (
    .a(IR[31:26]), .b(6'b000001), .eq(comparator_5_eq));  // open: gt, lt
  and and_2 (and_2_out, Beq3, equal3);
  MIPS_ALU mips_alu_1 (
    .X(A3), .Y(multiplexer_33_out), .AluOP(ALuOP3), .Equal(equal3), .Result(ALU3), .shamt(Shmat3));  // open: Result_2
  Adder #(.width(32)) adder_2 (.a(shifter_1_out), .b(PC3), .out(adder_2_out), .cin(1'b0));  // open: cout
  and and_3 (and_3_out, comparator_5_eq, comparator_4_eq);
  and and_4 (and_4_out, not_3_out, Bne3);
  not not_3 (not_3_out, equal3);
  Register #(.width(32), .trigger("rising"), .Select("low")) register_1 (
    .D(B3), .en(and_5_out), .Q(LedData), .clk(CLK), .clr(RST));
  and and_5 (and_5_out, Syscall3, equal3);
  Register #(.width(1), .trigger("rising"), .Select("low")) MemToReg_2 (
    .D(MemToReg_q), .Q(MemToReg_2_q), .clk(and_1_out), .clr(RST));  // open: en
  Register #(.width(1), .trigger("rising"), .Select("low")) RegDst_2 (
    .D(RegDst_q), .Q(RegDst_2_q), .clk(and_1_out), .clr(RST));  // open: en
  Register #(.width(1), .trigger("rising"), .Select("low")) RegWrite_2 (
    .D(RegWrite3), .Q(RegWrite_2_q), .clk(and_1_out), .clr(RST));  // open: en
  Register #(.width(1), .trigger("rising"), .Select("low")) MemWrite_2 (
    .D(MemWrite_q), .Q(MemWrite), .clk(and_1_out), .clr(RST));  // open: en
  Register #(.width(1), .trigger("rising"), .Select("low")) Syscall_2 (
    .D(Syscall3), .Q(Syscall4), .clk(and_1_out), .clr(RST));  // open: en
  Register #(.width(1), .trigger("rising"), .Select("low")) equal (
    .D(equal3), .Q(equal4), .clk(and_1_out), .clr(RST));  // open: en
  Register #(.width(1), .trigger("rising"), .Select("low")) Jal_2 (
    .D(Jal3), .Q(Jal_2_q), .clk(and_1_out), .clr(RST));  // open: en
  Register #(.width(32), .trigger("rising"), .Select("low")) IR_3 (
    .D(IRNO3), .Q(IR4), .clk(and_1_out), .clr(RST));  // open: en
  Register #(.width(32), .trigger("rising"), .Select("low")) PC_4 (
    .D(PC3), .Q(PC_4_q), .clk(and_1_out), .clr(RST));  // open: en
  Register #(.width(32), .trigger("rising"), .Select("low")) B_2 (
    .D(B3), .Q(MDin), .clk(and_1_out), .clr(RST));  // open: en
  Register #(.width(32), .trigger("rising"), .Select("low")) ALU (
    .D(ALU3), .Q(ALU4), .clk(and_1_out), .clr(RST));  // open: en
  Register #(.width(32), .trigger("rising"), .Select("low")) PCO_3 (
    .D(EX_PC), .Q(M_PC), .clk(and_1_out), .clr(RST));  // open: en
  // Mips_Probe mips_probe_9: pin names not known; wires that end beside it: IR4
  RAM #(.addrWidth(10), .dataWidth(32), .bus("separate"), .Select("high")) ram_1 (
    .addr(ALU4[11:2]), .din(MDin), .data(MD4), .str(MemWrite), .clk(CLK), .clr(RST));  // open: sel, ld
  Register #(.width(1), .trigger("rising"), .Select("low")) MemToReg_3 (
    .D(MemToReg_2_q), .Q(MemToReg5), .clk(and_1_out), .clr(RST));  // open: en
  Register #(.width(1), .trigger("rising"), .Select("low")) RegDst_3 (
    .D(RegDst_2_q), .Q(RegDst5), .clk(and_1_out), .clr(RST));  // open: en
  Register #(.width(1), .trigger("rising"), .Select("low")) RegWrite_3 (
    .D(RegWrite_2_q), .Q(RegWrite), .clk(and_1_out), .clr(RST));  // open: en
  Register #(.width(1), .trigger("rising"), .Select("low")) Syscall_3 (
    .D(Syscall4), .Q(Syscall5), .clk(and_1_out), .clr(RST));  // open: en
  Register #(.width(1), .trigger("rising"), .Select("low")) equal_2 (
    .D(equal4), .Q(equal5), .clk(and_1_out), .clr(RST));  // open: en
  Register #(.width(1), .trigger("rising"), .Select("low")) Jal_3 (
    .D(Jal_2_q), .Q(Jal5), .clk(and_1_out), .clr(RST));  // open: en
  Register #(.width(32), .trigger("rising"), .Select("low")) IR_4 (
    .D(IR4), .Q(IR5), .clk(and_1_out), .clr(RST));  // open: en
  Register #(.width(32), .trigger("rising"), .Select("low")) PC_5 (
    .D(PC_4_q), .Q(PC5), .clk(and_1_out), .clr(RST));  // open: en
  Register #(.width(32), .trigger("rising"), .Select("low")) ALU_2 (
    .D(ALU4), .Q(ALU5), .clk(and_1_out), .clr(RST));  // open: en
  Register #(.width(32), .trigger("rising"), .Select("low")) MD (
    .D(MD4), .Q(MD5), .clk(and_1_out), .clr(RST));  // open: en
  Register #(.width(32), .trigger("rising"), .Select("low")) PCO_4 (
    .D(M_PC), .Q(WB_PC), .clk(and_1_out), .clr(RST));  // open: en
  // Mips_Probe mips_probe_10: pin names not known; wires that end beside it: IR5
  Multiplexer #(.select(2), .width(32), .disabled("Z"), .enable("false")) multiplexer_34 (
    .in0(ALU5), .in1(MD5), .in2({32{1'b0}}), .out(RDin1), .sel({1'b0, MemToReg5}));  // open: in3

  // Other names for the same wires on the sheet: byteoff[1:0] = ALU4[1:0]; B4[31:0] = MDin; IR[5:0] = Func;
  //   IRNO2[31:0] = {IR, Func}; Shmat2[4:0] = IR[10:6]; OP[5:0] = IR[31:26]; MEM_PC[31:0] = M_PC;
  //   MemWrite4 = MemWrite; PC[31:0] = IF_PC; PCO1[31:0] = IF_PC; PCO3[31:0] = EX_PC; RegWrite5 = RegWrite;
  //   result[31:0] = ALU3; Syscall2 = Syscall; 总复位 = RST

  // Notes on the sheet:
  //   中断源
  //   时空图监测，可删除
  //   中断等待指示
  //   Syscall停机功能模块
  //   数码管输出
  //   流水调试日志用
  //   控制位
  //   暂停节拍，不能为0
  //   戳工具置1进入计数暂停模式，ctrl+k时钟自动运行到对应节拍暂停
  //   ctrl+k关闭时钟连续运行，将控制位置零，进入单步调试模式调试
  //   指令存储器
  //   contents of rom_1 (hex, n*v repeats v):
  //   20110020 20020022 8000c06 20110004 20120005 20130006 10000003 20110007 20120008 20130009 14110003
  //   2011000a 2012000b 2013000c c000c14 2002000a 0 0 0 c 2231ffff 0 0 0 112020 0 0 0 c 1620fff6 3e00008
  //   可计数暂停的时钟源
  //   IF/ID
  //   rs
  //   指令字
  //   rt
  //   rd
  //   JMP
  //   JR
  //   OP
  //   Func
  //   Syscall
  //   为方便自动评测，需要输出流水线各段保存的PC值，注意是PC不是PC+4，另外ID段寄存器写入信息，Mem段内存写入信息也要输出
  //   Beq
  //   Bne
  //   JAL
  //   ID/EX
  //   EX/MEM
  //   MEM/WB
endmodule

module \源寄存器使用情况  (
  input  OP0,
  input  OP1,
  input  OP2,
  input  OP3,
  input  OP4,
  input  OP5,
  input  F0,
  input  F1,
  input  F2,
  input  F3,
  input  F4,
  input  F5,
  output R1_used,
  output R2_used
);

  wire and_1_out, and_2_out, and_3_out, and_4_out, and_5_out, and_6_out, and_7_out, and_8_out, and_9_out,
       and_10_out, and_11_out, and_12_out, and_13_out, and_14_out, and_15_out, and_16_out, and_17_out,
       and_18_out, and_19_out, not_1_out, not_2_out, not_3_out, not_4_out, not_5_out, not_6_out, not_7_out,
       not_8_out, not_9_out, not_10_out, not_11_out, not_12_out, not_13_out, not_14_out, not_15_out,
       not_16_out, not_17_out, not_18_out, not_19_out, not_20_out, not_21_out, not_22_out, not_23_out,
       not_24_out, not_25_out, not_26_out, not_27_out, not_28_out, not_29_out, not_30_out, not_31_out,
       not_32_out, not_33_out, not_34_out, not_35_out, not_36_out, not_37_out, not_38_out, not_39_out,
       not_40_out, not_41_out, not_42_out, not_43_out, not_44_out, not_45_out, not_46_out, not_47_out,
       not_48_out, not_49_out, not_50_out, not_51_out, not_52_out, not_53_out, not_54_out, not_55_out,
       not_56_out, not_57_out, not_58_out, not_59_out, not_60_out, not_61_out, not_62_out, not_63_out,
       not_64_out, not_65_out, not_66_out, not_67_out, not_68_out, not_69_out, not_70_out, not_71_out,
       not_72_out, not_73_out, not_74_out, not_75_out, not_76_out, not_77_out, not_78_out, not_79_out,
       not_80_out, not_81_out, not_82_out, not_83_out, not_84_out, not_85_out, not_86_out, not_87_out,
       not_88_out, not_89_out, not_90_out, not_91_out, not_92_out, not_93_out, not_94_out, not_95_out,
       not_96_out, not_97_out, not_98_out, not_99_out, not_100_out, not_101_out, not_102_out, not_103_out,
       not_104_out, not_105_out, not_106_out, not_107_out;

  not not_1 (not_1_out, OP1);
  not not_2 (not_2_out, OP4);
  not not_3 (not_3_out, OP5);
  not not_4 (not_4_out, F0);
  not not_5 (not_5_out, F2);
  not not_6 (not_6_out, F3);
  not not_7 (not_7_out, F4);
  not not_8 (not_8_out, OP1);
  not not_9 (not_9_out, OP4);
  not not_10 (not_10_out, OP5);
  not not_11 (not_11_out, F1);
  not not_12 (not_12_out, F3);
  not not_13 (not_13_out, F4);
  not not_14 (not_14_out, OP1);
  not not_15 (not_15_out, OP4);
  not not_16 (not_16_out, OP5);
  not not_17 (not_17_out, F0);
  not not_18 (not_18_out, F1);
  not not_19 (not_19_out, F4);
  not not_20 (not_20_out, F5);
  not not_21 (not_21_out, OP1);
  not not_22 (not_22_out, OP4);
  not not_23 (not_23_out, OP5);
  not not_24 (not_24_out, F0);
  not not_25 (not_25_out, F1);
  not not_26 (not_26_out, F3);
  not not_27 (not_27_out, F4);
  not not_28 (not_28_out, OP1);
  not not_29 (not_29_out, OP4);
  not not_30 (not_30_out, OP5);
  not not_31 (not_31_out, F2);
  not not_32 (not_32_out, F4);
  not not_33 (not_33_out, OP1);
  not not_34 (not_34_out, OP4);
  not not_35 (not_35_out, OP5);
  not not_36 (not_36_out, F3);
  not not_37 (not_37_out, F4);
  not not_38 (not_38_out, OP2);
  not not_39 (not_39_out, OP4);
  not not_40 (not_40_out, OP5);
  not not_41 (not_41_out, OP0);
  not not_42 (not_42_out, OP1);
  not not_43 (not_43_out, OP3);
  not not_44 (not_44_out, OP4);
  not not_45 (not_45_out, OP1);
  not not_46 (not_46_out, OP4);
  not not_47 (not_47_out, OP5);
  not not_48 (not_48_out, OP1);
  not not_49 (not_49_out, OP4);
  not not_50 (not_50_out, OP5);
  not not_51 (not_51_out, OP2);
  not not_52 (not_52_out, OP4);
  not not_53 (not_53_out, OP0);
  not not_54 (not_54_out, OP1);
  not not_55 (not_55_out, OP3);
  not not_56 (not_56_out, OP4);
  not not_57 (not_57_out, OP5);
  not not_58 (not_58_out, F0);
  not not_59 (not_59_out, F2);
  not not_60 (not_60_out, F3);
  not not_61 (not_61_out, F4);
  not not_62 (not_62_out, OP0);
  not not_63 (not_63_out, OP1);
  not not_64 (not_64_out, OP3);
  not not_65 (not_65_out, OP4);
  not not_66 (not_66_out, OP5);
  not not_67 (not_67_out, F1);
  not not_68 (not_68_out, F3);
  not not_69 (not_69_out, F4);
  not not_70 (not_70_out, OP0);
  not not_71 (not_71_out, OP1);
  not not_72 (not_72_out, OP3);
  not not_73 (not_73_out, OP4);
  not not_74 (not_74_out, OP5);
  not not_75 (not_75_out, F0);
  not not_76 (not_76_out, F1);
  not not_77 (not_77_out, F4);
  not not_78 (not_78_out, F5);
  not not_79 (not_79_out, OP0);
  not not_80 (not_80_out, OP1);
  not not_81 (not_81_out, OP3);
  not not_82 (not_82_out, OP4);
  not not_83 (not_83_out, OP5);
  not not_84 (not_84_out, F2);
  not not_85 (not_85_out, F3);
  not not_86 (not_86_out, F4);
  not not_87 (not_87_out, F5);
  not not_88 (not_88_out, OP0);
  not not_89 (not_89_out, OP1);
  not not_90 (not_90_out, OP3);
  not not_91 (not_91_out, OP4);
  not not_92 (not_92_out, OP5);
  not not_93 (not_93_out, F2);
  not not_94 (not_94_out, F4);
  not not_95 (not_95_out, OP0);
  not not_96 (not_96_out, OP1);
  not not_97 (not_97_out, OP3);
  not not_98 (not_98_out, OP4);
  not not_99 (not_99_out, OP5);
  not not_100 (not_100_out, F3);
  not not_101 (not_101_out, F4);
  not not_102 (not_102_out, OP1);
  not not_103 (not_103_out, OP3);
  not not_104 (not_104_out, OP4);
  not not_105 (not_105_out, OP5);
  not not_106 (not_106_out, OP2);
  not not_107 (not_107_out, OP4);
  and and_1 (and_1_out, not_1_out, not_2_out, not_3_out, not_4_out, not_5_out, not_6_out, not_7_out, F5);
  and and_2 (and_2_out, not_8_out, not_9_out, not_10_out, not_11_out, not_12_out, not_13_out, F5);
  and and_3 (and_3_out, not_14_out, not_15_out, not_16_out, not_17_out, not_18_out, F3, not_19_out, not_20_out);
  and and_4 (and_4_out, not_21_out, not_22_out, not_23_out, not_24_out, not_25_out, F2, not_26_out, not_27_out);
  and and_5 (and_5_out, not_28_out, not_29_out, not_30_out, F1, not_31_out, F3, not_32_out, F5);
  and and_6 (and_6_out, not_33_out, not_34_out, not_35_out, F0, F2, not_36_out, not_37_out, F5);
  and and_7 (and_7_out, not_38_out, OP3, not_39_out, not_40_out);
  and and_8 (and_8_out, not_41_out, not_42_out, OP2, not_43_out, not_44_out);
  and and_9 (and_9_out, not_45_out, OP2, not_46_out, not_47_out);
  and and_10 (and_10_out, OP0, not_48_out, not_49_out, not_50_out);
  and and_11 (and_11_out, OP0, OP1, not_51_out, not_52_out, OP5);
  and and_12 (and_12_out, not_53_out, not_54_out, not_55_out, not_56_out, not_57_out, not_58_out, not_59_out, not_60_out, not_61_out);
  and and_13 (and_13_out, not_62_out, not_63_out, not_64_out, not_65_out, not_66_out, not_67_out, not_68_out, not_69_out, F5);
  and and_14 (and_14_out, not_70_out, not_71_out, not_72_out, not_73_out, not_74_out, not_75_out, not_76_out, F2, not_77_out, not_78_out);
  and and_15 (and_15_out, not_79_out, not_80_out, not_81_out, not_82_out, not_83_out, F1, not_84_out, not_85_out, not_86_out, not_87_out);
  and and_16 (and_16_out, not_88_out, not_89_out, not_90_out, not_91_out, not_92_out, F1, not_93_out, F3, not_94_out, F5);
  and and_17 (and_17_out, not_95_out, not_96_out, not_97_out, not_98_out, not_99_out, F0, F2, not_100_out, not_101_out, F5);
  and and_18 (and_18_out, not_102_out, OP2, not_103_out, not_104_out, not_105_out);
  and and_19 (and_19_out, OP0, OP1, not_106_out, not_107_out, OP5);
  or or_1 (R1_used, and_1_out, and_2_out, and_3_out, and_4_out, and_5_out, and_6_out, and_7_out, and_8_out, and_9_out, and_10_out, and_11_out);
  or or_2 (R2_used, and_12_out, and_13_out, and_14_out, and_15_out, and_16_out, and_17_out, and_18_out, and_19_out);
endmodule
module \数据相关检测  (
  input  [4:0] EX_WriteReg_num,
  input  R1_Used,
  input  [4:0] R1_num,
  input  R2_Used,
  input  [4:0] R2_num,
  input  [4:0] MEM_WriteReg_num,
  input  RegWrite_EX,
  input  RegWrite_MEM,
  output Yes
);

  wire and_1_out, and_2_out, and_3_out, and_4_out, and_5_out, and_6_out, comparator_1_eq, comparator_2_eq,
       comparator_3_eq, comparator_4_eq, comparator_5_eq, comparator_6_eq, comparator_7_eq, comparator_8_eq,
       not_1_out, not_2_out, or_1_out, or_2_out;

  Comparator #(.width(1), .mode("twosComplement")) comparator_1 (
    .a(RegWrite_EX), .b(1'b1), .eq(comparator_1_eq));  // open: gt, lt
  Comparator #(.width(1), .mode("twosComplement")) comparator_2 (
    .a(RegWrite_MEM), .b(1'b1), .eq(comparator_2_eq));  // open: gt, lt
  Comparator #(.width(5), .mode("twosComplement")) comparator_3 (
    .a(EX_WriteReg_num), .b({5{1'b0}}), .eq(comparator_3_eq));  // open: gt, lt
  Comparator #(.width(5), .mode("twosComplement")) comparator_4 (
    .a(MEM_WriteReg_num), .b({5{1'b0}}), .eq(comparator_4_eq));  // open: gt, lt
  not not_1 (not_1_out, comparator_3_eq);
  Comparator #(.width(5), .mode("twosComplement")) comparator_5 (
    .a(EX_WriteReg_num), .b(R1_num), .eq(comparator_5_eq));  // open: gt, lt
  Comparator #(.width(5), .mode("twosComplement")) comparator_6 (
    .a(EX_WriteReg_num), .b(R2_num), .eq(comparator_6_eq));  // open: gt, lt
  not not_2 (not_2_out, comparator_4_eq);
  Comparator #(.width(5), .mode("twosComplement")) comparator_7 (
    .a(MEM_WriteReg_num), .b(R1_num), .eq(comparator_7_eq));  // open: gt, lt
  Comparator #(.width(5), .mode("twosComplement")) comparator_8 (
    .a(MEM_WriteReg_num), .b(R2_num), .eq(comparator_8_eq));  // open: gt, lt
  and and_1 (and_1_out, R1_Used, comparator_5_eq);
  or or_1 (or_1_out, and_1_out, and_2_out);
  and and_2 (and_2_out, R2_Used, comparator_6_eq);
  and and_3 (and_3_out, R1_Used, comparator_7_eq);
  and and_4 (and_4_out, R2_Used, comparator_8_eq);
  or or_2 (or_2_out, and_3_out, and_4_out);
  and and_5 (and_5_out, not_1_out, comparator_1_eq, or_1_out);
  and and_6 (and_6_out, not_2_out, comparator_2_eq, or_2_out);
  or or_3 (Yes, and_5_out, and_6_out);
endmodule

module \重定向数据相关检测  (
  input  [4:0] EX_WriteReg_num,
  input  R1_Used,
  input  [4:0] R1_num,
  input  R2_Used,
  input  [4:0] R2_num,
  input  [4:0] MEM_WriteReg_num,
  input  RegWrite3,
  input  RegWrite4,
  input  EX_MemRead,
  output [1:0] RsForward,
  output Yes,
  output [1:0] RtForward,
  output LoadUse
);

  wire and_1_out, and_2_out, and_3_out, and_4_out, and_5_out, and_6_out, and_7_out, and_8_out, and_9_out,
       and_10_out, and_11_out, and_12_out, and_14_out, and_15_out, comparator_1_eq, comparator_2_eq,
       comparator_3_eq, comparator_4_eq, comparator_5_eq, comparator_6_eq, comparator_7_eq, comparator_8_eq,
       comparator_9_eq, comparator_10_eq, not_1_out, not_2_out, not_3_out, not_4_out, or_1_out, or_2_out,
       or_3_out;

  Comparator #(.width(1), .mode("twosComplement")) comparator_1 (
    .a(RegWrite3), .b(1'b1), .eq(comparator_1_eq));  // open: gt, lt
  Comparator #(.width(1), .mode("twosComplement")) comparator_2 (
    .a(RegWrite4), .b(1'b1), .eq(comparator_2_eq));  // open: gt, lt
  Comparator #(.width(5), .mode("twosComplement")) comparator_3 (
    .a(EX_WriteReg_num), .b({5{1'b0}}), .eq(comparator_3_eq));  // open: gt, lt
  not not_1 (not_1_out, comparator_3_eq);
  Comparator #(.width(5), .mode("twosComplement")) comparator_4 (
    .a(EX_WriteReg_num), .b(R1_num), .eq(comparator_4_eq));  // open: gt, lt
  Comparator #(.width(5), .mode("twosComplement")) comparator_5 (
    .a(MEM_WriteReg_num), .b({5{1'b0}}), .eq(comparator_5_eq));  // open: gt, lt
  Comparator #(.width(5), .mode("twosComplement")) comparator_6 (
    .a(R1_num), .b({5{1'b0}}), .eq(comparator_6_eq));  // open: gt, lt
  Comparator #(.width(5), .mode("twosComplement")) comparator_7 (
    .a(R2_num), .b({5{1'b0}}), .eq(comparator_7_eq));  // open: gt, lt
  Comparator #(.width(5), .mode("twosComplement")) comparator_8 (
    .a(EX_WriteReg_num), .b(R2_num), .eq(comparator_8_eq));  // open: gt, lt
  not not_2 (not_2_out, comparator_5_eq);
  Comparator #(.width(5), .mode("twosComplement")) comparator_9 (
    .a(MEM_WriteReg_num), .b(R1_num), .eq(comparator_9_eq));  // open: gt, lt
  Comparator #(.width(5), .mode("twosComplement")) comparator_10 (
    .a(MEM_WriteReg_num), .b(R2_num), .eq(comparator_10_eq));  // open: gt, lt
  not not_3 (not_3_out, comparator_6_eq);
  not not_4 (not_4_out, comparator_7_eq);
  and and_1 (and_1_out, not_1_out, R1_Used, comparator_4_eq);
  and and_2 (and_2_out, R2_Used, not_1_out, comparator_8_eq);
  and and_3 (and_3_out, R1_Used, not_2_out, comparator_9_eq);
  and and_4 (and_4_out, R2_Used, not_2_out, comparator_10_eq);
  or or_1 (or_1_out, and_1_out, and_2_out);
  or or_2 (or_2_out, and_3_out, and_4_out);
  and and_5 (and_5_out, R1_Used, not_3_out);
  and and_6 (and_6_out, R2_Used, not_4_out);
  or or_3 (or_3_out, or_1_out, or_2_out);
  and and_7 (and_7_out, comparator_4_eq, EX_MemRead);
  and and_8 (and_8_out, comparator_8_eq, EX_MemRead);
  and and_9 (and_9_out, and_5_out, and_7_out);
  and and_10 (and_10_out, and_6_out, and_8_out);
  and and_11 (and_11_out, and_1_out, comparator_1_eq);
  and and_12 (and_12_out, and_3_out, comparator_2_eq);
  and and_13 (Yes, or_3_out, comparator_1_eq);
  and and_14 (and_14_out, and_2_out, comparator_1_eq);
  and and_15 (and_15_out, and_4_out, comparator_2_eq);
  or or_4 (LoadUse, and_9_out, and_10_out);
  Priority_Encoder #(.select(2), .disabled("Z")) priority_encoder_1 (
    .in0(1'b1), .in1(and_12_out), .in2(and_11_out), .out(RsForward));  // open: in3, gs, en_out, en_in
  Priority_Encoder #(.select(2), .disabled("Z")) priority_encoder_2 (
    .in0(1'b1), .in1(and_15_out), .in2(and_14_out), .out(RtForward));  // open: in3, gs, en_out, en_in
endmodule

module \流水中断  (
  output RegWrite,
  output MemWrite,
  output [31:0] IF_PC,
  output [31:0] ID_PC,
  output [31:0] EX_PC,
  output [31:0] M_PC,
  output [31:0] WB_PC,
  output [31:0] RDin,
  output [31:0] MDin,
  output [31:0] LedData
);

  wire _1_out, _2_out, _3_out, ALuSrcB2, ALuSrcB3, and_3_out, and_4_out, and_5_out, and_6_out, and_7_out,
       and_8_out, Beq2, Beq3, Bne2, Bne3, \B系列3 , CLK, clock_1_out, clock_2_out, comparator_1_eq,
       comparator_2_eq, comparator_3_eq, comparator_4_eq, comparator_5_eq, comparator_6_eq, comparator_7_eq,
       comparator_8_eq, comparator_9_eq, comparator_11_eq, comparator_12_eq, comparator_12_lt,
       comparator_13_eq, comparator_14_eq, comparator_15_eq, d_ff_2_q, d_ff_3_q, d_ff_4_qn, d_ff_5_q, equal3,
       equal4, equal5, Eret, Go, IR1, IR2, IR3, IRA, IRB, IRC, Jal2, Jal3, Jal5, Jal_2_q, Jmp2, Jmp3, JR2,
       JR3, Loaduse, MemToReg2, MemToReg3, MemToReg5, MemToReg_2_q, MemWrite2, MemWrite_q,
       multiplexer_15_out, multiplexer_16_out, multiplexer_17_out, multiplexer_18_out, multiplexer_20_out,
       multiplexer_21_out, multiplexer_22_out, multiplexer_23_out, multiplexer_24_out, multiplexer_25_out,
       multiplexer_26_out, nand_1_out, not_1_out, not_2_out, not_4_out, not_5_out, or_2_out, or_3_out,
       or_4_out, or_5_out, or_7_out, or_8_out, or_9_out, or_10_out, or_13_out, or_14_out, \PC使能 , RegDst2,
       RegDst5, RegDst_2_q, RegDst_q, RegWrite2, RegWrite3, RegWrite4, RST, SignedExt, Syscall, Syscall3,
       Syscall4, Syscall5, W1, W2, W3, \中断可接收 , \中断按键参考电路_1_有新中断 , \分支气泡 , \数据相关 , \有中断_Eret ,
       \源寄存器使用情况_1_r1_used , \源寄存器使用情况_1_r2_used ;
  wire [1:0] multiplexer_34_out, multiplexer_35_out, RsForward2, RsForward3, RtForward2, RtForward3,
       \中断按键参考电路_1_优先中断编号 ;
  wire [1:1] comparator_10_eq;
  wire [3:0] ALuOP2, ALuOP3, multiplexer_19_out;
  wire [4:0] EX_WriteReg_num, MEM_WriteReg_num, multiplexer_9_out, multiplexer_10_out, multiplexer_11_out,
       multiplexer_13_out, multiplexer_14_out, multiplexer_32_out, Shmat3;
  wire [5:0] Func;
  wire [7:0] multiplexer_40_out;
  wire [12:0] CNT_num;
  wire [15:0] \LoadUse次数 , \总周期数 , \插入气泡数 , \无条件分支数 , \条件分支成功数 ;
  wire [31:0] A2, A3, ALU3, ALU4, ALU5, B2, B3, B4, bit_extender_2_out, bit_extender_3_out,
       bit_extender_4_out, \B系列地址3 , EX_IR, IF_IR, Imm2, Imm3, IR4, IR5, \J系列地址3 , MD4, MD5,
       multiplexer_1_out, multiplexer_2_out, multiplexer_4_out, multiplexer_6_out, multiplexer_7_out,
       multiplexer_8_out, multiplexer_27_out, multiplexer_28_out, multiplexer_29_out, multiplexer_30_out,
       multiplexer_31_out, multiplexer_33_out, multiplexer_38_out, multiplexer_39_out, NextPCNormal, PC1,
       PC2, PC3, PC5, PC_4_q, popeddata, ram_1_data, RealB3, shifter_1_out, \中断入口_返回地址 ;
  wire [31:6] ID_IR;

  Button \u_总复位  (.out(RST));
  // Probe on \总周期数 
  // Probe on \总周期数 
  Button \u_继续运行  (.out(Go));
  LED #(.active("true")) led_1 (.in(W1));
  LED #(.active("true")) led_2 (.in(W2));
  LED #(.active("true")) led_3 (.in(W3));
  Hex_Digit_Display hex_digit_display_1 (.value(LedData[31:28]));  // open: dp
  // Probe on IF_PC[19:0]
  // Mips_Probe mips_probe_1: pin names not known; wires that end beside it: IR1, IR2, IR3, IF_IR
  Button _1 (.out(_1_out));
  or or_1 (IR1, _1_out, IRA);
  not not_1 (not_1_out, Syscall5);
  Comparator #(.width(32), .mode("twosComplement")) comparator_1 (
    .a(EX_IR), .b(32'h40800000), .eq(comparator_1_eq));  // open: gt, lt
  Comparator #(.width(6), .mode("twosComplement")) comparator_2 (
    .a(IF_IR[31:26]), .b(6'b010000), .eq(comparator_2_eq));  // open: gt, lt
  Comparator #(.width(6), .mode("twosComplement")) comparator_3 (
    .a(IF_IR[5:0]), .b(6'b011000), .eq(comparator_3_eq));  // open: gt, lt
  Hex_Digit_Display hex_digit_display_2 (.value(LedData[27:24]));  // open: dp
  Hex_Digit_Display hex_digit_display_3 (.value(LedData[23:20]));  // open: dp
  // Probe on ID_PC[19:0]
  // Mips_Probe mips_probe_2: pin names not known; wires that end beside it: {ID_IR, Func}
  or or_2 (or_2_out, not_1_out, Go);
  or or_3 (or_3_out, equal5, not_1_out);
  Comparator #(.width(16), .mode("twosComplement")) comparator_4 (
    .a(16'h258), .b(\总周期数 ), .eq(comparator_4_eq));  // open: gt, lt
  Comparator #(.width(16), .mode("twosComplement")) comparator_5 (
    .a(\总周期数 ), .b(16'h1), .eq(comparator_5_eq));  // open: gt, lt
  Comparator #(.width(16), .mode("twosComplement")) comparator_6 (
    .a(\总周期数 ), .b(16'h4), .eq(comparator_6_eq));  // open: gt, lt
  Comparator #(.width(16), .mode("twosComplement")) comparator_7 (
    .a(\总周期数 ), .b(16'h7), .eq(comparator_7_eq));  // open: gt, lt
  or or_4 (or_4_out, comparator_7_eq, comparator_8_eq);
  Comparator #(.width(16), .mode("twosComplement")) comparator_8 (
    .a(\总周期数 ), .b(16'h241), .eq(comparator_8_eq));  // open: gt, lt
  \中断按键参考电路  \u_中断按键参考电路_1  (
    .\优先中断编号 (\中断按键参考电路_1_优先中断编号 ), .\_1号中断 (IR1), .\_2号中断 (IR2), .\_3号中断 (IR3), .\时钟 (CLK), .\异步清零信号 (RST),
    .\中断可接收 (\中断可接收 ), .\有新中断 (\中断按键参考电路_1_有新中断 ), .eret(Eret));
  or or_5 (or_5_out, comparator_1_eq, \中断可接收 );
  and and_1 (Eret, comparator_2_eq, comparator_3_eq);
  Comparator #(.width(32), .mode("twosComplement")) comparator_9 (
    .a(IF_IR), .b(32'h40000000), .eq(comparator_9_eq));  // open: gt, lt
  Comparator #(.width(32), .mode("unsigned")) comparator_10 (
    .a({ID_IR, Func}), .b({32{1'b0}}), .eq(comparator_10_eq[1]));  // open: gt, lt
  Hex_Digit_Display hex_digit_display_4 (.value(LedData[15:12]));  // open: dp
  Hex_Digit_Display hex_digit_display_5 (.value(LedData[19:16]));  // open: dp
  Button _2 (.out(_2_out));
  or or_6 (IR2, _2_out, IRB);
  D_Flip_Flop #(.trigger("falling"), .Pre_Clr_Positions("ABOVE_BELOW"), .NegatePresetClear("false"), .enable("false"), .NewFFLayout("true")) d_ff_1 (
    .clk(CLK), .D(or_3_out), .Q(\PC使能 ), .preset(or_2_out));  // open: Qn, reset
  or or_7 (or_7_out, comparator_4_eq, comparator_5_eq);
  Pull_Resistor #(.pull(0)) pull_resistor_1 (.node(IRA));
  assign IRA = or_7_out ? ~CLK : 1'bz;  // Controlled_Inverter controlled_inverter_1
  Pull_Resistor #(.pull(0)) pull_resistor_2 (.node(IRB));
  assign IRB = comparator_6_eq ? ~CLK : 1'bz;  // Controlled_Inverter controlled_inverter_2
  Pull_Resistor #(.pull(0)) pull_resistor_3 (.node(IRC));
  assign IRC = or_4_out ? ~CLK : 1'bz;  // Controlled_Inverter controlled_inverter_3
  D_Flip_Flop #(.trigger("rising"), .Pre_Clr_Positions("LEGACY"), .NegatePresetClear("false"), .enable("true"), .NewFFLayout("false")) d_ff_2 (
    .clk(CLK), .D(or_5_out), .Q(d_ff_2_q), .reset(RST));  // open: Qn, preset, en
  D_Flip_Flop #(.trigger("rising"), .Pre_Clr_Positions("LEGACY"), .NegatePresetClear("false"), .enable("true"), .NewFFLayout("false")) d_ff_3 (
    .clk(CLK), .D(or_8_out), .Q(d_ff_3_q), .reset(RST));  // open: Qn, preset, en
  or or_8 (or_8_out, Eret, comparator_9_eq);
  Multiplexer #(.select(2), .width(32), .disabled("Z"), .enable("false")) multiplexer_1 (
    .in0(ID_PC), .in1(NextPCNormal), .in2(IF_PC), .in3(NextPCNormal), .out(multiplexer_1_out),
    .sel({comparator_10_eq[1], \分支气泡 }));
  or or_9 (or_9_out, \中断可接收 , Eret);
  Hex_Digit_Display hex_digit_display_6 (.value(LedData[7:4]));  // open: dp
  Hex_Digit_Display hex_digit_display_7 (.value(LedData[11:8]));  // open: dp
  Clock #(.highDuration(1), .lowDuration(1)) clock_1 (.out(clock_1_out));
  // Probe on EX_PC[19:0]
  // Mips_Probe mips_probe_3: pin names not known; wires that end beside it: clock_1_out, EX_IR, CLK
  Button _3 (.out(_3_out));
  D_Flip_Flop #(.trigger("rising"), .Pre_Clr_Positions("LEGACY"), .NegatePresetClear("false"), .enable("true"), .NewFFLayout("false")) d_ff_4 (
    .Qn(d_ff_4_qn), .preset(d_ff_2_q), .reset(or_10_out));  // open: clk, D, Q, en
  or or_10 (or_10_out, RST, d_ff_3_q);
  \硬件堆栈  \u_硬件堆栈_1  (
    .push_pop(Eret), .Enable(or_9_out), .CLK(CLK), .\总复位 (RST), .pusheddata(multiplexer_1_out),
    .popeddata(popeddata));
  Hex_Digit_Display hex_digit_display_8 (.value(LedData[3:0]));  // open: dp
  or or_11 (IR3, _3_out, IRC);
  Multiplexer #(.select(2), .width(32), .disabled("Z"), .enable("false")) multiplexer_2 (
    .in1(32'h30ac), .in2(32'h3158), .in3(32'h3204), .out(multiplexer_2_out), .sel(\中断按键参考电路_1_优先中断编号 ));  // open: in0
  // Probe on \总周期数 
  // Probe on M_PC[19:0]
  // Mips_Probe mips_probe_4: pin names not known; wires that end beside it: IR4
  and and_2 (\中断可接收 , \中断按键参考电路_1_有新中断 , d_ff_4_qn);
  // Probe on \总周期数 
  // Probe on \无条件分支数 
  // Probe on \条件分支成功数 
  // Probe on \插入气泡数 
  // Probe on \LoadUse次数 
  Comparator #(.width(2), .mode("twosComplement")) comparator_11 (
    .a({\B系列3 , Jmp3}), .b(2'b00), .eq(comparator_11_eq));  // open: gt, lt
  Multiplexer #(.select(2), .width(32), .disabled("Z"), .enable("false")) multiplexer_3 (
    .in0(PC1), .in1(\J系列地址3 ), .in2(\B系列地址3 ), .out(NextPCNormal), .sel({\B系列3 , Jmp3}));  // open: in3
  Multiplexer #(.select(1), .width(32), .disabled("Z"), .enable("false")) multiplexer_4 (
    .in0(NextPCNormal), .in1(\中断入口_返回地址 ), .out(multiplexer_4_out), .sel(\有中断_Eret ));
  and and_3 (and_3_out, \PC使能 , not_2_out);
  not not_2 (not_2_out, Loaduse);
  and and_4 (and_4_out, \PC使能 , CLK);
  // Probe on IF_PC[11:0]
  // Probe on WB_PC[19:0]
  // Mips_Probe mips_probe_5: pin names not known; wires that end beside it: IR5
  not not_3 (\分支气泡 , comparator_11_eq);
  Register #(.width(32), .trigger("rising"), .Select("low")) PC (
    .D(multiplexer_4_out), .en(and_3_out), .Q(IF_PC), .clk(CLK), .clr(RST));
  Adder #(.width(32)) adder_1 (.a(IF_PC), .b(32'h4), .out(PC1));  // open: cin, cout
  or or_12 (\有中断_Eret , \中断可接收 , Eret);
  Multiplexer #(.select(1), .width(32), .disabled("Z"), .enable("false")) multiplexer_5 (
    .in0(multiplexer_2_out), .in1(popeddata), .out(\中断入口_返回地址 ), .sel(Eret));
  not not_4 (not_4_out, Loaduse);
  // Probe on EX_PC[11:0]
  // Probe on ID_PC[11:0]
  // Probe on M_PC[11:0]
  D_Flip_Flop #(.trigger("high"), .Pre_Clr_Positions("LEGACY"), .NegatePresetClear("false"), .enable("true"), .NewFFLayout("false")) d_ff_5 (.Q(d_ff_5_q));  // open: clk, D, Qn, preset, en, reset
  // Probe on 13'hfff
  // Probe on WB_PC[11:0]
  Comparator #(.width(13), .mode("twosComplement")) comparator_12 (
    .a(CNT_num), .b(13'hfff), .eq(comparator_12_eq), .lt(comparator_12_lt));  // open: gt
  Clock #(.highDuration(1), .lowDuration(1)) clock_2 (.out(clock_2_out));
  ROM #(.addrWidth(10), .dataWidth(32), .Select("high")) rom_1 (.addr(IF_PC[11:2]), .data(IF_IR));
  or or_13 (or_13_out, \有中断_Eret , \分支气泡 );
  nand nand_1 (nand_1_out, d_ff_5_q, comparator_12_eq);
  Counter #(.width(13), .max('h1fff), .ongoal("stay"), .trigger("rising"), .behavior("old")) counter_1 (
    .count(comparator_12_lt), .Q(CNT_num), .clk(clock_2_out));  // open: load, D, carry, clr, preset
  // Mips_Probe mips_probe_6: pin names not known; wires that end beside it: IF_IR
  assign CLK = nand_1_out ? clock_2_out : 1'bz;  // Controlled_Buffer controlled_buffer_1
  Multiplexer #(.select(1), .width(32), .disabled("Z"), .enable("false")) multiplexer_6 (
    .in0(IF_IR), .in1({32{1'b0}}), .out(multiplexer_6_out), .sel(or_13_out));
  Multiplexer #(.select(1), .width(32), .disabled("Z"), .enable("false")) multiplexer_7 (
    .in0(PC1), .in1({32{1'b0}}), .out(multiplexer_7_out), .sel(or_13_out));
  Multiplexer #(.select(1), .width(32), .disabled("Z"), .enable("false")) multiplexer_8 (
    .in0(IF_PC), .in1({32{1'b0}}), .out(multiplexer_8_out), .sel(or_13_out));
  assign \总周期数  = {{3{1'b0}}, CNT_num};  // Bit_Extender bit_extender_1
  Pull_Resistor #(.pull(1)) pull_resistor_4 (.node(CLK));
  Register #(.width(32), .trigger("rising"), .Select("low")) IR (
    .D(multiplexer_6_out), .en(not_4_out), .Q({ID_IR, Func}), .clk(and_4_out), .clr(RST));
  Register #(.width(32), .trigger("rising"), .Select("low")) PC_2 (
    .D(multiplexer_7_out), .en(not_4_out), .Q(PC2), .clk(and_4_out), .clr(RST));
  Register #(.width(32), .trigger("rising"), .Select("low")) PCO (
    .D(multiplexer_8_out), .en(not_4_out), .Q(ID_PC), .clk(and_4_out), .clr(RST));
  // Mips_Probe mips_probe_7: pin names not known; wires that end beside it: {ID_IR, Func}
  \单周期硬布线控制器  \u_单周期硬布线控制器_1  (
    .Func(Func), .OP(ID_IR[31:26]), .ALU_OP(ALuOP2), .MemToReg(MemToReg2), .MemWrite(MemWrite2),
    .ALU_SRC(ALuSrcB2), .RegWrite(RegWrite2), .SysCALL(Syscall), .SignedExt(SignedExt), .RegDst(RegDst2),
    .JR(JR2), .JMP(Jmp2), .Beq(Beq2), .JAL(Jal2), .Bne(Bne2));
  Multiplexer #(.select(1), .width(5), .disabled("Z"), .enable("false")) multiplexer_9 (
    .in0(ID_IR[25:21]), .in1(5'b00010), .out(multiplexer_9_out), .sel(Syscall));
  Multiplexer #(.select(2), .width(5), .disabled("Z"), .enable("false")) multiplexer_10 (
    .in0(IR5[20:16]), .in1(IR5[15:11]), .in2({5{1'b1}}), .out(multiplexer_10_out), .sel({Jal5, RegDst5}));  // open: in3
  Multiplexer #(.select(1), .width(5), .disabled("Z"), .enable("false")) multiplexer_11 (
    .in0(ID_IR[20:16]), .in1(5'b00100), .out(multiplexer_11_out), .sel(Syscall));
  or or_14 (or_14_out, or_13_out, Loaduse);
  assign bit_extender_2_out = {{16{1'b0}}, {ID_IR[15:6], Func}};  // Bit_Extender bit_extender_2
  Multiplexer #(.select(1), .width(32), .disabled("Z"), .enable("false")) multiplexer_12 (
    .in0(bit_extender_2_out), .in1(bit_extender_3_out), .out(Imm2), .sel(SignedExt));
  assign bit_extender_3_out = {{16{ID_IR[15]}}, {ID_IR[15:6], Func}};  // Bit_Extender bit_extender_3
  Multiplexer #(.select(2), .width(5), .disabled("Z"), .enable("false")) multiplexer_13 (
    .in0(ID_IR[20:16]), .in1(ID_IR[15:11]), .in2({5{1'b1}}), .out(multiplexer_13_out), .sel({Jal2, RegDst2}));  // open: in3
  \源寄存器使用情况  \u_源寄存器使用情况_1  (
    .OP0(ID_IR[26]), .OP1(ID_IR[27]), .OP2(ID_IR[28]), .OP3(ID_IR[29]), .OP4(ID_IR[30]), .OP5(ID_IR[31]),
    .F0(Func[0]), .F1(Func[1]), .F2(Func[2]), .F3(Func[3]), .F4(Func[4]), .F5(Func[5]),
    .R1_used(\源寄存器使用情况_1_r1_used ), .R2_used(\源寄存器使用情况_1_r2_used ));
  MIPS_Regifile mips_regifile_1 (
    .Din(RDin), .Clk(CLK), .R1(A2), .R2(B2), .WE(RegWrite), .W_num(multiplexer_10_out),
    .R1_num(multiplexer_9_out), .R2_num(multiplexer_11_out));
  Multiplexer #(.select(1), .width(5), .disabled("Z"), .enable("false")) multiplexer_14 (
    .in0(multiplexer_13_out), .in1({5{1'b0}}), .out(multiplexer_14_out), .sel(or_14_out));
  Multiplexer #(.select(1), .width(1), .disabled("Z"), .enable("false")) multiplexer_15 (
    .in0(MemToReg2), .in1(1'b0), .out(multiplexer_15_out), .sel(or_14_out));
  Multiplexer #(.select(1), .width(1), .disabled("Z"), .enable("false")) multiplexer_16 (
    .in0(RegDst2), .in1(1'b0), .out(multiplexer_16_out), .sel(or_14_out));
  Multiplexer #(.select(1), .width(1), .disabled("Z"), .enable("false")) multiplexer_17 (
    .in0(RegWrite2), .in1(1'b0), .out(multiplexer_17_out), .sel(or_14_out));
  Multiplexer #(.select(1), .width(1), .disabled("Z"), .enable("false")) multiplexer_18 (
    .in0(MemWrite2), .in1(1'b0), .out(multiplexer_18_out), .sel(or_14_out));
  Multiplexer #(.select(1), .width(4), .disabled("Z"), .enable("false")) multiplexer_19 (
    .in0(ALuOP2), .in1(4'b0000), .out(multiplexer_19_out), .sel(or_14_out));
  Multiplexer #(.select(1), .width(1), .disabled("Z"), .enable("false")) multiplexer_20 (
    .in0(ALuSrcB2), .in1(1'b0), .out(multiplexer_20_out), .sel(or_14_out));
  Multiplexer #(.select(1), .width(1), .disabled("Z"), .enable("false")) multiplexer_21 (
    .in0(Syscall), .in1(1'b0), .out(multiplexer_21_out), .sel(or_14_out));
  Multiplexer #(.select(1), .width(1), .disabled("Z"), .enable("false")) multiplexer_22 (
    .in0(Bne2), .in1(1'b0), .out(multiplexer_22_out), .sel(or_14_out));
  Multiplexer #(.select(1), .width(1), .disabled("Z"), .enable("false")) multiplexer_23 (
    .in0(Beq2), .in1(1'b0), .out(multiplexer_23_out), .sel(or_14_out));
  Multiplexer #(.select(1), .width(1), .disabled("Z"), .enable("false")) multiplexer_24 (
    .in0(Jal2), .in1(1'b0), .out(multiplexer_24_out), .sel(or_14_out));
  Multiplexer #(.select(1), .width(1), .disabled("Z"), .enable("false")) multiplexer_25 (
    .in0(Jmp2), .in1(1'b0), .out(multiplexer_25_out), .sel(or_14_out));
  Multiplexer #(.select(1), .width(1), .disabled("Z"), .enable("false")) multiplexer_26 (
    .in0(JR2), .in1(1'b0), .out(multiplexer_26_out), .sel(or_14_out));
  Multiplexer #(.select(1), .width(32), .disabled("Z"), .enable("false")) multiplexer_27 (
    .in0({ID_IR, Func}), .in1({32{1'b0}}), .out(multiplexer_27_out), .sel(or_14_out));
  Multiplexer #(.select(1), .width(32), .disabled("Z"), .enable("false")) multiplexer_28 (
    .in0(PC2), .in1({32{1'b0}}), .out(multiplexer_28_out), .sel(or_14_out));
  Multiplexer #(.select(1), .width(32), .disabled("Z"), .enable("false")) multiplexer_29 (
    .in0(A2), .in1({32{1'b0}}), .out(multiplexer_29_out), .sel(or_14_out));
  Multiplexer #(.select(1), .width(32), .disabled("Z"), .enable("false")) multiplexer_30 (
    .in0(B2), .in1({32{1'b0}}), .out(multiplexer_30_out), .sel(or_14_out));
  Multiplexer #(.select(1), .width(32), .disabled("Z"), .enable("false")) multiplexer_31 (
    .in0(Imm2), .in1({32{1'b0}}), .out(multiplexer_31_out), .sel(or_14_out));
  Multiplexer #(.select(1), .width(5), .disabled("Z"), .enable("false")) multiplexer_32 (
    .in0(ID_IR[10:6]), .in1({5{1'b0}}), .out(multiplexer_32_out), .sel(or_14_out));
  Multiplexer #(.select(1), .width(32), .disabled("Z"), .enable("false")) multiplexer_33 (
    .in0(ID_PC), .in1({32{1'b0}}), .out(multiplexer_33_out), .sel(or_14_out));
  Multiplexer #(.select(1), .width(2), .disabled("Z"), .enable("false")) multiplexer_34 (
    .in0(RsForward2), .in1(2'b00), .out(multiplexer_34_out), .sel(or_14_out));
  Multiplexer #(.select(1), .width(2), .disabled("Z"), .enable("false")) multiplexer_35 (
    .in0(RtForward2), .in1(2'b00), .out(multiplexer_35_out), .sel(or_14_out));
  Register #(.width(5), .trigger("rising"), .Select("low")) \u_假WriteReg_num  (
    .D(multiplexer_14_out), .Q(EX_WriteReg_num), .clk(and_4_out), .clr(RST));  // open: en
  Register #(.width(1), .trigger("rising"), .Select("low")) MemToReg (
    .D(multiplexer_15_out), .Q(MemToReg3), .clk(and_4_out), .clr(RST));  // open: en
  Register #(.width(1), .trigger("rising"), .Select("low")) RegDst (
    .D(multiplexer_16_out), .Q(RegDst_q), .clk(and_4_out), .clr(RST));  // open: en
  Register #(.width(1), .trigger("rising"), .Select("low")) u_RegWrite (
    .D(multiplexer_17_out), .Q(RegWrite3), .clk(and_4_out), .clr(RST));  // open: en
  Register #(.width(1), .trigger("rising"), .Select("low")) u_MemWrite (
    .D(multiplexer_18_out), .Q(MemWrite_q), .clk(and_4_out), .clr(RST));  // open: en
  Register #(.width(4), .trigger("rising"), .Select("low")) ALuOP (
    .D(multiplexer_19_out), .Q(ALuOP3), .clk(and_4_out), .clr(RST));  // open: en
  Register #(.width(1), .trigger("rising"), .Select("low")) ALuSrcB (
    .D(multiplexer_20_out), .Q(ALuSrcB3), .clk(and_4_out), .clr(RST));  // open: en
  Register #(.width(1), .trigger("rising"), .Select("low")) u_Syscall (
    .D(multiplexer_21_out), .Q(Syscall3), .clk(and_4_out), .clr(RST));  // open: en
  Register #(.width(1), .trigger("rising"), .Select("low")) Bne (
    .D(multiplexer_22_out), .Q(Bne3), .clk(and_4_out), .clr(RST));  // open: en
  Register #(.width(1), .trigger("rising"), .Select("low")) Beq (
    .D(multiplexer_23_out), .Q(Beq3), .clk(and_4_out), .clr(RST));  // open: en
  Register #(.width(1), .trigger("rising"), .Select("low")) Jal (
    .D(multiplexer_24_out), .Q(Jal3), .clk(and_4_out), .clr(RST));  // open: en
  Register #(.width(1), .trigger("rising"), .Select("low")) Jmp (
    .D(multiplexer_25_out), .Q(Jmp3), .clk(and_4_out), .clr(RST));  // open: en
  Register #(.width(1), .trigger("rising"), .Select("low")) JR (
    .D(multiplexer_26_out), .Q(JR3), .clk(and_4_out), .clr(RST));  // open: en
  Register #(.width(32), .trigger("rising"), .Select("low")) IR_2 (
    .D(multiplexer_27_out), .Q(EX_IR), .clk(and_4_out), .clr(RST));  // open: en
  Register #(.width(32), .trigger("rising"), .Select("low")) PC_3 (
    .D(multiplexer_28_out), .Q(PC3), .clk(and_4_out), .clr(RST));  // open: en
  Register #(.width(32), .trigger("rising"), .Select("low")) A (
    .D(multiplexer_29_out), .Q(A3), .clk(and_4_out), .clr(RST));  // open: en
  Register #(.width(32), .trigger("rising"), .Select("low")) B (
    .D(multiplexer_30_out), .Q(B3), .clk(and_4_out), .clr(RST));  // open: en
  Register #(.width(32), .trigger("rising"), .Select("low")) Imm (
    .D(multiplexer_31_out), .Q(Imm3), .clk(and_4_out), .clr(RST));  // open: en
  Register #(.width(5), .trigger("rising"), .Select("low")) Shmat (
    .D(multiplexer_32_out), .Q(Shmat3), .clk(and_4_out), .clr(RST));  // open: en
  Register #(.width(32), .trigger("rising"), .Select("low")) PCO_2 (
    .D(multiplexer_33_out), .Q(EX_PC), .clk(and_4_out), .clr(RST));  // open: en
  Register #(.width(2), .trigger("rising"), .Select("low")) RsForward (
    .D(multiplexer_34_out), .Q(RsForward3), .clk(and_4_out), .clr(RST));  // open: en
  Register #(.width(2), .trigger("rising"), .Select("low")) RtForward (
    .D(multiplexer_35_out), .Q(RtForward3), .clk(and_4_out), .clr(RST));  // open: en
  \重定向数据相关检测  \u_重定向数据相关检测_1  (
    .EX_WriteReg_num(EX_WriteReg_num), .R1_Used(\源寄存器使用情况_1_r1_used ), .R1_num(multiplexer_9_out),
    .R2_Used(\源寄存器使用情况_1_r2_used ), .R2_num(multiplexer_11_out), .MEM_WriteReg_num(MEM_WriteReg_num),
    .RegWrite3(RegWrite3), .Yes(\数据相关 ), .LoadUse(Loaduse), .EX_MemRead(MemToReg3), .RsForward(RsForward2),
    .RtForward(RtForward2), .RegWrite4(RegWrite4));
  Multiplexer #(.select(2), .width(32), .disabled("Z"), .enable("false")) multiplexer_36 (
    .in0(B3), .in1(RDin), .in2(ALU4), .out(RealB3), .sel(RtForward3));  // open: in3
  Multiplexer #(.select(1), .width(32), .disabled("Z"), .enable("false")) multiplexer_37 (
    .in0({EX_PC[31:28], EX_IR[25:0], 2'b00}), .in1(A3), .out(\J系列地址3 ), .sel(JR3));
  // Mips_Probe mips_probe_8: pin names not known; wires that end beside it: EX_IR
  Multiplexer #(.select(2), .width(32), .disabled("Z"), .enable("false")) multiplexer_38 (
    .in0(RealB3), .in1(Imm3), .in2(32'h22), .out(multiplexer_38_out), .sel({Syscall3, ALuSrcB3}));  // open: in3
  Shifter #(.width(32), .shift("ll")) shifter_1 (.in(Imm3), .\dist (5'b00010), .out(shifter_1_out));
  Adder #(.width(32)) adder_2 (.a(shifter_1_out), .b(PC3), .out(\B系列地址3 ), .cin(1'b0));  // open: cout
  Register #(.width(5), .trigger("rising"), .Select("low")) \u_假WriteReg_num_2  (
    .D(EX_WriteReg_num), .Q(MEM_WriteReg_num), .clk(and_4_out), .clr(RST));  // open: en
  Register #(.width(1), .trigger("rising"), .Select("low")) MemToReg_2 (
    .D(MemToReg3), .Q(MemToReg_2_q), .clk(and_4_out), .clr(RST));  // open: en
  Register #(.width(1), .trigger("rising"), .Select("low")) RegDst_2 (
    .D(RegDst_q), .Q(RegDst_2_q), .clk(and_4_out), .clr(RST));  // open: en
  Register #(.width(1), .trigger("rising"), .Select("low")) RegWrite_2 (
    .D(RegWrite3), .Q(RegWrite4), .clk(and_4_out), .clr(RST));  // open: en
  Register #(.width(1), .trigger("rising"), .Select("low")) MemWrite_2 (
    .D(MemWrite_q), .Q(MemWrite), .clk(and_4_out), .clr(RST));  // open: en
  Register #(.width(1), .trigger("rising"), .Select("low")) Syscall_2 (
    .D(Syscall3), .Q(Syscall4), .clk(and_4_out), .clr(RST));  // open: en
  Register #(.width(1), .trigger("rising"), .Select("low")) equal (
    .D(equal3), .Q(equal4), .clk(and_4_out), .clr(RST));  // open: en
  Register #(.width(1), .trigger("rising"), .Select("low")) Jal_2 (
    .D(Jal3), .Q(Jal_2_q), .clk(and_4_out), .clr(RST));  // open: en
  Register #(.width(32), .trigger("rising"), .Select("low")) IR_3 (
    .D(EX_IR), .Q(IR4), .clk(and_4_out), .clr(RST));  // open: en
  Register #(.width(32), .trigger("rising"), .Select("low")) PC_4 (
    .D(PC3), .Q(PC_4_q), .clk(and_4_out), .clr(RST));  // open: en
  Register #(.width(32), .trigger("rising"), .Select("low")) B_2 (
    .D(B3), .Q(B4), .clk(and_4_out), .clr(RST));  // open: en
  Register #(.width(32), .trigger("rising"), .Select("low")) ALU (
    .D(ALU3), .Q(ALU4), .clk(and_4_out), .clr(RST));  // open: en
  Register #(.width(32), .trigger("rising"), .Select("low")) RealB (
    .D(RealB3), .Q(MDin), .clk(and_4_out), .clr(RST));  // open: en
  Register #(.width(32), .trigger("rising"), .Select("low")) PCO_3 (
    .D(EX_PC), .Q(M_PC), .clk(and_4_out), .clr(RST));  // open: en
  or or_15 (\B系列3 , and_6_out, and_7_out, and_5_out);
  Multiplexer #(.select(2), .width(32), .disabled("Z"), .enable("false")) multiplexer_39 (
    .in0(A3), .in1(RDin), .in2(ALU4), .out(multiplexer_39_out), .sel(RsForward3));  // open: in3
  Comparator #(.width(32), .mode("twosComplement")) comparator_13 (
    .a(32'h1), .b(ALU3), .eq(comparator_13_eq));  // open: gt, lt
  Comparator #(.width(6), .mode("twosComplement")) comparator_14 (
    .a(EX_IR[31:26]), .b(6'b000001), .eq(comparator_14_eq));  // open: gt, lt
  and and_5 (and_5_out, Beq3, equal3);
  MIPS_ALU mips_alu_1 (
    .X(multiplexer_39_out), .Y(multiplexer_38_out), .AluOP(ALuOP3), .Equal(equal3), .Result(ALU3),
    .shamt(Shmat3));  // open: Result_2
  and and_6 (and_6_out, comparator_14_eq, comparator_13_eq);
  and and_7 (and_7_out, not_5_out, Bne3);
  not not_5 (not_5_out, equal3);
  Register #(.width(32), .trigger("rising"), .Select("low")) register_1 (
    .D(RealB3), .en(and_8_out), .Q(LedData), .clk(CLK), .clr(RST));
  and and_8 (and_8_out, Syscall3, equal3);
  Register #(.width(1), .trigger("rising"), .Select("low")) MemToReg_3 (
    .D(MemToReg_2_q), .Q(MemToReg5), .clk(and_4_out), .clr(RST));  // open: en
  Register #(.width(1), .trigger("rising"), .Select("low")) RegDst_3 (
    .D(RegDst_2_q), .Q(RegDst5), .clk(and_4_out), .clr(RST));  // open: en
  Register #(.width(1), .trigger("rising"), .Select("low")) RegWrite_3 (
    .D(RegWrite4), .Q(RegWrite), .clk(and_4_out), .clr(RST));  // open: en
  Register #(.width(1), .trigger("rising"), .Select("low")) Syscall_3 (
    .D(Syscall4), .Q(Syscall5), .clk(and_4_out), .clr(RST));  // open: en
  Register #(.width(1), .trigger("rising"), .Select("low")) equal_2 (
    .D(equal4), .Q(equal5), .clk(and_4_out), .clr(RST));  // open: en
  Register #(.width(1), .trigger("rising"), .Select("low")) Jal_3 (
    .D(Jal_2_q), .Q(Jal5), .clk(and_4_out), .clr(RST));  // open: en
  Register #(.width(32), .trigger("rising"), .Select("low")) IR_4 (
    .D(IR4), .Q(IR5), .clk(and_4_out), .clr(RST));  // open: en
  Register #(.width(32), .trigger("rising"), .Select("low")) PC_5 (
    .D(PC_4_q), .Q(PC5), .clk(and_4_out), .clr(RST));  // open: en
  Register #(.width(32), .trigger("rising"), .Select("low")) ALU_2 (
    .D(ALU4), .Q(ALU5), .clk(and_4_out), .clr(RST));  // open: en
  Register #(.width(32), .trigger("rising"), .Select("low")) MD (
    .D(MD4), .Q(MD5), .clk(and_4_out), .clr(RST));  // open: en
  Register #(.width(32), .trigger("rising"), .Select("low")) PCO_4 (
    .D(M_PC), .Q(WB_PC), .clk(and_4_out), .clr(RST));  // open: en
  // Mips_Probe mips_probe_9: pin names not known; wires that end beside it: IR4
  RAM #(.addrWidth(10), .dataWidth(32), .bus("separate"), .Select("high")) ram_1 (
    .addr(ALU4[11:2]), .din(MDin), .data(ram_1_data), .str(MemWrite), .clk(CLK), .clr(RST));  // open: sel, ld
  Comparator #(.width(6), .mode("twosComplement")) comparator_15 (
    .a(IR4[31:26]), .b(6'b100100), .eq(comparator_15_eq));  // open: gt, lt
  Multiplexer #(.select(2), .width(8), .disabled("Z"), .enable("false")) multiplexer_40 (
    .in0(ram_1_data[7:0]), .in1(ram_1_data[15:8]), .in2(ram_1_data[23:16]), .in3(ram_1_data[31:24]),
    .out(multiplexer_40_out), .sel(ALU4[1:0]));
  assign bit_extender_4_out = {{24{1'b0}}, multiplexer_40_out};  // Bit_Extender bit_extender_4
  Multiplexer #(.select(1), .width(32), .disabled("Z"), .enable("false")) multiplexer_41 (
    .in0(ram_1_data), .in1(bit_extender_4_out), .out(MD4), .sel(comparator_15_eq));
  // Mips_Probe mips_probe_10: pin names not known; wires that end beside it: IR5
  Multiplexer #(.select(2), .width(32), .disabled("Z"), .enable("false")) multiplexer_42 (
    .in0(ALU5), .in1(MD5), .in2(PC5), .out(RDin), .sel({Jal5, MemToReg5}));  // open: in3

  // Other names for the same wires on the sheet: IRNO3[31:0] = EX_IR; byteoff[1:0] = ALU4[1:0]; IRNO1[31:0] = IF_IR;
  //   ID_IR[5:0] = Func; IR[31:0] = {ID_IR, Func}; IRNO2[31:0] = {ID_IR, Func}; Shmat2[4:0] = ID_IR[10:6];
  //   OP[5:0] = ID_IR[31:26]; MEM_IR[31:0] = IR4; MEM_PC[31:0] = M_PC; MemWrite4 = MemWrite; PC[31:0] = IF_PC;
  //   PCO1[31:0] = IF_PC; PCO3[31:0] = EX_PC; RDin1[31:0] = RDin; RealB4[31:0] = MDin; RegWrite5 = RegWrite;
  //   result[31:0] = ALU3; Syscall2 = Syscall; WB_IR[31:0] = IR5; 总复位 = RST

  // Notes on the sheet:
  //   中断源
  //   时空图监测，可删除
  //   中断等待指示
  //   多级中断测试信号模拟器
  //   简化mtc0指令支持
  //   Eret指令支持
  //   简化mfc0指令支持
  //   Syscall停机功能模块
  //   数码管输出
  //   EPC硬件堆栈
  //   关中断与开中断寄存器
  //   中断支持硬件
  //   控制位
  //   流水调试日志用
  //   暂停节拍，不能为0
  //   戳工具置1进入计数暂停模式，ctrl+k时钟自动运行到对应节拍暂停
  //   ctrl+k关闭时钟连续运行，将控制位置零，进入单步调试模式调试
  //   指令存储器
  //   contents of rom_1 (hex, n*v repeats v):
  //   201d07d0 20100001 109fc0 139fc3 8021 2012000c 24160008 26100001 3210000f 20080008 20090001 139900
  //   2709825 132020 20020022 c 1094022 1500fff9 22100001 2018000f 2188024 108700 20080008 20090001 139902
  //   2709825 132021 20020022 c 1094022 1500fff9 108702 2c9b022 12c00001 8000c07 4020 1084027 84400
  //   3508ffff 82021 20020022 c 8000c01 afa20000 23bd0004 afa40000 23bd0004 afb00000 23bd0004 afb30000
  //   23bd0004 afb40000 23bd0004 afb50000 23bd0004 afb60000 23bd0004 40000000 20160001 20140003 20150001
  //   168020 108100 2149825 132020 20020022 c 1600fffa 295a022 1680fff7 40800000 23bdfffc 8fb60000
  //   23bdfffc 8fb50000 23bdfffc 8fb40000 23bdfffc 8fb30000 23bdfffc 8fb00000 23bdfffc 8fa40000 23bdfffc
  //   8fa20000 42000018 afa20000 23bd0004 afa40000 23bd0004 afb00000 23bd0004 afb30000 23bd0004 afb40000
  //   23bd0004 afb50000 23bd0004 afb60000 23bd0004 40000000 20160002 20140003 20150001 168020 108100
  //   2149825 132020 20020022 c 1600fffa 295a022 1680fff7 40800000 23bdfffc 8fb60000 23bdfffc 8fb50000
  //   23bdfffc 8fb40000 23bdfffc 8fb30000 23bdfffc 8fb00000 23bdfffc 8fa40000 23bdfffc 8fa20000 42000018
  //   afa20000 23bd0004 afa40000 23bd0004 afb00000 23bd0004 afb30000 23bd0004 afb40000 23bd0004 afb50000
  //   23bd0004 afb60000 23bd0004 40000000 20160003 20140003 20150001 168020 108100 2149825 132020 20020022
  //   c 1600fffa 295a022 1680fff7 40800000 23bdfffc 8fb60000 23bdfffc 8fb50000 23bdfffc 8fb40000 23bdfffc
  //   8fb30000 23bdfffc 8fb00000 23bdfffc 8fa40000 23bdfffc 8fa20000 42000018
  //   可计数暂停的时钟源
  //   IF/ID
  //   指令字
  //   JMP
  //   JR
  //   OP
  //   Func
  //   Syscall
  //   rs
  //   rt
  //   rd
  //   为方便自动评测，需要输出流水线各段保存的PC值，注意是PC不是PC+4，另外ID段寄存器写入信息，Mem段内存写入信息也要输出
  //   Beq
  //   Bne
  //   rd
  //   ID/EX
  //   EX/MEM
  //   MEM/WB
endmodule

module \加入动态分支预测的重定向  (
  output RegWrite,
  output MemWrite,
  output [31:0] IF_PC,
  output [31:0] ID_PC,
  output [31:0] EX_PC,
  output [31:0] M_PC,
  output [31:0] WB_PC,
  output [31:0] RDin,
  output [31:0] MDin,
  output [31:0] LedData
);

  wire ALuSrcB2, ALuSrcB3, and_1_out, and_2_out, and_4_out, and_5_out, and_6_out, and_7_out, Beq2, Beq3,
       Bne2, Bne3, \B系列3 , \B系列3指令 , CLK, clock_1_out, clock_2_out, comparator_1_eq, comparator_2_eq,
       comparator_3_eq, comparator_3_lt, comparator_4_eq, comparator_5_eq, comparator_6_eq, d_ff_2_q, equal3,
       equal4, equal5, EX_Branch, EX_PredictErr, Go, IR1, IR2, IR3, Jal2, Jal3, Jal5, Jal_2_q, Jmp2, Jmp3,
       JR2, JR3, Loaduse, MemToReg2, MemToReg3, MemToReg5, MemToReg_2_q, MemWrite2, MemWrite_q,
       multiplexer_6_out, multiplexer_16_out, multiplexer_17_out, multiplexer_18_out, multiplexer_19_out,
       multiplexer_21_out, multiplexer_22_out, multiplexer_23_out, multiplexer_24_out, multiplexer_25_out,
       multiplexer_26_out, multiplexer_27_out, multiplexer_28_out, nand_1_out, not_1_out, not_2_out,
       not_4_out, not_5_out, not_6_out, or_1_out, or_2_out, or_3_out, \PC使能 , predictjmp, predictjmp3,
       predictjmp_q, RegDst2, RegDst5, RegDst_2_q, RegDst_q, RegWrite2, RegWrite3, RegWrite4, RST, SignedExt,
       Syscall, Syscall3, Syscall4, Syscall5, W1, W2, W3, \分支气泡 , \数据相关 , \源寄存器使用情况_1_r1_used ,
       \源寄存器使用情况_1_r2_used ;
  wire [1:0] byteoff5, multiplexer_36_out, multiplexer_37_out, RsForward2, RsForward3, RtForward2, RtForward3;
  wire [3:0] ALuOP2, ALuOP3, multiplexer_20_out;
  wire [4:0] EX_WriteReg_num, MEM_WriteReg_num, multiplexer_10_out, multiplexer_11_out, multiplexer_12_out,
       multiplexer_14_out, multiplexer_15_out, multiplexer_34_out, Shmat3;
  wire [5:0] Func;
  wire [7:0] multiplexer_42_out;
  wire [12:0] CNT_num;
  wire [15:0] \LoadUse次数 , \插入气泡数 , \无条件分支数 , \条件分支成功数 ;
  wire [31:0] A2, A3, ALU3, ALU4, ALU5, B2, B3, B4, bit_extender_1_out, bit_extender_2_out,
       bit_extender_3_out, \B系列地址3 , EX_BranchPC, EX_IR, IF_IR, Imm2, Imm3, IR4, IR5, \J系列地址3 , MD4, MD5,
       multiplexer_3_out, multiplexer_4_out, multiplexer_5_out, multiplexer_7_out, multiplexer_8_out,
       multiplexer_9_out, multiplexer_29_out, multiplexer_30_out, multiplexer_31_out, multiplexer_32_out,
       multiplexer_33_out, multiplexer_35_out, multiplexer_40_out, multiplexer_41_out, NextPCNormal, PC1,
       PC2, PC3, PC5, PC_4_q, ram_1_data, RealB3, shifter_1_out, \新动态分支预测_1_jumpaddr ;
  wire [31:6] ID_IR;

  Button \u_总复位  (.out(RST));
  Button _1 (.out(IR1));
  Button _2 (.out(IR2));
  Button _3 (.out(IR3));
  // Probe on CNT_num
  // Probe on CNT_num
  Button \u_继续运行  (.out(Go));
  LED #(.active("true")) led_1 (.in(W1));
  LED #(.active("true")) led_2 (.in(W2));
  LED #(.active("true")) led_3 (.in(W3));
  Hex_Digit_Display hex_digit_display_1 (.value(LedData[31:28]));  // open: dp
  // Probe on IF_PC[19:0]
  // Mips_Probe mips_probe_1: pin names not known; wires that end beside it: IF_IR
  not not_1 (not_1_out, Syscall5);
  Hex_Digit_Display hex_digit_display_2 (.value(LedData[23:20]));  // open: dp
  Hex_Digit_Display hex_digit_display_3 (.value(LedData[27:24]));  // open: dp
  // Probe on ID_PC[19:0]
  // Mips_Probe mips_probe_2: pin names not known; wires that end beside it: {ID_IR, Func}
  or or_1 (or_1_out, not_1_out, Go);
  or or_2 (or_2_out, equal5, not_1_out);
  Hex_Digit_Display hex_digit_display_4 (.value(LedData[15:12]));  // open: dp
  Hex_Digit_Display hex_digit_display_5 (.value(LedData[19:16]));  // open: dp
  D_Flip_Flop #(.trigger("falling"), .Pre_Clr_Positions("ABOVE_BELOW"), .NegatePresetClear("false"), .enable("false"), .NewFFLayout("true")) d_ff_1 (
    .clk(CLK), .D(or_2_out), .Q(\PC使能 ), .preset(or_1_out));  // open: Qn, reset
  Multiplexer #(.select(1), .width(32), .disabled("Z"), .enable("false")) multiplexer_1 (
    .in0(\J系列地址3 ), .in1(\B系列地址3 ), .out(EX_BranchPC), .sel(\B系列3指令 ));
  Hex_Digit_Display hex_digit_display_6 (.value(LedData[7:4]));  // open: dp
  Hex_Digit_Display hex_digit_display_7 (.value(LedData[11:8]));  // open: dp
  Clock #(.highDuration(1), .lowDuration(1)) clock_1 (.out(clock_1_out));
  // Probe on EX_PC[19:0]
  // Mips_Probe mips_probe_3: pin names not known; wires that end beside it: clock_1_out, EX_IR, CLK
  Hex_Digit_Display hex_digit_display_8 (.value(LedData[3:0]));  // open: dp
  Multiplexer #(.select(2), .width(32), .disabled("Z"), .enable("false")) multiplexer_2 (
    .in0(PC3), .in1(EX_BranchPC), .in2(EX_BranchPC), .out(NextPCNormal), .sel({\B系列3 , Jmp3}));  // open: in3
  // Probe on CNT_num
  // Probe on M_PC[19:0]
  // Mips_Probe mips_probe_4: pin names not known; wires that end beside it: IR4
  Multiplexer #(.select(1), .width(32), .disabled("Z"), .enable("false")) multiplexer_3 (
    .in0(multiplexer_5_out), .in1(NextPCNormal), .out(multiplexer_3_out), .sel(EX_PredictErr));
  // Probe on CNT_num
  // Probe on \无条件分支数 
  // Probe on \条件分支成功数 
  // Probe on \插入气泡数 
  // Probe on \LoadUse次数 
  Comparator #(.width(2), .mode("twosComplement")) comparator_1 (
    .a({\B系列3 , Jmp3}), .b(2'b00), .eq(comparator_1_eq));  // open: gt, lt
  Multiplexer #(.select(1), .width(32), .disabled("Z"), .enable("false")) multiplexer_4 (
    .in0(multiplexer_3_out), .in1({32{1'b0}}), .out(multiplexer_4_out), .sel(1'b0));
  and and_1 (and_1_out, \PC使能 , not_2_out);
  not not_2 (not_2_out, Loaduse);
  and and_2 (and_2_out, \PC使能 , CLK);
  // Probe on IF_PC[11:0]
  // Probe on WB_PC[19:0]
  // Mips_Probe mips_probe_5: pin names not known; wires that end beside it: IR5
  not not_3 (\分支气泡 , comparator_1_eq);
  Register #(.width(32), .trigger("rising"), .Select("low")) PC (
    .D(multiplexer_4_out), .en(and_1_out), .Q(IF_PC), .clk(CLK), .clr(RST));
  Adder #(.width(32)) adder_1 (.a(IF_PC), .b(32'h4), .out(PC1));  // open: cin, cout
  \新动态分支预测  \u_新动态分支预测_1  (
    .CLK(CLK), .clear(RST), .PC(IF_PC), .EX_Branch(EX_Branch), .EX_BranchTaken(\分支气泡 ), .EX_PC(EX_PC),
    .EX_BranchAddr(EX_BranchPC), .PredictJump(predictjmp), .JumpAddr(\新动态分支预测_1_jumpaddr ));
  not not_4 (not_4_out, Loaduse);
  // Probe on ID_PC[11:0]
  // Probe on EX_PC[11:0]
  Multiplexer #(.select(1), .width(32), .disabled("Z"), .enable("false")) multiplexer_5 (
    .in0(PC1), .in1(\新动态分支预测_1_jumpaddr ), .out(multiplexer_5_out), .sel(predictjmp));
  // Probe on M_PC[11:0]
  D_Flip_Flop #(.trigger("high"), .Pre_Clr_Positions("LEGACY"), .NegatePresetClear("false"), .enable("true"), .NewFFLayout("false")) d_ff_2 (.Q(d_ff_2_q));  // open: clk, D, Qn, preset, en, reset
  // Probe on 13'h3e8
  not not_5 (not_5_out, comparator_2_eq);
  Comparator #(.width(1), .mode("twosComplement")) comparator_2 (
    .a(\分支气泡 ), .b(predictjmp3), .eq(comparator_2_eq));  // open: gt, lt
  // Probe on WB_PC[11:0]
  Comparator #(.width(13), .mode("twosComplement")) comparator_3 (
    .a(CNT_num), .b(13'h3e8), .eq(comparator_3_eq), .lt(comparator_3_lt));  // open: gt
  Clock #(.highDuration(1), .lowDuration(1)) clock_2 (.out(clock_2_out));
  ROM #(.addrWidth(10), .dataWidth(32), .Select("high")) rom_1 (.addr(IF_PC[11:2]), .data(IF_IR));
  and and_3 (EX_PredictErr, EX_Branch, not_5_out);
  nand nand_1 (nand_1_out, d_ff_2_q, comparator_3_eq);
  Counter #(.width(13), .max('h1fff), .ongoal("stay"), .trigger("rising"), .behavior("old")) counter_1 (
    .count(\PC使能 ), .Q(CNT_num), .clk(clock_2_out));  // open: load, D, carry, clr, preset
  // Mips_Probe mips_probe_6: pin names not known; wires that end beside it: IF_IR
  assign CLK = nand_1_out ? clock_2_out : 1'bz;  // Controlled_Buffer controlled_buffer_1
  Multiplexer #(.select(1), .width(1), .disabled("Z"), .enable("false")) multiplexer_6 (
    .in0(predictjmp), .in1(1'b0), .out(multiplexer_6_out), .sel(EX_PredictErr));
  Multiplexer #(.select(1), .width(32), .disabled("Z"), .enable("false")) multiplexer_7 (
    .in0(IF_IR), .in1({32{1'b0}}), .out(multiplexer_7_out), .sel(EX_PredictErr));
  Multiplexer #(.select(1), .width(32), .disabled("Z"), .enable("false")) multiplexer_8 (
    .in0(PC1), .in1({32{1'b0}}), .out(multiplexer_8_out), .sel(EX_PredictErr));
  Multiplexer #(.select(1), .width(32), .disabled("Z"), .enable("false")) multiplexer_9 (
    .in0(IF_PC), .in1({32{1'b0}}), .out(multiplexer_9_out), .sel(EX_PredictErr));
  Pull_Resistor #(.pull(1)) pull_resistor_1 (.node(CLK));
  Register #(.width(1), .trigger("rising"), .Select("low")) u_predictjmp (
    .D(multiplexer_6_out), .en(not_4_out), .Q(predictjmp_q), .clk(and_2_out), .clr(RST));
  Register #(.width(32), .trigger("rising"), .Select("low")) IR (
    .D(multiplexer_7_out), .en(not_4_out), .Q({ID_IR, Func}), .clk(and_2_out), .clr(RST));
  Register #(.width(32), .trigger("rising"), .Select("low")) PC_2 (
    .D(multiplexer_8_out), .en(not_4_out), .Q(PC2), .clk(and_2_out), .clr(RST));
  Register #(.width(32), .trigger("rising"), .Select("low")) PCO (
    .D(multiplexer_9_out), .en(not_4_out), .Q(ID_PC), .clk(and_2_out), .clr(RST));
  // Mips_Probe mips_probe_7: pin names not known; wires that end beside it: {ID_IR, Func}
  \单周期硬布线控制器  \u_单周期硬布线控制器_1  (
    .Func(Func), .OP(ID_IR[31:26]), .ALU_OP(ALuOP2), .MemToReg(MemToReg2), .MemWrite(MemWrite2),
    .ALU_SRC(ALuSrcB2), .RegWrite(RegWrite2), .SysCALL(Syscall), .SignedExt(SignedExt), .RegDst(RegDst2),
    .JR(JR2), .JMP(Jmp2), .Beq(Beq2), .JAL(Jal2), .Bne(Bne2));
  Multiplexer #(.select(1), .width(5), .disabled("Z"), .enable("false")) multiplexer_10 (
    .in0(ID_IR[25:21]), .in1(5'b00010), .out(multiplexer_10_out), .sel(Syscall));
  Multiplexer #(.select(2), .width(5), .disabled("Z"), .enable("false")) multiplexer_11 (
    .in0(IR5[20:16]), .in1(IR5[15:11]), .in2({5{1'b1}}), .out(multiplexer_11_out), .sel({Jal5, RegDst5}));  // open: in3
  Multiplexer #(.select(1), .width(5), .disabled("Z"), .enable("false")) multiplexer_12 (
    .in0(ID_IR[20:16]), .in1(5'b00100), .out(multiplexer_12_out), .sel(Syscall));
  or or_3 (or_3_out, EX_PredictErr, Loaduse);
  assign bit_extender_1_out = {{16{1'b0}}, {ID_IR[15:6], Func}};  // Bit_Extender bit_extender_1
  Multiplexer #(.select(1), .width(32), .disabled("Z"), .enable("false")) multiplexer_13 (
    .in0(bit_extender_1_out), .in1(bit_extender_2_out), .out(Imm2), .sel(SignedExt));
  assign bit_extender_2_out = {{16{ID_IR[15]}}, {ID_IR[15:6], Func}};  // Bit_Extender bit_extender_2
  Multiplexer #(.select(2), .width(5), .disabled("Z"), .enable("false")) multiplexer_14 (
    .in0(ID_IR[20:16]), .in1(ID_IR[15:11]), .in2({5{1'b1}}), .out(multiplexer_14_out), .sel({Jal2, RegDst2}));  // open: in3
  \源寄存器使用情况  \u_源寄存器使用情况_1  (
    .OP0(ID_IR[26]), .OP1(ID_IR[27]), .OP2(ID_IR[28]), .OP3(ID_IR[29]), .OP4(ID_IR[30]), .OP5(ID_IR[31]),
    .F0(Func[0]), .F1(Func[1]), .F2(Func[2]), .F3(Func[3]), .F4(Func[4]), .F5(Func[5]),
    .R1_used(\源寄存器使用情况_1_r1_used ), .R2_used(\源寄存器使用情况_1_r2_used ));
  MIPS_Regifile mips_regifile_1 (
    .Din(RDin), .Clk(CLK), .R1(A2), .R2(B2), .WE(RegWrite), .W_num(multiplexer_11_out),
    .R1_num(multiplexer_10_out), .R2_num(multiplexer_12_out));
  Multiplexer #(.select(1), .width(5), .disabled("Z"), .enable("false")) multiplexer_15 (
    .in0(multiplexer_14_out), .in1({5{1'b0}}), .out(multiplexer_15_out), .sel(or_3_out));
  Multiplexer #(.select(1), .width(1), .disabled("Z"), .enable("false")) multiplexer_16 (
    .in0(MemToReg2), .in1(1'b0), .out(multiplexer_16_out), .sel(or_3_out));
  Multiplexer #(.select(1), .width(1), .disabled("Z"), .enable("false")) multiplexer_17 (
    .in0(RegDst2), .in1(1'b0), .out(multiplexer_17_out), .sel(or_3_out));
  Multiplexer #(.select(1), .width(1), .disabled("Z"), .enable("false")) multiplexer_18 (
    .in0(RegWrite2), .in1(1'b0), .out(multiplexer_18_out), .sel(or_3_out));
  Multiplexer #(.select(1), .width(1), .disabled("Z"), .enable("false")) multiplexer_19 (
    .in0(MemWrite2), .in1(1'b0), .out(multiplexer_19_out), .sel(or_3_out));
  Multiplexer #(.select(1), .width(4), .disabled("Z"), .enable("false")) multiplexer_20 (
    .in0(ALuOP2), .in1(4'b0000), .out(multiplexer_20_out), .sel(or_3_out));
  Multiplexer #(.select(1), .width(1), .disabled("Z"), .enable("false")) multiplexer_21 (
    .in0(ALuSrcB2), .in1(1'b0), .out(multiplexer_21_out), .sel(or_3_out));
  Multiplexer #(.select(1), .width(1), .disabled("Z"), .enable("false")) multiplexer_22 (
    .in0(Syscall), .in1(1'b0), .out(multiplexer_22_out), .sel(or_3_out));
  Multiplexer #(.select(1), .width(1), .disabled("Z"), .enable("false")) multiplexer_23 (
    .in0(Bne2), .in1(1'b0), .out(multiplexer_23_out), .sel(or_3_out));
  Multiplexer #(.select(1), .width(1), .disabled("Z"), .enable("false")) multiplexer_24 (
    .in0(Beq2), .in1(1'b0), .out(multiplexer_24_out), .sel(or_3_out));
  Multiplexer #(.select(1), .width(1), .disabled("Z"), .enable("false")) multiplexer_25 (
    .in0(Jal2), .in1(1'b0), .out(multiplexer_25_out), .sel(or_3_out));
  Multiplexer #(.select(1), .width(1), .disabled("Z"), .enable("false")) multiplexer_26 (
    .in0(Jmp2), .in1(1'b0), .out(multiplexer_26_out), .sel(or_3_out));
  Multiplexer #(.select(1), .width(1), .disabled("Z"), .enable("false")) multiplexer_27 (
    .in0(JR2), .in1(1'b0), .out(multiplexer_27_out), .sel(or_3_out));
  Multiplexer #(.select(1), .width(1), .disabled("Z"), .enable("false")) multiplexer_28 (
    .in0(predictjmp_q), .in1(1'b0), .out(multiplexer_28_out), .sel(or_3_out));
  Multiplexer #(.select(1), .width(32), .disabled("Z"), .enable("false")) multiplexer_29 (
    .in0({ID_IR, Func}), .in1({32{1'b0}}), .out(multiplexer_29_out), .sel(or_3_out));
  Multiplexer #(.select(1), .width(32), .disabled("Z"), .enable("false")) multiplexer_30 (
    .in0(PC2), .in1({32{1'b0}}), .out(multiplexer_30_out), .sel(or_3_out));
  Multiplexer #(.select(1), .width(32), .disabled("Z"), .enable("false")) multiplexer_31 (
    .in0(A2), .in1({32{1'b0}}), .out(multiplexer_31_out), .sel(or_3_out));
  Multiplexer #(.select(1), .width(32), .disabled("Z"), .enable("false")) multiplexer_32 (
    .in0(B2), .in1({32{1'b0}}), .out(multiplexer_32_out), .sel(or_3_out));
  Multiplexer #(.select(1), .width(32), .disabled("Z"), .enable("false")) multiplexer_33 (
    .in0(Imm2), .in1({32{1'b0}}), .out(multiplexer_33_out), .sel(or_3_out));
  Multiplexer #(.select(1), .width(5), .disabled("Z"), .enable("false")) multiplexer_34 (
    .in0(ID_IR[10:6]), .in1({5{1'b0}}), .out(multiplexer_34_out), .sel(or_3_out));
  Multiplexer #(.select(1), .width(32), .disabled("Z"), .enable("false")) multiplexer_35 (
    .in0(ID_PC), .in1({32{1'b0}}), .out(multiplexer_35_out), .sel(or_3_out));
  Multiplexer #(.select(1), .width(2), .disabled("Z"), .enable("false")) multiplexer_36 (
    .in0(RsForward2), .in1(2'b00), .out(multiplexer_36_out), .sel(or_3_out));
  Multiplexer #(.select(1), .width(2), .disabled("Z"), .enable("false")) multiplexer_37 (
    .in0(RtForward2), .in1(2'b00), .out(multiplexer_37_out), .sel(or_3_out));
  Register #(.width(5), .trigger("rising"), .Select("low")) \u_假WriteReg_num  (
    .D(multiplexer_15_out), .Q(EX_WriteReg_num), .clk(and_2_out), .clr(RST));  // open: en
  Register #(.width(1), .trigger("rising"), .Select("low")) MemToReg (
    .D(multiplexer_16_out), .Q(MemToReg3), .clk(and_2_out), .clr(RST));  // open: en
  Register #(.width(1), .trigger("rising"), .Select("low")) RegDst (
    .D(multiplexer_17_out), .Q(RegDst_q), .clk(and_2_out), .clr(RST));  // open: en
  Register #(.width(1), .trigger("rising"), .Select("low")) u_RegWrite (
    .D(multiplexer_18_out), .Q(RegWrite3), .clk(and_2_out), .clr(RST));  // open: en
  Register #(.width(1), .trigger("rising"), .Select("low")) u_MemWrite (
    .D(multiplexer_19_out), .Q(MemWrite_q), .clk(and_2_out), .clr(RST));  // open: en
  Register #(.width(4), .trigger("rising"), .Select("low")) ALuOP (
    .D(multiplexer_20_out), .Q(ALuOP3), .clk(and_2_out), .clr(RST));  // open: en
  Register #(.width(1), .trigger("rising"), .Select("low")) ALuSrcB (
    .D(multiplexer_21_out), .Q(ALuSrcB3), .clk(and_2_out), .clr(RST));  // open: en
  Register #(.width(1), .trigger("rising"), .Select("low")) u_Syscall (
    .D(multiplexer_22_out), .Q(Syscall3), .clk(and_2_out), .clr(RST));  // open: en
  Register #(.width(1), .trigger("rising"), .Select("low")) Bne (
    .D(multiplexer_23_out), .Q(Bne3), .clk(and_2_out), .clr(RST));  // open: en
  Register #(.width(1), .trigger("rising"), .Select("low")) Beq (
    .D(multiplexer_24_out), .Q(Beq3), .clk(and_2_out), .clr(RST));  // open: en
  Register #(.width(1), .trigger("rising"), .Select("low")) Jal (
    .D(multiplexer_25_out), .Q(Jal3), .clk(and_2_out), .clr(RST));  // open: en
  Register #(.width(1), .trigger("rising"), .Select("low")) Jmp (
    .D(multiplexer_26_out), .Q(Jmp3), .clk(and_2_out), .clr(RST));  // open: en
  Register #(.width(1), .trigger("rising"), .Select("low")) JR (
    .D(multiplexer_27_out), .Q(JR3), .clk(and_2_out), .clr(RST));  // open: en
  Register #(.width(1), .trigger("rising"), .Select("low")) predictjmp_2 (
    .D(multiplexer_28_out), .Q(predictjmp3), .clk(and_2_out), .clr(RST));  // open: en
  Register #(.width(32), .trigger("rising"), .Select("low")) IR_2 (
    .D(multiplexer_29_out), .Q(EX_IR), .clk(and_2_out), .clr(RST));  // open: en
  Register #(.width(32), .trigger("rising"), .Select("low")) PC_3 (
    .D(multiplexer_30_out), .Q(PC3), .clk(and_2_out), .clr(RST));  // open: en
  Register #(.width(32), .trigger("rising"), .Select("low")) A (
    .D(multiplexer_31_out), .Q(A3), .clk(and_2_out), .clr(RST));  // open: en
  Register #(.width(32), .trigger("rising"), .Select("low")) B (
    .D(multiplexer_32_out), .Q(B3), .clk(and_2_out), .clr(RST));  // open: en
  Register #(.width(32), .trigger("rising"), .Select("low")) Imm (
    .D(multiplexer_33_out), .Q(Imm3), .clk(and_2_out), .clr(RST));  // open: en
  Register #(.width(5), .trigger("rising"), .Select("low")) Shmat (
    .D(multiplexer_34_out), .Q(Shmat3), .clk(and_2_out), .clr(RST));  // open: en
  Register #(.width(32), .trigger("rising"), .Select("low")) PCO_2 (
    .D(multiplexer_35_out), .Q(EX_PC), .clk(and_2_out), .clr(RST));  // open: en
  Register #(.width(2), .trigger("rising"), .Select("low")) RsForward (
    .D(multiplexer_36_out), .Q(RsForward3), .clk(and_2_out), .clr(RST));  // open: en
  Register #(.width(2), .trigger("rising"), .Select("low")) RtForward (
    .D(multiplexer_37_out), .Q(RtForward3), .clk(and_2_out), .clr(RST));  // open: en
  \重定向数据相关检测  \u_重定向数据相关检测_1  (
    .EX_WriteReg_num(EX_WriteReg_num), .R1_Used(\源寄存器使用情况_1_r1_used ), .R1_num(multiplexer_10_out),
    .R2_Used(\源寄存器使用情况_1_r2_used ), .R2_num(multiplexer_12_out), .MEM_WriteReg_num(MEM_WriteReg_num),
    .RegWrite3(RegWrite3), .Yes(\数据相关 ), .LoadUse(Loaduse), .EX_MemRead(MemToReg3), .RsForward(RsForward2),
    .RtForward(RtForward2), .RegWrite4(RegWrite4));
  Multiplexer #(.select(2), .width(32), .disabled("Z"), .enable("false")) multiplexer_38 (
    .in0(B3), .in1(RDin), .in2(ALU4), .out(RealB3), .sel(RtForward3));  // open: in3
  Multiplexer #(.select(1), .width(32), .disabled("Z"), .enable("false")) multiplexer_39 (
    .in0({EX_PC[31:28], EX_IR[25:0], 2'b00}), .in1(A3), .out(\J系列地址3 ), .sel(JR3));
  // Mips_Probe mips_probe_8: pin names not known; wires that end beside it: EX_IR
  or or_4 (\B系列3指令 , comparator_5_eq, Bne3, Beq3);
  Multiplexer #(.select(2), .width(32), .disabled("Z"), .enable("false")) multiplexer_40 (
    .in0(RealB3), .in1(Imm3), .in2(32'h22), .out(multiplexer_40_out), .sel({Syscall3, ALuSrcB3}));  // open: in3
  Shifter #(.width(32), .shift("ll")) shifter_1 (.in(Imm3), .\dist (5'b00010), .out(shifter_1_out));
  Adder #(.width(32)) adder_2 (.a(shifter_1_out), .b(PC3), .out(\B系列地址3 ), .cin(1'b0));  // open: cout
  Register #(.width(5), .trigger("rising"), .Select("low")) \u_假WriteReg_num_2  (
    .D(EX_WriteReg_num), .Q(MEM_WriteReg_num), .clk(and_2_out), .clr(RST));  // open: en
  Register #(.width(1), .trigger("rising"), .Select("low")) MemToReg_2 (
    .D(MemToReg3), .Q(MemToReg_2_q), .clk(and_2_out), .clr(RST));  // open: en
  Register #(.width(1), .trigger("rising"), .Select("low")) RegDst_2 (
    .D(RegDst_q), .Q(RegDst_2_q), .clk(and_2_out), .clr(RST));  // open: en
  Register #(.width(1), .trigger("rising"), .Select("low")) RegWrite_2 (
    .D(RegWrite3), .Q(RegWrite4), .clk(and_2_out), .clr(RST));  // open: en
  Register #(.width(1), .trigger("rising"), .Select("low")) MemWrite_2 (
    .D(MemWrite_q), .Q(MemWrite), .clk(and_2_out), .clr(RST));  // open: en
  Register #(.width(1), .trigger("rising"), .Select("low")) Syscall_2 (
    .D(Syscall3), .Q(Syscall4), .clk(and_2_out), .clr(RST));  // open: en
  Register #(.width(1), .trigger("rising"), .Select("low")) equal (
    .D(equal3), .Q(equal4), .clk(and_2_out), .clr(RST));  // open: en
  Register #(.width(1), .trigger("rising"), .Select("low")) Jal_2 (
    .D(Jal3), .Q(Jal_2_q), .clk(and_2_out), .clr(RST));  // open: en
  Register #(.width(32), .trigger("rising"), .Select("low")) IR_3 (
    .D(EX_IR), .Q(IR4), .clk(and_2_out), .clr(RST));  // open: en
  Register #(.width(32), .trigger("rising"), .Select("low")) PC_4 (
    .D(PC3), .Q(PC_4_q), .clk(and_2_out), .clr(RST));  // open: en
  Register #(.width(32), .trigger("rising"), .Select("low")) B_2 (
    .D(B3), .Q(B4), .clk(and_2_out), .clr(RST));  // open: en
  Register #(.width(32), .trigger("rising"), .Select("low")) ALU (
    .D(ALU3), .Q(ALU4), .clk(and_2_out), .clr(RST));  // open: en
  Register #(.width(32), .trigger("rising"), .Select("low")) RealB (
    .D(RealB3), .Q(MDin), .clk(and_2_out), .clr(RST));  // open: en
  Register #(.width(32), .trigger("rising"), .Select("low")) PCO_3 (
    .D(EX_PC), .Q(M_PC), .clk(and_2_out), .clr(RST));  // open: en
  or or_5 (\B系列3 , and_5_out, and_6_out, and_4_out);
  Multiplexer #(.select(2), .width(32), .disabled("Z"), .enable("false")) multiplexer_41 (
    .in0(A3), .in1(RDin), .in2(ALU4), .out(multiplexer_41_out), .sel(RsForward3));  // open: in3
  Comparator #(.width(32), .mode("twosComplement")) comparator_4 (
    .a(32'h1), .b(ALU3), .eq(comparator_4_eq));  // open: gt, lt
  Comparator #(.width(6), .mode("twosComplement")) comparator_5 (
    .a(EX_IR[31:26]), .b(6'b000001), .eq(comparator_5_eq));  // open: gt, lt
  and and_4 (and_4_out, Beq3, equal3);
  MIPS_ALU mips_alu_1 (
    .X(multiplexer_41_out), .Y(multiplexer_40_out), .AluOP(ALuOP3), .Equal(equal3), .Result(ALU3),
    .shamt(Shmat3));  // open: Result_2
  or or_6 (EX_Branch, JR3, Jal3, Jmp3, Beq3, Bne3, comparator_5_eq);
  and and_5 (and_5_out, comparator_5_eq, comparator_4_eq);
  and and_6 (and_6_out, not_6_out, Bne3);
  not not_6 (not_6_out, equal3);
  Register #(.width(32), .trigger("rising"), .Select("low")) register_1 (
    .D(RealB3), .en(and_7_out), .Q(LedData), .clk(CLK), .clr(RST));
  and and_7 (and_7_out, Syscall3, equal3);
  Register #(.width(1), .trigger("rising"), .Select("low")) MemToReg_3 (
    .D(MemToReg_2_q), .Q(MemToReg5), .clk(and_2_out), .clr(RST));  // open: en
  Register #(.width(1), .trigger("rising"), .Select("low")) RegDst_3 (
    .D(RegDst_2_q), .Q(RegDst5), .clk(and_2_out), .clr(RST));  // open: en
  Register #(.width(1), .trigger("rising"), .Select("low")) RegWrite_3 (
    .D(RegWrite4), .Q(RegWrite), .clk(and_2_out), .clr(RST));  // open: en
  Register #(.width(1), .trigger("rising"), .Select("low")) Syscall_3 (
    .D(Syscall4), .Q(Syscall5), .clk(and_2_out), .clr(RST));  // open: en
  Register #(.width(1), .trigger("rising"), .Select("low")) equal_2 (
    .D(equal4), .Q(equal5), .clk(and_2_out), .clr(RST));  // open: en
  Register #(.width(1), .trigger("rising"), .Select("low")) Jal_3 (
    .D(Jal_2_q), .Q(Jal5), .clk(and_2_out), .clr(RST));  // open: en
  Register #(.width(32), .trigger("rising"), .Select("low")) IR_4 (
    .D(IR4), .Q(IR5), .clk(and_2_out), .clr(RST));  // open: en
  Register #(.width(32), .trigger("rising"), .Select("low")) PC_5 (
    .D(PC_4_q), .Q(PC5), .clk(and_2_out), .clr(RST));  // open: en
  Register #(.width(32), .trigger("rising"), .Select("low")) ALU_2 (
    .D(ALU4), .Q(ALU5), .clk(and_2_out), .clr(RST));  // open: en
  Register #(.width(32), .trigger("rising"), .Select("low")) MD (
    .D(MD4), .Q(MD5), .clk(and_2_out), .clr(RST));  // open: en
  Register #(.width(32), .trigger("rising"), .Select("low")) PCO_4 (
    .D(M_PC), .Q(WB_PC), .clk(and_2_out), .clr(RST));  // open: en
  Register #(.width(2), .trigger("rising"), .Select("low")) byteoff (
    .D(ALU4[1:0]), .Q(byteoff5), .clk(and_2_out), .clr(RST));  // open: en
  // Mips_Probe mips_probe_9: pin names not known; wires that end beside it: IR4
  RAM #(.addrWidth(10), .dataWidth(32), .bus("separate"), .Select("high")) ram_1 (
    .addr(ALU4[11:2]), .din(MDin), .data(ram_1_data), .str(MemWrite), .clk(CLK), .clr(RST));  // open: sel, ld
  Comparator #(.width(6), .mode("twosComplement")) comparator_6 (
    .a(IR4[31:26]), .b(6'b100100), .eq(comparator_6_eq));  // open: gt, lt
  Multiplexer #(.select(2), .width(8), .disabled("Z"), .enable("false")) multiplexer_42 (
    .in0(ram_1_data[7:0]), .in1(ram_1_data[15:8]), .in2(ram_1_data[23:16]), .in3(ram_1_data[31:24]),
    .out(multiplexer_42_out), .sel(ALU4[1:0]));
  Multiplexer #(.select(1), .width(32), .disabled("Z"), .enable("false")) multiplexer_43 (
    .in0(ram_1_data), .in1(bit_extender_3_out), .out(MD4), .sel(comparator_6_eq));
  assign bit_extender_3_out = {{24{1'b0}}, multiplexer_42_out};  // Bit_Extender bit_extender_3
  // Mips_Probe mips_probe_10: pin names not known; wires that end beside it: IR5
  Multiplexer #(.select(2), .width(32), .disabled("Z"), .enable("false")) multiplexer_44 (
    .in0(ALU5), .in1(MD5), .in2(PC5), .out(RDin), .sel({Jal5, MemToReg5}));  // open: in3

  // Other names for the same wires on the sheet: byteoff[1:0] = ALU4[1:0]; IRNO1[31:0] = IF_IR; ID_IR[5:0] = Func;
  //   IR[31:0] = {ID_IR, Func}; IRNO2[31:0] = {ID_IR, Func}; Shmat2[4:0] = ID_IR[10:6]; OP[5:0] = ID_IR[31:26];
  //   IRNO3[31:0] = EX_IR; MEM_IR[31:0] = IR4; MEM_PC[31:0] = M_PC; MemWrite4 = MemWrite; PC[31:0] = IF_PC;
  //   PCO1[31:0] = IF_PC; PCO3[31:0] = EX_PC; RDin1[31:0] = RDin; RealB4[31:0] = MDin; RegWrite5 = RegWrite;
  //   result[31:0] = ALU3; Syscall2 = Syscall; WB_IR[31:0] = IR5; 总周期数[12:0] = CNT_num; 总复位 = RST

  // Notes on the sheet:
  //   中断源
  //   时空图监测，可删除
  //   中断等待指示
  //   上述逻辑用来比较的PC错误
  //   分支气泡信号没有换成Err
  //   Err错误后没有更新cache行中的跳转地址
  //   修改更新cache行时状态机初始化策略，1811到1809
  //   更新cache行目标地址时，错误的包含了顺序地址的情况
  //   Syscall停机功能模块
  //   EX.PredictErr逻辑错误，没比较跳转地址（不过后来发现是最后一个错误的锅
  //   数码管输出
  //   控制位
  //   流水调试日志用
  //   暂停节拍，不能为0
  //   戳工具置1进入计数暂停模式，ctrl+k时钟自动运行到对应节拍暂停
  //   ctrl+k关闭时钟连续运行，将控制位置零，进入单步调试模式调试
  //   指令存储器
  //   contents of rom_1 (hex, n*v repeats v):
  //   20110001 8000c05 20110001 20120002 20130003 8000c09 20110001 20120002 20130003 8000c0d 20110001
  //   20120002 20130003 8000c11 20110001 20120002 20130003 c000cf3 20100001 20110001 118fc0 112020
  //   20020022 c 118882 12200001 8000c15 112020 20020022 c 20110001 118880 112020 20020022 c 12200001
  //   8000c1f 20110001 118fc0 112020 20020022 c 1188c3 112020 20020022 c 118903 112020 20020022 c 118903
  //   112020 20020022 c 118903 112020 20020022 c 118903 112020 20020022 c 118903 112020 20020022 c 118903
  //   112020 20020022 c 118903 112020 20020022 c 20100001 109fc0 139fc3 8021 2012000c 24160003 26100001
  //   3210000f 20080008 20090001 139900 2709825 132020 20020022 c 1094022 1500fff9 22100001 2018000f
  //   2188024 108700 20080008 20090001 139902 2709825 132021 20020022 c 1094022 1500fff9 108702 2c9b022
  //   12c00001 8000c50 4020 1084027 84400 3508ffff 82021 20020022 c 2010ffff 20110000 ae300000 22100001
  //   22310004 ae300000 22100001 22310004 ae300000 22100001 22310004 ae300000 22100001 22310004 ae300000
  //   22100001 22310004 ae300000 22100001 22310004 ae300000 22100001 22310004 ae300000 22100001 22310004
  //   ae300000 22100001 22310004 ae300000 22100001 22310004 ae300000 22100001 22310004 ae300000 22100001
  //   22310004 ae300000 22100001 22310004 ae300000 22100001 22310004 ae300000 22100001 22310004 ae300000
  //   22100001 22310004 22100001 8020 2011003c 8e130000 8e340000 274402a 11000002 ae330000 ae140000
  //   2231fffc 1611fff8 102020 20020022 c 22100004 2011003c 1611fff2 20020032 c 20080001 20090003 20110876
  //   112020 20020022 c 200b0008 1118804 1318804 112020 20020022 c 216bffff 1560fff9 2002000a c 2008ffff
  //   20090000 20111997 112020 20020022 c 2288820 2e291949 1120fffa 2002000a c 20090000 200b0010 34118483
  //   20120404 118c00 129400 36318281 22520404 ad310000 2328820 21290004 216bffff 1560fffb 200b0020
  //   20090000 91310000 112020 20020022 c 21290001 216bffff 1560fff9 2002000a c 2011fff1 112020 20020022 c
  //   22310001 620fffb 2002000a c 20100000 22100001 102020 20020022 c 22100002 102020 20020022 c 22100003
  //   102020 20020022 c 22100004 102020 20020022 c 22100005 102020 20020022 c 22100006 102020 20020022 c
  //   22100007 102020 20020022 c 22100008 102020 20020022 20020022 c 3e00008
  //   可计数暂停的时钟源
  //   IF/ID
  //   指令字
  //   JMP
  //   JR
  //   OP
  //   Func
  //   Syscall
  //   rs
  //   rt
  //   rd
  //   为方便自动评测，需要输出流水线各段保存的PC值，注意是PC不是PC+4，另外ID段寄存器写入信息，Mem段内存写入信息也要输出
  //   Beq
  //   Bne
  //   rd
  //   ID/EX
  //   EX/MEM
  //   MEM/WB
endmodule

module \新动态分支预测  (
  input  CLK,
  input  clear,
  input  [31:0] PC,
  input  EX_Branch,
  input  EX_BranchTaken,
  input  [31:0] EX_PC,
  input  [31:0] EX_BranchAddr,
  output PredictJump,
  output [31:0] JumpAddr
);

  wire BranchNotFound, comparator_1_eq, comparator_1_gt, comparator_2_eq, comparator_2_gt, comparator_3_eq,
       comparator_3_gt, comparator_4_eq, comparator_4_gt, comparator_5_eq, comparator_6_eq, comparator_7_eq,
       comparator_8_eq, comparator_9_eq, comparator_10_eq, comparator_11_eq, comparator_12_eq,
       comparator_13_eq, comparator_14_eq, comparator_15_eq, comparator_16_eq, comparator_17_eq,
       comparator_18_eq, comparator_19_eq, comparator_20_eq, comparator_21_eq, comparator_21_gt,
       comparator_22_eq, comparator_22_gt, comparator_23_eq, comparator_23_gt, comparator_31_eq,
       comparator_32_eq, comparator_33_eq, comparator_34_eq, comparator_35_eq, comparator_36_eq,
       comparator_37_eq, comparator_38_eq, comparator_39_eq, find, hit0, hit1, hit2, hit3, hit4, hit5, hit6,
       hit7, L0, L1, L2, L3, L4, L5, L6, L7, multiplexer_25_out, multiplexer_26_out, multiplexer_27_out,
       multiplexer_28_out, multiplexer_29_out, multiplexer_30_out, multiplexer_31_out, multiplexer_32_out,
       multiplexer_33_out, multiplexer_34_out, multiplexer_35_out, multiplexer_36_out, multiplexer_37_out,
       multiplexer_38_out, multiplexer_39_out, multiplexer_40_out, not_1_out, not_2_out, not_3_out,
       not_4_out, not_5_out, not_6_out, not_7_out, not_8_out, not_9_out, or_1_out, or_2_out, or_3_out,
       or_4_out, or_5_out, or_6_out, or_7_out, or_8_out, or_9_out, or_10_out, or_11_out, or_12_out,
       or_13_out, or_14_out, or_15_out, or_16_out, or_17_out, or_18_out, or_19_out, or_20_out, or_21_out,
       or_22_out, or_23_out, or_24_out, or_25_out, or_26_out, or_27_out, or_28_out, or_29_out, or_30_out,
       or_31_out, or_32_out, or_33_out, or_34_out, or_35_out, or_36_out, or_37_out, or_38_out, or_39_out,
       or_40_out, SET0, SET1, SET2, SET3, SET4, SET5, SET6, SET7, valid0, valid1, valid2, valid3, valid4,
       valid5, valid6, valid7;
  wire [1:0] multiplexer_1_out, multiplexer_2_out, multiplexer_3_out, multiplexer_4_out, multiplexer_5_out,
       multiplexer_6_out, multiplexer_7_out, multiplexer_8_out, predictstat_2_q, predictstat_3_q,
       predictstat_4_q, predictstat_5_q, predictstat_6_q, predictstat_7_q, predictstat_8_q, predictstat_q,
       statdfa_2_b0, statdfa_3_b0, statdfa_4_b0, statdfa_5_b0, statdfa_6_b0, statdfa_7_b0, statdfa_8_b0,
       statdfa_b0;
  wire [2:0] multiplexer_18_out, multiplexer_20_out, multiplexer_22_out, multiplexer_24_out,
       multiplexer_41_out, multiplexer_43_out, multiplexer_45_out, multiplexer_46_out,
       priority_encoder_1_out, subtractor_1_out;
  wire [31:0] adder_1_out, adder_2_out, adder_3_out, adder_4_out, adder_5_out, adder_6_out, adder_7_out,
       adder_8_out, adder_9_out, adder_10_out, adder_11_out, adder_12_out, adder_13_out, adder_14_out,
       adder_15_out, adder_16_out, cnt0, cnt1, cnt2, cnt3, cnt4, cnt5, cnt6, cnt7, multiplexer_9_out,
       multiplexer_10_out, multiplexer_11_out, multiplexer_12_out, multiplexer_13_out, multiplexer_14_out,
       multiplexer_15_out, multiplexer_16_out, multiplexer_17_out, multiplexer_19_out, multiplexer_21_out,
       multiplexer_23_out, multiplexer_42_out, multiplexer_44_out, tag0, tag1, tag2, tag3, tag4, tag5, tag6,
       tag7, targetpc_2_q, targetpc_3_q, targetpc_4_q, targetpc_5_q, targetpc_6_q, targetpc_7_q,
       targetpc_8_q, targetpc_q;

  Register #(.width(1), .trigger("rising"), .Select("low")) valid (
    .D(1'b1), .en(SET0), .Q(valid0), .clk(CLK), .clr(clear), .cs(1'b0), .preset(1'b0));
  Register #(.width(1), .trigger("rising"), .Select("low")) valid_2 (
    .D(1'b1), .en(SET1), .Q(valid1), .clk(CLK), .clr(clear), .cs(1'b0), .preset(1'b0));
  Register #(.width(1), .trigger("rising"), .Select("low")) valid_3 (
    .D(1'b1), .en(SET2), .Q(valid2), .clk(CLK), .clr(clear), .cs(1'b0), .preset(1'b0));
  Register #(.width(1), .trigger("rising"), .Select("low")) valid_4 (
    .D(1'b1), .en(SET3), .Q(valid3), .clk(CLK), .clr(clear), .cs(1'b0), .preset(1'b0));
  Register #(.width(1), .trigger("rising"), .Select("low")) valid_5 (
    .D(1'b1), .en(SET4), .Q(valid4), .clk(CLK), .clr(clear), .cs(1'b0), .preset(1'b0));
  Register #(.width(1), .trigger("rising"), .Select("low")) valid_6 (
    .D(1'b1), .en(SET5), .Q(valid5), .clk(CLK), .clr(clear), .cs(1'b0), .preset(1'b0));
  Register #(.width(1), .trigger("rising"), .Select("low")) valid_7 (
    .D(1'b1), .en(SET6), .Q(valid6), .clk(CLK), .clr(clear), .cs(1'b0), .preset(1'b0));
  Register #(.width(1), .trigger("rising"), .Select("low")) valid_8 (
    .D(1'b1), .en(SET7), .Q(valid7), .clk(CLK), .clr(clear), .cs(1'b0), .preset(1'b0));
  Register #(.width(32), .trigger("rising"), .Select("low")) branchpc (
    .D(EX_PC), .en(SET0), .Q(tag0), .clk(CLK), .clr(clear), .cs(1'b0), .preset(1'b0));
  Register #(.width(32), .trigger("rising"), .Select("low")) branchpc_2 (
    .D(EX_PC), .en(SET1), .Q(tag1), .clk(CLK), .clr(clear), .cs(1'b0), .preset(1'b0));
  Register #(.width(32), .trigger("rising"), .Select("low")) branchpc_3 (
    .D(EX_PC), .en(SET2), .Q(tag2), .clk(CLK), .clr(clear), .cs(1'b0), .preset(1'b0));
  Register #(.width(32), .trigger("rising"), .Select("low")) branchpc_4 (
    .D(EX_PC), .en(SET3), .Q(tag3), .clk(CLK), .clr(clear), .cs(1'b0), .preset(1'b0));
  Register #(.width(32), .trigger("rising"), .Select("low")) branchpc_5 (
    .D(EX_PC), .en(SET4), .Q(tag4), .clk(CLK), .clr(clear), .cs(1'b0), .preset(1'b0));
  Register #(.width(32), .trigger("rising"), .Select("low")) branchpc_6 (
    .D(EX_PC), .en(SET5), .Q(tag5), .clk(CLK), .clr(clear), .cs(1'b0), .preset(1'b0));
  Register #(.width(32), .trigger("rising"), .Select("low")) branchpc_7 (
    .D(EX_PC), .en(SET6), .Q(tag6), .clk(CLK), .clr(clear), .cs(1'b0), .preset(1'b0));
  Register #(.width(32), .trigger("rising"), .Select("low")) branchpc_8 (
    .D(EX_PC), .en(SET7), .Q(tag7), .clk(CLK), .clr(clear), .cs(1'b0), .preset(1'b0));
  Multiplexer #(.select(1), .width(2), .disabled("Z"), .enable("false")) multiplexer_1 (
    .in0(statdfa_b0), .in1({EX_BranchTaken, 1'b1}), .out(multiplexer_1_out), .sel(SET0));
  or or_1 (or_1_out, hit0, SET0);
  Multiplexer #(.select(1), .width(2), .disabled("Z"), .enable("false")) multiplexer_2 (
    .in0(statdfa_2_b0), .in1({EX_BranchTaken, 1'b1}), .out(multiplexer_2_out), .sel(SET1));
  or or_2 (or_2_out, hit1, SET1);
  Multiplexer #(.select(1), .width(2), .disabled("Z"), .enable("false")) multiplexer_3 (
    .in0(statdfa_3_b0), .in1({EX_BranchTaken, 1'b1}), .out(multiplexer_3_out), .sel(SET2));
  or or_3 (or_3_out, hit2, SET2);
  or or_4 (or_4_out, hit3, SET3);
  or or_5 (or_5_out, hit4, SET4);
  or or_6 (or_6_out, hit5, SET5);
  or or_7 (or_7_out, hit6, SET6);
  or or_8 (or_8_out, hit7, SET7);
  Register #(.width(2), .trigger("rising"), .Select("low")) predictstat (
    .D(multiplexer_1_out), .en(or_1_out), .Q(predictstat_q), .clk(CLK), .clr(clear), .cs(1'b0), .preset(1'b0));
  Register #(.width(2), .trigger("rising"), .Select("low")) predictstat_2 (
    .D(multiplexer_2_out), .en(or_2_out), .Q(predictstat_2_q), .clk(CLK), .clr(clear), .cs(1'b0),
    .preset(1'b0));
  Register #(.width(2), .trigger("rising"), .Select("low")) predictstat_3 (
    .D(multiplexer_3_out), .en(or_3_out), .Q(predictstat_3_q), .clk(CLK), .clr(clear), .cs(1'b0),
    .preset(1'b0));
  Multiplexer #(.select(1), .width(2), .disabled("Z"), .enable("false")) multiplexer_4 (
    .in0(statdfa_4_b0), .in1({EX_BranchTaken, 1'b1}), .out(multiplexer_4_out), .sel(SET3));
  Register #(.width(2), .trigger("rising"), .Select("low")) predictstat_4 (
    .D(multiplexer_4_out), .en(or_4_out), .Q(predictstat_4_q), .clk(CLK), .clr(clear), .cs(1'b0),
    .preset(1'b0));
  Multiplexer #(.select(1), .width(2), .disabled("Z"), .enable("false")) multiplexer_5 (
    .in0(statdfa_5_b0), .in1({EX_BranchTaken, 1'b1}), .out(multiplexer_5_out), .sel(SET4));
  Register #(.width(2), .trigger("rising"), .Select("low")) predictstat_5 (
    .D(multiplexer_5_out), .en(or_5_out), .Q(predictstat_5_q), .clk(CLK), .clr(clear), .cs(1'b0),
    .preset(1'b0));
  Multiplexer #(.select(1), .width(2), .disabled("Z"), .enable("false")) multiplexer_6 (
    .in0(statdfa_6_b0), .in1({EX_BranchTaken, 1'b1}), .out(multiplexer_6_out), .sel(SET5));
  Register #(.width(2), .trigger("rising"), .Select("low")) predictstat_6 (
    .D(multiplexer_6_out), .en(or_6_out), .Q(predictstat_6_q), .clk(CLK), .clr(clear), .cs(1'b0),
    .preset(1'b0));
  Multiplexer #(.select(1), .width(2), .disabled("Z"), .enable("false")) multiplexer_7 (
    .in0(statdfa_7_b0), .in1({EX_BranchTaken, 1'b1}), .out(multiplexer_7_out), .sel(SET6));
  Register #(.width(2), .trigger("rising"), .Select("low")) predictstat_7 (
    .D(multiplexer_7_out), .en(or_7_out), .Q(predictstat_7_q), .clk(CLK), .clr(clear), .cs(1'b0),
    .preset(1'b0));
  Multiplexer #(.select(1), .width(2), .disabled("Z"), .enable("false")) multiplexer_8 (
    .in0(statdfa_8_b0), .in1({EX_BranchTaken, 1'b1}), .out(multiplexer_8_out), .sel(SET7));
  Register #(.width(2), .trigger("rising"), .Select("low")) predictstat_8 (
    .D(multiplexer_8_out), .en(or_8_out), .Q(predictstat_8_q), .clk(CLK), .clr(clear), .cs(1'b0),
    .preset(1'b0));
  assign PredictJump = L0 ? predictstat_q[1] : 1'bz;  // Controlled_Buffer controlled_buffer_1
  assign PredictJump = L1 ? predictstat_2_q[1] : 1'bz;  // Controlled_Buffer controlled_buffer_2
  assign PredictJump = L2 ? predictstat_3_q[1] : 1'bz;  // Controlled_Buffer controlled_buffer_3
  \双位预测状态机  statdfa (
    .A1(predictstat_q[1]), .A0(predictstat_q[0]), .branchyes(EX_BranchTaken), .B1(statdfa_b0[1]),
    .B0(statdfa_b0[0]));
  \双位预测状态机  statdfa_2 (
    .A1(predictstat_2_q[1]), .A0(predictstat_2_q[0]), .branchyes(EX_BranchTaken), .B1(statdfa_2_b0[1]),
    .B0(statdfa_2_b0[0]));
  \双位预测状态机  statdfa_3 (
    .A1(predictstat_3_q[1]), .A0(predictstat_3_q[0]), .branchyes(EX_BranchTaken), .B1(statdfa_3_b0[1]),
    .B0(statdfa_3_b0[0]));
  assign PredictJump = L3 ? predictstat_4_q[1] : 1'bz;  // Controlled_Buffer controlled_buffer_4
  \双位预测状态机  statdfa_4 (
    .A1(predictstat_4_q[1]), .A0(predictstat_4_q[0]), .branchyes(EX_BranchTaken), .B1(statdfa_4_b0[1]),
    .B0(statdfa_4_b0[0]));
  assign PredictJump = L4 ? predictstat_5_q[1] : 1'bz;  // Controlled_Buffer controlled_buffer_5
  \双位预测状态机  statdfa_5 (
    .A1(predictstat_5_q[1]), .A0(predictstat_5_q[0]), .branchyes(EX_BranchTaken), .B1(statdfa_5_b0[1]),
    .B0(statdfa_5_b0[0]));
  assign PredictJump = L5 ? predictstat_6_q[1] : 1'bz;  // Controlled_Buffer controlled_buffer_6
  \双位预测状态机  statdfa_6 (
    .A1(predictstat_6_q[1]), .A0(predictstat_6_q[0]), .branchyes(EX_BranchTaken), .B1(statdfa_6_b0[1]),
    .B0(statdfa_6_b0[0]));
  assign PredictJump = L6 ? predictstat_7_q[1] : 1'bz;  // Controlled_Buffer controlled_buffer_7
  \双位预测状态机  statdfa_7 (
    .A1(predictstat_7_q[1]), .A0(predictstat_7_q[0]), .branchyes(EX_BranchTaken), .B1(statdfa_7_b0[1]),
    .B0(statdfa_7_b0[0]));
  assign PredictJump = L7 ? predictstat_8_q[1] : 1'bz;  // Controlled_Buffer controlled_buffer_8
  \双位预测状态机  statdfa_8 (
    .A1(predictstat_8_q[1]), .A0(predictstat_8_q[0]), .branchyes(EX_BranchTaken), .B1(statdfa_8_b0[1]),
    .B0(statdfa_8_b0[0]));
  Pull_Resistor #(.pull(0)) pull_resistor_1 (.node(PredictJump));
  or or_9 (or_9_out, L0, SET0);
  or or_10 (or_10_out, L1, SET1);
  or or_11 (or_11_out, L2, SET2);
  or or_12 (or_12_out, L3, SET3);
  or or_13 (or_13_out, L4, SET4);
  or or_14 (or_14_out, L5, SET5);
  or or_15 (or_15_out, L6, SET6);
  or or_16 (or_16_out, L7, SET7);
  Register #(.width(32), .trigger("rising"), .Select("low")) counter (
    .D(multiplexer_9_out), .en(or_17_out), .Q(cnt0), .clk(CLK), .clr(clear), .cs(1'b0), .preset(1'b0));
  Multiplexer #(.select(1), .width(32), .disabled("Z"), .enable("false")) multiplexer_9 (
    .in0(adder_1_out), .in1({32{1'b0}}), .out(multiplexer_9_out), .sel(or_9_out));
  or or_17 (or_17_out, SET0, find);
  Register #(.width(32), .trigger("rising"), .Select("low")) counter_2 (
    .D(multiplexer_10_out), .en(or_18_out), .Q(cnt1), .clk(CLK), .clr(clear), .cs(1'b0), .preset(1'b0));
  Multiplexer #(.select(1), .width(32), .disabled("Z"), .enable("false")) multiplexer_10 (
    .in0(adder_2_out), .in1({32{1'b0}}), .out(multiplexer_10_out), .sel(or_10_out));
  or or_18 (or_18_out, SET1, find);
  Multiplexer #(.select(1), .width(32), .disabled("Z"), .enable("false")) multiplexer_11 (
    .in0(adder_3_out), .in1({32{1'b0}}), .out(multiplexer_11_out), .sel(or_11_out));
  Register #(.width(32), .trigger("rising"), .Select("low")) counter_3 (
    .D(multiplexer_11_out), .en(or_19_out), .Q(cnt2), .clk(CLK), .clr(clear), .cs(1'b0), .preset(1'b0));
  or or_19 (or_19_out, SET2, find);
  Multiplexer #(.select(1), .width(32), .disabled("Z"), .enable("false")) multiplexer_12 (
    .in0(adder_4_out), .in1({32{1'b0}}), .out(multiplexer_12_out), .sel(or_12_out));
  Register #(.width(32), .trigger("rising"), .Select("low")) counter_4 (
    .D(multiplexer_12_out), .en(or_20_out), .Q(cnt3), .clk(CLK), .clr(clear), .cs(1'b0), .preset(1'b0));
  or or_20 (or_20_out, SET3, find);
  Multiplexer #(.select(1), .width(32), .disabled("Z"), .enable("false")) multiplexer_13 (
    .in0(adder_5_out), .in1({32{1'b0}}), .out(multiplexer_13_out), .sel(or_13_out));
  Register #(.width(32), .trigger("rising"), .Select("low")) counter_5 (
    .D(multiplexer_13_out), .en(or_21_out), .Q(cnt4), .clk(CLK), .clr(clear), .cs(1'b0), .preset(1'b0));
  or or_21 (or_21_out, SET4, find);
  Multiplexer #(.select(1), .width(32), .disabled("Z"), .enable("false")) multiplexer_14 (
    .in0(adder_6_out), .in1({32{1'b0}}), .out(multiplexer_14_out), .sel(or_14_out));
  Register #(.width(32), .trigger("rising"), .Select("low")) counter_6 (
    .D(multiplexer_14_out), .en(or_22_out), .Q(cnt5), .clk(CLK), .clr(clear), .cs(1'b0), .preset(1'b0));
  or or_22 (or_22_out, SET5, find);
  Register #(.width(32), .trigger("rising"), .Select("low")) counter_7 (
    .D(multiplexer_15_out), .en(or_23_out), .Q(cnt6), .clk(CLK), .clr(clear), .cs(1'b0), .preset(1'b0));
  Multiplexer #(.select(1), .width(32), .disabled("Z"), .enable("false")) multiplexer_15 (
    .in0(adder_7_out), .in1({32{1'b0}}), .out(multiplexer_15_out), .sel(or_15_out));
  or or_23 (or_23_out, SET6, find);
  Multiplexer #(.select(1), .width(32), .disabled("Z"), .enable("false")) multiplexer_16 (
    .in0(adder_8_out), .in1({32{1'b0}}), .out(multiplexer_16_out), .sel(or_16_out));
  Register #(.width(32), .trigger("rising"), .Select("low")) counter_8 (
    .D(multiplexer_16_out), .en(or_24_out), .Q(cnt7), .clk(CLK), .clr(clear), .cs(1'b0), .preset(1'b0));
  or or_24 (or_24_out, SET7, find);
  Adder #(.width(32)) adder_1 (.a(cnt0), .b(32'h1), .out(adder_1_out), .cin(1'b0));  // open: cout
  Adder #(.width(32)) adder_2 (.a(cnt1), .b(32'h1), .out(adder_2_out), .cin(1'b0));  // open: cout
  Adder #(.width(32)) adder_3 (.a(cnt2), .b(32'h1), .out(adder_3_out), .cin(1'b0));  // open: cout
  Adder #(.width(32)) adder_4 (.a(cnt3), .b(32'h1), .out(adder_4_out), .cin(1'b0));  // open: cout
  Adder #(.width(32)) adder_5 (.a(cnt4), .b(32'h1), .out(adder_5_out), .cin(1'b0));  // open: cout
  Adder #(.width(32)) adder_6 (.a(cnt5), .b(32'h1), .out(adder_6_out), .cin(1'b0));  // open: cout
  Adder #(.width(32)) adder_7 (.a(cnt6), .b(32'h1), .out(adder_7_out), .cin(1'b0));  // open: cout
  Adder #(.width(32)) adder_8 (.a(cnt7), .b(32'h1), .out(adder_8_out), .cin(1'b0));  // open: cout
  or or_25 (or_25_out, hit0, SET0);
  or or_26 (or_26_out, hit1, SET1);
  or or_27 (or_27_out, hit2, SET2);
  Register #(.width(32), .trigger("rising"), .Select("low")) targetpc (
    .D(EX_BranchAddr), .en(or_25_out), .Q(targetpc_q), .clk(CLK), .clr(clear), .cs(1'b0), .preset(1'b0));
  Register #(.width(32), .trigger("rising"), .Select("low")) targetpc_2 (
    .D(EX_BranchAddr), .en(or_26_out), .Q(targetpc_2_q), .clk(CLK), .clr(clear), .cs(1'b0), .preset(1'b0));
  Register #(.width(32), .trigger("rising"), .Select("low")) targetpc_3 (
    .D(EX_BranchAddr), .en(or_27_out), .Q(targetpc_3_q), .clk(CLK), .clr(clear), .cs(1'b0), .preset(1'b0));
  Register #(.width(32), .trigger("rising"), .Select("low")) targetpc_4 (
    .D(EX_BranchAddr), .en(or_28_out), .Q(targetpc_4_q), .clk(CLK), .clr(clear), .cs(1'b0), .preset(1'b0));
  or or_28 (or_28_out, hit3, SET3);
  Register #(.width(32), .trigger("rising"), .Select("low")) targetpc_5 (
    .D(EX_BranchAddr), .en(or_29_out), .Q(targetpc_5_q), .clk(CLK), .clr(clear), .cs(1'b0), .preset(1'b0));
  or or_29 (or_29_out, hit4, SET4);
  Register #(.width(32), .trigger("rising"), .Select("low")) targetpc_6 (
    .D(EX_BranchAddr), .en(or_30_out), .Q(targetpc_6_q), .clk(CLK), .clr(clear), .cs(1'b0), .preset(1'b0));
  or or_30 (or_30_out, hit5, SET5);
  Register #(.width(32), .trigger("rising"), .Select("low")) targetpc_7 (
    .D(EX_BranchAddr), .en(or_31_out), .Q(targetpc_7_q), .clk(CLK), .clr(clear), .cs(1'b0), .preset(1'b0));
  or or_31 (or_31_out, hit6, SET6);
  Register #(.width(32), .trigger("rising"), .Select("low")) targetpc_8 (
    .D(EX_BranchAddr), .en(or_32_out), .Q(targetpc_8_q), .clk(CLK), .clr(clear), .cs(1'b0), .preset(1'b0));
  or or_32 (or_32_out, hit7, SET7);
  assign JumpAddr = L0 ? targetpc_q : 32'bz;  // Controlled_Buffer controlled_buffer_9
  assign JumpAddr = L1 ? targetpc_2_q : 32'bz;  // Controlled_Buffer controlled_buffer_10
  assign JumpAddr = L2 ? targetpc_3_q : 32'bz;  // Controlled_Buffer controlled_buffer_11
  assign JumpAddr = L3 ? targetpc_4_q : 32'bz;  // Controlled_Buffer controlled_buffer_12
  assign JumpAddr = L4 ? targetpc_5_q : 32'bz;  // Controlled_Buffer controlled_buffer_13
  assign JumpAddr = L5 ? targetpc_6_q : 32'bz;  // Controlled_Buffer controlled_buffer_14
  assign JumpAddr = L6 ? targetpc_7_q : 32'bz;  // Controlled_Buffer controlled_buffer_15
  assign JumpAddr = L7 ? targetpc_8_q : 32'bz;  // Controlled_Buffer controlled_buffer_16
  not not_1 (not_1_out, valid0);
  Adder #(.width(32)) adder_9 (.a(cnt0), .b({32{1'b0}}), .out(adder_9_out), .cin(not_1_out));  // open: cout
  not not_2 (not_2_out, valid1);
  Adder #(.width(32)) adder_10 (.a(cnt1), .b({32{1'b0}}), .out(adder_10_out), .cin(not_2_out));  // open: cout
  not not_3 (not_3_out, valid2);
  Adder #(.width(32)) adder_11 (.a(cnt2), .b({32{1'b0}}), .out(adder_11_out), .cin(not_3_out));  // open: cout
  not not_4 (not_4_out, valid3);
  Adder #(.width(32)) adder_12 (.a(cnt3), .b({32{1'b0}}), .out(adder_12_out), .cin(not_4_out));  // open: cout
  not not_5 (not_5_out, valid4);
  Adder #(.width(32)) adder_13 (.a(cnt4), .b({32{1'b0}}), .out(adder_13_out), .cin(not_5_out));  // open: cout
  not not_6 (not_6_out, valid5);
  Adder #(.width(32)) adder_14 (.a(cnt5), .b({32{1'b0}}), .out(adder_14_out), .cin(not_6_out));  // open: cout
  not not_7 (not_7_out, valid6);
  Adder #(.width(32)) adder_15 (.a(cnt6), .b({32{1'b0}}), .out(adder_15_out), .cin(not_7_out));  // open: cout
  not not_8 (not_8_out, valid7);
  Adder #(.width(32)) adder_16 (.a(cnt7), .b({32{1'b0}}), .out(adder_16_out), .cin(not_8_out));  // open: cout
  Comparator #(.width(32), .mode("unsigned")) comparator_1 (
    .a(adder_9_out), .b(adder_10_out), .gt(comparator_1_gt), .eq(comparator_1_eq));  // open: lt
  Comparator #(.width(32), .mode("unsigned")) comparator_2 (
    .a(adder_11_out), .b(adder_12_out), .gt(comparator_2_gt), .eq(comparator_2_eq));  // open: lt
  Comparator #(.width(32), .mode("unsigned")) comparator_3 (
    .a(adder_13_out), .b(adder_14_out), .gt(comparator_3_gt), .eq(comparator_3_eq));  // open: lt
  Comparator #(.width(32), .mode("unsigned")) comparator_4 (
    .a(adder_15_out), .b(adder_16_out), .gt(comparator_4_gt), .eq(comparator_4_eq));  // open: lt
  or or_33 (or_33_out, comparator_1_gt, comparator_1_eq);
  or or_34 (or_34_out, comparator_2_gt, comparator_2_eq);
  or or_35 (or_35_out, comparator_3_gt, comparator_3_eq);
  or or_36 (or_36_out, comparator_4_gt, comparator_4_eq);
  Comparator #(.width(32), .mode("twosComplement")) comparator_5 (
    .a(tag7), .b(PC), .eq(comparator_5_eq));  // open: gt, lt
  Comparator #(.width(32), .mode("twosComplement")) comparator_6 (
    .a(tag6), .b(PC), .eq(comparator_6_eq));  // open: gt, lt
  Comparator #(.width(32), .mode("twosComplement")) comparator_7 (
    .a(tag5), .b(PC), .eq(comparator_7_eq));  // open: gt, lt
  Comparator #(.width(32), .mode("twosComplement")) comparator_8 (
    .a(tag4), .b(PC), .eq(comparator_8_eq));  // open: gt, lt
  Comparator #(.width(32), .mode("twosComplement")) comparator_9 (
    .a(tag3), .b(PC), .eq(comparator_9_eq));  // open: gt, lt
  Comparator #(.width(32), .mode("twosComplement")) comparator_10 (
    .a(tag2), .b(PC), .eq(comparator_10_eq));  // open: gt, lt
  Comparator #(.width(32), .mode("twosComplement")) comparator_11 (
    .a(tag1), .b(PC), .eq(comparator_11_eq));  // open: gt, lt
  Comparator #(.width(32), .mode("twosComplement")) comparator_12 (
    .a(tag0), .b(PC), .eq(comparator_12_eq));  // open: gt, lt
  Comparator #(.width(32), .mode("twosComplement")) comparator_13 (
    .a(tag7), .b(EX_PC), .eq(comparator_13_eq));  // open: gt, lt
  Comparator #(.width(32), .mode("twosComplement")) comparator_14 (
    .a(tag6), .b(EX_PC), .eq(comparator_14_eq));  // open: gt, lt
  Comparator #(.width(32), .mode("twosComplement")) comparator_15 (
    .a(tag5), .b(EX_PC), .eq(comparator_15_eq));  // open: gt, lt
  Comparator #(.width(32), .mode("twosComplement")) comparator_16 (
    .a(tag4), .b(EX_PC), .eq(comparator_16_eq));  // open: gt, lt
  Comparator #(.width(32), .mode("twosComplement")) comparator_17 (
    .a(tag3), .b(EX_PC), .eq(comparator_17_eq));  // open: gt, lt
  Comparator #(.width(32), .mode("twosComplement")) comparator_18 (
    .a(tag2), .b(EX_PC), .eq(comparator_18_eq));  // open: gt, lt
  Comparator #(.width(32), .mode("twosComplement")) comparator_19 (
    .a(tag1), .b(EX_PC), .eq(comparator_19_eq));  // open: gt, lt
  Comparator #(.width(32), .mode("twosComplement")) comparator_20 (
    .a(tag0), .b(EX_PC), .eq(comparator_20_eq));  // open: gt, lt
  Multiplexer #(.select(1), .width(32), .disabled("Z"), .enable("false")) multiplexer_17 (
    .in0(adder_10_out), .in1(adder_9_out), .out(multiplexer_17_out), .sel(or_33_out));
  Multiplexer #(.select(1), .width(3), .disabled("Z"), .enable("false")) multiplexer_18 (
    .in0(3'b001), .in1(3'b000), .out(multiplexer_18_out), .sel(or_33_out));
  Multiplexer #(.select(1), .width(32), .disabled("Z"), .enable("false")) multiplexer_19 (
    .in0(adder_12_out), .in1(adder_11_out), .out(multiplexer_19_out), .sel(or_34_out));
  Multiplexer #(.select(1), .width(3), .disabled("Z"), .enable("false")) multiplexer_20 (
    .in0(3'b011), .in1(3'b010), .out(multiplexer_20_out), .sel(or_34_out));
  Multiplexer #(.select(1), .width(32), .disabled("Z"), .enable("false")) multiplexer_21 (
    .in0(adder_14_out), .in1(adder_13_out), .out(multiplexer_21_out), .sel(or_35_out));
  Multiplexer #(.select(1), .width(3), .disabled("Z"), .enable("false")) multiplexer_22 (
    .in0(3'b101), .in1(3'b100), .out(multiplexer_22_out), .sel(or_35_out));
  Multiplexer #(.select(1), .width(32), .disabled("Z"), .enable("false")) multiplexer_23 (
    .in0(adder_16_out), .in1(adder_15_out), .out(multiplexer_23_out), .sel(or_36_out));
  Multiplexer #(.select(1), .width(3), .disabled("Z"), .enable("false")) multiplexer_24 (
    .in0(3'b111), .in1(3'b110), .out(multiplexer_24_out), .sel(or_36_out));
  Multiplexer #(.select(1), .width(1), .disabled("Z"), .enable("false")) multiplexer_25 (
    .in0(1'b0), .in1(comparator_5_eq), .out(multiplexer_25_out), .sel(valid7));
  Multiplexer #(.select(1), .width(1), .disabled("Z"), .enable("false")) multiplexer_26 (
    .in0(1'b0), .in1(comparator_6_eq), .out(multiplexer_26_out), .sel(valid6));
  Multiplexer #(.select(1), .width(1), .disabled("Z"), .enable("false")) multiplexer_27 (
    .in0(1'b0), .in1(comparator_7_eq), .out(multiplexer_27_out), .sel(valid5));
  Multiplexer #(.select(1), .width(1), .disabled("Z"), .enable("false")) multiplexer_28 (
    .in0(1'b0), .in1(comparator_8_eq), .out(multiplexer_28_out), .sel(valid4));
  Multiplexer #(.select(1), .width(1), .disabled("Z"), .enable("false")) multiplexer_29 (
    .in0(1'b0), .in1(comparator_9_eq), .out(multiplexer_29_out), .sel(valid3));
  Multiplexer #(.select(1), .width(1), .disabled("Z"), .enable("false")) multiplexer_30 (
    .in0(1'b0), .in1(comparator_10_eq), .out(multiplexer_30_out), .sel(valid2));
  Multiplexer #(.select(1), .width(1), .disabled("Z"), .enable("false")) multiplexer_31 (
    .in0(1'b0), .in1(comparator_11_eq), .out(multiplexer_31_out), .sel(valid1));
  Multiplexer #(.select(1), .width(1), .disabled("Z"), .enable("false")) multiplexer_32 (
    .in0(1'b0), .in1(comparator_12_eq), .out(multiplexer_32_out), .sel(valid0));
  Multiplexer #(.select(1), .width(1), .disabled("Z"), .enable("false")) multiplexer_33 (
    .in0(1'b0), .in1(comparator_13_eq), .out(multiplexer_33_out), .sel(valid7));
  Multiplexer #(.select(1), .width(1), .disabled("Z"), .enable("false")) multiplexer_34 (
    .in0(1'b0), .in1(comparator_14_eq), .out(multiplexer_34_out), .sel(valid6));
  Multiplexer #(.select(1), .width(1), .disabled("Z"), .enable("false")) multiplexer_35 (
    .in0(1'b0), .in1(comparator_15_eq), .out(multiplexer_35_out), .sel(valid5));
  Multiplexer #(.select(1), .width(1), .disabled("Z"), .enable("false")) multiplexer_36 (
    .in0(1'b0), .in1(comparator_16_eq), .out(multiplexer_36_out), .sel(valid4));
  Multiplexer #(.select(1), .width(1), .disabled("Z"), .enable("false")) multiplexer_37 (
    .in0(1'b0), .in1(comparator_17_eq), .out(multiplexer_37_out), .sel(valid3));
  Multiplexer #(.select(1), .width(1), .disabled("Z"), .enable("false")) multiplexer_38 (
    .in0(1'b0), .in1(comparator_18_eq), .out(multiplexer_38_out), .sel(valid2));
  Multiplexer #(.select(1), .width(1), .disabled("Z"), .enable("false")) multiplexer_39 (
    .in0(1'b0), .in1(comparator_19_eq), .out(multiplexer_39_out), .sel(valid1));
  Multiplexer #(.select(1), .width(1), .disabled("Z"), .enable("false")) multiplexer_40 (
    .in0(1'b0), .in1(comparator_20_eq), .out(multiplexer_40_out), .sel(valid0));
  Comparator #(.width(32), .mode("unsigned")) comparator_21 (
    .a(multiplexer_17_out), .b(multiplexer_19_out), .gt(comparator_21_gt), .eq(comparator_21_eq));  // open: lt
  Comparator #(.width(32), .mode("unsigned")) comparator_22 (
    .a(multiplexer_21_out), .b(multiplexer_23_out), .gt(comparator_22_gt), .eq(comparator_22_eq));  // open: lt
  Priority_Encoder #(.select(3), .disabled("Z")) priority_encoder_1 (
    .in0(multiplexer_25_out), .in1(multiplexer_26_out), .in2(multiplexer_27_out), .in3(multiplexer_28_out),
    .in4(multiplexer_29_out), .in5(multiplexer_30_out), .in6(multiplexer_31_out), .in7(multiplexer_32_out),
    .out(priority_encoder_1_out), .gs(find), .en_in(1'b1));  // open: en_out
  or or_37 (or_37_out, comparator_21_gt, comparator_21_eq);
  or or_38 (or_38_out, comparator_22_gt, comparator_22_eq);
  Multiplexer #(.select(1), .width(3), .disabled("Z"), .enable("false")) multiplexer_41 (
    .in0(3'b000), .in1(priority_encoder_1_out), .out(multiplexer_41_out), .sel(find));
  and and_1 (hit7, multiplexer_33_out, EX_Branch);
  and and_2 (hit6, multiplexer_34_out, EX_Branch);
  and and_3 (hit5, multiplexer_35_out, EX_Branch);
  and and_4 (hit4, multiplexer_36_out, EX_Branch);
  and and_5 (hit3, multiplexer_37_out, EX_Branch);
  and and_6 (hit2, multiplexer_38_out, EX_Branch);
  and and_7 (hit1, multiplexer_39_out, EX_Branch);
  and and_8 (hit0, multiplexer_40_out, EX_Branch);
  Multiplexer #(.select(1), .width(32), .disabled("Z"), .enable("false")) multiplexer_42 (
    .in0(multiplexer_19_out), .in1(multiplexer_17_out), .out(multiplexer_42_out), .sel(or_37_out));
  Multiplexer #(.select(1), .width(3), .disabled("Z"), .enable("false")) multiplexer_43 (
    .in0(multiplexer_20_out), .in1(multiplexer_18_out), .out(multiplexer_43_out), .sel(or_37_out));
  Multiplexer #(.select(1), .width(32), .disabled("Z"), .enable("false")) multiplexer_44 (
    .in0(multiplexer_23_out), .in1(multiplexer_21_out), .out(multiplexer_44_out), .sel(or_38_out));
  Multiplexer #(.select(1), .width(3), .disabled("Z"), .enable("false")) multiplexer_45 (
    .in0(multiplexer_24_out), .in1(multiplexer_22_out), .out(multiplexer_45_out), .sel(or_38_out));
  Subtractor #(.width(3)) subtractor_1 (
    .a(3'b111), .b(multiplexer_41_out), .out(subtractor_1_out), .bin(1'b0));  // open: bout
  Comparator #(.width(32), .mode("unsigned")) comparator_23 (
    .a(multiplexer_42_out), .b(multiplexer_44_out), .gt(comparator_23_gt), .eq(comparator_23_eq));  // open: lt
  or or_39 (or_39_out, comparator_23_gt, comparator_23_eq);
  Multiplexer #(.select(1), .width(3), .disabled("Z"), .enable("false")) multiplexer_46 (
    .in0(multiplexer_45_out), .in1(multiplexer_43_out), .out(multiplexer_46_out), .sel(or_39_out));
  Comparator #(.width(3), .mode("twosComplement")) comparator_24 (
    .a(subtractor_1_out), .b(3'b000), .eq(L0));  // open: gt, lt
  Comparator #(.width(3), .mode("twosComplement")) comparator_25 (
    .a(subtractor_1_out), .b(3'b001), .eq(L1));  // open: gt, lt
  Comparator #(.width(3), .mode("twosComplement")) comparator_26 (
    .a(subtractor_1_out), .b(3'b010), .eq(L2));  // open: gt, lt
  Comparator #(.width(3), .mode("twosComplement")) comparator_27 (
    .a(subtractor_1_out), .b(3'b011), .eq(L3));  // open: gt, lt
  Comparator #(.width(3), .mode("twosComplement")) comparator_28 (
    .a(subtractor_1_out), .b(3'b100), .eq(L4));  // open: gt, lt
  Comparator #(.width(3), .mode("twosComplement")) comparator_29 (
    .a(subtractor_1_out), .b(3'b101), .eq(L5));  // open: gt, lt
  Comparator #(.width(3), .mode("twosComplement")) comparator_30 (
    .a(subtractor_1_out), .b(3'b110), .eq(L6));  // open: gt, lt
  Comparator #(.width(3), .mode("twosComplement")) comparator_31 (
    .a(subtractor_1_out), .b(3'b111), .eq(comparator_31_eq));  // open: gt, lt
  and and_9 (L7, comparator_31_eq, find);
  or or_40 (or_40_out, hit7, hit6, hit5, hit4, hit3, hit2, hit1, hit0);
  not not_9 (not_9_out, or_40_out);
  and and_10 (BranchNotFound, not_9_out, EX_Branch);
  Comparator #(.width(3), .mode("twosComplement")) comparator_32 (
    .a(multiplexer_46_out), .b(3'b000), .eq(comparator_32_eq));  // open: gt, lt
  Comparator #(.width(3), .mode("twosComplement")) comparator_33 (
    .a(multiplexer_46_out), .b(3'b001), .eq(comparator_33_eq));  // open: gt, lt
  Comparator #(.width(3), .mode("twosComplement")) comparator_34 (
    .a(multiplexer_46_out), .b(3'b010), .eq(comparator_34_eq));  // open: gt, lt
  Comparator #(.width(3), .mode("twosComplement")) comparator_35 (
    .a(multiplexer_46_out), .b(3'b011), .eq(comparator_35_eq));  // open: gt, lt
  Comparator #(.width(3), .mode("twosComplement")) comparator_36 (
    .a(multiplexer_46_out), .b(3'b100), .eq(comparator_36_eq));  // open: gt, lt
  Comparator #(.width(3), .mode("twosComplement")) comparator_37 (
    .a(multiplexer_46_out), .b(3'b101), .eq(comparator_37_eq));  // open: gt, lt
  Comparator #(.width(3), .mode("twosComplement")) comparator_38 (
    .a(multiplexer_46_out), .b(3'b110), .eq(comparator_38_eq));  // open: gt, lt
  Comparator #(.width(3), .mode("twosComplement")) comparator_39 (
    .a(multiplexer_46_out), .b(3'b111), .eq(comparator_39_eq));  // open: gt, lt
  and and_11 (SET0, BranchNotFound, comparator_32_eq);
  and and_12 (SET1, BranchNotFound, comparator_33_eq);
  and and_13 (SET2, BranchNotFound, comparator_34_eq);
  and and_14 (SET3, BranchNotFound, comparator_35_eq);
  and and_15 (SET4, BranchNotFound, comparator_36_eq);
  and and_16 (SET5, BranchNotFound, comparator_37_eq);
  and and_17 (SET6, BranchNotFound, comparator_38_eq);
  and and_18 (SET7, BranchNotFound, comparator_39_eq);

  // Other names for the same wires on the sheet: branchyes = EX_BranchTaken; enable = EX_Branch; Pr0 = PredictJump;
  //   Pr1 = PredictJump; Pr2 = PredictJump; Pr3 = PredictJump; Pr4 = PredictJump; Pr5 = PredictJump;
  //   Pr6 = PredictJump; Pr7 = PredictJump

  // Notes on the sheet:
  //   各种使能给错
endmodule

module \双位预测状态机  (
  input  A1,
  input  A0,
  input  branchyes,
  output B1,
  output B0
);

  wire and_1_out, and_2_out, and_3_out, and_4_out, not_1_out, not_2_out, not_3_out, not_4_out, not_5_out;

  not not_1 (not_1_out, A0);
  not not_2 (not_2_out, A1);
  not not_3 (not_3_out, A0);
  not not_4 (not_4_out, A0);
  not not_5 (not_5_out, branchyes);
  and and_1 (and_1_out, A0, branchyes);
  and and_2 (and_2_out, A1, not_1_out);
  and and_3 (and_3_out, not_2_out, not_3_out, branchyes);
  and and_4 (and_4_out, A1, not_4_out, not_5_out);
  or or_1 (B1, and_1_out, and_2_out);
  or or_2 (B0, and_3_out, and_4_out);
endmodule
module \动态分支预测与流水中断与重定向  (
  output RegWrite,
  output MemWrite,
  output [31:0] IF_PC,
  output [31:0] ID_PC,
  output [31:0] EX_PC,
  output [31:0] M_PC,
  output [31:0] WB_PC,
  output [31:0] RDin,
  output [31:0] MDin,
  output [31:0] LedData
);

  wire _1_2_out, _2_2_out, _3_2_out, ALuSrcB2, ALuSrcB3, and_3_out, and_4_out, and_6_out, and_7_out,
       and_8_out, and_9_out, Beq2, Beq3, Bne2, Bne3, \B系列3 , \B系列3指令 , CLK, clock_1_out, clock_2_out,
       comparator_1_eq, comparator_2_eq, comparator_3_eq, comparator_4_eq, comparator_5_eq, comparator_6_eq,
       comparator_7_eq, comparator_8_eq, comparator_9_eq, comparator_11_eq, comparator_12_eq,
       comparator_13_eq, comparator_13_lt, comparator_14_eq, comparator_15_eq, comparator_16_eq, d_ff_2_q,
       d_ff_3_q, d_ff_4_qn, d_ff_5_q, equal3, equal4, equal5, Eret, EX_Branch, EX_PredictErr, Go, IR1, IR2,
       IR3, IRA, IRB, IRC, Jal2, Jal3, Jal5, Jal_2_q, Jmp2, Jmp3, JR2, JR3, Loaduse, MemToReg2, MemToReg3,
       MemToReg5, MemToReg_2_q, MemWrite2, MemWrite_q, multiplexer_9_out, multiplexer_19_out,
       multiplexer_20_out, multiplexer_21_out, multiplexer_22_out, multiplexer_24_out, multiplexer_25_out,
       multiplexer_26_out, multiplexer_27_out, multiplexer_28_out, multiplexer_29_out, multiplexer_30_out,
       multiplexer_31_out, nand_1_out, not_1_out, not_2_out, not_4_out, not_5_out, not_6_out, or_2_out,
       or_3_out, or_4_out, or_5_out, or_7_out, or_8_out, or_9_out, or_10_out, or_12_out, or_14_out, \PC使能 ,
       predictjmp, predictjmp3, predictjmp_q, RegDst2, RegDst5, RegDst_2_q, RegDst_q, RegWrite2, RegWrite3,
       RegWrite4, RST, SignedExt, Syscall, Syscall3, Syscall4, Syscall5, W1, W2, W3, \中断可接收 ,
       \中断按键参考电路_1_有新中断 , \分支气泡 , \数据相关 , \有中断_Eret , \源寄存器使用情况_1_r1_used , \源寄存器使用情况_1_r2_used ;
  wire [1:0] byteoff5, multiplexer_39_out, multiplexer_40_out, RsForward2, RsForward3, RtForward2,
       RtForward3, \中断按键参考电路_1_优先中断编号 ;
  wire [1:1] comparator_10_eq;
  wire [3:0] ALuOP2, ALuOP3, multiplexer_23_out;
  wire [4:0] EX_WriteReg_num, MEM_WriteReg_num, multiplexer_13_out, multiplexer_14_out, multiplexer_15_out,
       multiplexer_17_out, multiplexer_18_out, multiplexer_37_out, Shmat3;
  wire [5:0] Func;
  wire [7:0] multiplexer_45_out;
  wire [12:0] CNT_num;
  wire [15:0] \LoadUse次数 , \插入气泡数 , \无条件分支数 , \条件分支成功数 ;
  wire [31:0] A2, A3, ALU3, ALU4, ALU5, B2, B3, B4, bit_extender_1_out, bit_extender_2_out,
       bit_extender_3_out, \B系列地址3 , EX_BranchPC, EX_IR, IF_IR, Imm2, Imm3, IR4, IR5, \J系列地址3 , MD4, MD5,
       multiplexer_2_out, multiplexer_4_out, multiplexer_5_out, multiplexer_6_out, multiplexer_8_out,
       multiplexer_10_out, multiplexer_11_out, multiplexer_12_out, multiplexer_32_out, multiplexer_33_out,
       multiplexer_34_out, multiplexer_35_out, multiplexer_36_out, multiplexer_38_out, multiplexer_43_out,
       multiplexer_44_out, NextPCNormal, PC1, PC2, PC3, PC5, PC_4_q, popeddata, ram_1_data, RealB3,
       shifter_1_out, \中断入口_返回地址 , \新动态分支预测_1_jumpaddr ;
  wire [31:6] ID_IR;

  Button \u_总复位  (.out(RST));
  Button _1 ();  // open: out
  Button _2 ();  // open: out
  Button _3 ();  // open: out
  // Probe on CNT_num
  // Probe on CNT_num
  Button \u_继续运行  (.out(Go));
  LED #(.active("true")) led_1 (.in(W1));
  LED #(.active("true")) led_2 (.in(W2));
  LED #(.active("true")) led_3 (.in(W3));
  Hex_Digit_Display hex_digit_display_1 (.value(LedData[31:28]));  // open: dp
  // Probe on IF_PC[19:0]
  // Mips_Probe mips_probe_1: pin names not known; wires that end beside it: IR1, IR2, IR3, IF_IR
  Button _1_2 (.out(_1_2_out));
  or or_1 (IR1, _1_2_out, IRA);
  not not_1 (not_1_out, Syscall5);
  Comparator #(.width(32), .mode("twosComplement")) comparator_1 (
    .a(EX_IR), .b(32'h40800000), .eq(comparator_1_eq));  // open: gt, lt
  Comparator #(.width(6), .mode("twosComplement")) comparator_2 (
    .a(IF_IR[31:26]), .b(6'b010000), .eq(comparator_2_eq));  // open: gt, lt
  Comparator #(.width(6), .mode("twosComplement")) comparator_3 (
    .a(IF_IR[5:0]), .b(6'b011000), .eq(comparator_3_eq));  // open: gt, lt
  Hex_Digit_Display hex_digit_display_2 (.value(LedData[27:24]));  // open: dp
  Hex_Digit_Display hex_digit_display_3 (.value(LedData[23:20]));  // open: dp
  // Probe on ID_PC[19:0]
  // Mips_Probe mips_probe_2: pin names not known; wires that end beside it: {ID_IR, Func}
  or or_2 (or_2_out, not_1_out, Go);
  or or_3 (or_3_out, equal5, not_1_out);
  Comparator #(.width(13), .mode("twosComplement")) comparator_4 (
    .a(13'h258), .b(CNT_num), .eq(comparator_4_eq));  // open: gt, lt
  Comparator #(.width(13), .mode("twosComplement")) comparator_5 (
    .a(CNT_num), .b(13'h1), .eq(comparator_5_eq));  // open: gt, lt
  Comparator #(.width(13), .mode("twosComplement")) comparator_6 (
    .a(CNT_num), .b(13'h4), .eq(comparator_6_eq));  // open: gt, lt
  Comparator #(.width(13), .mode("twosComplement")) comparator_7 (
    .a(CNT_num), .b(13'h7), .eq(comparator_7_eq));  // open: gt, lt
  or or_4 (or_4_out, comparator_7_eq, comparator_8_eq);
  Comparator #(.width(13), .mode("twosComplement")) comparator_8 (
    .a(CNT_num), .b(13'h241), .eq(comparator_8_eq));  // open: gt, lt
  \中断按键参考电路  \u_中断按键参考电路_1  (
    .\优先中断编号 (\中断按键参考电路_1_优先中断编号 ), .\_1号中断 (IR1), .\_2号中断 (IR2), .\_3号中断 (IR3), .\时钟 (CLK), .\异步清零信号 (RST),
    .\中断可接收 (\中断可接收 ), .\有新中断 (\中断按键参考电路_1_有新中断 ), .eret(Eret));
  or or_5 (or_5_out, comparator_1_eq, \中断可接收 );
  and and_1 (Eret, comparator_2_eq, comparator_3_eq);
  Comparator #(.width(32), .mode("twosComplement")) comparator_9 (
    .a(IF_IR), .b(32'h40000000), .eq(comparator_9_eq));  // open: gt, lt
  Comparator #(.width(32), .mode("unsigned")) comparator_10 (
    .a({ID_IR, Func}), .b({32{1'b0}}), .eq(comparator_10_eq[1]));  // open: gt, lt
  Hex_Digit_Display hex_digit_display_4 (.value(LedData[15:12]));  // open: dp
  Hex_Digit_Display hex_digit_display_5 (.value(LedData[19:16]));  // open: dp
  Button _2_2 (.out(_2_2_out));
  or or_6 (IR2, _2_2_out, IRB);
  D_Flip_Flop #(.trigger("falling"), .Pre_Clr_Positions("ABOVE_BELOW"), .NegatePresetClear("false"), .enable("false"), .NewFFLayout("true")) d_ff_1 (
    .clk(CLK), .D(or_3_out), .Q(\PC使能 ), .preset(or_2_out));  // open: Qn, reset
  Multiplexer #(.select(1), .width(32), .disabled("Z"), .enable("false")) multiplexer_1 (
    .in0(\J系列地址3 ), .in1(\B系列地址3 ), .out(EX_BranchPC), .sel(\B系列3指令 ));
  or or_7 (or_7_out, comparator_4_eq, comparator_5_eq);
  Pull_Resistor #(.pull(0)) pull_resistor_1 (.node(IRA));
  assign IRA = or_7_out ? ~CLK : 1'bz;  // Controlled_Inverter controlled_inverter_1
  Pull_Resistor #(.pull(0)) pull_resistor_2 (.node(IRB));
  assign IRB = comparator_6_eq ? ~CLK : 1'bz;  // Controlled_Inverter controlled_inverter_2
  Pull_Resistor #(.pull(0)) pull_resistor_3 (.node(IRC));
  assign IRC = or_4_out ? ~CLK : 1'bz;  // Controlled_Inverter controlled_inverter_3
  D_Flip_Flop #(.trigger("rising"), .Pre_Clr_Positions("LEGACY"), .NegatePresetClear("false"), .enable("true"), .NewFFLayout("false")) d_ff_2 (
    .clk(CLK), .D(or_5_out), .Q(d_ff_2_q), .reset(RST));  // open: Qn, preset, en
  D_Flip_Flop #(.trigger("rising"), .Pre_Clr_Positions("LEGACY"), .NegatePresetClear("false"), .enable("true"), .NewFFLayout("false")) d_ff_3 (
    .clk(CLK), .D(or_8_out), .Q(d_ff_3_q), .reset(RST));  // open: Qn, preset, en
  or or_8 (or_8_out, Eret, comparator_9_eq);
  Multiplexer #(.select(2), .width(32), .disabled("Z"), .enable("false")) multiplexer_2 (
    .in0(ID_PC), .in1(NextPCNormal), .in2(IF_PC), .in3(NextPCNormal), .out(multiplexer_2_out),
    .sel({comparator_10_eq[1], \分支气泡 }));
  or or_9 (or_9_out, \中断可接收 , Eret);
  Hex_Digit_Display hex_digit_display_6 (.value(LedData[7:4]));  // open: dp
  Hex_Digit_Display hex_digit_display_7 (.value(LedData[11:8]));  // open: dp
  Clock #(.highDuration(1), .lowDuration(1)) clock_1 (.out(clock_1_out));
  // Probe on EX_PC[19:0]
  // Mips_Probe mips_probe_3: pin names not known; wires that end beside it: clock_1_out, EX_IR, CLK
  Button _3_2 (.out(_3_2_out));
  D_Flip_Flop #(.trigger("rising"), .Pre_Clr_Positions("LEGACY"), .NegatePresetClear("false"), .enable("true"), .NewFFLayout("false")) d_ff_4 (
    .Qn(d_ff_4_qn), .preset(d_ff_2_q), .reset(or_10_out));  // open: clk, D, Q, en
  or or_10 (or_10_out, RST, d_ff_3_q);
  \硬件堆栈  \u_硬件堆栈_1  (
    .push_pop(Eret), .Enable(or_9_out), .CLK(CLK), .\总复位 (RST), .pusheddata(multiplexer_2_out),
    .popeddata(popeddata));
  Hex_Digit_Display hex_digit_display_8 (.value(LedData[3:0]));  // open: dp
  or or_11 (IR3, _3_2_out, IRC);
  Multiplexer #(.select(2), .width(32), .disabled("Z"), .enable("false")) multiplexer_3 (
    .in0(PC3), .in1(EX_BranchPC), .in2(EX_BranchPC), .out(NextPCNormal), .sel({\B系列3 , Jmp3}));  // open: in3
  Multiplexer #(.select(2), .width(32), .disabled("Z"), .enable("false")) multiplexer_4 (
    .in1(32'h30ac), .in2(32'h3158), .in3(32'h3204), .out(multiplexer_4_out), .sel(\中断按键参考电路_1_优先中断编号 ));  // open: in0
  // Probe on CNT_num
  // Probe on M_PC[19:0]
  // Mips_Probe mips_probe_4: pin names not known; wires that end beside it: IR4
  Multiplexer #(.select(1), .width(32), .disabled("Z"), .enable("false")) multiplexer_5 (
    .in0(multiplexer_8_out), .in1(NextPCNormal), .out(multiplexer_5_out), .sel(EX_PredictErr));
  and and_2 (\中断可接收 , \中断按键参考电路_1_有新中断 , d_ff_4_qn);
  // Probe on CNT_num
  // Probe on \无条件分支数 
  // Probe on \条件分支成功数 
  // Probe on \插入气泡数 
  // Probe on \LoadUse次数 
  Comparator #(.width(2), .mode("twosComplement")) comparator_11 (
    .a({\B系列3 , Jmp3}), .b(2'b00), .eq(comparator_11_eq));  // open: gt, lt
  Multiplexer #(.select(1), .width(32), .disabled("Z"), .enable("false")) multiplexer_6 (
    .in0(multiplexer_5_out), .in1(\中断入口_返回地址 ), .out(multiplexer_6_out), .sel(\有中断_Eret ));
  and and_3 (and_3_out, \PC使能 , not_2_out);
  not not_2 (not_2_out, Loaduse);
  or or_12 (or_12_out, \有中断_Eret , EX_PredictErr);
  and and_4 (and_4_out, \PC使能 , CLK);
  // Probe on IF_PC[11:0]
  // Probe on WB_PC[19:0]
  // Mips_Probe mips_probe_5: pin names not known; wires that end beside it: IR5
  not not_3 (\分支气泡 , comparator_11_eq);
  Register #(.width(32), .trigger("rising"), .Select("low")) PC (
    .D(multiplexer_6_out), .en(and_3_out), .Q(IF_PC), .clk(CLK), .clr(RST));
  Adder #(.width(32)) adder_1 (.a(IF_PC), .b(32'h4), .out(PC1));  // open: cin, cout
  \新动态分支预测  \u_新动态分支预测_1  (
    .CLK(CLK), .clear(RST), .PC(IF_PC), .EX_Branch(EX_Branch), .EX_BranchTaken(\分支气泡 ), .EX_PC(EX_PC),
    .EX_BranchAddr(EX_BranchPC), .PredictJump(predictjmp), .JumpAddr(\新动态分支预测_1_jumpaddr ));
  or or_13 (\有中断_Eret , \中断可接收 , Eret);
  Multiplexer #(.select(1), .width(32), .disabled("Z"), .enable("false")) multiplexer_7 (
    .in0(multiplexer_4_out), .in1(popeddata), .out(\中断入口_返回地址 ), .sel(Eret));
  not not_4 (not_4_out, Loaduse);
  // Probe on ID_PC[11:0]
  // Probe on EX_PC[11:0]
  Multiplexer #(.select(1), .width(32), .disabled("Z"), .enable("false")) multiplexer_8 (
    .in0(PC1), .in1(\新动态分支预测_1_jumpaddr ), .out(multiplexer_8_out), .sel(predictjmp));
  // Probe on M_PC[11:0]
  D_Flip_Flop #(.trigger("high"), .Pre_Clr_Positions("LEGACY"), .NegatePresetClear("false"), .enable("true"), .NewFFLayout("false")) d_ff_5 (.Q(d_ff_5_q));  // open: clk, D, Qn, preset, en, reset
  // Probe on 13'h3e8
  not not_5 (not_5_out, comparator_12_eq);
  Comparator #(.width(1), .mode("twosComplement")) comparator_12 (
    .a(\分支气泡 ), .b(predictjmp3), .eq(comparator_12_eq));  // open: gt, lt
  // Probe on WB_PC[11:0]
  Comparator #(.width(13), .mode("twosComplement")) comparator_13 (
    .a(CNT_num), .b(13'h3e8), .eq(comparator_13_eq), .lt(comparator_13_lt));  // open: gt
  Clock #(.highDuration(1), .lowDuration(1)) clock_2 (.out(clock_2_out));
  ROM #(.addrWidth(10), .dataWidth(32), .Select("high")) rom_1 (.addr(IF_PC[11:2]), .data(IF_IR));
  and and_5 (EX_PredictErr, EX_Branch, not_5_out);
  nand nand_1 (nand_1_out, d_ff_5_q, comparator_13_eq);
  Counter #(.width(13), .max('h1fff), .ongoal("stay"), .trigger("rising"), .behavior("old")) counter_1 (
    .count(\PC使能 ), .Q(CNT_num), .clk(clock_2_out));  // open: load, D, carry, clr, preset
  // Mips_Probe mips_probe_6: pin names not known; wires that end beside it: IF_IR
  assign CLK = nand_1_out ? clock_2_out : 1'bz;  // Controlled_Buffer controlled_buffer_1
  Multiplexer #(.select(1), .width(1), .disabled("Z"), .enable("false")) multiplexer_9 (
    .in0(predictjmp), .in1(1'b0), .out(multiplexer_9_out), .sel(or_12_out));
  Multiplexer #(.select(1), .width(32), .disabled("Z"), .enable("false")) multiplexer_10 (
    .in0(IF_IR), .in1({32{1'b0}}), .out(multiplexer_10_out), .sel(or_12_out));
  Multiplexer #(.select(1), .width(32), .disabled("Z"), .enable("false")) multiplexer_11 (
    .in0(PC1), .in1({32{1'b0}}), .out(multiplexer_11_out), .sel(or_12_out));
  Multiplexer #(.select(1), .width(32), .disabled("Z"), .enable("false")) multiplexer_12 (
    .in0(IF_PC), .in1({32{1'b0}}), .out(multiplexer_12_out), .sel(or_12_out));
  Pull_Resistor #(.pull(1)) pull_resistor_4 (.node(CLK));
  Register #(.width(1), .trigger("rising"), .Select("low")) u_predictjmp (
    .D(multiplexer_9_out), .en(not_4_out), .Q(predictjmp_q), .clk(and_4_out), .clr(RST));
  Register #(.width(32), .trigger("rising"), .Select("low")) IR (
    .D(multiplexer_10_out), .en(not_4_out), .Q({ID_IR, Func}), .clk(and_4_out), .clr(RST));
  Register #(.width(32), .trigger("rising"), .Select("low")) PC_2 (
    .D(multiplexer_11_out), .en(not_4_out), .Q(PC2), .clk(and_4_out), .clr(RST));
  Register #(.width(32), .trigger("rising"), .Select("low")) PCO (
    .D(multiplexer_12_out), .en(not_4_out), .Q(ID_PC), .clk(and_4_out), .clr(RST));
  // Mips_Probe mips_probe_7: pin names not known; wires that end beside it: {ID_IR, Func}
  \单周期硬布线控制器  \u_单周期硬布线控制器_1  (
    .Func(Func), .OP(ID_IR[31:26]), .ALU_OP(ALuOP2), .MemToReg(MemToReg2), .MemWrite(MemWrite2),
    .ALU_SRC(ALuSrcB2), .RegWrite(RegWrite2), .SysCALL(Syscall), .SignedExt(SignedExt), .RegDst(RegDst2),
    .JR(JR2), .JMP(Jmp2), .Beq(Beq2), .JAL(Jal2), .Bne(Bne2));
  Multiplexer #(.select(1), .width(5), .disabled("Z"), .enable("false")) multiplexer_13 (
    .in0(ID_IR[25:21]), .in1(5'b00010), .out(multiplexer_13_out), .sel(Syscall));
  Multiplexer #(.select(2), .width(5), .disabled("Z"), .enable("false")) multiplexer_14 (
    .in0(IR5[20:16]), .in1(IR5[15:11]), .in2({5{1'b1}}), .out(multiplexer_14_out), .sel({Jal5, RegDst5}));  // open: in3
  Multiplexer #(.select(1), .width(5), .disabled("Z"), .enable("false")) multiplexer_15 (
    .in0(ID_IR[20:16]), .in1(5'b00100), .out(multiplexer_15_out), .sel(Syscall));
  or or_14 (or_14_out, or_12_out, Loaduse);
  assign bit_extender_1_out = {{16{1'b0}}, {ID_IR[15:6], Func}};  // Bit_Extender bit_extender_1
  Multiplexer #(.select(1), .width(32), .disabled("Z"), .enable("false")) multiplexer_16 (
    .in0(bit_extender_1_out), .in1(bit_extender_2_out), .out(Imm2), .sel(SignedExt));
  assign bit_extender_2_out = {{16{ID_IR[15]}}, {ID_IR[15:6], Func}};  // Bit_Extender bit_extender_2
  Multiplexer #(.select(2), .width(5), .disabled("Z"), .enable("false")) multiplexer_17 (
    .in0(ID_IR[20:16]), .in1(ID_IR[15:11]), .in2({5{1'b1}}), .out(multiplexer_17_out), .sel({Jal2, RegDst2}));  // open: in3
  \源寄存器使用情况  \u_源寄存器使用情况_1  (
    .OP0(ID_IR[26]), .OP1(ID_IR[27]), .OP2(ID_IR[28]), .OP3(ID_IR[29]), .OP4(ID_IR[30]), .OP5(ID_IR[31]),
    .F0(Func[0]), .F1(Func[1]), .F2(Func[2]), .F3(Func[3]), .F4(Func[4]), .F5(Func[5]),
    .R1_used(\源寄存器使用情况_1_r1_used ), .R2_used(\源寄存器使用情况_1_r2_used ));
  MIPS_Regifile mips_regifile_1 (
    .Din(RDin), .Clk(CLK), .R1(A2), .R2(B2), .WE(RegWrite), .W_num(multiplexer_14_out),
    .R1_num(multiplexer_13_out), .R2_num(multiplexer_15_out));
  Multiplexer #(.select(1), .width(5), .disabled("Z"), .enable("false")) multiplexer_18 (
    .in0(multiplexer_17_out), .in1({5{1'b0}}), .out(multiplexer_18_out), .sel(or_14_out));
  Multiplexer #(.select(1), .width(1), .disabled("Z"), .enable("false")) multiplexer_19 (
    .in0(MemToReg2), .in1(1'b0), .out(multiplexer_19_out), .sel(or_14_out));
  Multiplexer #(.select(1), .width(1), .disabled("Z"), .enable("false")) multiplexer_20 (
    .in0(RegDst2), .in1(1'b0), .out(multiplexer_20_out), .sel(or_14_out));
  Multiplexer #(.select(1), .width(1), .disabled("Z"), .enable("false")) multiplexer_21 (
    .in0(RegWrite2), .in1(1'b0), .out(multiplexer_21_out), .sel(or_14_out));
  Multiplexer #(.select(1), .width(1), .disabled("Z"), .enable("false")) multiplexer_22 (
    .in0(MemWrite2), .in1(1'b0), .out(multiplexer_22_out), .sel(or_14_out));
  Multiplexer #(.select(1), .width(4), .disabled("Z"), .enable("false")) multiplexer_23 (
    .in0(ALuOP2), .in1(4'b0000), .out(multiplexer_23_out), .sel(or_14_out));
  Multiplexer #(.select(1), .width(1), .disabled("Z"), .enable("false")) multiplexer_24 (
    .in0(ALuSrcB2), .in1(1'b0), .out(multiplexer_24_out), .sel(or_14_out));
  Multiplexer #(.select(1), .width(1), .disabled("Z"), .enable("false")) multiplexer_25 (
    .in0(Syscall), .in1(1'b0), .out(multiplexer_25_out), .sel(or_14_out));
  Multiplexer #(.select(1), .width(1), .disabled("Z"), .enable("false")) multiplexer_26 (
    .in0(Bne2), .in1(1'b0), .out(multiplexer_26_out), .sel(or_14_out));
  Multiplexer #(.select(1), .width(1), .disabled("Z"), .enable("false")) multiplexer_27 (
    .in0(Beq2), .in1(1'b0), .out(multiplexer_27_out), .sel(or_14_out));
  Multiplexer #(.select(1), .width(1), .disabled("Z"), .enable("false")) multiplexer_28 (
    .in0(Jal2), .in1(1'b0), .out(multiplexer_28_out), .sel(or_14_out));
  Multiplexer #(.select(1), .width(1), .disabled("Z"), .enable("false")) multiplexer_29 (
    .in0(Jmp2), .in1(1'b0), .out(multiplexer_29_out), .sel(or_14_out));
  Multiplexer #(.select(1), .width(1), .disabled("Z"), .enable("false")) multiplexer_30 (
    .in0(JR2), .in1(1'b0), .out(multiplexer_30_out), .sel(or_14_out));
  Multiplexer #(.select(1), .width(1), .disabled("Z"), .enable("false")) multiplexer_31 (
    .in0(predictjmp_q), .in1(1'b0), .out(multiplexer_31_out), .sel(or_14_out));
  Multiplexer #(.select(1), .width(32), .disabled("Z"), .enable("false")) multiplexer_32 (
    .in0({ID_IR, Func}), .in1({32{1'b0}}), .out(multiplexer_32_out), .sel(or_14_out));
  Multiplexer #(.select(1), .width(32), .disabled("Z"), .enable("false")) multiplexer_33 (
    .in0(PC2), .in1({32{1'b0}}), .out(multiplexer_33_out), .sel(or_14_out));
  Multiplexer #(.select(1), .width(32), .disabled("Z"), .enable("false")) multiplexer_34 (
    .in0(A2), .in1({32{1'b0}}), .out(multiplexer_34_out), .sel(or_14_out));
  Multiplexer #(.select(1), .width(32), .disabled("Z"), .enable("false")) multiplexer_35 (
    .in0(B2), .in1({32{1'b0}}), .out(multiplexer_35_out), .sel(or_14_out));
  Multiplexer #(.select(1), .width(32), .disabled("Z"), .enable("false")) multiplexer_36 (
    .in0(Imm2), .in1({32{1'b0}}), .out(multiplexer_36_out), .sel(or_14_out));
  Multiplexer #(.select(1), .width(5), .disabled("Z"), .enable("false")) multiplexer_37 (
    .in0(ID_IR[10:6]), .in1({5{1'b0}}), .out(multiplexer_37_out), .sel(or_14_out));
  Multiplexer #(.select(1), .width(32), .disabled("Z"), .enable("false")) multiplexer_38 (
    .in0(ID_PC), .in1({32{1'b0}}), .out(multiplexer_38_out), .sel(or_14_out));
  Multiplexer #(.select(1), .width(2), .disabled("Z"), .enable("false")) multiplexer_39 (
    .in0(RsForward2), .in1(2'b00), .out(multiplexer_39_out), .sel(or_14_out));
  Multiplexer #(.select(1), .width(2), .disabled("Z"), .enable("false")) multiplexer_40 (
    .in0(RtForward2), .in1(2'b00), .out(multiplexer_40_out), .sel(or_14_out));
  Register #(.width(5), .trigger("rising"), .Select("low")) \u_假WriteReg_num  (
    .D(multiplexer_18_out), .Q(EX_WriteReg_num), .clk(and_4_out), .clr(RST));  // open: en
  Register #(.width(1), .trigger("rising"), .Select("low")) MemToReg (
    .D(multiplexer_19_out), .Q(MemToReg3), .clk(and_4_out), .clr(RST));  // open: en
  Register #(.width(1), .trigger("rising"), .Select("low")) RegDst (
    .D(multiplexer_20_out), .Q(RegDst_q), .clk(and_4_out), .clr(RST));  // open: en
  Register #(.width(1), .trigger("rising"), .Select("low")) u_RegWrite (
    .D(multiplexer_21_out), .Q(RegWrite3), .clk(and_4_out), .clr(RST));  // open: en
  Register #(.width(1), .trigger("rising"), .Select("low")) u_MemWrite (
    .D(multiplexer_22_out), .Q(MemWrite_q), .clk(and_4_out), .clr(RST));  // open: en
  Register #(.width(4), .trigger("rising"), .Select("low")) ALuOP (
    .D(multiplexer_23_out), .Q(ALuOP3), .clk(and_4_out), .clr(RST));  // open: en
  Register #(.width(1), .trigger("rising"), .Select("low")) ALuSrcB (
    .D(multiplexer_24_out), .Q(ALuSrcB3), .clk(and_4_out), .clr(RST));  // open: en
  Register #(.width(1), .trigger("rising"), .Select("low")) u_Syscall (
    .D(multiplexer_25_out), .Q(Syscall3), .clk(and_4_out), .clr(RST));  // open: en
  Register #(.width(1), .trigger("rising"), .Select("low")) Bne (
    .D(multiplexer_26_out), .Q(Bne3), .clk(and_4_out), .clr(RST));  // open: en
  Register #(.width(1), .trigger("rising"), .Select("low")) Beq (
    .D(multiplexer_27_out), .Q(Beq3), .clk(and_4_out), .clr(RST));  // open: en
  Register #(.width(1), .trigger("rising"), .Select("low")) Jal (
    .D(multiplexer_28_out), .Q(Jal3), .clk(and_4_out), .clr(RST));  // open: en
  Register #(.width(1), .trigger("rising"), .Select("low")) Jmp (
    .D(multiplexer_29_out), .Q(Jmp3), .clk(and_4_out), .clr(RST));  // open: en
  Register #(.width(1), .trigger("rising"), .Select("low")) JR (
    .D(multiplexer_30_out), .Q(JR3), .clk(and_4_out), .clr(RST));  // open: en
  Register #(.width(1), .trigger("rising"), .Select("low")) predictjmp_2 (
    .D(multiplexer_31_out), .Q(predictjmp3), .clk(and_4_out), .clr(RST));  // open: en
  Register #(.width(32), .trigger("rising"), .Select("low")) IR_2 (
    .D(multiplexer_32_out), .Q(EX_IR), .clk(and_4_out), .clr(RST));  // open: en
  Register #(.width(32), .trigger("rising"), .Select("low")) PC_3 (
    .D(multiplexer_33_out), .Q(PC3), .clk(and_4_out), .clr(RST));  // open: en
  Register #(.width(32), .trigger("rising"), .Select("low")) A (
    .D(multiplexer_34_out), .Q(A3), .clk(and_4_out), .clr(RST));  // open: en
  Register #(.width(32), .trigger("rising"), .Select("low")) B (
    .D(multiplexer_35_out), .Q(B3), .clk(and_4_out), .clr(RST));  // open: en
  Register #(.width(32), .trigger("rising"), .Select("low")) Imm (
    .D(multiplexer_36_out), .Q(Imm3), .clk(and_4_out), .clr(RST));  // open: en
  Register #(.width(5), .trigger("rising"), .Select("low")) Shmat (
    .D(multiplexer_37_out), .Q(Shmat3), .clk(and_4_out), .clr(RST));  // open: en
  Register #(.width(32), .trigger("rising"), .Select("low")) PCO_2 (
    .D(multiplexer_38_out), .Q(EX_PC), .clk(and_4_out), .clr(RST));  // open: en
  Register #(.width(2), .trigger("rising"), .Select("low")) RsForward (
    .D(multiplexer_39_out), .Q(RsForward3), .clk(and_4_out), .clr(RST));  // open: en
  Register #(.width(2), .trigger("rising"), .Select("low")) RtForward (
    .D(multiplexer_40_out), .Q(RtForward3), .clk(and_4_out), .clr(RST));  // open: en
  \重定向数据相关检测  \u_重定向数据相关检测_1  (
    .EX_WriteReg_num(EX_WriteReg_num), .R1_Used(\源寄存器使用情况_1_r1_used ), .R1_num(multiplexer_13_out),
    .R2_Used(\源寄存器使用情况_1_r2_used ), .R2_num(multiplexer_15_out), .MEM_WriteReg_num(MEM_WriteReg_num),
    .RegWrite3(RegWrite3), .Yes(\数据相关 ), .LoadUse(Loaduse), .EX_MemRead(MemToReg3), .RsForward(RsForward2),
    .RtForward(RtForward2), .RegWrite4(RegWrite4));
  Multiplexer #(.select(2), .width(32), .disabled("Z"), .enable("false")) multiplexer_41 (
    .in0(B3), .in1(RDin), .in2(ALU4), .out(RealB3), .sel(RtForward3));  // open: in3
  Multiplexer #(.select(1), .width(32), .disabled("Z"), .enable("false")) multiplexer_42 (
    .in0({EX_PC[31:28], EX_IR[25:0], 2'b00}), .in1(A3), .out(\J系列地址3 ), .sel(JR3));
  // Mips_Probe mips_probe_8: pin names not known; wires that end beside it: EX_IR
  or or_15 (\B系列3指令 , comparator_15_eq, Bne3, Beq3);
  Multiplexer #(.select(2), .width(32), .disabled("Z"), .enable("false")) multiplexer_43 (
    .in0(RealB3), .in1(Imm3), .in2(32'h22), .out(multiplexer_43_out), .sel({Syscall3, ALuSrcB3}));  // open: in3
  Shifter #(.width(32), .shift("ll")) shifter_1 (.in(Imm3), .\dist (5'b00010), .out(shifter_1_out));
  Adder #(.width(32)) adder_2 (.a(shifter_1_out), .b(PC3), .out(\B系列地址3 ), .cin(1'b0));  // open: cout
  Register #(.width(5), .trigger("rising"), .Select("low")) \u_假WriteReg_num_2  (
    .D(EX_WriteReg_num), .Q(MEM_WriteReg_num), .clk(and_4_out), .clr(RST));  // open: en
  Register #(.width(1), .trigger("rising"), .Select("low")) MemToReg_2 (
    .D(MemToReg3), .Q(MemToReg_2_q), .clk(and_4_out), .clr(RST));  // open: en
  Register #(.width(1), .trigger("rising"), .Select("low")) RegDst_2 (
    .D(RegDst_q), .Q(RegDst_2_q), .clk(and_4_out), .clr(RST));  // open: en
  Register #(.width(1), .trigger("rising"), .Select("low")) RegWrite_2 (
    .D(RegWrite3), .Q(RegWrite4), .clk(and_4_out), .clr(RST));  // open: en
  Register #(.width(1), .trigger("rising"), .Select("low")) MemWrite_2 (
    .D(MemWrite_q), .Q(MemWrite), .clk(and_4_out), .clr(RST));  // open: en
  Register #(.width(1), .trigger("rising"), .Select("low")) Syscall_2 (
    .D(Syscall3), .Q(Syscall4), .clk(and_4_out), .clr(RST));  // open: en
  Register #(.width(1), .trigger("rising"), .Select("low")) equal (
    .D(equal3), .Q(equal4), .clk(and_4_out), .clr(RST));  // open: en
  Register #(.width(1), .trigger("rising"), .Select("low")) Jal_2 (
    .D(Jal3), .Q(Jal_2_q), .clk(and_4_out), .clr(RST));  // open: en
  Register #(.width(32), .trigger("rising"), .Select("low")) IR_3 (
    .D(EX_IR), .Q(IR4), .clk(and_4_out), .clr(RST));  // open: en
  Register #(.width(32), .trigger("rising"), .Select("low")) PC_4 (
    .D(PC3), .Q(PC_4_q), .clk(and_4_out), .clr(RST));  // open: en
  Register #(.width(32), .trigger("rising"), .Select("low")) B_2 (
    .D(B3), .Q(B4), .clk(and_4_out), .clr(RST));  // open: en
  Register #(.width(32), .trigger("rising"), .Select("low")) ALU (
    .D(ALU3), .Q(ALU4), .clk(and_4_out), .clr(RST));  // open: en
  Register #(.width(32), .trigger("rising"), .Select("low")) RealB (
    .D(RealB3), .Q(MDin), .clk(and_4_out), .clr(RST));  // open: en
  Register #(.width(32), .trigger("rising"), .Select("low")) PCO_3 (
    .D(EX_PC), .Q(M_PC), .clk(and_4_out), .clr(RST));  // open: en
  or or_16 (\B系列3 , and_7_out, and_8_out, and_6_out);
  Multiplexer #(.select(2), .width(32), .disabled("Z"), .enable("false")) multiplexer_44 (
    .in0(A3), .in1(RDin), .in2(ALU4), .out(multiplexer_44_out), .sel(RsForward3));  // open: in3
  Comparator #(.width(32), .mode("twosComplement")) comparator_14 (
    .a(32'h1), .b(ALU3), .eq(comparator_14_eq));  // open: gt, lt
  Comparator #(.width(6), .mode("twosComplement")) comparator_15 (
    .a(EX_IR[31:26]), .b(6'b000001), .eq(comparator_15_eq));  // open: gt, lt
  and and_6 (and_6_out, Beq3, equal3);
  MIPS_ALU mips_alu_1 (
    .X(multiplexer_44_out), .Y(multiplexer_43_out), .AluOP(ALuOP3), .Equal(equal3), .Result(ALU3),
    .shamt(Shmat3));  // open: Result_2
  or or_17 (EX_Branch, JR3, Jal3, Jmp3, Beq3, Bne3, comparator_15_eq);
  and and_7 (and_7_out, comparator_15_eq, comparator_14_eq);
  and and_8 (and_8_out, not_6_out, Bne3);
  not not_6 (not_6_out, equal3);
  Register #(.width(32), .trigger("rising"), .Select("low")) register_1 (
    .D(RealB3), .en(and_9_out), .Q(LedData), .clk(CLK), .clr(RST));
  and and_9 (and_9_out, Syscall3, equal3);
  Register #(.width(1), .trigger("rising"), .Select("low")) MemToReg_3 (
    .D(MemToReg_2_q), .Q(MemToReg5), .clk(and_4_out), .clr(RST));  // open: en
  Register #(.width(1), .trigger("rising"), .Select("low")) RegDst_3 (
    .D(RegDst_2_q), .Q(RegDst5), .clk(and_4_out), .clr(RST));  // open: en
  Register #(.width(1), .trigger("rising"), .Select("low")) RegWrite_3 (
    .D(RegWrite4), .Q(RegWrite), .clk(and_4_out), .clr(RST));  // open: en
  Register #(.width(1), .trigger("rising"), .Select("low")) Syscall_3 (
    .D(Syscall4), .Q(Syscall5), .clk(and_4_out), .clr(RST));  // open: en
  Register #(.width(1), .trigger("rising"), .Select("low")) equal_2 (
    .D(equal4), .Q(equal5), .clk(and_4_out), .clr(RST));  // open: en
  Register #(.width(1), .trigger("rising"), .Select("low")) Jal_3 (
    .D(Jal_2_q), .Q(Jal5), .clk(and_4_out), .clr(RST));  // open: en
  Register #(.width(32), .trigger("rising"), .Select("low")) IR_4 (
    .D(IR4), .Q(IR5), .clk(and_4_out), .clr(RST));  // open: en
  Register #(.width(32), .trigger("rising"), .Select("low")) PC_5 (
    .D(PC_4_q), .Q(PC5), .clk(and_4_out), .clr(RST));  // open: en
  Register #(.width(32), .trigger("rising"), .Select("low")) ALU_2 (
    .D(ALU4), .Q(ALU5), .clk(and_4_out), .clr(RST));  // open: en
  Register #(.width(32), .trigger("rising"), .Select("low")) MD (
    .D(MD4), .Q(MD5), .clk(and_4_out), .clr(RST));  // open: en
  Register #(.width(32), .trigger("rising"), .Select("low")) PCO_4 (
    .D(M_PC), .Q(WB_PC), .clk(and_4_out), .clr(RST));  // open: en
  Register #(.width(2), .trigger("rising"), .Select("low")) byteoff (
    .D(ALU4[1:0]), .Q(byteoff5), .clk(and_4_out), .clr(RST));  // open: en
  // Mips_Probe mips_probe_9: pin names not known; wires that end beside it: IR4
  RAM #(.addrWidth(10), .dataWidth(32), .bus("separate"), .Select("high")) ram_1 (
    .addr(ALU4[11:2]), .din(MDin), .data(ram_1_data), .str(MemWrite), .clk(CLK), .clr(RST));  // open: sel, ld
  Comparator #(.width(6), .mode("twosComplement")) comparator_16 (
    .a(IR4[31:26]), .b(6'b100100), .eq(comparator_16_eq));  // open: gt, lt
  Multiplexer #(.select(2), .width(8), .disabled("Z"), .enable("false")) multiplexer_45 (
    .in0(ram_1_data[7:0]), .in1(ram_1_data[15:8]), .in2(ram_1_data[23:16]), .in3(ram_1_data[31:24]),
    .out(multiplexer_45_out), .sel(ALU4[1:0]));
  Multiplexer #(.select(1), .width(32), .disabled("Z"), .enable("false")) multiplexer_46 (
    .in0(ram_1_data), .in1(bit_extender_3_out), .out(MD4), .sel(comparator_16_eq));
  assign bit_extender_3_out = {{24{1'b0}}, multiplexer_45_out};  // Bit_Extender bit_extender_3
  // Mips_Probe mips_probe_10: pin names not known; wires that end beside it: IR5
  Multiplexer #(.select(2), .width(32), .disabled("Z"), .enable("false")) multiplexer_47 (
    .in0(ALU5), .in1(MD5), .in2(PC5), .out(RDin), .sel({Jal5, MemToReg5}));  // open: in3

  // Other names for the same wires on the sheet: byteoff[1:0] = ALU4[1:0]; IRNO1[31:0] = IF_IR; ID_IR[5:0] = Func;
  //   IR[31:0] = {ID_IR, Func}; IRNO2[31:0] = {ID_IR, Func}; Shmat2[4:0] = ID_IR[10:6]; OP[5:0] = ID_IR[31:26];
  //   IRNO3[31:0] = EX_IR; MEM_IR[31:0] = IR4; MEM_PC[31:0] = M_PC; MemWrite4 = MemWrite; PC[31:0] = IF_PC;
  //   PCO1[31:0] = IF_PC; PCO3[31:0] = EX_PC; RDin1[31:0] = RDin; RealB4[31:0] = MDin; RegWrite5 = RegWrite;
  //   result[31:0] = ALU3; Syscall2 = Syscall; WB_IR[31:0] = IR5; 总周期数[12:0] = CNT_num; 总复位 = RST

  // Notes on the sheet:
  //   中断源
  //   时空图监测，可删除
  //   中断等待指示
  //   多级中断测试信号模拟器
  //   简化mtc0指令支持
  //   Eret指令支持
  //   简化mfc0指令支持
  //   Syscall停机功能模块
  //   数码管输出
  //   EPC硬件堆栈
  //   关中断与开中断寄存器
  //   中断支持硬件
  //   控制位
  //   流水调试日志用
  //   暂停节拍，不能为0
  //   戳工具置1进入计数暂停模式，ctrl+k时钟自动运行到对应节拍暂停
  //   ctrl+k关闭时钟连续运行，将控制位置零，进入单步调试模式调试
  //   指令存储器
  //   contents of rom_1 (hex, n*v repeats v):
  //   201d07d0 20100001 109fc0 139fc3 8021 2012000c 24160008 26100001 3210000f 20080008 20090001 139900
  //   2709825 132020 20020022 c 1094022 1500fff9 22100001 2018000f 2188024 108700 20080008 20090001 139902
  //   2709825 132021 20020022 c 1094022 1500fff9 108702 2c9b022 12c00001 8000c07 4020 1084027 84400
  //   3508ffff 82021 20020022 c 8000c01 afa20000 23bd0004 afa40000 23bd0004 afb00000 23bd0004 afb30000
  //   23bd0004 afb40000 23bd0004 afb50000 23bd0004 afb60000 23bd0004 40000000 20160001 20140003 20150001
  //   168020 108100 2149825 132020 20020022 c 1600fffa 295a022 1680fff7 40800000 23bdfffc 8fb60000
  //   23bdfffc 8fb50000 23bdfffc 8fb40000 23bdfffc 8fb30000 23bdfffc 8fb00000 23bdfffc 8fa40000 23bdfffc
  //   8fa20000 42000018 afa20000 23bd0004 afa40000 23bd0004 afb00000 23bd0004 afb30000 23bd0004 afb40000
  //   23bd0004 afb50000 23bd0004 afb60000 23bd0004 40000000 20160002 20140003 20150001 168020 108100
  //   2149825 132020 20020022 c 1600fffa 295a022 1680fff7 40800000 23bdfffc 8fb60000 23bdfffc 8fb50000
  //   23bdfffc 8fb40000 23bdfffc 8fb30000 23bdfffc 8fb00000 23bdfffc 8fa40000 23bdfffc 8fa20000 42000018
  //   afa20000 23bd0004 afa40000 23bd0004 afb00000 23bd0004 afb30000 23bd0004 afb40000 23bd0004 afb50000
  //   23bd0004 afb60000 23bd0004 40000000 20160003 20140003 20150001 168020 108100 2149825 132020 20020022
  //   c 1600fffa 295a022 1680fff7 40800000 23bdfffc 8fb60000 23bdfffc 8fb50000 23bdfffc 8fb40000 23bdfffc
  //   8fb30000 23bdfffc 8fb00000 23bdfffc 8fa40000 23bdfffc 8fa20000 42000018
  //   可计数暂停的时钟源
  //   IF/ID
  //   指令字
  //   JMP
  //   JR
  //   OP
  //   Func
  //   Syscall
  //   rs
  //   rt
  //   rd
  //   为方便自动评测，需要输出流水线各段保存的PC值，注意是PC不是PC+4，另外ID段寄存器写入信息，Mem段内存写入信息也要输出
  //   Beq
  //   Bne
  //   rd
  //   ID/EX
  //   EX/MEM
  //   MEM/WB
endmodule
